// Logisim project 第6章例题电路的实现.circ as structural Verilog: 8 circuits, main circuit 例题6.1
module \例题6_1  (
  output Z
);

  wire clock_1_out, x, y1, y2;

  Clock #(.highDuration(1), .lowDuration(1)) clock_1 (.out(clock_1_out));
  Button u_x (.out(x));
  // Digital_Oscilloscope #(.nState(35), .frontlines("rising"), .showclock("true")) digital_oscilloscope_1: pin names not known; wires that end beside it: clock_1_out, x, y2, y1, Z
  J_K_Flip_Flop #(.trigger("falling"), .Pre_Clr_Positions("ABOVE_BELOW"), .NegatePresetClear("false"), .enable("false"), .NewFFLayout("true")) j_k_ff_1 (
    .J(1'b1), .clk(y1), .K(1'b1), .Q(y2));  // open: Qn, preset, reset
  J_K_Flip_Flop #(.trigger("falling"), .Pre_Clr_Positions("ABOVE_BELOW"), .NegatePresetClear("false"), .enable("false"), .NewFFLayout("true")) j_k_ff_2 (
    .J(1'b1), .clk(x), .K(1'b1), .Q(y1));  // open: Qn, preset, reset
  and and_1 (Z, y2, x, y1);
  // Probe on y2
  // Probe on y1

  // Notes on the sheet:
  //   y2
  //   y1
endmodule

module \例题6_2_1  (
  output Z
);

  wire and_1_out, and_2_out, and_3_out, and_4_out, and_5_out, clock_1_out, nand_1_out, nor_1_out, nor_2_out,
       not_1_out, not_2_out, not_3_out, not_4_out, not_5_out, s_r_ff_1_qn, s_r_ff_2_qn, x1, x2, x3, y1, y2;

  Clock #(.highDuration(1), .lowDuration(1)) clock_1 (.out(clock_1_out));
  Button u_x1 (.out(x1));
  Button u_x2 (.out(x2));
  Button u_x3 (.out(x3));
  // Digital_Oscilloscope #(.nState(35), .frontlines("rising"), .showclock("true")) digital_oscilloscope_1: pin names not known; wires that end beside it: clock_1_out, x1, x2, x3, y2, y1, Z
  not not_1 (not_1_out, x1);
  and and_1 (and_1_out, x2, y1);
  and and_2 (and_2_out, x3, x3);
  nand nand_1 (nand_1_out, x2, y2, s_r_ff_2_qn);
  and and_3 (and_3_out, x1, x1);
  and and_4 (and_4_out, x3, s_r_ff_1_qn);
  and and_5 (and_5_out, x2, y1);
  nor nor_1 (nor_1_out, and_1_out, and_2_out);
  nor nor_2 (nor_2_out, and_3_out, and_4_out, and_5_out);
  not not_2 (not_2_out, not_1_out);
  not not_3 (not_3_out, nor_1_out);
  not not_4 (not_4_out, nand_1_out);
  not not_5 (not_5_out, nor_2_out);
  S_R_Flip_Flop #(.trigger("latch"), .Pre_Clr_Positions("ABOVE_BELOW"), .NegatePresetClear("false"), .enable("false"), .NewFFLayout("true")) s_r_ff_1 (
    .S(not_2_out), .R(not_3_out), .Q(y2), .Qn(s_r_ff_1_qn));  // open: preset, reset
  S_R_Flip_Flop #(.trigger("latch"), .Pre_Clr_Positions("ABOVE_BELOW"), .NegatePresetClear("false"), .enable("false"), .NewFFLayout("true")) s_r_ff_2 (
    .S(not_4_out), .R(not_5_out), .Q(y1), .Qn(s_r_ff_2_qn));  // open: preset, reset
  // Probe on y2
  nor nor_3 (Z, y2, s_r_ff_2_qn);
  // Probe on y1

  // Notes on the sheet:
  //   y2
  //   y1
endmodule

module \例题6_2_2  (
  output Z
);

  wire and_1_out, and_2_out, and_3_out, and_4_out, and_5_out, clock_1_out, nand_1_out, nor_1_out, nor_2_out,
       not_1_out, not_2_out, not_3_out, not_4_out, not_5_out, s_r_ff_1_q, s_r_ff_1_qn, s_r_ff_2_q,
       s_r_ff_2_qn, x1, x2, x3, y1, y2, \延时_2_y , \延时_4_y ;

  Clock #(.highDuration(1), .lowDuration(1)) clock_1 (.out(clock_1_out));
  Button u_x1 (.out(x1));
  Button u_x2 (.out(x2));
  Button u_x3 (.out(x3));
  // Digital_Oscilloscope #(.nState(35), .frontlines("rising"), .showclock("true")) digital_oscilloscope_1: pin names not known; wires that end beside it: clock_1_out, x1, x2, x3, y2, y1, Z
  not not_1 (not_1_out, x1);
  and and_1 (and_1_out, x2, y1);
  and and_2 (and_2_out, x3, x3);
  nand nand_1 (nand_1_out, x2, y2, \延时_4_y );
  and and_3 (and_3_out, x1, x1);
  and and_4 (and_4_out, x3, \延时_2_y );
  and and_5 (and_5_out, x2, y1);
  nor nor_1 (nor_1_out, and_1_out, and_2_out);
  nor nor_2 (nor_2_out, and_3_out, and_4_out, and_5_out);
  not not_2 (not_2_out, not_1_out);
  not not_3 (not_3_out, nor_1_out);
  not not_4 (not_4_out, nand_1_out);
  not not_5 (not_5_out, nor_2_out);
  \延时  \u_延时_1  (.x(s_r_ff_1_q), .y(y2));
  S_R_Flip_Flop #(.trigger("latch"), .Pre_Clr_Positions("ABOVE_BELOW"), .NegatePresetClear("true"), .enable("false"), .NewFFLayout("true")) s_r_ff_1 (
    .S(not_2_out), .R(not_3_out), .Q(s_r_ff_1_q), .Qn(s_r_ff_1_qn));  // open: preset, reset
  \延时  \u_延时_2  (.x(s_r_ff_1_qn), .y(\延时_2_y ));
  \延时  \u_延时_3  (.x(s_r_ff_2_q), .y(y1));
  S_R_Flip_Flop #(.trigger("latch"), .Pre_Clr_Positions("ABOVE_BELOW"), .NegatePresetClear("true"), .enable("false"), .NewFFLayout("true")) s_r_ff_2 (
    .S(not_4_out), .R(not_5_out), .Q(s_r_ff_2_q), .Qn(s_r_ff_2_qn));  // open: preset, reset
  \延时  \u_延时_4  (.x(s_r_ff_2_qn), .y(\延时_4_y ));
  // Probe on y2
  nor nor_3 (Z, y2, \延时_4_y );
  // Probe on y1

  // Notes on the sheet:
  //   y2
  //   y1
endmodule

module \例题6_3  (
  output Z
);

  wire and_1_out, and_2_out, and_3_out, and_4_out, clock_1_out, d_ff_1_qn, d_ff_2_qn, or_1_out, or_2_out, x1,
       x2, y1, y2;

  Button u_x1 (.out(x1));
  Button u_x2 (.out(x2));
  Clock #(.highDuration(1), .lowDuration(1)) clock_1 (.out(clock_1_out));
  // Digital_Oscilloscope #(.nState(35), .frontlines("rising"), .showclock("true")) digital_oscilloscope_1: pin names not known; wires that end beside it: clock_1_out, x1, x2, Z
  and and_1 (and_1_out, d_ff_1_qn, x1);
  and and_2 (and_2_out, y1, x2);
  and and_3 (and_3_out, x2, y2);
  and and_4 (and_4_out, x1, y1);
  or or_1 (or_1_out, and_1_out, and_2_out, and_3_out);
  or or_2 (or_2_out, and_3_out, and_4_out);
  D_Flip_Flop #(.trigger("falling"), .Pre_Clr_Positions("ABOVE_BELOW"), .NegatePresetClear("false"), .enable("false"), .NewFFLayout("true")) d_ff_1 (
    .clk(or_1_out), .D(d_ff_1_qn), .Q(y2), .Qn(d_ff_1_qn));  // open: preset, reset
  D_Flip_Flop #(.trigger("falling"), .Pre_Clr_Positions("ABOVE_BELOW"), .NegatePresetClear("false"), .enable("false"), .NewFFLayout("true")) d_ff_2 (
    .clk(or_2_out), .D(d_ff_2_qn), .Q(y1), .Qn(d_ff_2_qn));  // open: preset, reset
  // Probe on y2
  and and_5 (Z, y2, y1);
  // Probe on y1
endmodule

module \例题6_4  (
  output y3,
  output y2,
  output Z,
  output y1,
  output y3_2,
  output y2_2,
  output Z_2,
  output y1_2
);

  wire clock_1_out, comparator_1_eq, not_1_out, not_2_out, not_3_out, not_4_out, x;

  Button u_x (.out(x));
  not not_1 (not_1_out, y2_2);
  not not_2 (not_2_out, y1_2);
  not not_3 (not_3_out, x);
  T_Flip_Flop #(.trigger("falling"), .Pre_Clr_Positions("ABOVE_BELOW"), .NegatePresetClear("false"), .enable("false"), .NewFFLayout("true")) t_ff_1 (
    .clk(y2), .T(1'b1), .Q(y3));  // open: Qn, preset, reset
  T_Flip_Flop #(.trigger("falling"), .Pre_Clr_Positions("ABOVE_BELOW"), .NegatePresetClear("false"), .enable("false"), .NewFFLayout("true")) t_ff_2 (
    .clk(y1), .T(1'b1), .Q(y2));  // open: Qn, preset, reset
  T_Flip_Flop #(.trigger("falling"), .Pre_Clr_Positions("ABOVE_BELOW"), .NegatePresetClear("false"), .enable("false"), .NewFFLayout("true")) t_ff_3 (
    .clk(x), .T(1'b1), .Q(y1));  // open: Qn, preset, reset
  T_Flip_Flop #(.trigger("rising"), .Pre_Clr_Positions("ABOVE_BELOW"), .NegatePresetClear("false"), .enable("false"), .NewFFLayout("true")) t_ff_4 (
    .clk(not_1_out), .T(1'b1), .Q(y3_2));  // open: Qn, preset, reset
  T_Flip_Flop #(.trigger("rising"), .Pre_Clr_Positions("ABOVE_BELOW"), .NegatePresetClear("false"), .enable("false"), .NewFFLayout("true")) t_ff_5 (
    .clk(not_2_out), .T(1'b1), .Q(y2_2));  // open: Qn, preset, reset
  T_Flip_Flop #(.trigger("rising"), .Pre_Clr_Positions("ABOVE_BELOW"), .NegatePresetClear("false"), .enable("false"), .NewFFLayout("true")) t_ff_6 (
    .clk(not_3_out), .T(1'b1), .Q(y1_2));  // open: Qn, preset, reset
  and and_1 (Z, y2, y3, y1, x);
  and and_2 (Z_2, y2_2, y3_2, y1_2, x);
  Clock #(.highDuration(1), .lowDuration(1)) clock_1 (.out(clock_1_out));
  // Digital_Oscilloscope #(.nState(35), .frontlines("rising"), .showclock("true")) digital_oscilloscope_1: pin names not known; wires that end beside it: clock_1_out, x, y3, y2, y1, Z, y3_2, y2_2, y1_2, Z_2
  Comparator #(.width(4), .mode("twosComplement")) comparator_1 (
    .a({y1, y2, y3, Z}), .b({y1_2, y2_2, y3_2, Z_2}), .eq(comparator_1_eq));  // open: gt, lt
  not not_4 (not_4_out, comparator_1_eq);
  // Buzzer #(.freq_measure("Hz"), .vol_width(7)) buzzer_1: pin names not known; wires that end beside it: not_4_out
  LED #(.active("false")) led_1 (.in(comparator_1_eq));

  // Other names for the same wires on the sheet: ZZ = Z_2; yy3 = y3_2; yy2 = y2_2; yy1 = y1_2

  // Notes on the sheet:
  //   下降沿触发的T触发器
  //   上升沿触发的T触发器
endmodule

module \例题6_5  (
  input  X2,
  input  X1,
  output Z,
  output Y2,
  output Y1
);

  wire and_2_out, and_3_out, and_4_out, digital_oscilloscope_1_p1, not_1_out, not_2_out, y1_t, y2_t;

  and and_1 (Z, y1_t, y2_t);
  \延时  \u_延时_1  (.x(Y2), .y(y2_t));
  or or_1 (Y2, and_2_out, and_3_out);
  and and_2 (and_2_out, y2_t, X1, X2);
  not not_1 (not_1_out, X1);
  \延时  \u_延时_2  (.x(Y1), .y(y1_t));
  and and_3 (and_3_out, not_1_out, X2, not_2_out);
  not not_2 (not_2_out, y1_t);
  or or_2 (Y1, and_4_out, X1);
  and and_4 (and_4_out, y1_t, X2);
  // Digital_Oscilloscope #(.nState(35), .frontlines("rising"), .showclock("true")) digital_oscilloscope_1: pin names not known; wires that end beside it: digital_oscilloscope_1_p1, X2, X1, y2_t, y1_t, Z
  Clock #(.highDuration(1), .lowDuration(1)) clock_1 (.out(digital_oscilloscope_1_p1));
endmodule

module \例题6_11  (
  output Z,
  output Y2,
  output Y1
);

  wire nand_1_out, nand_3_out, nand_5_out, not_2_out, not_3_out, x1, x2, x2_out, y1_t, y2_t;

  not not_1 (Z, nand_1_out);
  nand nand_1 (nand_1_out, x2, y2_t);
  not not_2 (not_2_out, x2);
  Counter #(.width(1), .max('h1), .ongoal("wrap"), .trigger("rising"), .behavior("new")) counter_1 (
    .Q(x2), .clk(x2_out));  // open: load, D, count, carry, clr, preset, down
  Clock #(.highDuration(1), .lowDuration(1)) u_x2 (.out(x2_out));
  \延时  \u_延时_1  (.x(Y2), .y(y2_t));
  nand nand_2 (Y2, nand_1_out, nand_3_out);
  nand nand_3 (nand_3_out, not_2_out, not_3_out, y1_t);
  \延时  \u_延时_2  (.x(Y1), .y(y1_t));
  not not_3 (not_3_out, x1);
  Button u_x1 (.out(x1));
  nand nand_4 (Y1, nand_5_out, not_3_out);
  nand nand_5 (nand_5_out, nand_1_out, y1_t);
  // Digital_Oscilloscope #(.nState(35), .frontlines("rising"), .showclock("true")) digital_oscilloscope_1: pin names not known; wires that end beside it: x2, x1, Z
endmodule

module \延时  (
  input  x,
  output y
);

  wire CP_out;

  Clock #(.highDuration(1), .lowDuration(1)) CP (.out(CP_out));
  D_Flip_Flop #(.trigger("rising"), .Pre_Clr_Positions("ABOVE_BELOW"), .NegatePresetClear("false"), .enable("false"), .NewFFLayout("true")) d_ff_1 (
    .clk(CP_out), .D(x), .Q(y));  // open: Qn, preset, reset

  // Notes on the sheet:
  //   延时
endmodule
