// Logisim project 第2章习题电路的实现.circ as structural Verilog: 23 circuits, main circuit 习题2.1
module \习题2_1  (
  input  A,
  input  B,
  input  C,
  output F
);

  wire or_1_out;

  or or_1 (or_1_out, A, B);
  and and_1 (F, or_1_out, C);
endmodule

module \习题2_2_1  (
  output F,
  output F_2
);

  wire A, and_1_out, and_2_out, and_3_out, and_4_out, B, button_1_out, buzzer_1_p1, C, clock_1_out,
       comparator_1_eq, not_1_out, not_2_out, not_3_out, not_4_out;

  Counter #(.width(3), .max('h7), .ongoal("wrap"), .trigger("rising"), .behavior("new")) counter_1 (
    .Q({A, B, C}), .clk(clock_1_out), .clr(button_1_out));  // open: load, D, count, carry, preset, down
  Clock #(.highDuration(1), .lowDuration(1)) clock_1 (.out(clock_1_out));
  Button button_1 (.out(button_1_out));
  // Probe on A
  // Probe on B
  // Probe on C
  // Probe on A
  // Probe on B
  // Probe on C
  not not_1 (not_1_out, A);
  not not_2 (not_2_out, A);
  not not_3 (not_3_out, B);
  not not_4 (not_4_out, C);
  and and_1 (and_1_out, A, B);
  and and_2 (and_2_out, not_1_out, C);
  and and_3 (and_3_out, A, not_3_out);
  and and_4 (and_4_out, not_2_out, not_4_out);
  nor nor_1 (F, and_1_out, and_2_out);
  or or_1 (F_2, and_3_out, and_4_out);
  Comparator #(.width(1), .mode("twosComplement")) comparator_1 (.a(F), .b(F_2), .eq(comparator_1_eq));  // open: gt, lt
  // Buzzer #(.freq_measure("Hz"), .vol_width(7)) buzzer_1: pin names not known; wires that end beside it: buzzer_1_p1
  not not_5 (buzzer_1_p1, comparator_1_eq);
  LED #(.active("false")) led_1 (.in(comparator_1_eq));
endmodule

module \习题2_2_2  (
  output F,
  output F_2
);

  wire A, and_1_out, and_2_out, and_3_out, and_4_out, B, button_1_out, buzzer_1_p1, clock_1_out,
       comparator_1_eq, not_1_out, not_2_out;

  Counter #(.width(2), .max('h3), .ongoal("wrap"), .trigger("rising"), .behavior("new")) counter_1 (
    .Q({A, B}), .clk(clock_1_out), .clr(button_1_out));  // open: load, D, count, carry, preset, down
  Clock #(.highDuration(1), .lowDuration(1)) clock_1 (.out(clock_1_out));
  Button button_1 (.out(button_1_out));
  // Probe on A
  // Probe on B
  not not_1 (not_1_out, A);
  not not_2 (not_2_out, B);
  and and_1 (and_1_out, A, B);
  and and_2 (and_2_out, A, not_2_out);
  and and_3 (and_3_out, not_1_out, B);
  and and_4 (and_4_out, not_1_out, not_2_out);
  or or_1 (F, and_1_out, and_2_out, and_3_out, and_4_out);
  Comparator #(.width(1), .mode("twosComplement")) comparator_1 (
    .a(F), .b(1'b1), .eq(comparator_1_eq));  // open: gt, lt
  // Buzzer #(.freq_measure("Hz"), .vol_width(7)) buzzer_1: pin names not known; wires that end beside it: buzzer_1_p1
  not not_3 (buzzer_1_p1, comparator_1_eq);
  LED #(.active("false")) led_1 (.in(comparator_1_eq));

  assign F_2 = 1'b1;
endmodule

module \习题2_2_3  (
  output F,
  output F_2
);

  wire A, and_1_out, and_2_out, and_3_out, B, button_1_out, buzzer_1_p1, C, clock_1_out, comparator_1_eq,
       nand_1_out, not_1_out, not_2_out;

  Counter #(.width(3), .max('h7), .ongoal("wrap"), .trigger("rising"), .behavior("new")) counter_1 (
    .Q({A, B, C}), .clk(clock_1_out), .clr(button_1_out));  // open: load, D, count, carry, preset, down
  Clock #(.highDuration(1), .lowDuration(1)) clock_1 (.out(clock_1_out));
  Button button_1 (.out(button_1_out));
  // Probe on A
  // Probe on B
  // Probe on C
  // Probe on A
  // Probe on B
  // Probe on C
  nand nand_1 (nand_1_out, A, B, C);
  not not_1 (not_1_out, B);
  not not_2 (not_2_out, C);
  and and_1 (and_1_out, A, not_1_out, not_2_out);
  and and_2 (and_2_out, A, C, not_1_out);
  and and_3 (and_3_out, A, B, not_2_out);
  and and_4 (F, A, nand_1_out);
  or or_1 (F_2, and_1_out, and_2_out, and_3_out);
  Comparator #(.width(1), .mode("twosComplement")) comparator_1 (.a(F), .b(F_2), .eq(comparator_1_eq));  // open: gt, lt
  // Buzzer #(.freq_measure("Hz"), .vol_width(7)) buzzer_1: pin names not known; wires that end beside it: buzzer_1_p1
  not not_3 (buzzer_1_p1, comparator_1_eq);
  LED #(.active("false")) led_1 (.in(comparator_1_eq));
endmodule

module \习题2_2_4  (
  output F,
  output F_2
);

  wire A, and_1_out, and_2_out, and_3_out, and_4_out, and_5_out, B, button_1_out, buzzer_1_p1, C,
       clock_1_out, comparator_1_eq, not_1_out, not_2_out, not_3_out, not_4_out, not_5_out, not_6_out;

  Counter #(.width(3), .max('h7), .ongoal("wrap"), .trigger("rising"), .behavior("new")) counter_1 (
    .Q({A, B, C}), .clk(clock_1_out), .clr(button_1_out));  // open: load, D, count, carry, preset, down
  Clock #(.highDuration(1), .lowDuration(1)) clock_1 (.out(clock_1_out));
  Button button_1 (.out(button_1_out));
  // Probe on A
  // Probe on B
  // Probe on C
  // Probe on A
  // Probe on B
  // Probe on C
  not not_1 (not_1_out, A);
  not not_2 (not_2_out, B);
  not not_3 (not_3_out, C);
  not not_4 (not_4_out, A);
  not not_5 (not_5_out, B);
  not not_6 (not_6_out, C);
  and and_1 (and_1_out, A, B, C);
  and and_2 (and_2_out, not_1_out, not_2_out, not_3_out);
  and and_3 (and_3_out, not_5_out, A);
  and and_4 (and_4_out, B, not_6_out);
  and and_5 (and_5_out, not_4_out, C);
  or or_1 (F, and_1_out, and_2_out);
  nor nor_1 (F_2, and_3_out, and_4_out, and_5_out);
  Comparator #(.width(1), .mode("twosComplement")) comparator_1 (.a(F), .b(F_2), .eq(comparator_1_eq));  // open: gt, lt
  // Buzzer #(.freq_measure("Hz"), .vol_width(7)) buzzer_1: pin names not known; wires that end beside it: buzzer_1_p1
  not not_7 (buzzer_1_p1, comparator_1_eq);
  LED #(.active("false")) led_1 (.in(comparator_1_eq));
endmodule

module \习题2_3_1  (
  output F1,
  output F2
);

  wire A, and_1_out, and_2_out, B, button_1_out, buzzer_1_p1, clock_1_out, comparator_1_eq, not_1_out,
       not_2_out, not_3_out, not_4_out, or_1_out, or_2_out;

  Counter #(.width(2), .max('h3), .ongoal("wrap"), .trigger("rising"), .behavior("new")) counter_1 (
    .Q({A, B}), .clk(clock_1_out), .clr(button_1_out));  // open: load, D, count, carry, preset, down
  Clock #(.highDuration(1), .lowDuration(1)) clock_1 (.out(clock_1_out));
  Button button_1 (.out(button_1_out));
  // Probe on A
  // Probe on B
  // Probe on A
  // Probe on B
  not not_1 (not_1_out, A);
  not not_2 (not_2_out, B);
  not not_3 (not_3_out, A);
  not not_4 (not_4_out, B);
  and and_1 (and_1_out, A, not_2_out);
  and and_2 (and_2_out, not_1_out, B);
  or or_1 (or_1_out, A, B);
  or or_2 (or_2_out, not_4_out, not_3_out);
  or or_3 (F1, and_1_out, and_2_out);
  and and_3 (F2, or_1_out, or_2_out);
  Comparator #(.width(1), .mode("twosComplement")) comparator_1 (.a(F1), .b(F2), .eq(comparator_1_eq));  // open: gt, lt
  // Buzzer #(.freq_measure("Hz"), .vol_width(7)) buzzer_1: pin names not known; wires that end beside it: buzzer_1_p1
  not not_5 (buzzer_1_p1, comparator_1_eq);
  LED #(.active("false")) led_1 (.in(comparator_1_eq));
endmodule

module \习题2_3_2  (
  output F3,
  output F4
);

  wire A, and_1_out, and_2_out, B, button_1_out, buzzer_1_p1, clock_1_out, comparator_1_eq, not_1_out,
       not_2_out, not_3_out, not_4_out, or_1_out, or_2_out;

  Counter #(.width(2), .max('h3), .ongoal("wrap"), .trigger("rising"), .behavior("new")) counter_1 (
    .Q({A, B}), .clk(clock_1_out), .clr(button_1_out));  // open: load, D, count, carry, preset, down
  Clock #(.highDuration(1), .lowDuration(1)) clock_1 (.out(clock_1_out));
  Button button_1 (.out(button_1_out));
  // Probe on A
  // Probe on B
  // Probe on A
  // Probe on B
  not not_1 (not_1_out, A);
  not not_2 (not_2_out, B);
  not not_3 (not_3_out, A);
  not not_4 (not_4_out, B);
  or or_1 (or_1_out, not_1_out, not_2_out);
  or or_2 (or_2_out, A, B);
  and and_1 (and_1_out, A, B);
  and and_2 (and_2_out, not_4_out, not_3_out);
  and and_3 (F3, or_1_out, or_2_out);
  nor nor_1 (F4, and_1_out, and_2_out);
  Comparator #(.width(1), .mode("twosComplement")) comparator_1 (.a(F3), .b(F4), .eq(comparator_1_eq));  // open: gt, lt
  // Buzzer #(.freq_measure("Hz"), .vol_width(7)) buzzer_1: pin names not known; wires that end beside it: buzzer_1_p1
  not not_5 (buzzer_1_p1, comparator_1_eq);
  LED #(.active("false")) led_1 (.in(comparator_1_eq));
endmodule

module \习题2_4_1  (
  output F,
  output nF
);

  wire A, and_1_out, and_2_out, and_3_out, and_4_out, B, button_1_out, buzzer_1_p1, clock_1_out,
       comparator_1_eq, not_1_out, not_2_out, not_3_out, not_4_out, not_5_out;

  Counter #(.width(2), .max('h3), .ongoal("wrap"), .trigger("rising"), .behavior("new")) counter_1 (
    .Q({A, B}), .clk(clock_1_out), .clr(button_1_out));  // open: load, D, count, carry, preset, down
  Clock #(.highDuration(1), .lowDuration(1)) clock_1 (.out(clock_1_out));
  Button button_1 (.out(button_1_out));
  // Probe on A
  // Probe on B
  // Probe on A
  // Probe on B
  not not_1 (not_1_out, A);
  not not_2 (not_2_out, B);
  not not_3 (not_3_out, A);
  not not_4 (not_4_out, B);
  and and_1 (and_1_out, A, B);
  and and_2 (and_2_out, not_1_out, not_2_out);
  and and_3 (and_3_out, not_3_out, B);
  and and_4 (and_4_out, A, not_4_out);
  or or_1 (F, and_1_out, and_2_out);
  or or_2 (nF, and_3_out, and_4_out);
  not not_5 (not_5_out, nF);
  Comparator #(.width(1), .mode("twosComplement")) comparator_1 (
    .a(F), .b(not_5_out), .eq(comparator_1_eq));  // open: gt, lt
  // Buzzer #(.freq_measure("Hz"), .vol_width(7)) buzzer_1: pin names not known; wires that end beside it: buzzer_1_p1
  not not_6 (buzzer_1_p1, comparator_1_eq);
  LED #(.active("false")) led_1 (.in(comparator_1_eq));
endmodule

module \习题2_4_2  (
  output F,
  output nF
);

  wire A, and_1_out, and_2_out, and_3_out, and_4_out, and_5_out, B, button_1_out, buzzer_1_p1, C,
       clock_1_out, comparator_1_eq, D, E, not_1_out, not_2_out, not_3_out, not_4_out, not_5_out, not_6_out,
       not_7_out, or_1_out, or_2_out, or_3_out;

  Counter #(.width(5), .max('h1f), .ongoal("wrap"), .trigger("rising"), .behavior("new")) counter_1 (
    .Q({A, B, C, D, E}), .clk(clock_1_out), .clr(button_1_out));  // open: load, D, count, carry, preset, down
  Clock #(.highDuration(1), .lowDuration(1)) clock_1 (.out(clock_1_out));
  Button button_1 (.out(button_1_out));
  // Probe on A
  // Probe on B
  // Probe on C
  // Probe on D
  // Probe on E
  // Probe on A
  // Probe on B
  // Probe on C
  // Probe on D
  // Probe on E
  not not_1 (not_1_out, A);
  and and_1 (and_1_out, D, E);
  not not_2 (not_2_out, E);
  not not_3 (not_3_out, A);
  not not_4 (not_4_out, B);
  not not_5 (not_5_out, C);
  not not_6 (not_6_out, D);
  or or_1 (or_1_out, A, B);
  or or_2 (or_2_out, not_1_out, C);
  or or_3 (or_3_out, C, and_1_out);
  and and_2 (and_2_out, E, not_4_out, not_3_out);
  and and_3 (and_3_out, A, not_5_out, E);
  and and_4 (and_4_out, not_5_out, not_6_out, E);
  and and_5 (and_5_out, or_1_out, or_2_out, or_3_out);
  or or_4 (F, and_5_out, not_2_out);
  not not_7 (not_7_out, nF);
  or or_5 (nF, and_2_out, and_3_out, and_4_out);
  // Buzzer #(.freq_measure("Hz"), .vol_width(1)) buzzer_1: pin names not known; wires that end beside it: buzzer_1_p1
  not not_8 (buzzer_1_p1, comparator_1_eq);
  Comparator #(.width(1), .mode("twosComplement")) comparator_1 (
    .a(F), .b(not_7_out), .eq(comparator_1_eq));  // open: gt, lt
  LED #(.active("false")) led_1 (.in(comparator_1_eq));
endmodule

module \习题2_4_3  (
  output F,
  output nF
);

  wire A, and_1_out, and_2_out, and_3_out, B, button_1_out, buzzer_1_p1, C, clock_1_out, comparator_1_eq, D,
       nand_1_out, not_1_out, not_2_out, not_3_out, not_4_out, not_5_out, or_1_out, or_2_out;

  Counter #(.width(4), .max('hf), .ongoal("wrap"), .trigger("rising"), .behavior("new")) counter_1 (
    .Q({A, B, C, D}), .clk(clock_1_out), .clr(button_1_out));  // open: load, D, count, carry, preset, down
  Clock #(.highDuration(1), .lowDuration(1)) clock_1 (.out(clock_1_out));
  Button button_1 (.out(button_1_out));
  // Probe on A
  // Probe on B
  // Probe on C
  // Probe on D
  // Probe on A
  // Probe on B
  // Probe on C
  // Probe on D
  not not_1 (not_1_out, A);
  nand nand_1 (nand_1_out, A, C);
  not not_2 (not_2_out, B);
  not not_3 (not_3_out, C);
  not not_4 (not_4_out, D);
  or or_1 (or_1_out, not_1_out, B);
  and and_1 (and_1_out, nand_1_out, D);
  or or_2 (or_2_out, C, and_1_out);
  and and_2 (and_2_out, A, not_2_out);
  and and_3 (and_3_out, not_3_out, not_4_out);
  and and_4 (F, or_1_out, or_2_out);
  not not_5 (not_5_out, nF);
  or or_3 (nF, and_2_out, and_3_out);
  Comparator #(.width(1), .mode("twosComplement")) comparator_1 (
    .a(F), .b(not_5_out), .eq(comparator_1_eq));  // open: gt, lt
  // Buzzer #(.freq_measure("Hz"), .vol_width(1)) buzzer_1: pin names not known; wires that end beside it: buzzer_1_p1
  not not_6 (buzzer_1_p1, comparator_1_eq);
  LED #(.active("false")) led_1 (.in(comparator_1_eq));
endmodule

module \习题2_4_4  (
  output F,
  output nF
);

  wire A, and_1_out, and_2_out, and_3_out, and_4_out, and_5_out, B, button_1_out, buzzer_1_p1, C,
       clock_1_out, comparator_1_eq, D, E, G, not_1_out, not_2_out, not_3_out, not_4_out, not_5_out,
       not_6_out, not_7_out, or_1_out, or_2_out;

  Counter #(.width(6), .max('h3f), .ongoal("wrap"), .trigger("rising"), .behavior("new")) counter_1 (
    .Q({A, B, C, D, E, G}), .clk(clock_1_out), .clr(button_1_out));  // open: load, D, count, carry, preset, down
  Clock #(.highDuration(1), .lowDuration(1)) clock_1 (.out(clock_1_out));
  Button button_1 (.out(button_1_out));
  // Probe on A
  // Probe on B
  // Probe on C
  // Probe on D
  // Probe on E
  // Probe on G
  // Probe on A
  // Probe on B
  // Probe on C
  // Probe on D
  // Probe on E
  // Probe on G
  not not_1 (not_1_out, B);
  and and_1 (and_1_out, C, not_2_out);
  not not_2 (not_2_out, D);
  not not_3 (not_3_out, E);
  not not_4 (not_4_out, A);
  not not_5 (not_5_out, C);
  not not_6 (not_6_out, G);
  or or_1 (or_1_out, and_1_out, not_3_out);
  and and_2 (and_2_out, or_1_out, G);
  and and_3 (and_3_out, B, not_5_out, E);
  and and_4 (and_4_out, B, D, E);
  and and_5 (and_5_out, B, not_6_out);
  or or_2 (or_2_out, not_1_out, and_2_out);
  and and_6 (F, A, or_2_out);
  not not_7 (not_7_out, nF);
  or or_3 (nF, not_4_out, and_3_out, and_4_out, and_5_out);
  // Buzzer #(.freq_measure("Hz"), .vol_width(1)) buzzer_1: pin names not known; wires that end beside it: buzzer_1_p1
  not not_8 (buzzer_1_p1, comparator_1_eq);
  Comparator #(.width(1), .mode("twosComplement")) comparator_1 (
    .a(F), .b(not_7_out), .eq(comparator_1_eq));  // open: gt, lt
  LED #(.active("false")) led_1 (.in(comparator_1_eq));
endmodule

module \习题2_6_1  (
  output F,
  output F_2
);

  wire A, and_1_out, and_2_out, and_3_out, and_4_out, and_5_out, B, button_1_out, buzzer_1_p1, C,
       clock_1_out, comparator_1_eq, not_1_out, not_2_out, not_3_out;

  Counter #(.width(3), .max('h7), .ongoal("wrap"), .trigger("rising"), .behavior("new")) counter_1 (
    .Q({A, B, C}), .clk(clock_1_out), .clr(button_1_out));  // open: load, D, count, carry, preset, down
  Clock #(.highDuration(1), .lowDuration(1)) clock_1 (.out(clock_1_out));
  Button button_1 (.out(button_1_out));
  // Probe on A
  // Probe on B
  // Probe on C
  // Probe on A
  // Probe on B
  // Probe on C
  not not_1 (not_1_out, A);
  not not_2 (not_2_out, B);
  not not_3 (not_3_out, A);
  and and_1 (and_1_out, A, B);
  and and_2 (and_2_out, not_3_out, C);
  and and_3 (and_3_out, A, B);
  and and_4 (and_4_out, not_1_out, C, not_2_out);
  and and_5 (and_5_out, B, C);
  or or_1 (F, and_3_out, and_4_out, and_5_out);
  or or_2 (F_2, and_1_out, and_2_out);
  Comparator #(.width(1), .mode("twosComplement")) comparator_1 (.a(F), .b(F_2), .eq(comparator_1_eq));  // open: gt, lt
  // Buzzer #(.freq_measure("Hz"), .vol_width(7)) buzzer_1: pin names not known; wires that end beside it: buzzer_1_p1
  not not_4 (buzzer_1_p1, comparator_1_eq);
  LED #(.active("false")) led_1 (.in(comparator_1_eq));
endmodule

module \习题2_6_2  (
  output F,
  output F_2
);

  wire A, and_1_out, and_2_out, B, button_1_out, buzzer_1_p1, C, clock_1_out, comparator_1_eq, D, not_1_out;

  Counter #(.width(4), .max('hf), .ongoal("wrap"), .trigger("rising"), .behavior("new")) counter_1 (
    .Q({A, B, C, D}), .clk(clock_1_out), .clr(button_1_out));  // open: load, D, count, carry, preset, down
  Clock #(.highDuration(1), .lowDuration(1)) clock_1 (.out(clock_1_out));
  Button button_1 (.out(button_1_out));
  // Probe on A
  // Probe on B
  // Probe on C
  // Probe on D
  // Probe on A
  // Probe on B
  // Probe on C
  // Probe on D
  not not_1 (not_1_out, B);
  and and_1 (and_1_out, A, not_1_out);
  and and_2 (and_2_out, B, C, D);
  or or_1 (F, and_1_out, B, and_2_out);
  or or_2 (F_2, A, B);
  Comparator #(.width(1), .mode("twosComplement")) comparator_1 (.a(F), .b(F_2), .eq(comparator_1_eq));  // open: gt, lt
  // Buzzer #(.freq_measure("Hz"), .vol_width(1)) buzzer_1: pin names not known; wires that end beside it: buzzer_1_p1
  not not_2 (buzzer_1_p1, comparator_1_eq);
  LED #(.active("false")) led_1 (.in(comparator_1_eq));
endmodule

module \习题2_6_3  (
  output F,
  output F_2
);

  wire A, button_1_out, C, clock_1_out, comparator_1_eq, not_1_out, not_2_out, not_3_out, or_1_out, or_2_out,
       or_3_out;

  Counter #(.width(3), .max('h7), .ongoal("wrap"), .trigger("rising"), .behavior("new")) counter_1 (
    .Q({A, F_2, C}), .clk(clock_1_out), .clr(button_1_out));  // open: load, D, count, carry, preset, down
  Clock #(.highDuration(1), .lowDuration(1)) clock_1 (.out(clock_1_out));
  Button button_1 (.out(button_1_out));
  // Probe on A
  // Probe on F_2
  // Probe on C
  // Probe on A
  // Probe on F_2
  // Probe on C
  not not_1 (not_1_out, A);
  not not_2 (not_2_out, C);
  or or_1 (or_1_out, A, F_2, C);
  or or_2 (or_2_out, not_1_out, F_2);
  or or_3 (or_3_out, A, F_2, not_2_out);
  and and_1 (F, or_1_out, or_2_out, or_3_out);
  Comparator #(.width(1), .mode("twosComplement")) comparator_1 (.a(F), .b(F_2), .eq(comparator_1_eq));  // open: gt, lt
  not not_3 (not_3_out, comparator_1_eq);
  // Buzzer #(.freq_measure("Hz"), .vol_width(7)) buzzer_1: pin names not known; wires that end beside it: not_3_out
  LED #(.active("false")) led_1 (.in(comparator_1_eq));

  // Other names for the same wires on the sheet: B = F_2
endmodule

module \习题2_6_4  (
  output F,
  output F_2
);

  wire A, and_1_out, and_2_out, and_3_out, and_4_out, B, button_1_out, buzzer_1_p1, C, clock_1_out,
       comparator_1_eq, D, not_1_out, not_2_out, not_3_out, or_1_out, or_2_out;

  Counter #(.width(4), .max('hf), .ongoal("wrap"), .trigger("rising"), .behavior("new")) counter_1 (
    .Q({A, B, C, D}), .clk(clock_1_out), .clr(button_1_out));  // open: load, D, count, carry, preset, down
  Clock #(.highDuration(1), .lowDuration(1)) clock_1 (.out(clock_1_out));
  Button button_1 (.out(button_1_out));
  // Probe on A
  // Probe on B
  // Probe on C
  // Probe on D
  // Probe on A
  // Probe on B
  // Probe on C
  // Probe on D
  not not_1 (not_1_out, B);
  not not_2 (not_2_out, C);
  not not_3 (not_3_out, D);
  and and_1 (and_1_out, A, C);
  or or_1 (or_1_out, not_1_out, not_2_out);
  and and_2 (and_2_out, A, C);
  or or_2 (or_2_out, B, and_1_out);
  and and_3 (and_3_out, C, B);
  and and_4 (and_4_out, or_2_out, not_3_out, or_1_out);
  or or_3 (F, and_3_out, and_4_out, D);
  or or_4 (F_2, and_2_out, B, D);
  Comparator #(.width(1), .mode("twosComplement")) comparator_1 (.a(F), .b(F_2), .eq(comparator_1_eq));  // open: gt, lt
  // Buzzer #(.freq_measure("Hz"), .vol_width(1)) buzzer_1: pin names not known; wires that end beside it: buzzer_1_p1
  not not_4 (buzzer_1_p1, comparator_1_eq);
  LED #(.active("false")) led_1 (.in(comparator_1_eq));
endmodule

module \习题2_7_1  (
  output F,
  output F_2,
  output F_3
);

  wire A, and_1_out, and_2_out, and_3_out, and_4_out, and_5_out, and_6_out, and_7_out, and_8_out, and_9_out,
       and_10_out, and_11_out, and_12_out, B, button_1_out, buzzer_1_p1, buzzer_2_p1, C, clock_1_out,
       comparator_1_eq, comparator_2_eq, D, not_1_out, not_2_out, not_3_out, not_4_out, not_6_out, not_7_out,
       not_8_out, not_9_out, not_10_out, or_1_out, or_2_out, or_3_out, or_4_out, or_5_out, or_6_out,
       or_7_out, or_8_out;

  Counter #(.width(4), .max('hf), .ongoal("wrap"), .trigger("rising"), .behavior("new")) counter_1 (
    .Q({A, B, C, D}), .clk(clock_1_out), .clr(button_1_out));  // open: load, D, count, carry, preset, down
  Clock #(.highDuration(1), .lowDuration(1)) clock_1 (.out(clock_1_out));
  Button button_1 (.out(button_1_out));
  // Probe on A
  // Probe on B
  // Probe on C
  // Probe on D
  // Probe on A
  // Probe on B
  // Probe on C
  // Probe on D
  not not_1 (not_1_out, A);
  not not_2 (not_2_out, C);
  not not_3 (not_3_out, D);
  not not_4 (not_4_out, A);
  // NOT_Gate not_5 has open pins: in=B, out=open
  not not_6 (not_6_out, C);
  not not_7 (not_7_out, D);
  // Probe on A
  // Probe on B
  // Probe on C
  // Probe on D
  not not_8 (not_8_out, A);
  not not_9 (not_9_out, C);
  not not_10 (not_10_out, D);
  and and_1 (and_1_out, B, not_8_out);
  and and_2 (and_2_out, B, not_9_out, not_10_out);
  and and_3 (and_3_out, C, B);
  and and_4 (and_4_out, A, B, not_9_out, D);
  and and_5 (and_5_out, not_1_out, B, not_2_out, not_3_out);
  and and_6 (and_6_out, not_1_out, B, not_2_out, D);
  and and_7 (and_7_out, not_1_out, B, C, not_3_out);
  and and_8 (and_8_out, not_1_out, B, C, D);
  and and_9 (and_9_out, A, B, not_2_out, not_3_out);
  and and_10 (and_10_out, A, B, not_2_out, D);
  and and_11 (and_11_out, A, B, C, not_3_out);
  and and_12 (and_12_out, A, B, C, D);
  or or_1 (or_1_out, not_4_out, B, not_6_out, not_7_out);
  or or_2 (or_2_out, not_4_out, B, not_6_out, D);
  or or_3 (or_3_out, not_4_out, B, C, not_7_out);
  or or_4 (or_4_out, not_4_out, B, C, D);
  or or_5 (or_5_out, A, B, not_6_out, not_7_out);
  or or_6 (or_6_out, A, B, not_6_out, D);
  or or_7 (or_7_out, A, B, C, not_7_out);
  or or_8 (or_8_out, A, B, C, D);
  or or_9 (F, and_1_out, and_2_out, and_3_out, and_4_out);
  or or_10 (F_2, and_5_out, and_6_out, and_7_out, and_8_out, and_9_out, and_10_out, and_11_out, and_12_out);
  and and_13 (F_3, or_1_out, or_2_out, or_3_out, or_4_out, or_5_out, or_6_out, or_7_out, or_8_out);
  // Buzzer #(.freq_measure("Hz"), .vol_width(1)) buzzer_1: pin names not known; wires that end beside it: buzzer_1_p1
  not not_11 (buzzer_1_p1, comparator_1_eq);
  Comparator #(.width(1), .mode("twosComplement")) comparator_1 (.a(F), .b(F_2), .eq(comparator_1_eq));  // open: gt, lt
  Comparator #(.width(1), .mode("twosComplement")) comparator_2 (.a(F), .b(F_3), .eq(comparator_2_eq));  // open: gt, lt
  LED #(.active("false")) led_1 (.in(comparator_1_eq));
  // Buzzer #(.freq_measure("Hz"), .vol_width(1)) buzzer_2: pin names not known; wires that end beside it: buzzer_2_p1
  not not_12 (buzzer_2_p1, comparator_2_eq);
  LED #(.active("false")) led_2 (.in(comparator_2_eq));
endmodule

module \习题2_7_2  (
  output F,
  output F_2,
  output F_3
);

  wire A, and_1_out, and_2_out, and_3_out, and_4_out, and_5_out, and_6_out, and_7_out, and_8_out, and_9_out,
       and_10_out, and_11_out, and_12_out, and_13_out, and_14_out, and_15_out, and_16_out, B, button_1_out,
       buzzer_1_p1, buzzer_2_p1, C, clock_1_out, comparator_1_eq, comparator_2_eq, D, nor_1_out, not_1_out,
       not_2_out, not_3_out, not_4_out, not_5_out, not_6_out, not_7_out, not_8_out, or_1_out, or_2_out,
       or_3_out;

  Counter #(.width(4), .max('hf), .ongoal("wrap"), .trigger("rising"), .behavior("new")) counter_1 (
    .Q({A, B, C, D}), .clk(clock_1_out), .clr(button_1_out));  // open: load, D, count, carry, preset, down
  Clock #(.highDuration(1), .lowDuration(1)) clock_1 (.out(clock_1_out));
  Button button_1 (.out(button_1_out));
  // Probe on A
  // Probe on B
  // Probe on C
  // Probe on D
  // Probe on A
  // Probe on B
  // Probe on C
  // Probe on D
  not not_1 (not_1_out, A);
  not not_2 (not_2_out, B);
  not not_3 (not_3_out, C);
  not not_4 (not_4_out, D);
  not not_5 (not_5_out, C);
  not not_6 (not_6_out, D);
  // Probe on A
  // Probe on B
  // Probe on C
  // Probe on D
  not not_7 (not_7_out, A);
  not not_8 (not_8_out, B);
  and and_1 (and_1_out, C, D);
  and and_2 (and_2_out, not_1_out, B, not_3_out, not_4_out);
  and and_3 (and_3_out, not_1_out, B, not_3_out, D);
  and and_4 (and_4_out, not_1_out, B, C, not_4_out);
  and and_5 (and_5_out, not_1_out, B, C, D);
  and and_6 (and_6_out, A, B, not_3_out, not_4_out);
  and and_7 (and_7_out, A, B, not_3_out, D);
  and and_8 (and_8_out, A, B, C, not_4_out);
  and and_9 (and_9_out, A, B, C, D);
  and and_10 (and_10_out, not_1_out, not_2_out, C, D);
  and and_11 (and_11_out, A, not_2_out, not_3_out, not_4_out);
  and and_12 (and_12_out, A, not_2_out, not_3_out, D);
  and and_13 (and_13_out, A, not_2_out, C, not_4_out);
  and and_14 (and_14_out, A, not_2_out, C, D);
  or or_1 (or_1_out, A, B, C, D);
  or or_2 (or_2_out, A, B, C, not_6_out);
  or or_3 (or_3_out, A, B, not_5_out, D);
  and and_15 (and_15_out, not_7_out, not_8_out);
  and and_16 (and_16_out, A, B, D);
  nor nor_1 (nor_1_out, and_15_out, and_16_out);
  or or_4 (F, nor_1_out, B, and_1_out);
  or or_5 (F_2, and_2_out, and_3_out, and_4_out, and_5_out, and_6_out, and_7_out, and_8_out, and_9_out, and_10_out, and_11_out, and_12_out, and_13_out, and_14_out);
  and and_17 (F_3, or_1_out, or_2_out, or_3_out);
  // Buzzer #(.freq_measure("Hz"), .vol_width(1)) buzzer_1: pin names not known; wires that end beside it: buzzer_1_p1
  not not_9 (buzzer_1_p1, comparator_1_eq);
  Comparator #(.width(1), .mode("twosComplement")) comparator_1 (.a(F), .b(F_2), .eq(comparator_1_eq));  // open: gt, lt
  Comparator #(.width(1), .mode("twosComplement")) comparator_2 (.a(F), .b(F_3), .eq(comparator_2_eq));  // open: gt, lt
  LED #(.active("false")) led_1 (.in(comparator_1_eq));
  // Buzzer #(.freq_measure("Hz"), .vol_width(1)) buzzer_2: pin names not known; wires that end beside it: buzzer_2_p1
  not not_10 (buzzer_2_p1, comparator_2_eq);
  LED #(.active("false")) led_2 (.in(comparator_2_eq));
endmodule

module \习题2_8_1  (
  output F,
  output F_2,
  output F_3
);

  wire A, and_1_out, and_2_out, and_3_out, and_4_out, and_5_out, and_6_out, and_7_out, B, button_1_out,
       buzzer_1_p1, buzzer_2_p1, C, clock_1_out, comparator_1_eq, comparator_2_eq, D, not_1_out, not_2_out,
       not_3_out, not_4_out, not_5_out, not_6_out, not_7_out, not_8_out, not_9_out, or_1_out, or_2_out;

  Counter #(.width(4), .max('hf), .ongoal("wrap"), .trigger("rising"), .behavior("new")) counter_1 (
    .Q({A, B, C, D}), .clk(clock_1_out), .clr(button_1_out));  // open: load, D, count, carry, preset, down
  Clock #(.highDuration(1), .lowDuration(1)) clock_1 (.out(clock_1_out));
  Button button_1 (.out(button_1_out));
  // Probe on A
  // Probe on B
  // Probe on C
  // Probe on D
  // Probe on A
  // Probe on B
  // Probe on C
  // Probe on D
  // Probe on A
  // Probe on B
  // Probe on C
  // Probe on D
  not not_1 (not_1_out, A);
  not not_2 (not_2_out, B);
  not not_3 (not_3_out, C);
  not not_4 (not_4_out, A);
  not not_5 (not_5_out, B);
  not not_6 (not_6_out, C);
  not not_7 (not_7_out, A);
  not not_8 (not_8_out, B);
  not not_9 (not_9_out, C);
  and and_1 (and_1_out, not_4_out, not_5_out);
  and and_2 (and_2_out, A, C);
  and and_3 (and_3_out, B, not_6_out);
  or or_1 (or_1_out, not_7_out, B, C);
  or or_2 (or_2_out, not_9_out, not_8_out, A);
  and and_4 (and_4_out, not_1_out, not_2_out);
  and and_5 (and_5_out, not_1_out, not_3_out, D);
  and and_6 (and_6_out, A, C);
  and and_7 (and_7_out, B, not_3_out);
  and and_8 (F_3, or_1_out, or_2_out);
  or or_3 (F, and_4_out, and_5_out, and_6_out, and_7_out);
  or or_4 (F_2, and_1_out, and_2_out, and_3_out);
  Comparator #(.width(1), .mode("twosComplement")) comparator_1 (.a(F), .b(F_2), .eq(comparator_1_eq));  // open: gt, lt
  Comparator #(.width(1), .mode("twosComplement")) comparator_2 (.a(F), .b(F_3), .eq(comparator_2_eq));  // open: gt, lt
  // Buzzer #(.freq_measure("Hz"), .vol_width(1)) buzzer_1: pin names not known; wires that end beside it: buzzer_1_p1
  not not_10 (buzzer_1_p1, comparator_1_eq);
  LED #(.active("false")) led_1 (.in(comparator_1_eq));
  // Buzzer #(.freq_measure("Hz"), .vol_width(1)) buzzer_2: pin names not known; wires that end beside it: buzzer_2_p1
  not not_11 (buzzer_2_p1, comparator_2_eq);
  LED #(.active("false")) led_2 (.in(comparator_2_eq));
endmodule

module \习题2_8_2  (
  output F,
  output F_2
);

  wire A, and_1_out, and_2_out, and_3_out, B, button_1_out, buzzer_1_p1, C, clock_1_out, comparator_1_eq, D,
       not_1_out, not_2_out, not_3_out, or_1_out, or_2_out;

  Counter #(.width(4), .max('hf), .ongoal("wrap"), .trigger("rising"), .behavior("new")) counter_1 (
    .Q({A, B, C, D}), .clk(clock_1_out), .clr(button_1_out));  // open: load, D, count, carry, preset, down
  Clock #(.highDuration(1), .lowDuration(1)) clock_1 (.out(clock_1_out));
  Button button_1 (.out(button_1_out));
  // Probe on A
  // Probe on B
  // Probe on C
  // Probe on D
  // Probe on A
  // Probe on B
  // Probe on C
  // Probe on D
  not not_1 (not_1_out, B);
  not not_2 (not_2_out, C);
  not not_3 (not_3_out, D);
  and and_1 (and_1_out, C, B);
  or or_1 (or_1_out, not_1_out, not_2_out);
  and and_2 (and_2_out, A, D);
  or or_2 (or_2_out, B, and_2_out);
  and and_3 (and_3_out, or_1_out, or_2_out, not_3_out);
  or or_3 (F, and_1_out, and_3_out, D);
  or or_4 (F_2, B, D);
  Comparator #(.width(1), .mode("twosComplement")) comparator_1 (.a(F), .b(F_2), .eq(comparator_1_eq));  // open: gt, lt
  // Buzzer #(.freq_measure("Hz"), .vol_width(1)) buzzer_1: pin names not known; wires that end beside it: buzzer_1_p1
  not not_4 (buzzer_1_p1, comparator_1_eq);
  LED #(.active("false")) led_1 (.in(comparator_1_eq));
endmodule

module \习题2_8_3  (
  output F,
  output F_2,
  output F_3,
  output F_4
);

  wire A, and_2_out, and_3_out, and_4_out, and_5_out, and_6_out, and_7_out, and_8_out, and_9_out, and_10_out,
       and_11_out, and_12_out, and_13_out, and_14_out, B, button_1_out, buzzer_1_p1, buzzer_2_p1, C,
       clock_1_out, comparator_1_eq, comparator_2_eq, D, not_1_out, not_2_out, not_3_out, not_4_out,
       not_5_out, not_6_out, or_1_out, or_2_out;

  Counter #(.width(4), .max('hf), .ongoal("wrap"), .trigger("rising"), .behavior("new")) counter_1 (
    .Q({A, B, C, D}), .clk(clock_1_out), .clr(button_1_out));  // open: load, D, count, carry, preset, down
  Clock #(.highDuration(1), .lowDuration(1)) clock_1 (.out(clock_1_out));
  Button button_1 (.out(button_1_out));
  // Probe on A
  // Probe on B
  // Probe on C
  // Probe on D
  // Probe on A
  // Probe on B
  // Probe on C
  // Probe on D
  not not_1 (not_1_out, A);
  not not_2 (not_2_out, B);
  not not_3 (not_3_out, C);
  not not_4 (not_4_out, D);
  not not_5 (not_5_out, D);
  // Probe on A
  // Probe on B
  // Probe on C
  // Probe on D
  not not_6 (not_6_out, D);
  or or_1 (or_1_out, C, B);
  or or_2 (or_2_out, not_5_out, A);
  and and_1 (F_3, or_1_out, or_2_out);
  and and_2 (and_2_out, B, A);
  and and_3 (and_3_out, A, C);
  and and_4 (and_4_out, B, not_6_out);
  and and_5 (and_5_out, C, not_6_out);
  and and_6 (and_6_out, not_1_out, not_2_out, C, not_4_out);
  and and_7 (and_7_out, not_1_out, B, not_3_out, not_4_out);
  and and_8 (and_8_out, not_1_out, B, C, not_4_out);
  and and_9 (and_9_out, A, not_2_out, C, not_4_out);
  and and_10 (and_10_out, A, not_2_out, C, D);
  and and_11 (and_11_out, A, B, not_3_out, not_4_out);
  and and_12 (and_12_out, A, B, not_3_out, D);
  and and_13 (and_13_out, A, B, C, not_4_out);
  and and_14 (and_14_out, A, B, C, D);
  or or_3 (F, and_2_out, and_3_out, and_4_out, and_5_out);
  or or_4 (F_2, and_6_out, and_7_out, and_8_out, and_9_out, and_10_out, and_11_out, and_12_out, and_13_out, and_14_out);
  Comparator #(.width(1), .mode("twosComplement")) comparator_1 (.a(F), .b(F_2), .eq(comparator_1_eq));  // open: gt, lt
  // Buzzer #(.freq_measure("Hz"), .vol_width(1)) buzzer_1: pin names not known; wires that end beside it: buzzer_1_p1
  not not_7 (buzzer_1_p1, comparator_1_eq);
  LED #(.active("false")) led_1 (.in(comparator_1_eq));
  // Buzzer #(.freq_measure("Hz"), .vol_width(1)) buzzer_2: pin names not known; wires that end beside it: buzzer_2_p1
  not not_8 (buzzer_2_p1, comparator_2_eq);
  LED #(.active("false")) led_2 (.in(comparator_2_eq));
  Comparator #(.width(1), .mode("twosComplement")) comparator_2 (
    .a(F_2), .b(F_3), .eq(comparator_2_eq));  // open: gt, lt
endmodule

module \习题2_9_1  (
  output F,
  output G
);

  wire A, and_1_out, and_2_out, and_3_out, and_4_out, and_5_out, and_6_out, and_7_out, and_8_out, B,
       button_1_out, buzzer_1_p1, C, clock_1_out, comparator_1_eq, D, not_1_out, not_2_out, not_3_out,
       not_4_out, not_5_out, not_6_out, not_7_out, not_8_out;

  Counter #(.width(4), .max('hf), .ongoal("wrap"), .trigger("rising"), .behavior("new")) counter_1 (
    .Q({A, B, C, D}), .clk(clock_1_out), .clr(button_1_out));  // open: load, D, count, carry, preset, down
  Clock #(.highDuration(1), .lowDuration(1)) clock_1 (.out(clock_1_out));
  Button button_1 (.out(button_1_out));
  // Probe on A
  // Probe on B
  // Probe on C
  // Probe on D
  // Probe on A
  // Probe on B
  // Probe on C
  // Probe on D
  not not_1 (not_1_out, A);
  not not_2 (not_2_out, B);
  not not_3 (not_3_out, C);
  not not_4 (not_4_out, D);
  not not_5 (not_5_out, A);
  not not_6 (not_6_out, B);
  not not_7 (not_7_out, C);
  and and_1 (and_1_out, A, B, D);
  and and_2 (and_2_out, not_5_out, not_7_out, D);
  and and_3 (and_3_out, C, D);
  and and_4 (and_4_out, not_6_out, D);
  and and_5 (and_5_out, not_1_out, not_4_out);
  and and_6 (and_6_out, not_2_out, not_4_out);
  and and_7 (and_7_out, not_3_out, not_4_out);
  and and_8 (and_8_out, not_4_out, A, C);
  or or_1 (F, and_5_out, and_6_out, and_7_out, and_8_out);
  not not_8 (not_8_out, G);
  or or_2 (G, and_1_out, and_2_out, and_3_out, and_4_out);
  Comparator #(.width(1), .mode("twosComplement")) comparator_1 (
    .a(F), .b(not_8_out), .eq(comparator_1_eq));  // open: gt, lt
  // Buzzer #(.freq_measure("Hz"), .vol_width(1)) buzzer_1: pin names not known; wires that end beside it: buzzer_1_p1
  not not_9 (buzzer_1_p1, comparator_1_eq);
  LED #(.active("false")) led_1 (.in(comparator_1_eq));
endmodule

module \习题2_9_2  (
  output F,
  output G
);

  wire A, and_1_out, and_2_out, and_3_out, and_4_out, and_5_out, and_6_out, and_7_out, and_8_out, and_9_out,
       B, button_1_out, buzzer_1_p1, C, clock_1_out, comparator_1_eq, nor_1_out, not_1_out, not_2_out,
       not_3_out, not_4_out, or_1_out, or_2_out;

  Counter #(.width(3), .max('h7), .ongoal("wrap"), .trigger("rising"), .behavior("new")) counter_1 (
    .Q({A, B, C}), .clk(clock_1_out), .clr(button_1_out));  // open: load, D, count, carry, preset, down
  Clock #(.highDuration(1), .lowDuration(1)) clock_1 (.out(clock_1_out));
  Button button_1 (.out(button_1_out));
  // Probe on A
  // Probe on B
  // Probe on C
  // Probe on A
  // Probe on B
  // Probe on C
  not not_1 (not_1_out, A);
  not not_2 (not_2_out, B);
  not not_3 (not_3_out, C);
  or or_1 (or_1_out, B, C, A);
  and and_1 (and_1_out, A, B);
  and and_2 (and_2_out, B, C);
  and and_3 (and_3_out, C, A);
  and and_4 (and_4_out, A, B, C);
  and and_5 (and_5_out, not_2_out, A);
  and and_6 (and_6_out, not_1_out, B);
  or or_2 (or_2_out, and_5_out, and_6_out);
  not not_4 (not_4_out, or_2_out);
  and and_7 (and_7_out, or_1_out, nor_1_out);
  nor nor_1 (nor_1_out, and_1_out, and_2_out, and_3_out);
  and and_8 (and_8_out, or_2_out, not_3_out);
  and and_9 (and_9_out, not_4_out, C);
  or or_3 (F, and_8_out, and_9_out);
  or or_4 (G, and_7_out, and_4_out);
  Comparator #(.width(1), .mode("twosComplement")) comparator_1 (.a(F), .b(G), .eq(comparator_1_eq));  // open: gt, lt
  // Buzzer #(.freq_measure("Hz"), .vol_width(7)) buzzer_1: pin names not known; wires that end beside it: buzzer_1_p1
  not not_5 (buzzer_1_p1, comparator_1_eq);
  LED #(.active("false")) led_1 (.in(comparator_1_eq));
endmodule

module \习题2_11  (
  output F,
  output F_2,
  output F_3
);

  wire A, and_1_out, and_2_out, and_3_out, and_4_out, and_5_out, and_6_out, and_7_out, and_8_out, and_9_out,
       and_10_out, and_11_out, and_12_out, and_13_out, and_14_out, and_15_out, and_16_out, B, button_1_out,
       buzzer_1_p1, buzzer_2_p1, C, clock_1_out, comparator_1_eq, comparator_2_eq, D, not_1_out, not_2_out,
       not_3_out, not_4_out, not_5_out, not_6_out, not_7_out, not_8_out;

  Clock #(.highDuration(1), .lowDuration(1)) clock_1 (.out(clock_1_out));
  Button button_1 (.out(button_1_out));
  // Probe on A
  // Probe on B
  // Probe on C
  // Probe on D
  Counter #(.width(4), .max('hf), .ongoal("wrap"), .trigger("rising"), .behavior("new")) counter_1 (
    .Q({A, B, C, D}), .clk(clock_1_out), .clr(button_1_out));  // open: load, D, count, carry, preset, down
  not not_1 (not_1_out, A);
  not not_2 (not_2_out, B);
  not not_3 (not_3_out, C);
  not not_4 (not_4_out, D);
  // Probe on A
  // Probe on B
  // Probe on C
  // Probe on D
  // Probe on A
  // Probe on B
  // Probe on C
  // Probe on D
  not not_5 (not_5_out, B);
  not not_6 (not_6_out, D);
  not not_7 (not_7_out, B);
  not not_8 (not_8_out, D);
  and and_1 (and_1_out, B, D);
  and and_2 (and_2_out, not_5_out, not_6_out);
  and and_3 (and_3_out, C, not_5_out);
  and and_4 (and_4_out, B, D);
  and and_5 (and_5_out, not_7_out, not_8_out);
  and and_6 (and_6_out, C, D);
  and and_7 (and_7_out, not_1_out, not_2_out, not_3_out, not_4_out);
  and and_8 (and_8_out, not_1_out, not_2_out, C, not_4_out);
  and and_9 (and_9_out, not_1_out, not_2_out, C, D);
  and and_10 (and_10_out, not_1_out, B, not_3_out, D);
  and and_11 (and_11_out, not_1_out, B, C, D);
  and and_12 (and_12_out, A, not_2_out, not_3_out, not_4_out);
  and and_13 (and_13_out, A, not_2_out, C, not_4_out);
  and and_14 (and_14_out, A, not_2_out, C, D);
  and and_15 (and_15_out, A, B, not_3_out, D);
  and and_16 (and_16_out, A, B, C, D);
  or or_1 (F, and_1_out, and_2_out, and_3_out);
  or or_2 (F_2, and_4_out, and_5_out, and_6_out);
  or or_3 (F_3, and_7_out, and_8_out, and_9_out, and_10_out, and_11_out, and_12_out, and_13_out, and_14_out, and_15_out, and_16_out);
  // Buzzer #(.freq_measure("Hz"), .vol_width(1)) buzzer_1: pin names not known; wires that end beside it: buzzer_1_p1
  not not_9 (buzzer_1_p1, comparator_1_eq);
  LED #(.active("false")) led_1 (.in(comparator_1_eq));
  Comparator #(.width(1), .mode("twosComplement")) comparator_1 (.a(F), .b(F_3), .eq(comparator_1_eq));  // open: gt, lt
  // Buzzer #(.freq_measure("Hz"), .vol_width(1)) buzzer_2: pin names not known; wires that end beside it: buzzer_2_p1
  not not_10 (buzzer_2_p1, comparator_2_eq);
  Comparator #(.width(1), .mode("twosComplement")) comparator_2 (
    .a(F_2), .b(F_3), .eq(comparator_2_eq));  // open: gt, lt
  LED #(.active("false")) led_2 (.in(comparator_2_eq));
endmodule
