// Logisim project 第三章习题的仿真结果.circ as structural Verilog: 3 circuits, main circuit 3.14
module _3_14 (
);

  wire A, B, CLK, CP, D, digital_oscilloscope_1_p7, nQ, programmablegenerator_1_p1, Q;
  wire [0:0] counter_1_q;

  Clock #(.highDuration(1), .lowDuration(1)) clock_1 (.out(CLK));
  // ProgrammableGenerator #(.nState(4), .Contents("2 8*3 7 8*3")) programmablegenerator_1: pin names not known; wires that end beside it: programmablegenerator_1_p1, A
  Counter #(.width(2), .max('h3), .ongoal("wrap"), .trigger("rising"), .behavior("new")) counter_1 (
    .Q({CP, counter_1_q[0]}), .clk(CLK));  // open: load, D, count, carry, clr, preset, down
  // ProgrammableGenerator #(.nState(4), .Contents("2 16*3 7 16*3")) programmablegenerator_2: pin names not known; wires that end beside it: B
  // Digital_Oscilloscope #(.nState(35), .frontlines("rising"), .showclock("true")) digital_oscilloscope_1: pin names not known; wires that end beside it: CLK, CP, A, B, D, Q, digital_oscilloscope_1_p7, digital_oscilloscope_1_p7
  or or_1 (D, A, B);
  D_Flip_Flop #(.trigger("rising"), .Pre_Clr_Positions("ABOVE_BELOW"), .NegatePresetClear("false"), .enable("false"), .NewFFLayout("true")) d_ff_1 (
    .clk(CP), .D(D), .Q(Q), .Qn(nQ));  // open: preset, reset
endmodule

module _3_15 (
);

  wire A, CLK, CP, j_k_ff_2_qn, Q1, Q2;
  wire [0:0] counter_1_q;

  // Digital_Oscilloscope #(.nState(35), .frontlines("rising"), .showclock("true")) digital_oscilloscope_1: pin names not known; wires that end beside it: CLK, CP, A, Q1, Q2
  Clock #(.highDuration(1), .lowDuration(1)) clock_1 (.out(CLK));
  Counter #(.width(2), .max('h3), .ongoal("wrap"), .trigger("rising"), .behavior("new")) counter_1 (
    .Q({CP, counter_1_q[0]}), .clk(CLK));  // open: load, D, count, carry, clr, preset, down
  J_K_Flip_Flop #(.trigger("rising"), .Pre_Clr_Positions("ABOVE_BELOW"), .NegatePresetClear("false"), .enable("false"), .NewFFLayout("true")) j_k_ff_1 (
    .J(1'b1), .clk(A), .K(1'b1), .Q(Q1), .reset(j_k_ff_2_qn));  // open: Qn, preset
  // ProgrammableGenerator #(.nState(4), .Contents("4 12*7")) programmablegenerator_1: pin names not known; wires that end beside it: Q1, A
  J_K_Flip_Flop #(.trigger("rising"), .Pre_Clr_Positions("ABOVE_BELOW"), .NegatePresetClear("false"), .enable("false"), .NewFFLayout("true")) j_k_ff_2 (
    .J(Q1), .clk(CP), .K(1'b1), .Q(Q2), .Qn(j_k_ff_2_qn));  // open: preset, reset
endmodule

module _3_14_2 (
);

  wire A, B, CLK, CP, D, digital_oscilloscope_1_p7, nQ, Q;
  wire [0:0] counter_1_q;

  Clock #(.highDuration(1), .lowDuration(1)) clock_1 (.out(CLK));
  // ProgrammableGenerator #(.nState(4), .Contents("2 8*3 7 8*3")) programmablegenerator_1: pin names not known; wires that end beside it: A
  Counter #(.width(2), .max('h3), .ongoal("wrap"), .trigger("rising"), .behavior("new")) counter_1 (
    .Q({CP, counter_1_q[0]}), .clk(CLK));  // open: load, D, count, carry, clr, preset, down
  // ProgrammableGenerator #(.nState(4), .Contents("2 16*3 7 16*3")) programmablegenerator_2: pin names not known; wires that end beside it: B, D
  // Digital_Oscilloscope #(.nState(35), .frontlines("rising"), .showclock("true")) digital_oscilloscope_1: pin names not known; wires that end beside it: CLK, CP, A, B, D, Q, digital_oscilloscope_1_p7, digital_oscilloscope_1_p7
  nand nand_1 (D, A, B);
  T_Flip_Flop #(.trigger("rising"), .Pre_Clr_Positions("ABOVE_BELOW"), .NegatePresetClear("false"), .enable("false"), .NewFFLayout("true")) t_ff_1 (
    .clk(CP), .T(D), .Q(Q), .Qn(nQ));  // open: preset, reset
endmodule
