// Logisim project 37220232203808_宋浩元_第一次实验设计文件.circ as structural Verilog: 6 circuits, main circuit 2.2(1)
// F
module _2_2_1 (
  output F,
  output F2
);

  wire A, and_1_out, and_2_out, and_3_out, and_4_out, B, button_1_out, buzzer_1_p1, C, clock_1_out,
       comparator_1_eq, not_1_out, not_2_out, not_3_out, not_4_out;

  Counter #(.width(3), .max('h7), .ongoal("wrap"), .trigger("rising"), .behavior("new")) counter_1 (
    .Q({C, B, A}), .clk(clock_1_out), .clr(button_1_out));  // open: load, D, count, carry, preset, down
  Clock #(.highDuration(1), .lowDuration(1)) clock_1 (.out(clock_1_out));
  Button button_1 (.out(button_1_out));
  not not_1 (not_1_out, A);
  not not_2 (not_2_out, B);
  not not_3 (not_3_out, A);
  not not_4 (not_4_out, C);
  and and_1 (and_1_out, A, B);
  and and_2 (and_2_out, not_1_out, C);
  and and_3 (and_3_out, A, not_2_out);
  and and_4 (and_4_out, not_3_out, not_4_out);
  nor nor_1 (F, and_1_out, and_2_out);
  or or_1 (F2, and_3_out, and_4_out);
  Comparator #(.width(1), .mode("twosComplement")) comparator_1 (.a(F), .b(F2), .eq(comparator_1_eq));  // open: gt, lt
  // Buzzer #(.freq_measure("Hz"), .vol_width(1)) buzzer_1: pin names not known; wires that end beside it: buzzer_1_p1
  not not_5 (buzzer_1_p1, comparator_1_eq);
  LED #(.active("false")) led_1 (.in(comparator_1_eq));
endmodule

module _2_3_1 (
  output F,
  output F2
);

  wire A, and_1_out, and_2_out, B, button_1_out, buzzer_1_p1, clock_1_out, comparator_1_eq, not_1_out,
       not_2_out, not_3_out, not_4_out, or_1_out, or_2_out;

  Counter #(.width(2), .max('h3), .ongoal("wrap"), .trigger("rising"), .behavior("new")) counter_1 (
    .Q({B, A}), .clk(clock_1_out), .clr(button_1_out));  // open: load, D, count, carry, preset, down
  Clock #(.highDuration(1), .lowDuration(1)) clock_1 (.out(clock_1_out));
  Button button_1 (.out(button_1_out));
  not not_1 (not_1_out, B);
  not not_2 (not_2_out, A);
  not not_3 (not_3_out, A);
  not not_4 (not_4_out, B);
  and and_1 (and_1_out, A, not_1_out);
  and and_2 (and_2_out, not_2_out, B);
  or or_1 (or_1_out, not_3_out, not_4_out);
  or or_2 (or_2_out, A, B);
  or or_3 (F, and_1_out, and_2_out);
  and and_3 (F2, or_1_out, or_2_out);
  // Buzzer #(.freq_measure("Hz"), .vol_width(1)) buzzer_1: pin names not known; wires that end beside it: buzzer_1_p1
  not not_5 (buzzer_1_p1, comparator_1_eq);
  Comparator #(.width(1), .mode("twosComplement")) comparator_1 (.a(F), .b(F2), .eq(comparator_1_eq));  // open: gt, lt
  LED #(.active("false")) led_1 (.in(comparator_1_eq));
endmodule

module _2_4 (
  output F,
  output F2
);

  wire A, and_1_out, and_2_out, and_3_out, B, button_1_out, buzzer_1_p1, clock_1_out, comparator_1_eq,
       not_1_out, not_2_out, not_3_out, not_4_out, or_1_out, or_2_out;

  Clock #(.highDuration(1), .lowDuration(1)) clock_1 (.out(clock_1_out));
  Button button_1 (.out(button_1_out));
  Counter #(.width(2), .max('h3), .ongoal("wrap"), .trigger("rising"), .behavior("new")) counter_1 (
    .Q({B, A}), .clk(clock_1_out), .clr(button_1_out));  // open: load, D, count, carry, preset, down
  not not_1 (not_1_out, A);
  not not_2 (not_2_out, B);
  and and_1 (and_1_out, A, B);
  not not_3 (not_3_out, A);
  and and_2 (and_2_out, not_3_out, not_4_out);
  not not_4 (not_4_out, B);
  or or_1 (or_1_out, not_1_out, not_2_out);
  or or_2 (or_2_out, A, B);
  or or_3 (F, and_1_out, and_2_out);
  and and_3 (and_3_out, or_1_out, or_2_out);
  not not_5 (F2, and_3_out);
  Comparator #(.width(1), .mode("twosComplement")) comparator_1 (.a(F), .b(F2), .eq(comparator_1_eq));  // open: gt, lt
  // Buzzer #(.freq_measure("Hz"), .vol_width(1)) buzzer_1: pin names not known; wires that end beside it: buzzer_1_p1
  not not_6 (buzzer_1_p1, comparator_1_eq);
  LED #(.active("false")) led_1 (.in(comparator_1_eq));
endmodule

module _2_7_1 (
  output F,
  output F2,
  output F3
);

  wire A, and_1_out, and_2_out, and_3_out, and_4_out, button_1_out, buzzer_1_p1, buzzer_2_p1, C, clock_1_out,
       comparator_1_eq, comparator_2_eq, D, not_1_out, not_2_out, not_3_out, not_4_out;

  Clock #(.highDuration(1), .lowDuration(1)) clock_1 (.out(clock_1_out));
  Button button_1 (.out(button_1_out));
  Counter #(.width(4), .max('hf), .ongoal("wrap"), .trigger("rising"), .behavior("new")) counter_1 (
    .Q({D, C, F2, A}), .clk(clock_1_out), .clr(button_1_out));  // open: load, D, count, carry, preset, down
  not not_1 (not_1_out, C);
  not not_2 (not_2_out, D);
  not not_3 (not_3_out, A);
  not not_4 (not_4_out, C);
  and and_1 (and_1_out, F2, not_1_out, not_2_out);
  and and_2 (and_2_out, not_3_out, F2);
  and and_3 (and_3_out, A, F2, not_4_out, D);
  and and_4 (and_4_out, F2, C);
  or or_1 (F, and_1_out, and_2_out, and_3_out, and_4_out);
  Comparator #(.width(1), .mode("twosComplement")) comparator_1 (.a(F), .b(F2), .eq(comparator_1_eq));  // open: gt, lt
  // Buzzer #(.freq_measure("Hz"), .vol_width(1)) buzzer_1: pin names not known; wires that end beside it: buzzer_1_p1
  not not_5 (buzzer_1_p1, comparator_1_eq);
  LED #(.active("false")) led_1 (.in(comparator_1_eq));
  // Buzzer #(.freq_measure("Hz"), .vol_width(1)) buzzer_2: pin names not known; wires that end beside it: buzzer_2_p1
  not not_6 (buzzer_2_p1, comparator_2_eq);
  Comparator #(.width(1), .mode("twosComplement")) comparator_2 (.a(F), .b(F2), .eq(comparator_2_eq));  // open: gt, lt
  LED #(.active("false")) led_2 (.in(comparator_2_eq));

  assign F3 = F2;

  // Other names for the same wires on the sheet: B = F2
endmodule

module _2_8_1 (
  output F,
  output F_2,
  output F_3
);

  wire A, and_1_out, and_2_out, and_3_out, and_4_out, and_5_out, and_6_out, and_7_out, B, button_1_out,
       buzzer_1_p1, buzzer_2_p1, C, clock_1_out, comparator_1_eq, comparator_2_eq, D, not_1_out, not_2_out,
       not_3_out, not_4_out, not_5_out, not_6_out, not_7_out, not_8_out, not_9_out, not_10_out, not_11_out,
       or_1_out, or_2_out;

  Clock #(.highDuration(1), .lowDuration(1)) clock_1 (.out(clock_1_out));
  Button button_1 (.out(button_1_out));
  Counter #(.width(4), .max('hf), .ongoal("wrap"), .trigger("rising"), .behavior("new")) counter_1 (
    .Q({D, C, B, A}), .clk(clock_1_out), .clr(button_1_out));  // open: load, D, count, carry, preset, down
  not not_1 (not_1_out, A);
  not not_2 (not_2_out, B);
  not not_3 (not_3_out, A);
  not not_4 (not_4_out, C);
  not not_5 (not_5_out, C);
  not not_6 (not_6_out, A);
  and and_1 (and_1_out, not_6_out, not_7_out);
  not not_7 (not_7_out, B);
  and and_2 (and_2_out, B, not_8_out);
  not not_8 (not_8_out, C);
  and and_3 (and_3_out, A, C);
  or or_1 (or_1_out, A, not_9_out, not_10_out);
  not not_9 (not_9_out, A);
  not not_10 (not_10_out, C);
  not not_11 (not_11_out, A);
  or or_2 (or_2_out, not_11_out, A, C);
  and and_4 (and_4_out, not_1_out, not_2_out);
  and and_5 (and_5_out, not_3_out, not_4_out, D);
  and and_6 (and_6_out, A, C);
  and and_7 (and_7_out, B, not_5_out);
  or or_3 (F_2, and_1_out, and_2_out, and_3_out);
  and and_8 (F_3, or_1_out, or_2_out);
  or or_4 (F, and_4_out, and_5_out, and_6_out, and_7_out);
  // Buzzer #(.freq_measure("Hz"), .vol_width(1)) buzzer_1: pin names not known; wires that end beside it: buzzer_1_p1
  not not_12 (buzzer_1_p1, comparator_1_eq);
  Comparator #(.width(1), .mode("twosComplement")) comparator_1 (.a(F), .b(F_2), .eq(comparator_1_eq));  // open: gt, lt
  LED #(.active("false")) led_1 (.in(comparator_1_eq));
  // Buzzer #(.freq_measure("Hz"), .vol_width(1)) buzzer_2: pin names not known; wires that end beside it: buzzer_2_p1
  not not_13 (buzzer_2_p1, comparator_2_eq);
  Comparator #(.width(1), .mode("twosComplement")) comparator_2 (
    .a(F_2), .b(F_3), .eq(comparator_2_eq));  // open: gt, lt
  LED #(.active("false")) led_2 (.in(comparator_2_eq));
endmodule

module _2_9_1 (
  output F,
  output G
);

  wire A, and_1_out, and_2_out, and_3_out, and_4_out, and_5_out, and_6_out, and_7_out, and_8_out, and_9_out,
       and_10_out, and_11_out, B, button_1_out, buzzer_1_p1, C, clock_1_out, comparator_1_eq, nor_1_out,
       nor_2_out, not_1_out, not_2_out, not_3_out, not_4_out, not_5_out, or_1_out, or_2_out;

  Clock #(.highDuration(1), .lowDuration(1)) clock_1 (.out(clock_1_out));
  Button button_1 (.out(button_1_out));
  Counter #(.width(3), .max('h7), .ongoal("wrap"), .trigger("rising"), .behavior("new")) counter_1 (
    .Q({C, B, A}), .clk(clock_1_out), .clr(button_1_out));  // open: load, D, count, carry, preset, down
  not not_1 (not_1_out, B);
  not not_2 (not_2_out, A);
  not not_3 (not_3_out, B);
  not not_4 (not_4_out, A);
  and and_1 (and_1_out, A, B);
  and and_2 (and_2_out, B, C);
  and and_3 (and_3_out, A, C);
  and and_4 (and_4_out, A, not_1_out);
  and and_5 (and_5_out, not_2_out, B);
  and and_6 (and_6_out, A, not_3_out);
  and and_7 (and_7_out, not_4_out, B);
  nor nor_1 (nor_1_out, and_1_out, and_2_out, and_3_out);
  or or_1 (or_1_out, A, B, C);
  or or_2 (or_2_out, and_4_out, and_5_out);
  and and_8 (and_8_out, or_2_out, not_5_out);
  not not_5 (not_5_out, C);
  nor nor_2 (nor_2_out, and_6_out, and_7_out);
  and and_9 (and_9_out, nor_2_out, C);
  and and_10 (and_10_out, nor_1_out, or_1_out);
  and and_11 (and_11_out, A, B, C);
  or or_3 (F, and_8_out, and_9_out);
  or or_4 (G, and_10_out, and_11_out);
  // Buzzer #(.freq_measure("Hz"), .vol_width(1)) buzzer_1: pin names not known; wires that end beside it: buzzer_1_p1
  not not_6 (buzzer_1_p1, comparator_1_eq);
  Comparator #(.width(1), .mode("twosComplement")) comparator_1 (.a(F), .b(G), .eq(comparator_1_eq));  // open: gt, lt
  LED #(.active("false")) led_1 (.in(comparator_1_eq));
endmodule
