// Logisim project 第7章习题电路的实现.circ as structural Verilog: 5 circuits, main circuit 74193芯片
// 74193
module \_74193芯片  (
  input  A,
  input  B,
  input  C,
  input  D,
  input  CPu,
  input  CPd,
  input  CLR,
  input  nLD,
  output Qa,
  output Qb,
  output Qc,
  output Qd_,
  output nQcc,
  output nQcb
);

  wire counter_1_carry, CP, EN, Inv, LOAD, not_1_out, or_1_out;
  wire [3:0] OUT, register_1_q;

  // Probe on {D, C, B, A}
  and and_1 (CP, CPu, CPd);
  or or_1 (or_1_out, CLR, LOAD);
  nor nor_1 (LOAD, CLR, nLD);
  // Probe on OUT
  Counter #(.width(4), .max('hf), .ongoal("wrap"), .trigger("rising"), .behavior("new")) counter_1 (
    .load(1'b0), .D({D, C, B, A}), .count(EN), .Q(OUT), .carry(counter_1_carry), .clk(CP), .clr(or_1_out),
    .preset(1'b0), .down(Inv));
  D_Flip_Flop #(.trigger("rising"), .Pre_Clr_Positions("ABOVE_BELOW"), .NegatePresetClear("false"), .enable("false"), .NewFFLayout("true")) d_ff_1 (
    .clk(CP), .D(counter_1_carry), .Qn(nQcb));  // open: Q, preset, reset
  and and_2 (EN, nLD, ~CLR);  // AND_Gate
  Register #(.width(4), .trigger("rising"), .Select("low")) register_1 (
    .D({D, C, B, A}), .Q(register_1_q), .clk(LOAD), .clr(CLR));  // open: en
  not not_1 (not_1_out, CPu);
  // Probe on register_1_q
  Register #(.width(1), .trigger("rising"), .Select("low")) register_2 (
    .Q(Inv), .clr(not_1_out), .preset(CPu));  // open: D, en, clk, cs
  Adder #(.width(4)) adder_1 (.a(register_1_q), .b(OUT), .out({Qd_, Qc, Qb, Qa}));  // open: cin, cout
  // Probe on {Qd_, Qc, Qb, Qa}

  assign nQcc = nQcb;

  // Other names for the same wires on the sheet: ABCD[3:0] = {D, C, B, A}

  // Notes on the sheet:
  //   74193芯片（双时钟4位二进制同步可逆计数器）
endmodule

// 74290
module \_74290芯片  (
  input  CPa,
  input  CPb,
  input  R0a,
  input  R0b,
  input  R9a,
  input  R9b,
  input  S1,
  input  S0,
  output Qa,
  output Qb,
  output Qc,
  output Qd
);

  wire and_1_out, and_4_out, and_5_out, and_6_out, CLR, nand_1_out, or_1_out, or_2_out, or_3_out, or_4_out,
       SEL1;
  wire [0:0] _1Q;
  wire [2:2] SEL2;
  wire [3:0] _3Q, _4Q, multiplexer_1_out;
  wire [3:1] _2Q;

  and and_1 (and_1_out, R0a, R0b);
  nand nand_1 (nand_1_out, R9a, R9b);
  and and_2 (CLR, and_1_out, nand_1_out);
  and and_3 (SEL1, R9a, R9b);
  nor nor_1 (SEL2[2], CLR, SEL1);
  Counter #(.width(3), .max('h7), .ongoal("wrap"), .trigger("falling"), .behavior("new")) counter_1 (
    .Q(_2Q), .clk(CPb), .clr(or_1_out));  // open: load, D, count, carry, preset, down
  or or_1 (or_1_out, and_5_out, CLR);
  Counter #(.width(4), .max('hf), .ongoal("wrap"), .trigger("falling"), .behavior("new")) counter_2 (
    .Q(_3Q), .clk(CPa), .clr(or_3_out));  // open: load, D, count, carry, preset, down
  Counter #(.width(3), .max('h7), .ongoal("wrap"), .trigger("falling"), .behavior("new")) counter_3 (
    .Q(_4Q[3:1]), .clk(CPb), .clr(or_2_out));  // open: load, D, count, carry, preset, down
  or or_2 (or_2_out, and_4_out, CLR);
  Counter #(.width(1), .max('h1), .ongoal("wrap"), .trigger("falling"), .behavior("new")) counter_4 (
    .Q(_1Q[0]), .clk(CPa), .clr(CLR));  // open: load, D, count, carry, preset, down
  // Probe on _3Q
  or or_3 (or_3_out, and_6_out, CLR);
  and and_4 (and_4_out, _4Q[1], _4Q[3]);
  and and_5 (and_5_out, _2Q[1], _2Q[3]);
  or or_4 (or_4_out, _4Q[1], _4Q[2], _4Q[3]);
  and and_6 (and_6_out, _3Q[1], _3Q[3]);
  T_Flip_Flop #(.trigger("falling"), .Pre_Clr_Positions("ABOVE_BELOW"), .NegatePresetClear("false"), .enable("false"), .NewFFLayout("true")) t_ff_1 (
    .clk(or_4_out), .T(1'b1), .Q(_4Q[0]));  // open: Qn, preset, reset
  Multiplexer #(.select(1), .width(4), .disabled("Z"), .enable("false")) multiplexer_1 (
    .in0(4'b0000), .in1(4'b1001), .out(multiplexer_1_out), .sel(SEL1));
  Multiplexer #(.select(3), .width(4), .disabled("Z"), .enable("false")) multiplexer_2 (
    .in0(multiplexer_1_out), .in1(multiplexer_1_out), .in2(multiplexer_1_out), .in3(multiplexer_1_out),
    .in4({3'b000, _1Q[0]}), .in5({_2Q, 1'b0}), .in6(_3Q), .in7(_4Q), .out({Qd, Qc, Qb, Qa}),
    .sel({SEL2[2], S1, S0}));

  // Other names for the same wires on the sheet: _1Qa = _1Q[0]; _2Qb = _2Q[1]; _2Qc = _2Q[2]; _2Qd = _2Q[3];
  //   _3Qa = _3Q[0]; _3Qb = _3Q[1]; _3Qc = _3Q[2]; _3Qd = _3Q[3]; _4Qa = _4Q[0]; _4Qb = _4Q[1]; _4Qc = _4Q[2];
  //   _4Qd = _4Q[3]; SEL2[1:0] = {S1, S0}; T = SEL2[2]

  // Notes on the sheet:
  //   74290芯片（二-五-十进制加法计数器）
endmodule

// 74194
module \_74194芯片  (
  input  nCLR,
  input  CP,
  input  S1,
  input  S0,
  input  DR,
  input  DL,
  input  D,
  input  C,
  input  B,
  input  A,
  output Qd,
  output Qc,
  output Qb,
  output Qa
);

  wire Din, Load, nCLR_t, not_2_out, SEL1, SEL2, shift_register_1_out;
  wire [3:0] QL;

  not not_1 (nCLR_t, nCLR);
  not not_2 (not_2_out, S1);
  Multiplexer #(.select(1), .width(1), .disabled("Z"), .enable("false")) multiplexer_1 (
    .in0(DR), .in1(DL), .out(Din), .sel(SEL1));
  nand nand_1 (SEL1, not_2_out, S0);
  not not_3 (SEL2, S0);
  and and_1 (Load, S1, S0);
  Shift_Register #(.width(1), .length(4), .parallel("true"), .trigger("rising")) shift_register_1 (
    .shift(CP), .in(Din), .clk(CP), .out(shift_register_1_out), .load(Load), .clr(nCLR_t), .d0(D),
    .q0(QL[0]), .d1(C), .q1(QL[1]), .d2(B), .q2(QL[2]), .d3(A), .q3(QL[3]));
  Multiplexer #(.select(1), .width(4), .disabled("Z"), .enable("false")) multiplexer_2 (
    .in0({QL[0], QL[1], QL[2], QL[3]}), .in1(QL), .out({Qd, Qc, Qb, Qa}), .sel(SEL2));
  // Probe on shift_register_1_out
  // Probe on {Qd, Qc, Qb, Qa}
  // Probe on {QL[0], QL[1], QL[2], QL[3]}
  // Probe on QL

  // Other names for the same wires on the sheet: EN = CP; QR[3:0] = {QL[0], QL[1], QL[2], QL[3]}

  // Notes on the sheet:
  //   74194芯片（4位双向移位寄存器）
endmodule

module _7_9 (
  output Qa,
  output Qb,
  output Qc,
  output Qd,
  output [3:0] out_5
);

  wire and_1_out, clock_1_out;

  Clock #(.highDuration(1), .lowDuration(1)) clock_1 (.out(clock_1_out));
  \_74193芯片  \u_74193芯片_1  (
    .CPu(clock_1_out), .CPd(1'b1), .CLR(and_1_out), .nLD(1'b1), .Qa(out_5[0]), .Qb(out_5[1]), .Qc(out_5[2]),
    .Qd_(out_5[3]));  // open: A, B, C, D, nQcc, nQcb
  and and_1 (and_1_out, out_5[2], out_5[3]);

  assign Qa = out_5[0];
  assign Qb = out_5[1];
  assign Qc = out_5[2];
  assign Qd = out_5[3];
endmodule

module _7_10 (
  input  nCLR,
  output Qd,
  output Qc,
  output Qb
);

  wire and_1_out, and_2_out, and_3_out, CP, not_1_out, not_2_out, not_3_out, or_1_out;

  Clock #(.highDuration(1), .lowDuration(1)) clock_1 (.out(CP));
  // Digital_Oscilloscope #(.nState(20), .frontlines("rising"), .showclock("true")) digital_oscilloscope_1: pin names not known; wires that end beside it: CP, Qb
  not not_1 (not_1_out, Qd);
  not not_2 (not_2_out, Qb);
  not not_3 (not_3_out, Qc);
  \_74194芯片  \u_74194芯片_1  (
    .nCLR(nCLR), .CP(CP), .S1(1'b0), .S0(1'b1), .DR(or_1_out), .Qd(Qd), .Qc(Qc), .Qb(Qb));  // open: DL, D, C, B, A, Qa
  and and_1 (and_1_out, not_2_out, Qd);
  and and_2 (and_2_out, not_2_out, not_3_out);
  and and_3 (and_3_out, Qb, Qc, not_1_out);
  or or_1 (or_1_out, and_1_out, and_2_out, and_3_out);

  // Other names for the same wires on the sheet: Z = Qb

  // Notes on the sheet:
  //      S1
  //   S0
endmodule
