// Logisim project 第四章习题的实现.circ as structural Verilog: 9 circuits, main circuit 4.1
module _4_1 (
  output F,
  output F_2
);

  wire A, and_1_out, and_2_out, and_3_out, and_4_out, and_5_out, B, button_1_out, buzzer_1_p1, C,
       clock_1_out, comparator_1_eq, nand_1_out, nand_2_out, nand_3_out, not_1_out, not_2_out, not_3_out;

  Clock #(.highDuration(1), .lowDuration(1)) clock_1 (.out(clock_1_out));
  Button button_1 (.out(button_1_out));
  Counter #(.width(3), .max('h7), .ongoal("wrap"), .trigger("rising"), .behavior("new")) counter_1 (
    .Q({A, B, C}), .clk(clock_1_out), .clr(button_1_out));  // open: load, D, count, carry, preset, down
  nand nand_1 (nand_1_out, A, B, C);
  nand nand_2 (nand_2_out, A, B, C);
  nand nand_3 (nand_3_out, A, B, C);
  and and_1 (and_1_out, nand_1_out, A);
  and and_2 (and_2_out, nand_2_out, B);
  and and_3 (and_3_out, nand_3_out, C);
  nor nor_1 (F, and_1_out, and_2_out, and_3_out);
  not not_1 (not_1_out, A);
  not not_2 (not_2_out, B);
  not not_3 (not_3_out, C);
  and and_4 (and_4_out, A, B, C);
  and and_5 (and_5_out, not_1_out, not_2_out, not_3_out);
  or or_1 (F_2, and_4_out, and_5_out);
  Comparator #(.width(1), .mode("twosComplement")) comparator_1 (.a(F), .b(F_2), .eq(comparator_1_eq));  // open: gt, lt
  // Buzzer #(.freq_measure("Hz"), .vol_width(7)) buzzer_1: pin names not known; wires that end beside it: buzzer_1_p1
  not not_4 (buzzer_1_p1, comparator_1_eq);
  LED #(.active("false")) led_1 (.in(comparator_1_eq));
endmodule

module _4_2 (
  output W,
  output X,
  output Y,
  output Z
);

  wire and_1_out, and_2_out, and_3_out, and_4_out, and_5_out, and_6_out, B, button_1_out, C, clock_1_out, D,
       not_1_out, not_2_out, not_3_out, not_4_out, not_5_out, not_6_out;

  Counter #(.width(4), .max('hf), .ongoal("wrap"), .trigger("rising"), .behavior("new")) counter_1 (
    .Q({D, C, B, W}), .clk(clock_1_out), .clr(button_1_out));  // open: load, D, count, carry, preset, down
  Clock #(.highDuration(1), .lowDuration(1)) clock_1 (.out(clock_1_out));
  Button button_1 (.out(button_1_out));
  not not_1 (not_1_out, W);
  not not_2 (not_2_out, B);
  not not_3 (not_3_out, B);
  not not_4 (not_4_out, C);
  not not_5 (not_5_out, C);
  not not_6 (not_6_out, D);
  and and_1 (and_1_out, not_1_out, B);
  and and_2 (and_2_out, W, not_2_out);
  and and_3 (and_3_out, not_3_out, C);
  and and_4 (and_4_out, B, not_4_out);
  and and_5 (and_5_out, not_5_out, D);
  and and_6 (and_6_out, C, not_6_out);
  or or_1 (X, and_1_out, and_2_out);
  or or_2 (Y, and_3_out, and_4_out);
  or or_3 (Z, and_5_out, and_6_out);

  // Other names for the same wires on the sheet: A = W
endmodule

module _4_4 (
  output A,
  output B
);

  wire A1, A2, and_3_out, and_4_out, and_5_out, and_6_out, B1, B2, button_1_out, clock_1_out,
       comparator_1_gt, nand_1_out, not_1_out, not_2_out, not_3_out, not_4_out, or_1_out;

  Clock #(.highDuration(1), .lowDuration(1)) clock_1 (.out(clock_1_out));
  Counter #(.width(4), .max('hf), .ongoal("wrap"), .trigger("rising"), .behavior("new")) counter_1 (
    .Q({B2, B1, A2, A1}), .clk(clock_1_out), .clr(button_1_out));  // open: load, D, count, carry, preset, down
  Button button_1 (.out(button_1_out));
  and and_1 (A, A1, A2);
  and and_2 (B, B1, B2);
  not not_1 (not_1_out, B2);
  not not_2 (not_2_out, B2);
  not not_3 (not_3_out, B1);
  not not_4 (not_4_out, B1);
  Comparator #(.width(1), .mode("twosComplement")) comparator_1 (.a(A), .b(B), .gt(comparator_1_gt));  // open: eq, lt
  and and_3 (and_3_out, A2, not_1_out);
  and and_4 (and_4_out, A1, not_2_out, not_3_out);
  and and_5 (and_5_out, A2, A1, not_4_out);
  or or_1 (or_1_out, and_3_out, and_4_out, and_5_out);
  and and_6 (and_6_out, or_1_out, comparator_1_gt);
  nand nand_1 (nand_1_out, or_1_out, comparator_1_gt);
  // XOR_Gate xor_1 has open pins: in0=and_6_out, in1=nand_1_out, out=open
endmodule

module _4_5 (
  output W,
  output X,
  output Y,
  output Z
);

  wire and_1_out, and_2_out, B, button_1_out, C, clock_1_out, D, or_1_out;

  Clock #(.highDuration(1), .lowDuration(1)) clock_1 (.out(clock_1_out));
  Counter #(.width(4), .max('hf), .ongoal("wrap"), .trigger("rising"), .behavior("new")) counter_1 (
    .Q({D, C, B, W}), .clk(clock_1_out), .clr(button_1_out));  // open: load, D, count, carry, preset, down
  Button button_1 (.out(button_1_out));
  or or_1 (or_1_out, B, C, D);
  xor odd_parity_1 (Y, W, C, D);
  not not_1 (Z, D);
  and and_1 (and_1_out, W, or_1_out);
  and and_2 (and_2_out, B, C, D);
  or or_2 (X, and_1_out, and_2_out);

  // Other names for the same wires on the sheet: A = W
endmodule

module _4_8 (
  output F
);

  wire A, and_1_out, and_2_out, B, button_1_out, C, clock_1_out, D;

  Clock #(.highDuration(1), .lowDuration(1)) clock_1 (.out(clock_1_out));
  Counter #(.width(4), .max('hf), .ongoal("wrap"), .trigger("rising"), .behavior("new")) counter_1 (
    .Q({D, C, B, A}), .clk(clock_1_out), .clr(button_1_out));  // open: load, D, count, carry, preset, down
  Button button_1 (.out(button_1_out));
  and and_1 (and_1_out, B, C);
  and and_2 (and_2_out, B, D);
  or or_1 (F, A, and_1_out, and_2_out);
endmodule

module _4_9 (
  output F
);

  wire A, B, button_1_out, C, clock_1_out, D;

  Clock #(.highDuration(1), .lowDuration(1)) clock_1 (.out(clock_1_out));
  Counter #(.width(4), .max('hf), .ongoal("wrap"), .trigger("rising"), .behavior("new")) counter_1 (
    .Q({D, C, B, A}), .clk(clock_1_out), .clr(button_1_out));  // open: load, D, count, carry, preset, down
  Button button_1 (.out(button_1_out));
  xnor even_parity_1 (F, A, B, C, D);
endmodule

module _4_10 (
  output F,
  output G
);

  wire A, and_1_out, and_2_out, and_3_out, and_4_out, and_5_out, and_6_out, and_7_out, and_8_out, and_9_out,
       B, button_1_out, C, clock_1_out, M, not_1_out, not_2_out, not_3_out, not_4_out, not_5_out, not_6_out,
       not_7_out, not_8_out, not_9_out, not_10_out;

  Counter #(.width(4), .max('hf), .ongoal("wrap"), .trigger("rising"), .behavior("new")) counter_1 (
    .Q({M, C, B, A}), .clk(clock_1_out), .clr(button_1_out));  // open: load, D, count, carry, preset, down
  Clock #(.highDuration(1), .lowDuration(1)) clock_1 (.out(clock_1_out));
  Button button_1 (.out(button_1_out));
  not not_1 (not_1_out, A);
  not not_2 (not_2_out, B);
  not not_3 (not_3_out, A);
  not not_4 (not_4_out, C);
  not not_5 (not_5_out, B);
  not not_6 (not_6_out, C);
  not not_7 (not_7_out, M);
  not not_8 (not_8_out, M);
  not not_9 (not_9_out, A);
  not not_10 (not_10_out, A);
  and and_1 (and_1_out, not_1_out, not_2_out, C);
  and and_2 (and_2_out, not_3_out, B, not_4_out);
  and and_3 (and_3_out, A, not_5_out, not_6_out);
  and and_4 (and_4_out, A, B, C);
  and and_5 (and_5_out, B, C);
  and and_6 (and_6_out, not_7_out, A, C);
  and and_7 (and_7_out, not_8_out, A, B);
  and and_8 (and_8_out, M, not_9_out, C);
  and and_9 (and_9_out, M, not_10_out, B);
  or or_1 (F, and_1_out, and_2_out, and_3_out, and_4_out);
  or or_2 (G, and_5_out, and_6_out, and_7_out, and_8_out, and_9_out);
endmodule

module _4_12_a (
  output F
);

  wire A, B, button_1_out, C, clock_1_out, not_1_out, not_2_out, not_3_out, or_1_out, or_2_out;

  Clock #(.highDuration(1), .lowDuration(1)) clock_1 (.out(clock_1_out));
  Button button_1 (.out(button_1_out));
  Counter #(.width(3), .max('h7), .ongoal("wrap"), .trigger("rising"), .behavior("new")) counter_1 (
    .Q({A, B, C}), .clk(clock_1_out), .clr(button_1_out));  // open: load, D, count, carry, preset, down
  not not_1 (not_1_out, B);
  not not_2 (not_2_out, A);
  not not_3 (not_3_out, C);
  or or_1 (or_1_out, A, not_1_out);
  or or_2 (or_2_out, not_2_out, not_3_out);
  and and_1 (F, or_1_out, or_2_out);
endmodule

module _4_12_b (
  output F
);

  wire A, B, button_1_out, C, clock_1_out, not_1_out, not_2_out, not_3_out, or_1_out, or_2_out, or_3_out;

  Clock #(.highDuration(1), .lowDuration(1)) clock_1 (.out(clock_1_out));
  Button button_1 (.out(button_1_out));
  Counter #(.width(3), .max('h7), .ongoal("wrap"), .trigger("rising"), .behavior("new")) counter_1 (
    .Q({A, B, C}), .clk(clock_1_out), .clr(button_1_out));  // open: load, D, count, carry, preset, down
  or or_1 (or_1_out, A, not_1_out);
  not not_1 (not_1_out, B);
  not not_2 (not_2_out, A);
  or or_2 (or_2_out, not_2_out, not_3_out);
  not not_3 (not_3_out, C);
  or or_3 (or_3_out, B, C);
  and and_1 (F, or_1_out, or_2_out, or_3_out);
endmodule
