// Logisim project 第6章习题电路的实现.circ as structural Verilog
module _6_1 (
  output Z
);

  wire and_1_out, button_1_out, clock_1_out, digital_oscilloscope_1_p1, digital_oscilloscope_1_p2, Q1, Q2;

  Button button_1 (.out(button_1_out));
  and and_1 (and_1_out, button_1_out, Q1);
  Clock #(.highDuration(1), .lowDuration(1)) clock_1 (.out(clock_1_out));
  // Digital_Oscilloscope #(.nState(30), .frontlines("rising"), .showclock("true")) digital_oscilloscope_1: pin names not known; wires that end beside it: digital_oscilloscope_1_p1, digital_oscilloscope_1_p2, clock_1_out, button_1_out, Q1, Q2, Z
  D_Flip_Flop #(.trigger("falling"), .Pre_Clr_Positions("ABOVE_BELOW"), .NegatePresetClear("false"), .enable("false"), .NewFFLayout("true")) D2 (
    .clk(and_1_out), .D(digital_oscilloscope_1_p2), .Q(Q2), .Qn(digital_oscilloscope_1_p2));  // open: preset, reset
  D_Flip_Flop #(.trigger("falling"), .Pre_Clr_Positions("ABOVE_BELOW"), .NegatePresetClear("false"), .enable("false"), .NewFFLayout("true")) D1 (
    .clk(button_1_out), .D(digital_oscilloscope_1_p2), .Q(Q1), .Qn(digital_oscilloscope_1_p1));  // open: preset, reset
  and and_2 (Z, Q2, button_1_out, Q1);
endmodule

module _6_4 (
  output Q2,
  output Q1
);

  wire CP, D1_qn;

  Clock #(.highDuration(1), .lowDuration(1)) u_CP (.out(CP));
  // Digital_Oscilloscope #(.nState(15), .frontlines("rising"), .showclock("true")) digital_oscilloscope_1: pin names not known; wires that end beside it: CP, Q1, Q2
  T_Flip_Flop #(.trigger("falling"), .Pre_Clr_Positions("ABOVE_BELOW"), .NegatePresetClear("false"), .enable("false"), .NewFFLayout("true")) T2 (
    .clk(Q1), .T(1'b1), .Q(Q2));  // open: Qn, preset, reset
  D_Flip_Flop #(.trigger("falling"), .Pre_Clr_Positions("ABOVE_BELOW"), .NegatePresetClear("false"), .enable("false"), .NewFFLayout("true")) D1 (
    .clk(CP), .D(D1_qn), .Q(Q1), .Qn(D1_qn));  // open: preset, reset
endmodule

module _6_5 (
  output Z
);

  wire and_1_out, and_2_out, and_3_out, CP_out, D1_qn, D2_qn, D3_qn, or_1_out, Q1, Q2, Q3;

  Clock #(.highDuration(1), .lowDuration(1)) CP (.out(CP_out));
  and and_1 (and_1_out, Q3, D2_qn, D1_qn);
  and and_2 (and_2_out, D1_qn, D2_qn, D3_qn);
  // Digital_Oscilloscope #(.nState(20), .frontlines("rising"), .showclock("true")) digital_oscilloscope_1: pin names not known; wires that end beside it: CP_out, Q3, Q2, Q1, Z
  or or_1 (or_1_out, and_1_out, and_2_out);
  and and_3 (and_3_out, D2_qn, D1_qn);
  D_Flip_Flop #(.trigger("falling"), .Pre_Clr_Positions("ABOVE_BELOW"), .NegatePresetClear("false"), .enable("false"), .NewFFLayout("true")) D3 (
    .clk(or_1_out), .D(D3_qn), .Q(Q3), .Qn(D3_qn));  // open: preset, reset
  D_Flip_Flop #(.trigger("falling"), .Pre_Clr_Positions("ABOVE_BELOW"), .NegatePresetClear("false"), .enable("false"), .NewFFLayout("true")) D2 (
    .clk(D1_qn), .D(and_3_out), .Q(Q2), .Qn(D2_qn));  // open: preset, reset
  D_Flip_Flop #(.trigger("falling"), .Pre_Clr_Positions("ABOVE_BELOW"), .NegatePresetClear("false"), .enable("false"), .NewFFLayout("true")) D1 (
    .clk(CP_out), .D(D1_qn), .Q(Q1), .Qn(D1_qn));  // open: preset, reset
  and and_4 (Z, D3_qn, D2_qn, D1_qn);
endmodule

module _6_6 (
  output Z
);

  wire and_1_out, and_2_out, and_3_out, and_4_out, digital_oscilloscope_1_p1, or_1_out, or_2_out, Q1, Q2,
       T1_qn, T2_qn, X1, X2;

  Button u_X2 (.out(X2));
  Button u_X1 (.out(X1));
  // Digital_Oscilloscope #(.nState(20), .frontlines("rising"), .showclock("true")) digital_oscilloscope_1: pin names not known; wires that end beside it: digital_oscilloscope_1_p1, X1, X2, Q1, Q2, Z
  Clock #(.highDuration(1), .lowDuration(1)) clock_1 (.out(digital_oscilloscope_1_p1));
  and and_1 (and_1_out, Q2, X2);
  or or_1 (or_1_out, and_1_out, and_2_out);
  and and_2 (and_2_out, T2_qn, X1, Q1);
  and and_3 (and_3_out, Q1, X2);
  or or_2 (or_2_out, and_3_out, and_4_out);
  and and_4 (and_4_out, X1, T1_qn);
  T_Flip_Flop #(.trigger("falling"), .Pre_Clr_Positions("ABOVE_BELOW"), .NegatePresetClear("false"), .enable("false"), .NewFFLayout("true")) T2 (
    .clk(or_1_out), .T(1'b1), .Q(Q2), .Qn(T2_qn));  // open: preset, reset
  T_Flip_Flop #(.trigger("falling"), .Pre_Clr_Positions("ABOVE_BELOW"), .NegatePresetClear("false"), .enable("false"), .NewFFLayout("true")) T1 (
    .clk(or_2_out), .T(1'b1), .Q(Q1), .Qn(T1_qn));  // open: preset, reset
  and and_5 (Z, Q2, X2, Q1);
endmodule

module _6_9 (
  input  in_1,
  input  in_2,
  output Z,
  output Y2,
  output Y1
);

  wire clock_1_out, nand_1_out, nand_2_out, nand_3_out, nand_4_out, not_1_out, not_2_out;

  not not_1 (not_1_out, Y1);
  Clock #(.highDuration(1), .lowDuration(1)) clock_1 (.out(clock_1_out));
  // Digital_Oscilloscope #(.nState(20), .frontlines("rising"), .showclock("true")) digital_oscilloscope_1: pin names not known; wires that end beside it: clock_1_out, in_1, in_2, Y1, Y2, Z
  nand nand_1 (nand_1_out, Y2, Y1);
  nand nand_2 (nand_2_out, in_1, Y2, in_2);
  nand nand_3 (nand_3_out, in_1, not_1_out, not_2_out);
  not not_2 (not_2_out, in_2);
  nand nand_4 (nand_4_out, in_1, Y1);
  not not_3 (Z, nand_1_out);
  nand nand_5 (Y2, nand_2_out, nand_3_out);
  nand nand_6 (Y1, not_2_out, nand_4_out);

  // Other names for the same wires on the sheet: X1 = in_1; X2 = in_2
endmodule

module _6_13 (
  input  X1,
  input  X2,
  output Y1,
  output Z,
  output Y2
);

  wire and_1_out, and_2_out, and_3_out, and_4_out, and_5_out, and_6_out, clock_1_out, not_1_out, not_2_out,
       not_3_out;

  Clock #(.highDuration(1), .lowDuration(1)) clock_1 (.out(clock_1_out));
  // Digital_Oscilloscope #(.nState(20), .frontlines("rising"), .showclock("true")) digital_oscilloscope_1: pin names not known; wires that end beside it: clock_1_out, X2, X1, Y2, Y1, Z
  and and_1 (and_1_out, Y2, X2);
  not not_1 (not_1_out, X1);
  and and_2 (and_2_out, not_1_out, Y2);
  and and_3 (and_3_out, not_1_out, Y1, X2);
  and and_4 (and_4_out, X1, X2);
  not not_2 (not_2_out, X2);
  and and_5 (and_5_out, not_2_out, not_1_out, Y2);
  and and_6 (and_6_out, X2, Y2, not_3_out);
  not not_3 (not_3_out, Y1);
  or or_1 (Y1, and_1_out, and_2_out, and_3_out);
  or or_2 (Y2, and_4_out, and_5_out, and_6_out);
  and and_7 (Z, Y1, Y2);
endmodule

module _6_15 (
  input  X2,
  input  X1,
  output out_3
);

  wire clock_1_out, digital_oscilloscope_1_p13, nand_1_out, nand_2_out, nand_3_out, nand_4_out, not_1_out,
       not_2_out, not_3_out;

  not not_1 (not_1_out, X2);
  not not_2 (not_2_out, X1);
  Clock #(.highDuration(1), .lowDuration(1)) clock_1 (.out(clock_1_out));
  not not_3 (not_3_out, nand_4_out);
  // Digital_Oscilloscope #(.nState(10), .frontlines("rising"), .showclock("true")) digital_oscilloscope_1: pin names not known; wires that end beside it: not_1_out, not_1_out, X2, X2, not_2_out, not_2_out, clock_1_out, X1, X2, out_3, X1, X1, digital_oscilloscope_1_p13
  nand nand_1 (nand_1_out, nand_4_out, digital_oscilloscope_1_p13);
  nand nand_2 (nand_2_out, nand_4_out, X2);
  nand nand_3 (nand_3_out, digital_oscilloscope_1_p13, not_3_out);
  nand nand_4 (nand_4_out, not_1_out, nand_1_out);
  nand nand_5 (digital_oscilloscope_1_p13, not_2_out, nand_2_out, nand_3_out);
  not not_4 (out_3, nand_2_out);

  // Other names for the same wires on the sheet: Z = out_3
endmodule
