// Logisim project 第7章习题电路的实现.circ as structural Verilog
module _7_1 (
  input  in_1,
  input  in_2,
  input  in_3,
  input  in_4,
  input  in_5,
  output [3:0] out_6
);

  wire A0, A1, A2, A3, button_1_out, clock_1_out;
  wire [3:0] counter_1_q;

  Counter #(.width(4), .max('hf), .ongoal("wrap"), .trigger("rising"), .behavior("new")) counter_1 (
    .Q(counter_1_q), .clk(clock_1_out), .clr(button_1_out));  // open: load, D, count, carry, preset, down
  Clock #(.highDuration(1), .lowDuration(1)) clock_1 (.out(clock_1_out));
  Button button_1 (.out(button_1_out));
  not not_1 (A0, counter_1_q[0]);
  not not_2 (A1, counter_1_q[1]);
  not not_3 (A2, counter_1_q[2]);
  not not_4 (A3, counter_1_q[3]);
  _74283 #(.VccGndPorts("false"), .ShowInternalStructure("false")) u_74283_1 (
    .pin1(out_6[1]), .pin2(A1), .pin3(in_3), .pin4(out_6[0]), .pin5(in_4), .pin6(A0), .pin7(in_5),
    .pin15(A2), .pin14(in_2), .pin13(out_6[2]), .pin12(in_1), .pin11(A3), .pin10(out_6[3]));  // open: pin9

  // Other names for the same wires on the sheet: M = in_5; F0 = out_6[0]; F1 = out_6[1]; F2 = out_6[2]; F3 = out_6[3]
endmodule

module _7_2 (
  input  in_1,
  input  in_2,
  input  in_3,
  input  in_4,
  input  in_5,
  output [6:0] out_6
);

  wire A0, A1, button_1_out, button_2_out, C0, C1, C2, C3, clock_1_out, clock_2_out, D1, D2, D3;

  Counter #(.width(4), .max('hf), .ongoal("wrap"), .trigger("rising"), .behavior("new")) counter_1 (
    .Q({out_6[6:5], A1, A0}), .clk(clock_1_out), .clr(button_1_out));  // open: load, D, count, carry, preset, down
  Clock #(.highDuration(1), .lowDuration(1)) clock_1 (.out(clock_1_out));
  Button button_1 (.out(button_1_out));
  Counter #(.width(4), .max('hf), .ongoal("wrap"), .trigger("rising"), .behavior("new")) counter_2 (
    .Q({C3, C2, C1, C0}), .clk(clock_2_out), .clr(button_2_out));  // open: load, D, count, carry, preset, down
  Clock #(.highDuration(1), .lowDuration(1)) clock_2 (.out(clock_2_out));
  Button button_2 (.out(button_2_out));
  _74283 #(.VccGndPorts("false"), .ShowInternalStructure("false")) u_74283_1 (
    .pin1(D2), .pin2(in_2), .pin3(A1), .pin4(D1), .pin5(A0), .pin6(in_1), .pin7(in_3), .pin15(A0),
    .pin14(out_6[5]), .pin13(D3), .pin12(out_6[6]), .pin11(A1), .pin10(out_6[4]));  // open: pin9
  _74283 #(.VccGndPorts("false"), .ShowInternalStructure("false")) u_74283_2 (
    .pin1(out_6[1]), .pin2(D1), .pin3(C1), .pin4(out_6[0]), .pin5(C0), .pin6(in_4), .pin7(in_5), .pin15(D2),
    .pin14(C2), .pin13(out_6[2]), .pin12(C3), .pin11(D3), .pin10(out_6[3]));  // open: pin9

  // Other names for the same wires on the sheet: B2 = A0; B3 = A1; B0 = in_1; B1 = in_2; D0 = in_4; F0 = D1; F1 = D2;
  //   F2 = D3; M1 = in_3; M2 = in_5; F4 = out_6[0]; F5 = out_6[1]; F6 = out_6[2]; F7 = out_6[3]; F3 = out_6[4];
  //   A2 = out_6[5]; A3 = out_6[6]
endmodule

module _7_3 (
  input  in_1,
  input  in_2,
  input  in_3,
  output [3:0] out_4,
  output [3:0] out_5
);

  wire A0, A1, A2, A3, and_1_out, and_2_out, and_3_out, and_4_out, and_5_out, and_6_out, and_7_out,
       and_8_out, B0, B1, B2, B3, button_1_out, button_2_out, C0, C1, C2, C3, clock_1_out, clock_2_out, D0,
       D1, D2, D3, F4, F5, F6, F7, G1, G2, not_1_out;

  Counter #(.width(4), .max('hf), .ongoal("wrap"), .trigger("rising"), .behavior("new")) counter_1 (
    .Q({A3, A2, A1, A0}), .clk(clock_1_out), .clr(button_1_out));  // open: load, D, count, carry, preset, down
  Clock #(.highDuration(1), .lowDuration(1)) clock_1 (.out(clock_1_out));
  Button button_1 (.out(button_1_out));
  Counter #(.width(4), .max('hf), .ongoal("wrap"), .trigger("rising"), .behavior("new")) counter_2 (
    .Q({B3, B2, B1, B0}), .clk(clock_2_out), .clr(button_2_out));  // open: load, D, count, carry, preset, down
  Clock #(.highDuration(1), .lowDuration(1)) clock_2 (.out(clock_2_out));
  Button button_2 (.out(button_2_out));
  _74283 #(.VccGndPorts("false"), .ShowInternalStructure("false")) u_74283_1 (
    .pin1(C1), .pin2(B1), .pin3(A1), .pin4(C0), .pin5(A0), .pin6(B0), .pin7(in_1), .pin15(B2), .pin14(A2),
    .pin13(C2), .pin12(A3), .pin11(B3), .pin10(C3), .pin9(G1));
  not not_1 (not_1_out, out_5[0]);
  or or_1 (out_5[0], G1, G2);
  and and_1 (and_1_out, C0, not_1_out);
  and and_2 (and_2_out, C1, not_1_out);
  and and_3 (and_3_out, C2, not_1_out);
  and and_4 (and_4_out, C3, not_1_out);
  and and_5 (and_5_out, F4, out_5[0]);
  and and_6 (and_6_out, F5, out_5[0]);
  and and_7 (and_7_out, F6, out_5[0]);
  and and_8 (and_8_out, F7, out_5[0]);
  _74283 #(.VccGndPorts("false"), .ShowInternalStructure("false")) u_74283_2 (
    .pin1(F5), .pin2(D1), .pin3(C1), .pin4(F4), .pin5(C0), .pin6(D0), .pin7(in_2), .pin15(D2), .pin14(C2),
    .pin13(F6), .pin12(C3), .pin11(D3), .pin10(F7), .pin9(G2));
  or or_2 (out_4[0], and_1_out, and_5_out);
  or or_3 (out_4[1], and_2_out, and_6_out);
  or or_4 (out_4[2], and_3_out, and_7_out);
  or or_5 (out_4[3], and_4_out, and_8_out);

  assign out_5[3:1] = {3{in_3}};
  // also tied to GND on the sheet: {D1, D3}
  // also tied to VCC on the sheet: {D0, D2}

  // Other names for the same wires on the sheet: F0 = C0; F1 = C1; F2 = C2; F3 = C3; M1 = in_1; M2 = in_2
endmodule

module _3_8 (
  input  S1,
  input  nS2,
  input  nS3,
  input  A2,
  input  A1,
  input  A0,
  output nY0,
  output nY1,
  output nY2,
  output nY3,
  output nY4,
  output nY5,
  output nY6,
  output nY7
);

  wire and_1_out, decoder_1_out0, decoder_1_out1, decoder_1_out2, decoder_1_out3, decoder_1_out4,
       decoder_1_out5, decoder_1_out6, decoder_1_out7, not_1_out, not_2_out, not_3_out, not_4_out, not_5_out,
       not_6_out, not_7_out, not_8_out, not_9_out, not_10_out, not_11_out, or_1_out;

  not not_1 (not_1_out, nS2);
  not not_2 (not_2_out, nS3);
  not not_3 (not_3_out, S1);
  and and_1 (and_1_out, S1, not_1_out, not_2_out);
  or or_1 (or_1_out, not_3_out, nS2, nS3);
  Decoder #(.select(3), .tristate("false"), .disabled("Z"), .enable("true")) decoder_1 (
    .out0(decoder_1_out0), .out1(decoder_1_out1), .out2(decoder_1_out2), .out3(decoder_1_out3),
    .out4(decoder_1_out4), .out5(decoder_1_out5), .out6(decoder_1_out6), .out7(decoder_1_out7),
    .sel({A2, A1, A0}), .en(and_1_out));
  not not_4 (not_4_out, decoder_1_out0);
  not not_5 (not_5_out, decoder_1_out1);
  not not_6 (not_6_out, decoder_1_out2);
  not not_7 (not_7_out, decoder_1_out3);
  not not_8 (not_8_out, decoder_1_out4);
  not not_9 (not_9_out, decoder_1_out5);
  not not_10 (not_10_out, decoder_1_out6);
  not not_11 (not_11_out, decoder_1_out7);
  or or_2 (nY0, or_1_out, not_4_out);
  or or_3 (nY1, or_1_out, not_5_out);
  or or_4 (nY2, or_1_out, not_6_out);
  or or_5 (nY3, or_1_out, not_7_out);
  or or_6 (nY4, or_1_out, not_8_out);
  or or_7 (nY5, or_1_out, not_9_out);
  or or_8 (nY6, or_1_out, not_10_out);
  or or_9 (nY7, or_1_out, not_11_out);
endmodule

module _7_4 (
  input  in_1,
  output F1,
  output F2,
  output F3
);

  wire A, B, C, clock_1_out, n3_8_1_ny0, n3_8_1_ny2, n3_8_1_ny3, n3_8_1_ny4, n3_8_1_ny6, n3_8_1_ny7;

  Clock #(.highDuration(1), .lowDuration(1)) clock_1 (.out(clock_1_out));
  Counter #(.width(3), .max('h7), .ongoal("wrap"), .trigger("rising"), .behavior("new")) counter_1 (
    .Q({C, B, A}), .clk(clock_1_out));  // open: load, D, count, carry, clr, preset, down
  or or_1 (F1, n3_8_1_ny0, n3_8_1_ny2, n3_8_1_ny3);
  _3_8 u_3_8_1 (
    .S1(1'b1), .nS2(in_1), .nS3(in_1), .A2(A), .A1(B), .A0(C), .nY0(n3_8_1_ny0), .nY2(n3_8_1_ny2),
    .nY3(n3_8_1_ny3), .nY4(n3_8_1_ny4), .nY6(n3_8_1_ny6), .nY7(n3_8_1_ny7));  // open: nY1, nY5
  or or_2 (F2, n3_8_1_ny0, n3_8_1_ny2, n3_8_1_ny4, n3_8_1_ny6);
  or or_3 (F3, n3_8_1_ny3, n3_8_1_ny0, n3_8_1_ny4, n3_8_1_ny7);
endmodule

module _74148 (
  input  nI0,
  input  nI1,
  input  nI2,
  input  nI3,
  input  nI4,
  input  nI5,
  input  nI6,
  input  nI7,
  input  nIS,
  output QS,
  output nQEX,
  output nQA,
  output nQB,
  output nQC
);

  wire and_1_out, not_1_out, not_2_out, not_3_out, not_4_out, not_5_out, not_6_out, not_7_out, not_8_out,
       not_9_out, not_10_out, not_11_out, not_12_out, not_13_out, or_1_out, priority_encoder_1_en_out;
  wire [2:0] priority_encoder_1_out;

  and and_1 (and_1_out, nI0, nI1, nI2, nI3, nI4, nI5, nI6, nI7);
  not not_1 (not_1_out, nI0);
  not not_2 (not_2_out, nI1);
  not not_3 (not_3_out, nI2);
  not not_4 (not_4_out, nI3);
  not not_5 (not_5_out, nI4);
  not not_6 (not_6_out, nI5);
  not not_7 (not_7_out, nI6);
  not not_8 (not_8_out, nI7);
  not not_9 (not_9_out, nIS);
  Priority_Encoder #(.select(3), .disabled(0)) priority_encoder_1 (
    .in0(not_1_out), .in1(not_2_out), .in2(not_3_out), .in3(not_4_out), .in4(not_5_out), .in5(not_6_out),
    .in6(not_7_out), .in7(not_8_out), .out(priority_encoder_1_out), .en_out(priority_encoder_1_en_out),
    .en_in(not_9_out));  // open: gs
  or or_1 (or_1_out, and_1_out, nIS);
  not not_10 (not_10_out, and_1_out);
  or or_2 (QS, not_10_out, nIS);
  or or_3 (nQEX, priority_encoder_1_en_out, nIS);
  not not_11 (not_11_out, priority_encoder_1_out[0]);
  not not_12 (not_12_out, priority_encoder_1_out[1]);
  not not_13 (not_13_out, priority_encoder_1_out[2]);
  or or_4 (nQA, or_1_out, not_11_out);
  or or_5 (nQB, or_1_out, not_12_out);
  or or_6 (nQC, or_1_out, not_13_out);
endmodule

module _7_6 (
  input  in_1,
  input  in_2,
  input  in_3,
  input  in_4,
  input  in_5,
  input  in_6,
  input  in_7,
  input  in_8,
  input  in_9,
  output nQEX,
  output nQC,
  output nQB,
  output nQA,
  output QS
);

  _74148 u_74148_1 (
    .nI0(in_9), .nI1(in_8), .nI2(in_7), .nI3(in_6), .nI4(in_5), .nI5(in_4), .nI6(in_3), .nI7(in_2),
    .nIS(in_1), .QS(QS), .nQEX(nQEX), .nQA(nQA), .nQB(nQB), .nQC(nQC));
endmodule

module _74153 (
  input  _1D0,
  input  _2D0,
  input  _1D1,
  input  _2D1,
  input  _1D2,
  input  _2D2,
  input  _1D3,
  input  _2D3,
  input  A1,
  input  A0,
  input  G1,
  input  G2,
  output _1Y,
  output _2Y
);

  wire multiplexer_1_out, multiplexer_2_out, not_1_out, not_2_out;

  Multiplexer #(.select(2), .width(1), .disabled("Z"), .enable("true")) multiplexer_1 (
    .in0(_1D0), .in1(_1D1), .in2(_1D2), .in3(_1D3), .out(multiplexer_1_out), .sel({A1, A0}), .en(not_1_out));
  not not_1 (not_1_out, G1);
  and and_1 (_1Y, multiplexer_1_out, not_1_out);
  Multiplexer #(.select(2), .width(1), .disabled("Z"), .enable("true")) multiplexer_2 (
    .in0(_2D0), .in1(_2D1), .in2(_2D2), .in3(_2D3), .out(multiplexer_2_out), .sel({A1, A0}), .en(not_2_out));
  not not_2 (not_2_out, G2);
  and and_2 (_2Y, multiplexer_2_out, not_2_out);
endmodule

module _7_7 (
  input  in_1,
  input  in_2,
  output [3:0] out_3
);

  wire and_1_out, and_2_out, and_3_out, and_4_out, and_5_out, and_6_out, and_7_out, button_1_out,
       clock_1_out, D0, D1, D2, D3, not_1_out, not_2_out, not_3_out, not_4_out, not_5_out, not_6_out,
       not_7_out, not_8_out, not_9_out, not_10_out, or_1_out, or_2_out, or_3_out;

  Counter #(.width(4), .max('hf), .ongoal("wrap"), .trigger("rising"), .behavior("new")) counter_1 (
    .Q({D3, D2, D1, D0}), .clk(clock_1_out), .clr(button_1_out));  // open: load, D, count, carry, preset, down
  Clock #(.highDuration(1), .lowDuration(1)) clock_1 (.out(clock_1_out));
  Button button_1 (.out(button_1_out));
  or or_1 (or_1_out, and_1_out, and_2_out, D3);
  and and_1 (and_1_out, D2, D0);
  and and_2 (and_2_out, D2, D1);
  not not_1 (not_1_out, or_1_out);
  not not_2 (not_2_out, or_2_out);
  or or_2 (or_2_out, and_4_out, and_3_out, and_5_out);
  and and_3 (and_3_out, D2, not_5_out, not_3_out);
  and and_4 (and_4_out, not_4_out, D0);
  not not_3 (not_3_out, D0);
  not not_4 (not_4_out, D2);
  not not_5 (not_5_out, D1);
  _74153 u_74153_1 (
    ._1D0(1'b1), ._2D0(1'b1), ._1D1(D1), ._2D1(D1), ._1D2(D2), ._2D2(D2), ._1D3(D3), ._2D3(D3), .A1(in_1),
    .A0(in_2), .G1(not_1_out), .G2(not_2_out), ._1Y(out_3[3]), ._2Y(out_3[2]));
  and and_5 (and_5_out, not_7_out, not_6_out, D1);
  not not_6 (not_6_out, D2);
  not not_7 (not_7_out, D3);
  not not_8 (not_8_out, or_3_out);
  or or_3 (or_3_out, and_6_out, and_7_out);
  and and_6 (and_6_out, not_9_out, not_10_out);
  and and_7 (and_7_out, D0, D1);
  not not_9 (not_9_out, D0);
  not not_10 (not_10_out, D1);
  _74153 u_74153_2 (
    ._1D0(1'b1), ._2D0(1'b1), ._1D1(D1), ._2D1(D1), ._1D2(D2), ._2D2(D2), ._1D3(D3), ._2D3(D3), .A1(1'b0),
    .A0(1'b0), .G1(not_8_out), .G2(D0), ._1Y(out_3[1]), ._2Y(out_3[0]));
endmodule

module _7_8 (
  input  A,
  input  B,
  input  C,
  output out_4
);

  wire not_1_out;

  not not_1 (not_1_out, C);
  _74153 u_74153_1 (
    ._1D0(not_1_out), ._1D1(1'b0), ._1D2(1'b0), ._1D3(C), .A1(A), .A0(B), .G1(1'b0), ._1Y(out_4));  // open: _2D0, _2D1, _2D2, _2D3, G2, _2Y
endmodule
