// Logisim project 第1次实验设计文件.circ as structural Verilog: 7 circuits, main circuit 习题2.2（4）
module \习题2_2_4  (
  output F,
  output F_2
);

  wire A, and_1_out, and_2_out, and_3_out, and_4_out, and_5_out, B, button_1_out, buzzer_1_p1, C,
       clock_1_out, comparator_1_eq, not_1_out, not_2_out, not_3_out, not_4_out, not_5_out, not_6_out;

  Counter #(.width(3), .max('h7), .ongoal("wrap"), .trigger("rising"), .behavior("new")) counter_1 (
    .Q({A, B, C}), .clk(clock_1_out), .clr(button_1_out));  // open: load, D, count, carry, preset, down
  Clock #(.highDuration(1), .lowDuration(1)) clock_1 (.out(clock_1_out));
  Button button_1 (.out(button_1_out));
  // Probe on A
  // Probe on B
  // Probe on C
  // Probe on A
  // Probe on B
  // Probe on C
  not not_1 (not_1_out, A);
  not not_2 (not_2_out, B);
  not not_3 (not_3_out, C);
  not not_4 (not_4_out, A);
  not not_5 (not_5_out, B);
  not not_6 (not_6_out, C);
  and and_1 (and_1_out, A, B, C);
  and and_2 (and_2_out, not_1_out, not_2_out, not_3_out);
  and and_3 (and_3_out, not_5_out, A);
  and and_4 (and_4_out, B, not_6_out);
  and and_5 (and_5_out, not_4_out, C);
  or or_1 (F, and_1_out, and_2_out);
  nor nor_1 (F_2, and_3_out, and_4_out, and_5_out);
  Comparator #(.width(1), .mode("twosComplement")) comparator_1 (.a(F), .b(F_2), .eq(comparator_1_eq));  // open: gt, lt
  // Buzzer #(.freq_measure("Hz"), .vol_width(7)) buzzer_1: pin names not known; wires that end beside it: buzzer_1_p1
  not not_7 (buzzer_1_p1, comparator_1_eq);
  LED #(.active("false")) led_1 (.in(comparator_1_eq));
endmodule

module \习题2_3_2  (
  output F,
  output F_2
);

  wire A, and_1_out, and_2_out, B, button_1_out, buzzer_1_p1, clock_1_out, comparator_1_eq, not_1_out,
       not_2_out, not_3_out, not_4_out, or_1_out, or_2_out;
  wire [2:2] counter_1_q;

  Counter #(.width(3), .max('h7), .ongoal("wrap"), .trigger("rising"), .behavior("new")) counter_1 (
    .Q({counter_1_q[2], B, A}), .clk(clock_1_out), .clr(button_1_out));  // open: load, D, count, carry, preset, down
  Clock #(.highDuration(1), .lowDuration(1)) clock_1 (.out(clock_1_out));
  Button button_1 (.out(button_1_out));
  // Probe on A
  // Probe on B
  // Probe on A
  // Probe on B
  not not_1 (not_1_out, A);
  not not_2 (not_2_out, B);
  not not_3 (not_3_out, A);
  not not_4 (not_4_out, B);
  or or_1 (or_1_out, A, B);
  or or_2 (or_2_out, not_1_out, not_2_out);
  and and_1 (and_1_out, A, B);
  and and_2 (and_2_out, not_4_out, not_3_out);
  and and_3 (F, or_1_out, or_2_out);
  nor nor_1 (F_2, and_1_out, and_2_out);
  Comparator #(.width(1), .mode("twosComplement")) comparator_1 (.a(F), .b(F_2), .eq(comparator_1_eq));  // open: gt, lt
  // Buzzer #(.freq_measure("Hz"), .vol_width(7)) buzzer_1: pin names not known; wires that end beside it: buzzer_1_p1
  not not_5 (buzzer_1_p1, comparator_1_eq);
  LED #(.active("false")) led_1 (.in(comparator_1_eq));
endmodule

module \习题2_4_2  (
  output F,
  output F_2
);

  wire A, and_1_out, and_2_out, and_3_out, and_4_out, and_5_out, and_6_out, B, button_1_out, buzzer_1_p1, C,
       clock_1_out, comparator_1_eq, D, E, not_1_out, not_2_out, not_3_out, not_4_out, not_5_out, not_6_out,
       not_7_out, or_1_out, or_2_out, or_3_out, or_4_out, or_5_out;

  Counter #(.width(5), .max('h1f), .ongoal("wrap"), .trigger("rising"), .behavior("new")) counter_1 (
    .Q({E, D, C, B, A}), .clk(clock_1_out), .clr(button_1_out));  // open: load, D, count, carry, preset, down
  Clock #(.highDuration(1), .lowDuration(1)) clock_1 (.out(clock_1_out));
  Button button_1 (.out(button_1_out));
  // Probe on A
  // Probe on B
  // Probe on C
  // Probe on D
  // Probe on E
  // Probe on A
  not not_1 (not_1_out, A);
  // Probe on B
  not not_2 (not_2_out, B);
  // Probe on C
  not not_3 (not_3_out, C);
  // Probe on D
  not not_4 (not_4_out, D);
  // Probe on E
  not not_5 (not_5_out, E);
  not not_6 (not_6_out, A);
  and and_1 (and_1_out, D, E);
  not not_7 (not_7_out, E);
  or or_1 (or_1_out, not_4_out, not_5_out);
  or or_2 (or_2_out, A, B);
  or or_3 (or_3_out, not_6_out, C);
  or or_4 (or_4_out, C, and_1_out);
  and and_2 (and_2_out, A, not_3_out);
  and and_3 (and_3_out, not_1_out, not_2_out);
  and and_4 (and_4_out, not_3_out, or_1_out);
  and and_5 (and_5_out, or_2_out, or_3_out, or_4_out);
  or or_5 (or_5_out, and_2_out, and_3_out, and_4_out);
  or or_6 (F, and_5_out, not_7_out);
  and and_6 (and_6_out, or_5_out, E);
  not not_8 (F_2, and_6_out);
  Comparator #(.width(1), .mode("twosComplement")) comparator_1 (.a(F), .b(F_2), .eq(comparator_1_eq));  // open: gt, lt
  // Buzzer #(.freq_measure("Hz"), .vol_width(7)) buzzer_1: pin names not known; wires that end beside it: buzzer_1_p1
  not not_9 (buzzer_1_p1, comparator_1_eq);
  LED #(.active("false")) led_1 (.in(comparator_1_eq));
endmodule

module \习题2_6_4  (
  output F,
  output F_2
);

  wire A, and_1_out, and_2_out, and_3_out, and_4_out, B, button_1_out, C, clock_1_out, comparator_1_eq, D,
       not_2_out, not_3_out, not_4_out, not_5_out, or_1_out, or_2_out;

  Counter #(.width(4), .max('hf), .ongoal("wrap"), .trigger("rising"), .behavior("new")) counter_1 (
    .Q({D, C, B, A}), .clk(clock_1_out), .clr(button_1_out));  // open: load, D, count, carry, preset, down
  Clock #(.highDuration(1), .lowDuration(1)) clock_1 (.out(clock_1_out));
  Button button_1 (.out(button_1_out));
  // Probe on A
  // Probe on B
  // NOT_Gate not_1 has open pins: in=A, out=open
  not not_2 (not_2_out, B);
  // Probe on C
  not not_3 (not_3_out, C);
  // Probe on D
  not not_4 (not_4_out, D);
  // Probe on A
  // Probe on B
  // Probe on C
  // Probe on D
  and and_1 (and_1_out, A, C);
  and and_2 (and_2_out, A, C);
  or or_1 (or_1_out, and_1_out, B);
  or or_2 (or_2_out, not_2_out, not_3_out);
  and and_3 (and_3_out, or_1_out, or_2_out, not_4_out);
  and and_4 (and_4_out, B, C);
  or or_3 (F_2, and_2_out, B, D);
  or or_4 (F, and_3_out, and_4_out, D);
  Comparator #(.width(1), .mode("twosComplement")) comparator_1 (.a(F), .b(F_2), .eq(comparator_1_eq));  // open: gt, lt
  not not_5 (not_5_out, comparator_1_eq);
  // Buzzer #(.freq_measure("Hz"), .vol_width(7)) buzzer_1: pin names not known; wires that end beside it: not_5_out
  LED #(.active("false")) led_1 (.in(comparator_1_eq));
endmodule

module \习题2_7_2  (
  output F,
  output F_2,
  output F_3,
  output F_4
);

  wire A, a_t, and_1_out, and_2_out, and_3_out, and_4_out, and_5_out, and_6_out, and_7_out, and_8_out,
       and_9_out, and_10_out, and_11_out, and_12_out, and_13_out, and_14_out, and_15_out, and_16_out,
       and_17_out, and_18_out, and_19_out, B, b_t, button_1_out, button_2_out, buzzer_1_p1, buzzer_2_p1, C,
       c_t, clock_1_out, clock_2_out, comparator_1_eq, comparator_2_eq, D, d_t, nor_1_out, nor_2_out,
       not_1_out, not_2_out, not_3_out, not_4_out, not_7_out, not_8_out, not_9_out, not_10_out, not_13_out,
       not_14_out, or_3_out, or_4_out, or_5_out;

  Counter #(.width(4), .max('hf), .ongoal("wrap"), .trigger("rising"), .behavior("new")) counter_1 (
    .Q({D, C, B, A}), .clk(clock_1_out), .clr(button_1_out));  // open: load, D, count, carry, preset, down
  Clock #(.highDuration(1), .lowDuration(1)) clock_1 (.out(clock_1_out));
  Button button_1 (.out(button_1_out));
  // Probe on A
  // Probe on B
  // Probe on C
  // Probe on D
  Clock #(.highDuration(1), .lowDuration(1)) clock_2 (.out(clock_2_out));
  Button button_2 (.out(button_2_out));
  // Probe on a_t
  // Probe on b_t
  // Probe on c_t
  // Probe on d_t
  // Probe on A
  // Probe on B
  not not_1 (not_1_out, A);
  not not_2 (not_2_out, B);
  not not_3 (not_3_out, C);
  not not_4 (not_4_out, D);
  Counter #(.width(4), .max('hf), .ongoal("wrap"), .trigger("rising"), .behavior("new")) counter_2 (
    .Q({d_t, c_t, b_t, a_t}), .clk(clock_2_out), .clr(button_2_out));  // open: load, D, count, carry, preset, down
  // NOT_Gate not_5 has open pins: in=a_t, out=open
  // NOT_Gate not_6 has open pins: in=b_t, out=open
  not not_7 (not_7_out, c_t);
  not not_8 (not_8_out, d_t);
  not not_9 (not_9_out, A);
  not not_10 (not_10_out, B);
  // Probe on C
  // NOT_Gate not_11 has open pins: in=C, out=open
  // Probe on D
  // NOT_Gate not_12 has open pins: in=D, out=open
  // Probe on a_t
  // Probe on b_t
  // Probe on c_t
  // Probe on d_t
  and and_1 (and_1_out, not_9_out, not_10_out);
  and and_2 (and_2_out, A, B, D);
  not not_13 (not_13_out, a_t);
  not not_14 (not_14_out, b_t);
  // NOT_Gate not_15 has open pins: in=c_t, out=open
  // NOT_Gate not_16 has open pins: in=d_t, out=open
  nor nor_1 (nor_1_out, and_1_out, and_2_out);
  and and_3 (and_3_out, C, D);
  and and_4 (and_4_out, not_1_out, B, not_3_out, not_4_out);
  and and_5 (and_5_out, not_1_out, B, not_3_out, D);
  and and_6 (and_6_out, not_1_out, B, C, not_4_out);
  and and_7 (and_7_out, not_1_out, B, C, D);
  and and_8 (and_8_out, A, B, not_3_out, not_4_out);
  and and_9 (and_9_out, A, B, not_3_out, D);
  and and_10 (and_10_out, A, B, C, not_4_out);
  and and_11 (and_11_out, A, B, C, D);
  and and_12 (and_12_out, not_1_out, not_2_out, C, D);
  and and_13 (and_13_out, A, not_2_out, not_3_out, not_4_out);
  and and_14 (and_14_out, A, not_2_out, not_3_out, D);
  and and_15 (and_15_out, A, not_2_out, C, not_4_out);
  and and_16 (and_16_out, A, not_2_out, C, D);
  and and_17 (and_17_out, not_13_out, not_14_out);
  and and_18 (and_18_out, a_t, b_t, d_t);
  and and_19 (and_19_out, c_t, d_t);
  or or_1 (F, nor_1_out, B, and_3_out);
  nor nor_2 (nor_2_out, and_17_out, and_18_out);
  or or_2 (F_3, nor_2_out, b_t, and_19_out);
  or or_3 (or_3_out, a_t, b_t, c_t, d_t);
  or or_4 (or_4_out, a_t, b_t, c_t, not_8_out);
  or or_5 (or_5_out, a_t, b_t, not_7_out, d_t);
  or or_6 (F_2, and_4_out, and_5_out, and_6_out, and_7_out, and_8_out, and_9_out, and_10_out, and_11_out, and_12_out, and_13_out, and_14_out, and_15_out, and_16_out);
  and and_20 (F_4, or_3_out, or_4_out, or_5_out);
  Comparator #(.width(1), .mode("twosComplement")) comparator_1 (.a(F), .b(F_2), .eq(comparator_1_eq));  // open: gt, lt
  // Buzzer #(.freq_measure("Hz"), .vol_width(7)) buzzer_1: pin names not known; wires that end beside it: buzzer_1_p1
  not not_17 (buzzer_1_p1, comparator_1_eq);
  LED #(.active("false")) led_1 (.in(comparator_1_eq));
  Comparator #(.width(1), .mode("twosComplement")) comparator_2 (
    .a(F_3), .b(F_4), .eq(comparator_2_eq));  // open: gt, lt
  // Buzzer #(.freq_measure("Hz"), .vol_width(7)) buzzer_2: pin names not known; wires that end beside it: buzzer_2_p1
  not not_18 (buzzer_2_p1, comparator_2_eq);
  LED #(.active("false")) led_2 (.in(comparator_2_eq));
endmodule

module \习题2_8_2  (
  output F,
  output F_2
);

  wire A, and_1_out, and_2_out, and_3_out, B, button_1_out, buzzer_1_p1, C, clock_1_out, comparator_1_eq, D,
       not_2_out, not_3_out, not_4_out, or_1_out, or_2_out;

  Counter #(.width(4), .max('hf), .ongoal("wrap"), .trigger("rising"), .behavior("new")) counter_1 (
    .Q({D, C, B, A}), .clk(clock_1_out), .clr(button_1_out));  // open: load, D, count, carry, preset, down
  Clock #(.highDuration(1), .lowDuration(1)) clock_1 (.out(clock_1_out));
  Button button_1 (.out(button_1_out));
  // Probe on A
  // Probe on B
  // NOT_Gate not_1 has open pins: in=A, out=open
  not not_2 (not_2_out, B);
  // Probe on C
  not not_3 (not_3_out, C);
  // Probe on D
  not not_4 (not_4_out, D);
  // Probe on A
  // Probe on B
  // Probe on C
  // Probe on D
  and and_1 (and_1_out, A, D);
  or or_1 (or_1_out, and_1_out, B);
  or or_2 (or_2_out, not_2_out, not_3_out);
  and and_2 (and_2_out, or_1_out, or_2_out, not_4_out);
  and and_3 (and_3_out, B, C);
  or or_3 (F_2, B, D);
  or or_4 (F, and_2_out, and_3_out, D);
  Comparator #(.width(1), .mode("twosComplement")) comparator_1 (.a(F), .b(F_2), .eq(comparator_1_eq));  // open: gt, lt
  // Buzzer #(.freq_measure("Hz"), .vol_width(7)) buzzer_1: pin names not known; wires that end beside it: buzzer_1_p1
  not not_5 (buzzer_1_p1, comparator_1_eq);
  LED #(.active("false")) led_1 (.in(comparator_1_eq));
endmodule

module \习题2_9_2  (
  output F,
  output F_2
);

  wire A, and_1_out, and_2_out, and_3_out, and_4_out, and_5_out, and_6_out, and_7_out, and_8_out, and_9_out,
       B, button_1_out, buzzer_1_p1, C, clock_1_out, comparator_1_eq, nor_1_out, not_1_out, not_2_out,
       not_3_out, not_4_out, or_1_out, or_2_out;

  Counter #(.width(3), .max('h7), .ongoal("wrap"), .trigger("rising"), .behavior("new")) counter_1 (
    .Q({A, B, C}), .clk(clock_1_out), .clr(button_1_out));  // open: load, D, count, carry, preset, down
  Clock #(.highDuration(1), .lowDuration(1)) clock_1 (.out(clock_1_out));
  Button button_1 (.out(button_1_out));
  // Probe on A
  // Probe on B
  // Probe on C
  not not_1 (not_1_out, A);
  not not_2 (not_2_out, B);
  not not_3 (not_3_out, C);
  // Probe on A
  // Probe on B
  // Probe on C
  and and_1 (and_1_out, not_1_out, B);
  and and_2 (and_2_out, A, not_2_out);
  or or_1 (or_1_out, and_1_out, and_2_out);
  or or_2 (or_2_out, B, C, A);
  and and_3 (and_3_out, A, B);
  and and_4 (and_4_out, B, C);
  and and_5 (and_5_out, C, A);
  and and_6 (and_6_out, A, B, C);
  not not_4 (not_4_out, or_1_out);
  nor nor_1 (nor_1_out, and_3_out, and_4_out, and_5_out);
  and and_7 (and_7_out, or_1_out, not_3_out);
  and and_8 (and_8_out, not_4_out, C);
  and and_9 (and_9_out, or_2_out, nor_1_out);
  or or_3 (F, and_7_out, and_8_out);
  or or_4 (F_2, and_9_out, and_6_out);
  Comparator #(.width(1), .mode("twosComplement")) comparator_1 (.a(F), .b(F_2), .eq(comparator_1_eq));  // open: gt, lt
  // Buzzer #(.freq_measure("Hz"), .vol_width(7)) buzzer_1: pin names not known; wires that end beside it: buzzer_1_p1
  not not_5 (buzzer_1_p1, comparator_1_eq);
  LED #(.active("false")) led_1 (.in(comparator_1_eq));
endmodule
