// Logisim project 第7章习题电路的实现（第2部分）.circ as structural Verilog: 4 circuits, main circuit 74193芯片
// 74193
module \_74193芯片  (
  input  A,
  input  B,
  input  C,
  input  D,
  input  CPu,
  input  CPd,
  input  CLR,
  input  nLD,
  output Qa,
  output Qb,
  output Qc,
  output Qd_,
  output nQcc,
  output nQcb
);

  wire counter_1_carry, CP, EN, Inv, LOAD, not_1_out, or_1_out;
  wire [3:0] OUT, register_1_q;

  // Probe on {D, C, B, A}
  and and_1 (CP, CPu, CPd);
  or or_1 (or_1_out, CLR, LOAD);
  nor nor_1 (LOAD, CLR, nLD);
  // Probe on OUT
  Counter #(.width(4), .max('hf), .ongoal("wrap"), .trigger("rising"), .behavior("new")) counter_1 (
    .load(1'b0), .D({D, C, B, A}), .count(EN), .Q(OUT), .carry(counter_1_carry), .clk(CP), .clr(or_1_out),
    .preset(1'b0), .down(Inv));
  D_Flip_Flop #(.trigger("rising"), .Pre_Clr_Positions("ABOVE_BELOW"), .NegatePresetClear("false"), .enable("false"), .NewFFLayout("true")) d_ff_1 (
    .clk(CP), .D(counter_1_carry), .Qn(nQcb));  // open: Q, preset, reset
  and and_2 (EN, nLD, ~CLR);  // AND_Gate
  Register #(.width(4), .trigger("rising"), .Select("low")) register_1 (
    .D({D, C, B, A}), .Q(register_1_q), .clk(LOAD), .clr(CLR));  // open: en
  not not_1 (not_1_out, CPu);
  // Probe on register_1_q
  Register #(.width(1), .trigger("rising"), .Select("low")) register_2 (
    .Q(Inv), .clr(not_1_out), .preset(CPu));  // open: D, en, clk, cs
  Adder #(.width(4)) adder_1 (.a(register_1_q), .b(OUT), .out({Qd_, Qc, Qb, Qa}));  // open: cin, cout
  // Probe on {Qd_, Qc, Qb, Qa}

  assign nQcc = nQcb;

  // Other names for the same wires on the sheet: ABCD[3:0] = {D, C, B, A}

  // Notes on the sheet:
  //   74193芯片（双时钟4位二进制同步可逆计数器）
endmodule

// 74194
module \_74194芯片  (
  input  nCLR,
  input  CP,
  input  S1,
  input  S0,
  input  DR,
  input  DL,
  input  D,
  input  C,
  input  B,
  input  A,
  output Qd,
  output Qc,
  output Qb,
  output Qa
);

  wire Din, Load, nCLR_t, not_2_out, SEL1, SEL2, shift_register_1_out;
  wire [3:0] QL;

  not not_1 (nCLR_t, nCLR);
  not not_2 (not_2_out, S1);
  Multiplexer #(.select(1), .width(1), .disabled("Z"), .enable("false")) multiplexer_1 (
    .in0(DR), .in1(DL), .out(Din), .sel(SEL1));
  nand nand_1 (SEL1, not_2_out, S0);
  not not_3 (SEL2, S0);
  and and_1 (Load, S1, S0);
  Shift_Register #(.width(1), .length(4), .parallel("true"), .trigger("rising")) shift_register_1 (
    .shift(CP), .in(Din), .clk(CP), .out(shift_register_1_out), .load(Load), .clr(nCLR_t), .d0(D),
    .q0(QL[0]), .d1(C), .q1(QL[1]), .d2(B), .q2(QL[2]), .d3(A), .q3(QL[3]));
  Multiplexer #(.select(1), .width(4), .disabled("Z"), .enable("false")) multiplexer_2 (
    .in0({QL[0], QL[1], QL[2], QL[3]}), .in1(QL), .out({Qd, Qc, Qb, Qa}), .sel(SEL2));
  // Probe on shift_register_1_out
  // Probe on {Qd, Qc, Qb, Qa}
  // Probe on {QL[0], QL[1], QL[2], QL[3]}
  // Probe on QL

  // Other names for the same wires on the sheet: EN = CP; QR[3:0] = {QL[0], QL[1], QL[2], QL[3]}

  // Notes on the sheet:
  //   74194芯片（4位双向移位寄存器）
endmodule

module \习题7_9  (
  output Qa,
  output Qb,
  output Qc,
  output Qd
);

  wire and_1_out, CP_out;

  Clock #(.highDuration(1), .lowDuration(1)) CP (.out(CP_out));
  and and_1 (and_1_out, Qc, Qd);
  \_74193芯片  \u_74193芯片_1  (
    .CPu(CP_out), .CPd(1'b1), .CLR(and_1_out), .nLD(1'b1), .Qa(Qa), .Qb(Qb), .Qc(Qc), .Qd_(Qd));  // open: A, B, C, D, nQcc, nQcb
  // Probe on {Qd, Qc, Qb, Qa}
endmodule

module \习题7_10  (
  input  S1,
  input  S0,
  input  nCLR,
  output Qd,
  output Qc,
  output Qb
);

  wire and_1_out, CP, xor_1_out, Z;

  // Digital_Oscilloscope #(.nState(35), .frontlines("rising"), .showclock("true")) digital_oscilloscope_1: pin names not known; wires that end beside it: CP, Z
  Clock #(.highDuration(1), .lowDuration(1)) u_CP (.out(CP));
  \_74194芯片  \u_74194芯片_1  (
    .nCLR(nCLR), .CP(CP), .S1(S1), .S0(S0), .DR(xor_1_out), .D(1'b1), .C(1'b0), .B(1'b1), .Qd(Qd), .Qc(Qc),
    .Qb(Qb));  // open: DL, A, Qa
  not not_1 (Z, Qb);
  and and_1 (and_1_out, Qd, ~Qc);  // AND_Gate
  xor xor_1 (xor_1_out, and_1_out, ~Qb);  // XOR_Gate

  // Notes on the sheet:
  //   DR
endmodule
