// Logisim project 第4章习题电路的实现.circ as structural Verilog: 8 circuits, main circuit 习题4.1
module \习题4_1  (
  output F,
  output F_2
);

  wire A, and_1_out, and_2_out, and_3_out, and_4_out, and_5_out, B, button_1_out, buzzer_1_p1, C,
       clock_1_out, comparator_1_eq, nand_1_out, nand_2_out, nand_3_out, not_1_out, not_2_out, not_3_out;

  Clock #(.highDuration(1), .lowDuration(1)) clock_1 (.out(clock_1_out));
  Button button_1 (.out(button_1_out));
  Counter #(.width(3), .max('h7), .ongoal("wrap"), .trigger("rising"), .behavior("new")) counter_1 (
    .Q({A, B, C}), .clk(clock_1_out), .clr(button_1_out));  // open: load, D, count, carry, preset, down
  nand nand_1 (nand_1_out, A, B, C);
  nand nand_2 (nand_2_out, A, B, C);
  nand nand_3 (nand_3_out, A, B, C);
  and and_1 (and_1_out, nand_1_out, A);
  and and_2 (and_2_out, nand_2_out, B);
  and and_3 (and_3_out, nand_3_out, C);
  nor nor_1 (F, and_1_out, and_2_out, and_3_out);
  not not_1 (not_1_out, A);
  not not_2 (not_2_out, B);
  not not_3 (not_3_out, C);
  and and_4 (and_4_out, A, B, C);
  and and_5 (and_5_out, not_1_out, not_2_out, not_3_out);
  or or_1 (F_2, and_4_out, and_5_out);
  Comparator #(.width(1), .mode("twosComplement")) comparator_1 (.a(F), .b(F_2), .eq(comparator_1_eq));  // open: gt, lt
  // Buzzer #(.freq_measure("Hz"), .vol_width(7)) buzzer_1: pin names not known; wires that end beside it: buzzer_1_p1
  not not_4 (buzzer_1_p1, comparator_1_eq);
  LED #(.active("false")) led_1 (.in(comparator_1_eq));
endmodule

module \习题4_3  (
  output W,
  output X,
  output Y,
  output Z,
  output W_2,
  output X_2,
  output Y_2,
  output Z_2
);

  wire B, button_1_out, C, clock_1_out, comparator_1_eq, D, not_1_out;
  wire [3:0] and_1_out, and_2_out, rom_2_data;

  Clock #(.highDuration(1), .lowDuration(1)) clock_1 (.out(clock_1_out));
  Button button_1 (.out(button_1_out));
  Counter #(.width(4), .max('hf), .ongoal("wrap"), .trigger("rising"), .behavior("new")) counter_1 (
    .Q({W, B, C, D}), .clk(clock_1_out), .clr(button_1_out));  // open: load, D, count, carry, preset, down
  // Probe on W
  // Probe on B
  // Probe on C
  // Probe on D
  xor xor_1 (X, W, B);
  xor xor_2 (Y, B, C);
  xor xor_3 (Z, C, D);
  ROM #(.addrWidth(4), .dataWidth(4), .Select("low")) rom_1 (.addr({W, B, C, D}), .data({W_2, X_2, Y_2, Z_2}));
  ROM #(.addrWidth(4), .dataWidth(4), .Select("low")) rom_2 (.addr({W, B, C, D}), .data(rom_2_data));
  assign and_1_out = {W_2, X_2, Y_2, Z_2} & rom_2_data;  // AND_Gate and_1, 4 bits wide
  assign and_2_out = {W, X, Y, Z} & rom_2_data;  // AND_Gate and_2, 4 bits wide
  not not_1 (not_1_out, comparator_1_eq);
  Comparator #(.width(4), .mode("twosComplement")) comparator_1 (
    .a(and_2_out), .b(and_1_out), .eq(comparator_1_eq));  // open: gt, lt
  // Buzzer #(.freq_measure("Hz"), .vol_width(7)) buzzer_1: pin names not known; wires that end beside it: not_1_out
  LED #(.active("false")) led_1 (.in(comparator_1_eq));

  // Other names for the same wires on the sheet: A = W

  // Notes on the sheet:
  //   ROM1
  //   ROM2
  //   contents of rom_1 (hex, n*v repeats v):
  //   0 1 3 2 6 7 5 4 c d
  //   contents of rom_2 (hex, n*v repeats v):
  //   10*f
endmodule

module \习题4_4  (
  output F,
  output F_2
);

  wire A1, A2, B1, B2, button_1_out, clock_1_out, comparator_1_eq, nand_1_out, nand_2_out, nand_3_out,
       not_1_out, not_2_out;

  Counter #(.width(4), .max('hf), .ongoal("wrap"), .trigger("rising"), .behavior("new")) counter_1 (
    .Q({A2, B2, A1, B1}), .clk(clock_1_out), .clr(button_1_out));  // open: load, D, count, carry, preset, down
  Clock #(.highDuration(1), .lowDuration(1)) clock_1 (.out(clock_1_out));
  Button button_1 (.out(button_1_out));
  // Probe on A2
  // Probe on B2
  // Probe on A1
  // Probe on B1
  not not_1 (not_1_out, B2);
  not not_2 (not_2_out, B1);
  nand nand_1 (nand_1_out, A2, not_1_out);
  nand nand_2 (nand_2_out, not_1_out, A1, not_2_out);
  nand nand_3 (nand_3_out, A1, not_2_out, A2);
  ROM #(.addrWidth(4), .dataWidth(1), .Select("low")) rom_1 (.addr({A2, B2, A1, B1}), .data(F_2));
  nand nand_4 (F, nand_1_out, nand_2_out, nand_3_out);
  Comparator #(.width(1), .mode("twosComplement")) comparator_1 (.a(F), .b(F_2), .eq(comparator_1_eq));  // open: gt, lt
  // Buzzer #(.freq_measure("Hz"), .vol_width(7)) buzzer_1: pin names not known
  // NOT_Gate not_3 has open pins: in=comparator_1_eq, out=open
  LED #(.active("false")) led_1 (.in(comparator_1_eq));

  // Notes on the sheet:
  //   ROM1
  //   ROM2
  //   contents of rom_1 (hex, n*v repeats v):
  //   0 0 1 5*0 4*1 0 0 1
endmodule

module \习题4_5  (
  output X,
  output Y,
  output Z,
  output W,
  output X_2,
  output Y_2,
  output Z_2,
  output W_2
);

  wire and_1_out, and_2_out, and_3_out, and_4_out, and_5_out, and_6_out, and_7_out, and_8_out, B,
       button_1_out, buzzer_1_p1, C, clock_1_out, comparator_1_eq, D, not_1_out, not_2_out;
  wire [3:0] and_9_out, and_10_out, rom_2_data;

  Clock #(.highDuration(1), .lowDuration(1)) clock_1 (.out(clock_1_out));
  Button button_1 (.out(button_1_out));
  Counter #(.width(4), .max('hf), .ongoal("wrap"), .trigger("rising"), .behavior("new")) counter_1 (
    .Q({X, B, C, D}), .clk(clock_1_out), .clr(button_1_out));  // open: load, D, count, carry, preset, down
  // Probe on X
  // Probe on B
  // Probe on C
  // Probe on D
  not not_1 (not_1_out, X);
  not not_2 (not_2_out, C);
  not not_3 (W, D);
  and and_1 (and_1_out, X, B);
  and and_2 (and_2_out, X, C);
  and and_3 (and_3_out, X, D);
  and and_4 (and_4_out, B, C, D);
  or or_1 (Y, and_1_out, and_2_out, and_3_out, and_4_out);
  and and_5 (and_5_out, X, not_2_out, W);
  and and_6 (and_6_out, X, C, D);
  and and_7 (and_7_out, not_1_out, not_2_out, D);
  and and_8 (and_8_out, not_1_out, C, W);
  or or_2 (Z, and_5_out, and_6_out, and_7_out, and_8_out);
  ROM #(.addrWidth(4), .dataWidth(4), .Select("low")) rom_1 (.addr({X, B, C, D}), .data({X_2, Y_2, Z_2, W_2}));
  ROM #(.addrWidth(4), .dataWidth(4), .Select("low")) rom_2 (.addr({X, B, C, D}), .data(rom_2_data));
  assign and_9_out = {X_2, Y_2, Z_2, W_2} & rom_2_data;  // AND_Gate and_9, 4 bits wide
  assign and_10_out = {X, Y, Z, W} & rom_2_data;  // AND_Gate and_10, 4 bits wide
  Comparator #(.width(4), .mode("twosComplement")) comparator_1 (
    .a(and_10_out), .b(and_9_out), .eq(comparator_1_eq));  // open: gt, lt
  // Buzzer #(.freq_measure("Hz"), .vol_width(7)) buzzer_1: pin names not known; wires that end beside it: buzzer_1_p1
  not not_4 (buzzer_1_p1, comparator_1_eq);
  LED #(.active("false")) led_1 (.in(comparator_1_eq));

  // Other names for the same wires on the sheet: A = X

  // Notes on the sheet:
  //   ROM1
  //   ROM2
  //   contents of rom_1 (hex, n*v repeats v):
  //   4*0 1 2 3 4 b c d e f
  //   contents of rom_2 (hex, n*v repeats v):
  //   0 0 0 10*f
endmodule

module \习题4_8  (
  output F,
  output F_2
);

  wire A, and_1_out, and_2_out, and_3_out, and_4_out, B, button_1_out, C, clock_1_out, comparator_1_eq, D,
       not_1_out, rom_2_data;

  Counter #(.width(4), .max('hf), .ongoal("wrap"), .trigger("rising"), .behavior("new")) counter_1 (
    .Q({A, B, C, D}), .clk(clock_1_out), .clr(button_1_out));  // open: load, D, count, carry, preset, down
  Clock #(.highDuration(1), .lowDuration(1)) clock_1 (.out(clock_1_out));
  Button button_1 (.out(button_1_out));
  // Probe on A
  // Probe on B
  // Probe on C
  // Probe on D
  and and_1 (and_1_out, B, C);
  and and_2 (and_2_out, B, D);
  ROM #(.addrWidth(4), .dataWidth(1), .Select("low")) rom_1 (.addr({A, B, C, D}), .data(F_2));
  ROM #(.addrWidth(4), .dataWidth(1), .Select("low")) rom_2 (.addr({A, B, C, D}), .data(rom_2_data));
  or or_1 (F, A, and_1_out, and_2_out);
  and and_3 (and_3_out, F_2, rom_2_data);
  and and_4 (and_4_out, F, rom_2_data);
  Comparator #(.width(1), .mode("twosComplement")) comparator_1 (
    .a(and_4_out), .b(and_3_out), .eq(comparator_1_eq));  // open: gt, lt
  not not_1 (not_1_out, comparator_1_eq);
  // Buzzer #(.freq_measure("Hz"), .vol_width(7)) buzzer_1: pin names not known; wires that end beside it: not_1_out
  LED #(.active("false")) led_1 (.in(comparator_1_eq));

  // Notes on the sheet:
  //   ROM1
  //   ROM2
  //   ROM2
  //   contents of rom_1 (hex, n*v repeats v):
  //   5*0 5*1
  //   contents of rom_2 (hex, n*v repeats v):
  //   10*1
endmodule

module \习题4_9  (
  output F,
  output F_2
);

  wire A, and_1_out, and_2_out, B, button_1_out, buzzer_1_p1, C, clock_1_out, comparator_1_eq, D, rom_2_data;

  Counter #(.width(4), .max('hf), .ongoal("wrap"), .trigger("rising"), .behavior("new")) counter_1 (
    .Q({A, B, C, D}), .clk(clock_1_out), .clr(button_1_out));  // open: load, D, count, carry, preset, down
  Clock #(.highDuration(1), .lowDuration(1)) clock_1 (.out(clock_1_out));
  Button button_1 (.out(button_1_out));
  // Probe on A
  // Probe on B
  // Probe on C
  // Probe on D
  ROM #(.addrWidth(4), .dataWidth(1), .Select("low")) rom_1 (.addr({A, B, C, D}), .data(F_2));
  ROM #(.addrWidth(4), .dataWidth(1), .Select("low")) rom_2 (.addr({A, B, C, D}), .data(rom_2_data));
  xnor xnor_1 (F, A, B, C, D);
  and and_1 (and_1_out, F_2, rom_2_data);
  and and_2 (and_2_out, F, rom_2_data);
  Comparator #(.width(1), .mode("twosComplement")) comparator_1 (
    .a(and_2_out), .b(and_1_out), .eq(comparator_1_eq));  // open: gt, lt
  // Buzzer #(.freq_measure("Hz"), .vol_width(7)) buzzer_1: pin names not known; wires that end beside it: buzzer_1_p1
  not not_1 (buzzer_1_p1, comparator_1_eq);
  LED #(.active("false")) led_1 (.in(comparator_1_eq));

  // Notes on the sheet:
  //   ROM1
  //   ROM2
  //   contents of rom_1 (hex, n*v repeats v):
  //   1 0 0 1 0 1 1 0 0 1 1
  //   contents of rom_2 (hex, n*v repeats v):
  //   10*1
endmodule

module \习题4_10  (
  input  S,
  input  F,
  output [1:0] F_2
);

  wire A, and_1_out, and_2_out, and_3_out, B, button_1_out, C, clock_1_out, comparator_1_eq, M, not_1_out,
       xor_1_out;

  Counter #(.width(4), .max('hf), .ongoal("wrap"), .trigger("rising"), .behavior("new")) counter_1 (
    .Q({A, M, B, C}), .clk(clock_1_out), .clr(button_1_out));  // open: load, D, count, carry, preset, down
  Clock #(.highDuration(1), .lowDuration(1)) clock_1 (.out(clock_1_out));
  Button button_1 (.out(button_1_out));
  // Probe on A
  // Probe on M
  // Probe on B
  // Probe on C
  xor xor_1 (xor_1_out, A, M);
  and and_1 (and_1_out, xor_1_out, C);
  and and_2 (and_2_out, xor_1_out, B);
  and and_3 (and_3_out, B, C);
  xor xor_2 (S, A, B, C);
  xor xor_3 (F, and_1_out, and_2_out, and_3_out);
  ROM #(.addrWidth(4), .dataWidth(2), .Select("low")) rom_1 (.addr({A, B, C, M}), .data(F_2));
  Comparator #(.width(2), .mode("twosComplement")) comparator_1 (
    .a({S, F}), .b(F_2), .eq(comparator_1_eq));  // open: gt, lt
  not not_1 (not_1_out, comparator_1_eq);
  // Buzzer #(.freq_measure("Hz"), .vol_width(7)) buzzer_1: pin names not known; wires that end beside it: not_1_out
  LED #(.active("false")) led_1 (.in(comparator_1_eq));

  // Notes on the sheet:
  //   ROM1
  //   contents of rom_1 (hex, n*v repeats v):
  //   0 0 2 3 2 3 1 1 2 2 1 0 1 0 3 3
endmodule

module \习题4_12_3  (
  output F,
  output F_2
);

  wire A, B, button_1_out, buzzer_1_p1, C, clock_1_out, comparator_1_eq, not_1_out, not_2_out, not_3_out,
       not_4_out, not_5_out, not_6_out, or_1_out, or_2_out, or_3_out, or_4_out, or_5_out;

  Clock #(.highDuration(1), .lowDuration(1)) clock_1 (.out(clock_1_out));
  Button button_1 (.out(button_1_out));
  Counter #(.width(3), .max('h7), .ongoal("wrap"), .trigger("rising"), .behavior("new")) counter_1 (
    .Q({A, B, C}), .clk(clock_1_out), .clr(button_1_out));  // open: load, D, count, carry, preset, down
  // Probe on A
  // Probe on B
  // Probe on C
  // Probe on A
  // Probe on B
  // Probe on C
  not not_1 (not_1_out, A);
  not not_2 (not_2_out, B);
  not not_3 (not_3_out, C);
  not not_4 (not_4_out, A);
  not not_5 (not_5_out, B);
  not not_6 (not_6_out, C);
  or or_1 (or_1_out, A, not_2_out);
  or or_2 (or_2_out, not_1_out, not_3_out);
  or or_3 (or_3_out, A, not_5_out);
  or or_4 (or_4_out, not_4_out, not_6_out);
  or or_5 (or_5_out, not_6_out, not_5_out);
  and and_1 (F, or_3_out, or_4_out, or_5_out);
  and and_2 (F_2, or_1_out, or_2_out);
  Comparator #(.width(1), .mode("twosComplement")) comparator_1 (.a(F), .b(F_2), .eq(comparator_1_eq));  // open: gt, lt
  // Buzzer #(.freq_measure("Hz"), .vol_width(7)) buzzer_1: pin names not known; wires that end beside it: buzzer_1_p1
  not not_7 (buzzer_1_p1, comparator_1_eq);
  LED #(.active("false")) led_1 (.in(comparator_1_eq));
endmodule
