// Logisim project 第6章习题电路的实现.circ as structural Verilog: 8 circuits, main circuit 习题6.1
module \习题6_1  (
  output Z
);

  wire and_1_out, clock_1_out, d_ff_1_qn, x, y1, y2;

  Clock #(.highDuration(1), .lowDuration(1)) clock_1 (.out(clock_1_out));
  Button u_x (.out(x));
  // Digital_Oscilloscope #(.nState(20), .frontlines("rising"), .showclock("true")) digital_oscilloscope_1: pin names not known; wires that end beside it: clock_1_out, x, y2, y1, Z
  and and_1 (and_1_out, x, y1);
  D_Flip_Flop #(.trigger("falling"), .Pre_Clr_Positions("ABOVE_BELOW"), .NegatePresetClear("false"), .enable("false"), .NewFFLayout("true")) d_ff_1 (
    .clk(and_1_out), .D(d_ff_1_qn), .Q(y2), .Qn(d_ff_1_qn));  // open: preset, reset
  D_Flip_Flop #(.trigger("falling"), .Pre_Clr_Positions("ABOVE_BELOW"), .NegatePresetClear("false"), .enable("false"), .NewFFLayout("true")) d_ff_2 (
    .clk(x), .D(d_ff_1_qn), .Q(y1));  // open: Qn, preset, reset
  and and_2 (Z, y2, x, y1);
  // Probe on y2
  // Probe on y1
endmodule

module \延时  (
  input  x,
  output y
);

  wire CP_out;

  Clock #(.highDuration(1), .lowDuration(1)) CP (.out(CP_out));
  D_Flip_Flop #(.trigger("rising"), .Pre_Clr_Positions("ABOVE_BELOW"), .NegatePresetClear("false"), .enable("false"), .NewFFLayout("true")) d_ff_1 (
    .clk(CP_out), .D(x), .Q(y));  // open: Qn, preset, reset

  // Notes on the sheet:
  //   延时
endmodule

module \习题6_4  (
);

  wire clock_1_out, CP_out, d_ff_1_qn, y1, y2;

  Clock #(.highDuration(1), .lowDuration(1)) clock_1 (.out(clock_1_out));
  // Digital_Oscilloscope #(.nState(20), .frontlines("rising"), .showclock("true")) digital_oscilloscope_1: pin names not known; wires that end beside it: clock_1_out, y2, y1
  Clock #(.highDuration(1), .lowDuration(1)) CP (.out(CP_out));
  D_Flip_Flop #(.trigger("falling"), .Pre_Clr_Positions("ABOVE_BELOW"), .NegatePresetClear("false"), .enable("false"), .NewFFLayout("true")) d_ff_1 (
    .clk(CP_out), .D(d_ff_1_qn), .Q(y1), .Qn(d_ff_1_qn));  // open: preset, reset
  T_Flip_Flop #(.trigger("falling"), .Pre_Clr_Positions("ABOVE_BELOW"), .NegatePresetClear("false"), .enable("false"), .NewFFLayout("true")) t_ff_1 (
    .clk(y1), .T(1'b1), .Q(y2));  // open: Qn, preset, reset
  // Probe on y1
  // Probe on y2
endmodule

module \习题6_5  (
  output Z
);

  wire and_1_out, clock_1_out, d_ff_1_qn, d_ff_2_qn, d_ff_3_qn, x, y0, y1, y2;

  Clock #(.highDuration(1), .lowDuration(1)) clock_1 (.out(clock_1_out));
  Button u_x (.out(x));
  // Digital_Oscilloscope #(.nState(20), .frontlines("rising"), .showclock("true")) digital_oscilloscope_1: pin names not known; wires that end beside it: clock_1_out, x, y2, y1, y0, Z
  and and_1 (and_1_out, d_ff_2_qn, d_ff_3_qn, x);
  D_Flip_Flop #(.trigger("rising"), .Pre_Clr_Positions("ABOVE_BELOW"), .NegatePresetClear("false"), .enable("false"), .NewFFLayout("true")) d_ff_1 (
    .clk(and_1_out), .D(d_ff_1_qn), .Q(y2), .Qn(d_ff_1_qn));  // open: preset, reset
  D_Flip_Flop #(.trigger("rising"), .Pre_Clr_Positions("ABOVE_BELOW"), .NegatePresetClear("false"), .enable("false"), .NewFFLayout("true")) d_ff_2 (
    .clk(y0), .D(d_ff_2_qn), .Q(y1), .Qn(d_ff_2_qn));  // open: preset, reset
  D_Flip_Flop #(.trigger("falling"), .Pre_Clr_Positions("ABOVE_BELOW"), .NegatePresetClear("false"), .enable("false"), .NewFFLayout("true")) d_ff_3 (
    .clk(x), .D(d_ff_3_qn), .Q(y0), .Qn(d_ff_3_qn));  // open: preset, reset
  // Probe on y2
  // Probe on y1
  // Probe on y0
  and and_2 (Z, y2, y1, y0, x);
endmodule

module \习题6_6  (
  input  X2,
  input  X1,
  output Z
);

  wire and_1_out, and_2_out, and_3_out, and_4_out, clock_1_out, or_1_out, or_2_out, t_ff_1_qn, t_ff_2_qn, y1,
       y2;

  Clock #(.highDuration(1), .lowDuration(1)) clock_1 (.out(clock_1_out));
  // Digital_Oscilloscope #(.nState(20), .frontlines("rising"), .showclock("true")) digital_oscilloscope_1: pin names not known; wires that end beside it: clock_1_out, X2, X1, y2, y1, Z
  and and_1 (and_1_out, y1, t_ff_1_qn, X2);
  and and_2 (and_2_out, y2, X2);
  and and_3 (and_3_out, X1, t_ff_2_qn);
  and and_4 (and_4_out, y1, X2);
  or or_1 (or_1_out, and_1_out, and_2_out);
  or or_2 (or_2_out, and_3_out, and_4_out);
  T_Flip_Flop #(.trigger("falling"), .Pre_Clr_Positions("ABOVE_BELOW"), .NegatePresetClear("false"), .enable("false"), .NewFFLayout("true")) t_ff_1 (
    .clk(or_1_out), .T(1'b1), .Q(y2), .Qn(t_ff_1_qn));  // open: preset, reset
  T_Flip_Flop #(.trigger("falling"), .Pre_Clr_Positions("ABOVE_BELOW"), .NegatePresetClear("false"), .enable("false"), .NewFFLayout("true")) t_ff_2 (
    .clk(or_2_out), .T(1'b1), .Q(y1), .Qn(t_ff_2_qn));  // open: preset, reset
  // Probe on y2
  and and_5 (Z, or_1_out, X2, y1);
  // Probe on y1
endmodule

module \习题6_9  (
  input  X2,
  input  X1,
  output Z
);

  wire and_1_out, and_2_out, and_3_out, digital_oscilloscope_1_p1, y1, y2, \延时_1_y , \延时_2_y ;

  // Digital_Oscilloscope #(.nState(20), .frontlines("rising"), .showclock("true")) digital_oscilloscope_1: pin names not known; wires that end beside it: digital_oscilloscope_1_p1, X2, X1, y2, y1, Z
  Clock #(.highDuration(1), .lowDuration(1)) clock_1 (.out(digital_oscilloscope_1_p1));
  \延时  \u_延时_1  (.x(y2), .y(\延时_1_y ));
  and and_1 (and_1_out, ~\延时_2_y , ~X2, X1);  // AND_Gate
  and and_2 (and_2_out, \延时_1_y , X1, X2);
  \延时  \u_延时_2  (.x(y1), .y(\延时_2_y ));
  and and_3 (and_3_out, X1, \延时_2_y );
  // Probe on y2
  or or_1 (y2, and_1_out, and_2_out);
  // Probe on y1
  or or_2 (y1, X2, and_3_out);
  and and_4 (Z, \延时_1_y , \延时_2_y );
endmodule

module \习题6_13  (
  input  X2,
  input  X1,
  output Z
);

  wire and_1_out, and_2_out, and_3_out, and_4_out, and_6_out, clock_1_out, y1, y2, \延时_1_y , \延时_2_y ;

  Clock #(.highDuration(1), .lowDuration(1)) clock_1 (.out(clock_1_out));
  // Digital_Oscilloscope #(.nState(20), .frontlines("rising"), .showclock("true")) digital_oscilloscope_1: pin names not known; wires that end beside it: clock_1_out, X2, X1, y2, y1, Z
  and and_1 (and_1_out, X2, ~X1, \延时_2_y );  // AND_Gate
  and and_2 (and_2_out, \延时_1_y , ~X1);  // AND_Gate
  and and_3 (and_3_out, \延时_1_y , X2);
  and and_4 (and_4_out, ~\延时_2_y , \延时_1_y , X1);  // AND_Gate
  and and_5 (and_4_out, ~X1, ~X2, \延时_1_y );  // AND_Gate
  and and_6 (and_6_out, X2, X1);
  \延时  \u_延时_1  (.x(y2), .y(\延时_1_y ));
  or or_1 (y2, and_1_out, and_2_out, and_3_out);
  or or_2 (y1, and_4_out, and_4_out, and_6_out);
  \延时  \u_延时_2  (.x(y1), .y(\延时_2_y ));
  // Probe on y2
  // Probe on y1
  and and_7 (Z, and_1_out, \延时_2_y );
endmodule

module \习题6_15  (
  input  X2,
  input  X1
);

  wire clock_1_out, nand_1_out, nand_2_out, nand_3_out, nand_4_out, nand_5_out, nand_6_out, nand_7_out,
       nand_8_out, nand_9_out, nand_10_out, y1, y2, Z;

  Clock #(.highDuration(1), .lowDuration(1)) clock_1 (.out(clock_1_out));
  // Digital_Oscilloscope #(.nState(20), .frontlines("rising"), .showclock("true")) digital_oscilloscope_1: pin names not known; wires that end beside it: clock_1_out, X2, X1, y2, y1, Z
  \延时  \u_延时_1  (.x(nand_9_out), .y(y2));
  \延时  \u_延时_2  (.x(nand_10_out), .y(y1));
  nand nand_1 (nand_1_out, y2, y2);
  nand nand_2 (nand_2_out, X2, X2);
  nand nand_3 (nand_3_out, y2, y1);
  nand nand_4 (nand_4_out, X1, X1);
  nand nand_5 (nand_5_out, y1, nand_1_out);
  nand nand_6 (nand_6_out, X2, y2);
  nand nand_7 (nand_7_out, y1, nand_8_out);
  nand nand_8 (nand_8_out, y2, y2);
  nand nand_9 (nand_9_out, nand_2_out, nand_3_out);
  // Probe on nand_9_out
  // Probe on nand_10_out
  nand nand_10 (nand_10_out, nand_4_out, nand_5_out, nand_6_out);
  nand nand_11 (Z, nand_7_out, nand_7_out);
endmodule
