// Logisim project 第7章习题电路的实现（第1部分）.circ as structural Verilog: 10 circuits, main circuit 7.1
module _7_1 (
);

  wire button_1_out, clock_1_out, n74283_1_pin3, n74283_1_pin7;
  wire [3:0] counter_1_q, n74283_1_pin4;

  Clock #(.highDuration(1), .lowDuration(1)) clock_1 (.out(clock_1_out));
  Button button_1 (.out(button_1_out));
  Counter #(.width(4), .max('hf), .ongoal("wrap"), .trigger("rising"), .behavior("new")) counter_1 (
    .Q(counter_1_q), .clk(clock_1_out), .clr(button_1_out));  // open: load, D, count, carry, preset, down
  _74283 #(.VccGndPorts("false"), .ShowInternalStructure("false")) u_74283_1 (
    .pin1(n74283_1_pin4[1]), .pin2(counter_1_q[1]), .pin3(n74283_1_pin3), .pin4(n74283_1_pin4[0]),
    .pin5(n74283_1_pin3), .pin6(counter_1_q[0]), .pin7(n74283_1_pin7), .pin15(counter_1_q[2]),
    .pin14(n74283_1_pin3), .pin13(n74283_1_pin4[2]), .pin12(n74283_1_pin7), .pin11(counter_1_q[3]),
    .pin10(n74283_1_pin4[3]));  // open: pin9
  // Probe on n74283_1_pin4
  // also tied to GND on the sheet: n74283_1_pin7
  // also tied to VCC on the sheet: n74283_1_pin3
endmodule

module _7_2 (
);

  wire button_1_out, button_2_out, clock_1_out, clock_2_out, n74283_1_pin2, n74283_1_pin6, n74283_1_pin7;
  wire [3:0] n74283_1_pin5, n74283_2_pin6;
  wire [6:1] n74283_2_pin4;

  Clock #(.highDuration(1), .lowDuration(1)) clock_1 (.out(clock_1_out));
  Button button_1 (.out(button_1_out));
  // Probe on n74283_1_pin5
  _74283 #(.VccGndPorts("false"), .ShowInternalStructure("false")) u_74283_1 (
    .pin1(n74283_2_pin4[4]), .pin2(n74283_1_pin2), .pin3(n74283_1_pin5[1]), .pin4(n74283_2_pin4[3]),
    .pin5(n74283_1_pin5[0]), .pin6(n74283_1_pin6), .pin7(n74283_1_pin7), .pin14(n74283_1_pin5[2]),
    .pin13(n74283_2_pin4[5]), .pin12(n74283_1_pin5[3]), .pin10(n74283_2_pin4[6]));  // open: pin15, pin11, pin9
  Counter #(.width(4), .max('hf), .ongoal("wrap"), .trigger("rising"), .behavior("new")) A (
    .Q(n74283_1_pin5), .clk(clock_1_out), .clr(button_1_out));  // open: load, D, count, carry, preset, down
  _74283 #(.VccGndPorts("false"), .ShowInternalStructure("false")) u_74283_2 (
    .pin1(n74283_2_pin4[2]), .pin2(n74283_2_pin6[2]), .pin3(n74283_1_pin5[1]), .pin4(n74283_2_pin4[1]),
    .pin5(n74283_1_pin5[0]), .pin6(n74283_2_pin6[1]), .pin7(n74283_1_pin7), .pin15(n74283_2_pin6[3]),
    .pin14(n74283_1_pin5[2]), .pin13(n74283_1_pin2), .pin12(n74283_1_pin5[3]), .pin11(n74283_1_pin7),
    .pin10(n74283_1_pin6));  // open: pin9
  Counter #(.width(4), .max('hf), .ongoal("wrap"), .trigger("rising"), .behavior("new")) B (
    .Q(n74283_2_pin6), .clk(clock_2_out), .clr(button_2_out));  // open: load, D, count, carry, preset, down
  Clock #(.highDuration(1), .lowDuration(1)) clock_2 (.out(clock_2_out));
  Button button_2 (.out(button_2_out));
  // Probe on n74283_2_pin6
  // Probe on {n74283_2_pin4, n74283_2_pin6[0]}
  // also tied to GND on the sheet: n74283_1_pin7
endmodule

module _7_3 (
);

  wire and_1_out, and_2_out, button_1_out, button_2_out, clock_1_out, clock_2_out, n74283_1_pin1,
       n74283_1_pin4, n74283_1_pin9, n74283_1_pin10, n74283_1_pin13, n74283_2_pin2, n74283_2_pin6;
  wire [3:0] A_q, B_q;
  wire [4:0] n74283_2_pin4;

  Counter #(.width(4), .max('hf), .ongoal("wrap"), .trigger("rising"), .behavior("new")) A (
    .Q(A_q), .clk(clock_1_out), .clr(button_1_out));  // open: load, D, count, carry, preset, down
  Clock #(.highDuration(1), .lowDuration(1)) clock_1 (.out(clock_1_out));
  Button button_1 (.out(button_1_out));
  // Probe on A_q
  Clock #(.highDuration(1), .lowDuration(1)) clock_2 (.out(clock_2_out));
  Button button_2 (.out(button_2_out));
  Counter #(.width(4), .max('hf), .ongoal("wrap"), .trigger("rising"), .behavior("new")) B (
    .Q(B_q), .clk(clock_2_out), .clr(button_2_out));  // open: load, D, count, carry, preset, down
  // Probe on B_q
  _74283 #(.VccGndPorts("false"), .ShowInternalStructure("false")) u_74283_1 (
    .pin1(n74283_1_pin1), .pin2(B_q[1]), .pin3(A_q[1]), .pin4(n74283_1_pin4), .pin5(A_q[0]), .pin6(B_q[0]),
    .pin15(B_q[2]), .pin14(A_q[2]), .pin13(n74283_1_pin13), .pin12(A_q[3]), .pin11(B_q[3]),
    .pin10(n74283_1_pin10), .pin9(n74283_1_pin9));  // open: pin7
  _74283 #(.VccGndPorts("false"), .ShowInternalStructure("false")) u_74283_2 (
    .pin1(n74283_2_pin4[1]), .pin2(n74283_2_pin2), .pin3(n74283_1_pin1), .pin4(n74283_2_pin4[0]),
    .pin5(n74283_1_pin4), .pin6(n74283_2_pin6), .pin15(n74283_2_pin2), .pin14(n74283_1_pin13),
    .pin13(n74283_2_pin4[2]), .pin12(n74283_1_pin10), .pin11(n74283_2_pin6), .pin10(n74283_2_pin4[3]),
    .pin9(n74283_2_pin4[4]));  // open: pin7
  and and_1 (and_1_out, n74283_1_pin10, n74283_1_pin13);
  and and_2 (and_2_out, n74283_1_pin10, n74283_1_pin1);
  or or_1 (n74283_2_pin2, n74283_1_pin9, and_1_out, and_2_out);
  // Probe on n74283_2_pin4
  // also tied to GND on the sheet: n74283_2_pin6
endmodule

module _7_4 (
);

  wire button_1_out, clock_1_out, F1, F2, F3, n74138_1_ny0, n74138_1_ny1, n74138_1_ny2, n74138_1_ny3,
       n74138_1_ny6, n74138_1_ny7;
  wire [2:0] A_q;

  Counter #(.width(3), .max('h7), .ongoal("wrap"), .trigger("rising"), .behavior("new")) A (
    .Q(A_q), .clk(clock_1_out), .clr(button_1_out));  // open: load, D, count, carry, preset, down
  Clock #(.highDuration(1), .lowDuration(1)) clock_1 (.out(clock_1_out));
  Button button_1 (.out(button_1_out));
  // Probe on A_q
  _74138 u_74138_1 (
    .S1(1'b1), .nS2(1'b0), .nS3(1'b0), .A2(A_q[0]), .A1(A_q[1]), .A0(A_q[2]), .nY0(n74138_1_ny0),
    .nY1(n74138_1_ny1), .nY2(n74138_1_ny2), .nY3(n74138_1_ny3), .nY6(n74138_1_ny6), .nY7(n74138_1_ny7));  // open: nY4, nY5
  nand nand_1 (F1, n74138_1_ny0, n74138_1_ny6, n74138_1_ny2);
  nand nand_2 (F2, n74138_1_ny0, n74138_1_ny1, n74138_1_ny2, n74138_1_ny3, n74138_1_ny6, n74138_1_ny7);
  nand nand_3 (F3, n74138_1_ny0, n74138_1_ny1, n74138_1_ny7, n74138_1_ny6);
endmodule

module _7_6 (
);

  wire nQA, nQB, nQC, nQEX, OS;

  _74LS148 u_74ls148_1 (
    .nI0(1'b1), .nI1(1'b0), .nI2(1'b0), .nI3(1'b0), .nI4(1'b1), .nI5(1'b0), .nI6(1'b1), .nI7(1'b1),
    .nIs(1'b0), .Os(OS), .nQex(nQEX), .nQa(nQA), .nQb(nQB), .nQc(nQC));
endmodule

module _7_7 (
);

  wire A, and_1_out, B, button_1_out, C, clock_1_out, D, nand_1_out, not_1_out, not_2_out, not_3_out,
       xor_1_out;
  wire [3:0] d__1y;

  Clock #(.highDuration(1), .lowDuration(1)) clock_1 (.out(clock_1_out));
  Button button_1 (.out(button_1_out));
  // Probe on {A, B, C, D}
  _74153 u_a (
    ._1D0(1'b0), ._1D1(1'b0), ._1D2(and_1_out), ._1D3(1'b1), .A1(A), .A0(B), ._1G(1'b0), ._1Y(d__1y[3]));  // open: _2D0, _2D1, _2D2, _2D3, _2G, _2Y
  and and_1 (and_1_out, C, D);
  Counter #(.width(4), .max('hf), .ongoal("wrap"), .trigger("rising"), .behavior("new")) A_2 (
    .Q({A, B, C, D}), .clk(clock_1_out), .clr(button_1_out));  // open: load, D, count, carry, preset, down
  _74153 u_b (
    ._1D0(1'b0), ._1D1(nand_1_out), ._1D2(and_1_out), ._1D3(1'b0), .A1(A), .A0(B), ._1G(1'b0), ._1Y(d__1y[2]));  // open: _2D0, _2D1, _2D2, _2D3, _2G, _2Y
  not not_1 (not_1_out, C);
  not not_2 (not_2_out, D);
  nand nand_1 (nand_1_out, not_1_out, not_2_out);
  _74153 u_c (
    ._1D0(1'b0), ._1D1(xor_1_out), ._1D2(xor_1_out), ._1D3(1'b0), .A1(A), .A0(B), ._1G(1'b0), ._1Y(d__1y[1]));  // open: _2D0, _2D1, _2D2, _2D3, _2G, _2Y
  xor xor_1 (xor_1_out, C, D);
  _74153 u_d (
    ._1D0(1'b0), ._1D1(not_3_out), ._1D2(not_3_out), ._1D3(1'b1), .A1(A), .A0(B), ._1G(1'b0), ._1Y(d__1y[0]));  // open: _2D0, _2D1, _2D2, _2D3, _2G, _2Y
  not not_3 (not_3_out, D);
  // Probe on d__1y
endmodule

module _7_8 (
);

  wire A, B, button_1_out, C, clock_1_out, not_1_out, tunnel;

  Clock #(.highDuration(1), .lowDuration(1)) clock_1 (.out(clock_1_out));
  Button button_1 (.out(button_1_out));
  // Probe on {A, B, C}
  Counter #(.width(3), .max('h7), .ongoal("wrap"), .trigger("rising"), .behavior("new")) u_A (
    .Q({A, B, C}), .clk(clock_1_out), .clr(button_1_out));  // open: load, D, count, carry, preset, down
  not not_1 (not_1_out, C);
  _74153 u_74153_1 (
    ._1D0(not_1_out), ._1D1(1'b0), ._1D2(1'b0), ._1D3(C), .A1(A), .A0(B), ._1G(1'b0), ._1Y(tunnel));  // open: _2D0, _2D1, _2D2, _2D3, _2G, _2Y
endmodule

module _74138 (
  input  S1,
  input  nS2,
  input  nS3,
  input  A2,
  input  A1,
  input  A0,
  output nY0,
  output nY1,
  output nY2,
  output nY3,
  output nY4,
  output nY5,
  output nY6,
  output nY7
);

  wire and_1_out, decoder_1_out0, decoder_1_out1, decoder_1_out2, decoder_1_out3, decoder_1_out4,
       decoder_1_out5, decoder_1_out6, decoder_1_out7, not_1_out, not_2_out, not_3_out, not_4_out, not_5_out,
       not_6_out, not_7_out, not_8_out, not_9_out, not_10_out, not_11_out, or_1_out;

  not not_1 (not_1_out, S1);
  not not_2 (not_2_out, nS2);
  not not_3 (not_3_out, nS3);
  or or_1 (or_1_out, not_1_out, nS2, nS3);
  and and_1 (and_1_out, S1, not_2_out, not_3_out);
  Decoder #(.select(3), .tristate("false"), .disabled("Z"), .enable("true")) decoder_1 (
    .out0(decoder_1_out0), .out1(decoder_1_out1), .out2(decoder_1_out2), .out3(decoder_1_out3),
    .out4(decoder_1_out4), .out5(decoder_1_out5), .out6(decoder_1_out6), .out7(decoder_1_out7),
    .sel({A2, A1, A0}), .en(and_1_out));
  not not_4 (not_4_out, decoder_1_out0);
  not not_5 (not_5_out, decoder_1_out1);
  not not_6 (not_6_out, decoder_1_out2);
  not not_7 (not_7_out, decoder_1_out3);
  not not_8 (not_8_out, decoder_1_out4);
  not not_9 (not_9_out, decoder_1_out5);
  not not_10 (not_10_out, decoder_1_out6);
  not not_11 (not_11_out, decoder_1_out7);
  or or_2 (nY0, or_1_out, not_4_out);
  or or_3 (nY1, or_1_out, not_5_out);
  or or_4 (nY2, or_1_out, not_6_out);
  or or_5 (nY3, or_1_out, not_7_out);
  or or_6 (nY4, or_1_out, not_8_out);
  or or_7 (nY5, or_1_out, not_9_out);
  or or_8 (nY6, or_1_out, not_10_out);
  or or_9 (nY7, or_1_out, not_11_out);
endmodule

module _74LS148 (
  input  nI0,
  input  nI1,
  input  nI2,
  input  nI3,
  input  nI4,
  input  nI5,
  input  nI6,
  input  nI7,
  input  nIs,
  output Os,
  output nQex,
  output nQa,
  output nQb,
  output nQc
);

  wire and_1_out, not_1_out, not_2_out, not_3_out, not_4_out, not_5_out, not_6_out, not_7_out, not_8_out,
       not_9_out, not_10_out, not_11_out, not_12_out, not_13_out, or_2_out, priority_encoder_1_en_out;
  wire [2:0] priority_encoder_1_out;

  and and_1 (and_1_out, nI0, nI1, nI2, nI3, nI4, nI5, nI6, nI7);
  not not_1 (not_1_out, nI0);
  not not_2 (not_2_out, nI1);
  not not_3 (not_3_out, nI2);
  not not_4 (not_4_out, nI3);
  not not_5 (not_5_out, nI4);
  not not_6 (not_6_out, nI5);
  not not_7 (not_7_out, nI6);
  not not_8 (not_8_out, nI7);
  Priority_Encoder #(.select(3), .disabled(0)) priority_encoder_1 (
    .in0(not_1_out), .in1(not_2_out), .in2(not_3_out), .in3(not_4_out), .in4(not_5_out), .in5(not_6_out),
    .in6(not_7_out), .in7(not_8_out), .out(priority_encoder_1_out), .en_out(priority_encoder_1_en_out),
    .en_in(not_9_out));  // open: gs
  not not_9 (not_9_out, nIs);
  not not_10 (not_10_out, and_1_out);
  or or_1 (nQex, nIs, priority_encoder_1_en_out);
  not not_11 (not_11_out, priority_encoder_1_out[0]);
  not not_12 (not_12_out, priority_encoder_1_out[1]);
  not not_13 (not_13_out, priority_encoder_1_out[2]);
  or or_2 (or_2_out, and_1_out, nIs);
  or or_3 (Os, not_10_out, nIs);
  or or_4 (nQa, or_2_out, not_11_out);
  or or_5 (nQb, or_2_out, not_12_out);
  or or_6 (nQc, not_13_out, or_2_out);
endmodule

module _74153 (
  input  _1D0,
  input  _2D0,
  input  _1D1,
  input  _2D1,
  input  _1D2,
  input  _2D2,
  input  _1D3,
  input  _2D3,
  input  A1,
  input  A0,
  input  _1G,
  input  _2G,
  output _1Y,
  output _2Y
);

  wire multiplexer_1_out, multiplexer_2_out, not_1_out, not_2_out;

  not not_1 (not_1_out, _1G);
  Multiplexer #(.select(2), .width(1), .disabled("Z"), .enable("true")) multiplexer_1 (
    .in0(_1D0), .in1(_1D1), .in2(_1D2), .in3(_1D3), .out(multiplexer_1_out), .sel({A1, A0}), .en(not_1_out));
  and and_1 (_1Y, multiplexer_1_out, not_1_out);
  not not_2 (not_2_out, _2G);
  Multiplexer #(.select(2), .width(1), .disabled("Z"), .enable("true")) multiplexer_2 (
    .in0(_2D0), .in1(_2D1), .in2(_2D2), .in3(_2D3), .out(multiplexer_2_out), .sel({A1, A0}), .en(not_2_out));
  and and_2 (_2Y, multiplexer_2_out, not_2_out);
endmodule
