// Logisim project 第5章习题电路的实现.circ as structural Verilog: 7 circuits, main circuit 习题5.4
module \习题5_4  (
  input  x,
  output Z
);

  wire and_1_out, CP_out, not_1_out, not_2_out, Y1_q, Y2_q;

  Clock #(.highDuration(1), .lowDuration(1)) CP (.out(CP_out));
  not not_1 (not_1_out, x);
  and and_1 (and_1_out, Y2_q, x);
  J_K_Flip_Flop #(.trigger("falling"), .Pre_Clr_Positions("ABOVE_BELOW"), .NegatePresetClear("false"), .enable("false"), .NewFFLayout("true")) Y2 (
    .J(x), .clk(CP_out), .K(not_1_out), .Q(Y2_q));  // open: Qn, preset, reset
  J_K_Flip_Flop #(.trigger("falling"), .Pre_Clr_Positions("ABOVE_BELOW"), .NegatePresetClear("false"), .enable("false"), .NewFFLayout("true")) Y1 (
    .J(and_1_out), .clk(CP_out), .K(not_2_out), .Q(Y1_q));  // open: Qn, preset, reset
  not not_2 (not_2_out, x);
  and and_2 (Z, Y2_q, x, Y1_q);
endmodule

module \习题5_6  (
  input  x,
  output Z
);

  wire and_1_out, and_2_out, CP_out, not_1_out, xor_1_out, Y1_q, Y1_qn, Y2_q, Y2_qn;

  Clock #(.highDuration(1), .lowDuration(1)) CP (.out(CP_out));
  xor xor_1 (xor_1_out, Y1_q, x);
  not not_1 (not_1_out, x);
  J_K_Flip_Flop #(.trigger("falling"), .Pre_Clr_Positions("ABOVE_BELOW"), .NegatePresetClear("false"), .enable("false"), .NewFFLayout("true")) Y2 (
    .J(xor_1_out), .clk(CP_out), .K(xor_1_out), .Q(Y2_q), .Qn(Y2_qn));  // open: preset, reset
  J_K_Flip_Flop #(.trigger("falling"), .Pre_Clr_Positions("ABOVE_BELOW"), .NegatePresetClear("false"), .enable("false"), .NewFFLayout("true")) Y1 (
    .J(1'b1), .clk(CP_out), .K(1'b1), .Q(Y1_q), .Qn(Y1_qn));  // open: preset, reset
  and and_1 (and_1_out, Y1_qn, Y2_qn, x);
  or or_1 (Z, and_1_out, and_2_out);
  and and_2 (and_2_out, Y2_q, Y1_q, not_1_out);
endmodule

module \习题5_8  (
  input  x,
  output Z
);

  wire and_1_out, and_2_out, and_3_out, and_4_out, CP_out, t_ff_1_q, t_ff_2_q, t_ff_3_q, t_ff_4_q, xor_1_out,
       xor_2_out, xor_3_out, xor_4_out;

  Clock #(.highDuration(1), .lowDuration(1)) CP (.out(CP_out));
  xor xor_1 (xor_1_out, t_ff_1_q, t_ff_2_q);
  xor xor_2 (xor_2_out, t_ff_2_q, t_ff_3_q);
  xor xor_3 (xor_3_out, t_ff_3_q, t_ff_4_q);
  xor xor_4 (xor_4_out, t_ff_4_q, x);
  T_Flip_Flop #(.trigger("rising"), .Pre_Clr_Positions("ABOVE_BELOW"), .NegatePresetClear("false"), .enable("false"), .NewFFLayout("true")) t_ff_1 (
    .clk(CP_out), .T(xor_1_out), .Q(t_ff_1_q));  // open: Qn, preset, reset
  T_Flip_Flop #(.trigger("rising"), .Pre_Clr_Positions("ABOVE_BELOW"), .NegatePresetClear("false"), .enable("false"), .NewFFLayout("true")) t_ff_2 (
    .clk(CP_out), .T(xor_2_out), .Q(t_ff_2_q));  // open: Qn, preset, reset
  T_Flip_Flop #(.trigger("rising"), .Pre_Clr_Positions("ABOVE_BELOW"), .NegatePresetClear("false"), .enable("false"), .NewFFLayout("true")) t_ff_3 (
    .clk(CP_out), .T(xor_3_out), .Q(t_ff_3_q));  // open: Qn, preset, reset
  T_Flip_Flop #(.trigger("rising"), .Pre_Clr_Positions("ABOVE_BELOW"), .NegatePresetClear("false"), .enable("false"), .NewFFLayout("true")) t_ff_4 (
    .clk(CP_out), .T(xor_4_out), .Q(t_ff_4_q));  // open: Qn, preset, reset
  and and_1 (and_1_out, ~t_ff_1_q, ~t_ff_3_q, ~t_ff_4_q);  // AND_Gate
  and and_2 (and_2_out, ~t_ff_2_q, ~t_ff_3_q, ~t_ff_4_q);  // AND_Gate
  and and_3 (and_3_out, t_ff_1_q, t_ff_3_q, t_ff_4_q);
  and and_4 (and_4_out, t_ff_2_q, t_ff_3_q, t_ff_4_q);
  or or_1 (Z, and_1_out, and_2_out, and_3_out, and_4_out);

  // Notes on the sheet:
  //   T3
  //   T2
  //   T1
  //   T0
endmodule

module \习题5_12_D  (
  input  x,
  output Z
);

  wire and_1_out, and_2_out, and_3_out, and_4_out, and_5_out, and_6_out, and_7_out, CP_out, d_ff_1_q,
       d_ff_1_qn, d_ff_2_q, d_ff_2_qn, not_1_out, or_1_out, or_2_out;

  Clock #(.highDuration(1), .lowDuration(1)) CP (.out(CP_out));
  not not_1 (not_1_out, x);
  and and_1 (and_1_out, d_ff_2_q, not_1_out);
  and and_2 (and_2_out, d_ff_2_qn, x);
  or or_1 (or_1_out, and_1_out, and_2_out, and_3_out);
  and and_3 (and_3_out, d_ff_1_qn, x);
  and and_4 (and_4_out, not_1_out, d_ff_1_qn);
  and and_5 (and_5_out, x, d_ff_1_q);
  or or_2 (or_2_out, and_4_out, and_5_out);
  D_Flip_Flop #(.trigger("rising"), .Pre_Clr_Positions("ABOVE_BELOW"), .NegatePresetClear("true"), .enable("false"), .NewFFLayout("true")) d_ff_1 (
    .clk(CP_out), .D(or_1_out), .Q(d_ff_1_q), .Qn(d_ff_1_qn));  // open: preset, reset
  D_Flip_Flop #(.trigger("rising"), .Pre_Clr_Positions("ABOVE_BELOW"), .NegatePresetClear("true"), .enable("false"), .NewFFLayout("true")) d_ff_2 (
    .clk(CP_out), .D(or_2_out), .Q(d_ff_2_q), .Qn(d_ff_2_qn));  // open: preset, reset
  and and_6 (and_6_out, d_ff_1_q, not_1_out);
  and and_7 (and_7_out, d_ff_1_q, d_ff_2_qn);
  or or_3 (Z, and_6_out, and_7_out);

  // Notes on the sheet:
  //   D2
  //   D1
endmodule

module \习题5_12_T  (
  input  x,
  output Z
);

  wire and_1_out, and_2_out, and_3_out, and_4_out, CP_out, nand_1_out, not_1_out, not_2_out, not_3_out,
       not_4_out, or_1_out, t_ff_1_q, t_ff_1_qn, t_ff_2_q, xor_1_out;

  not not_1 (not_1_out, t_ff_2_q);
  Clock #(.highDuration(1), .lowDuration(1)) CP (.out(CP_out));
  and and_1 (and_1_out, t_ff_1_q, not_1_out, not_2_out);
  not not_2 (not_2_out, x);
  and and_2 (and_2_out, not_4_out, t_ff_2_q);
  and and_3 (and_3_out, x, t_ff_1_qn);
  and and_4 (and_4_out, x, t_ff_2_q);
  or or_1 (or_1_out, and_1_out, and_2_out, and_3_out, and_4_out);
  xor xor_1 (xor_1_out, x, t_ff_1_q, not_3_out);
  not not_3 (not_3_out, t_ff_2_q);
  not not_4 (not_4_out, t_ff_1_q);
  T_Flip_Flop #(.trigger("rising"), .Pre_Clr_Positions("ABOVE_BELOW"), .NegatePresetClear("false"), .enable("false"), .NewFFLayout("true")) t_ff_1 (
    .clk(CP_out), .T(or_1_out), .Q(t_ff_1_q), .Qn(t_ff_1_qn));  // open: preset, reset
  T_Flip_Flop #(.trigger("rising"), .Pre_Clr_Positions("ABOVE_BELOW"), .NegatePresetClear("false"), .enable("false"), .NewFFLayout("true")) t_ff_2 (
    .clk(CP_out), .T(xor_1_out), .Q(t_ff_2_q));  // open: Qn, preset, reset
  nand nand_1 (nand_1_out, t_ff_2_q, x);
  and and_5 (Z, t_ff_1_q, nand_1_out);

  // Notes on the sheet:
  //   T2
  //   T1
endmodule

module \习题5_12_J_K  (
  input  x,
  output Z
);

  wire CP_out, j_k_ff_1_q, j_k_ff_1_qn, j_k_ff_2_q, nand_1_out, not_1_out, or_1_out, xor_1_out, xor_2_out,
       xor_3_out;

  Clock #(.highDuration(1), .lowDuration(1)) CP (.out(CP_out));
  xor xor_1 (xor_1_out, x, not_1_out);
  not not_1 (not_1_out, j_k_ff_2_q);
  xor xor_2 (xor_2_out, x, j_k_ff_1_q);
  J_K_Flip_Flop #(.trigger("falling"), .Pre_Clr_Positions("ABOVE_BELOW"), .NegatePresetClear("false"), .enable("false"), .NewFFLayout("true")) j_k_ff_1 (
    .J(or_1_out), .clk(CP_out), .K(xor_1_out), .Q(j_k_ff_1_q), .Qn(j_k_ff_1_qn));  // open: preset, reset
  or or_1 (or_1_out, x, j_k_ff_2_q);
  J_K_Flip_Flop #(.trigger("falling"), .Pre_Clr_Positions("ABOVE_BELOW"), .NegatePresetClear("false"), .enable("false"), .NewFFLayout("true")) j_k_ff_2 (
    .J(xor_3_out), .clk(CP_out), .K(xor_2_out), .Q(j_k_ff_2_q));  // open: Qn, preset, reset
  xor xor_3 (xor_3_out, x, j_k_ff_1_qn);
  nand nand_1 (nand_1_out, x, j_k_ff_2_q);
  and and_1 (Z, j_k_ff_1_q, nand_1_out);

  // Notes on the sheet:
  //   J-K2
  //   J-K1
endmodule

module \习题5_15  (
);

  wire and_1_out, and_2_out, and_3_out, and_4_out, CP_out, not_1_out, or_1_out, t_ff_1_q, t_ff_2_q, t_ff_3_q,
       t_ff_4_q;

  Clock #(.highDuration(1), .lowDuration(1)) CP (.out(CP_out));
  and and_1 (and_1_out, t_ff_1_q, t_ff_4_q);
  and and_2 (and_2_out, t_ff_3_q, t_ff_4_q, t_ff_2_q);
  not not_1 (not_1_out, t_ff_1_q);
  or or_1 (or_1_out, and_1_out, and_2_out);
  and and_3 (and_3_out, t_ff_3_q, t_ff_4_q);
  and and_4 (and_4_out, not_1_out, t_ff_4_q);
  T_Flip_Flop #(.trigger("rising"), .Pre_Clr_Positions("ABOVE_BELOW"), .NegatePresetClear("false"), .enable("false"), .NewFFLayout("true")) t_ff_1 (
    .clk(CP_out), .T(or_1_out), .Q(t_ff_1_q));  // open: Qn, preset, reset
  T_Flip_Flop #(.trigger("rising"), .Pre_Clr_Positions("ABOVE_BELOW"), .NegatePresetClear("false"), .enable("false"), .NewFFLayout("true")) t_ff_2 (
    .clk(CP_out), .T(and_3_out), .Q(t_ff_2_q));  // open: Qn, preset, reset
  T_Flip_Flop #(.trigger("rising"), .Pre_Clr_Positions("ABOVE_BELOW"), .NegatePresetClear("false"), .enable("false"), .NewFFLayout("true")) t_ff_3 (
    .clk(CP_out), .T(and_4_out), .Q(t_ff_3_q));  // open: Qn, preset, reset
  T_Flip_Flop #(.trigger("rising"), .Pre_Clr_Positions("ABOVE_BELOW"), .NegatePresetClear("false"), .enable("false"), .NewFFLayout("true")) t_ff_4 (
    .clk(CP_out), .T(1'b1), .Q(t_ff_4_q));  // open: Qn, preset, reset

  // Notes on the sheet:
  //   T3
  //   T2
  //   T1
  //   T0
endmodule
