// Logisim project 第5章习题电路的实现.circ as structural Verilog
module _5_4 (
  input  X,
  output Z
);

  wire and_1_out, CP, not_1_out, not_2_out, y1, y2;

  Clock #(.highDuration(1), .lowDuration(1)) clock_1 (.out(CP));
  not not_1 (not_1_out, CP);
  // Digital_Oscilloscope #(.nState(20), .frontlines("rising"), .showclock("true")) digital_oscilloscope_1: pin names not known; wires that end beside it: CP, X, y1, y2, Z
  and and_1 (and_1_out, X, y1);
  not not_2 (not_2_out, X);
  and and_2 (Z, y2, X, y1);
  J_K_Flip_Flop #(.trigger("rising"), .Pre_Clr_Positions("ABOVE_BELOW"), .NegatePresetClear("false"), .enable("false"), .NewFFLayout("true")) u_y2 (
    .J(and_1_out), .clk(not_1_out), .K(not_2_out), .Q(y2));  // open: Qn, preset, reset
  J_K_Flip_Flop #(.trigger("rising"), .Pre_Clr_Positions("ABOVE_BELOW"), .NegatePresetClear("false"), .enable("false"), .NewFFLayout("true")) u_y1 (
    .J(X), .clk(not_1_out), .K(not_2_out), .Q(y1));  // open: Qn, preset, reset
endmodule

module _5_6 (
  input  in_1,
  input  X,
  output Z
);

  wire and_1_out, and_2_out, cp, not_1_out, not_2_out, xor_1_out, y1, y1_qn, y2, y2_qn;

  Clock #(.highDuration(1), .lowDuration(1)) u_CP (.out(cp));
  not not_1 (not_1_out, cp);
  // Digital_Oscilloscope #(.nState(20), .frontlines("rising"), .showclock("true")) digital_oscilloscope_1: pin names not known; wires that end beside it: cp, X, y1, y2, Z
  xor xor_1 (xor_1_out, X, y1);
  J_K_Flip_Flop #(.trigger("rising"), .Pre_Clr_Positions("ABOVE_BELOW"), .NegatePresetClear("false"), .enable("false"), .NewFFLayout("true")) u_y2 (
    .J(xor_1_out), .clk(not_1_out), .K(xor_1_out), .Q(y2), .Qn(y2_qn));  // open: preset, reset
  J_K_Flip_Flop #(.trigger("rising"), .Pre_Clr_Positions("ABOVE_BELOW"), .NegatePresetClear("false"), .enable("false"), .NewFFLayout("true")) u_y1 (
    .J(in_1), .clk(not_1_out), .K(in_1), .Q(y1), .Qn(y1_qn));  // open: preset, reset
  and and_1 (and_1_out, X, y2_qn, y1_qn);
  and and_2 (and_2_out, y2, y1, not_2_out);
  not not_2 (not_2_out, X);
  or or_1 (Z, and_1_out, and_2_out);
endmodule

module _5_8 (
  input  X,
  output Z
);

  wire and_1_out, and_2_out, and_3_out, and_4_out, and_5_out, and_6_out, and_7_out, and_8_out, and_9_out,
       and_10_out, and_11_out, and_12_out, and_13_out, and_14_out, and_15_out, and_16_out, and_17_out,
       and_18_out, and_19_out, and_20_out, CP, not_1_out, or_1_out, or_2_out, or_3_out, or_4_out, T1_qn,
       T2_qn, T3_qn, T4_qn, Y1, Y2, Y3;

  Clock #(.highDuration(1), .lowDuration(1)) clock_1 (.out(CP));
  not not_1 (not_1_out, X);
  and and_1 (and_1_out, X, T4_qn, T3_qn);
  or or_1 (or_1_out, and_1_out, and_2_out, and_3_out, and_4_out, and_5_out);
  and and_2 (and_2_out, Y3, Y1);
  and and_3 (and_3_out, X, Y3, T3_qn);
  and and_4 (and_4_out, T4_qn, Y2, Y1);
  and and_5 (and_5_out, T4_qn, T3_qn, T2_qn, T1_qn);
  and and_6 (and_6_out, Y2, T1_qn);
  or or_2 (or_2_out, and_6_out, and_7_out, and_8_out, and_9_out, and_10_out, and_11_out);
  and and_7 (and_7_out, Y3, Y2, Y1);
  and and_8 (and_8_out, not_1_out, T4_qn, Y3);
  and and_9 (and_9_out, not_1_out, T4_qn, T2_qn, Y1);
  and and_10 (and_10_out, X, T4_qn, T3_qn, Y2);
  and and_11 (and_11_out, X, T4_qn, T3_qn, T2_qn, T1_qn);
  or or_3 (or_3_out, X, and_12_out, and_13_out, and_14_out);
  and and_12 (and_12_out, not_1_out, Y2, T1_qn);
  and and_13 (and_13_out, not_1_out, Y3, Y3);
  and and_14 (and_14_out, X, Y3);
  or or_4 (or_4_out, Y3, and_15_out, and_16_out, and_17_out, and_18_out);
  and and_15 (and_15_out, X, Y3);
  and and_16 (and_16_out, Y3, Y3, Y2, Y1);
  and and_17 (and_17_out, T4_qn, Y3, T2_qn, Y1);
  and and_18 (and_18_out, X, T4_qn, Y2, Y1);
  T_Flip_Flop #(.trigger("rising"), .Pre_Clr_Positions("ABOVE_BELOW"), .NegatePresetClear("false"), .enable("false"), .NewFFLayout("true")) T1 (
    .clk(CP), .T(or_1_out), .Q(Y1), .Qn(T1_qn));  // open: preset, reset
  T_Flip_Flop #(.trigger("rising"), .Pre_Clr_Positions("ABOVE_BELOW"), .NegatePresetClear("false"), .enable("false"), .NewFFLayout("true")) T2 (
    .clk(CP), .T(or_2_out), .Q(Y2), .Qn(T2_qn));  // open: preset, reset
  T_Flip_Flop #(.trigger("rising"), .Pre_Clr_Positions("ABOVE_BELOW"), .NegatePresetClear("false"), .enable("false"), .NewFFLayout("true")) T3 (
    .clk(CP), .T(or_3_out), .Q(Y3), .Qn(T3_qn));  // open: preset, reset
  T_Flip_Flop #(.trigger("rising"), .Pre_Clr_Positions("ABOVE_BELOW"), .NegatePresetClear("false"), .enable("false"), .NewFFLayout("true")) T4 (
    .clk(CP), .T(or_4_out), .Q(Y3), .Qn(T4_qn));  // open: preset, reset
  and and_19 (and_19_out, not_1_out, Y2, T1_qn);
  and and_20 (and_20_out, X, Y3, T3_qn);
  or or_5 (Z, and_19_out, and_20_out);
  // Digital_Oscilloscope #(.nState(20), .frontlines("rising"), .showclock("true")) digital_oscilloscope_1: pin names not known; wires that end beside it: X, not_1_out, CP, X, Y1, Y2, Y3, Y3, Z

  // Other names for the same wires on the sheet: Y4 = Y3
endmodule

module _5_12 (
  input  X,
  output Z
);

  wire and_1_out, and_2_out, and_3_out, and_4_out, and_5_out, and_6_out, and_7_out, and_8_out, and_9_out,
       and_10_out, CP, digital_oscilloscope_1_p1, not_1_out, or_1_out, or_2_out, or_3_out, or_4_out, Y1, Y2,
       Y2_qn;

  Clock #(.highDuration(1), .lowDuration(1)) clock_1 (.out(CP));
  not not_1 (not_1_out, X);
  and and_1 (and_1_out, not_1_out, Y2_qn);
  and and_2 (and_2_out, X, Y2);
  and and_3 (and_3_out, not_1_out, Y2);
  and and_4 (and_4_out, X, Y2_qn);
  and and_5 (and_5_out, X, Y2_qn);
  and and_6 (and_6_out, Y2_qn, Y1);
  and and_7 (and_7_out, not_1_out, digital_oscilloscope_1_p1);
  and and_8 (and_8_out, X, Y1);
  or or_1 (or_1_out, and_1_out, and_2_out);
  or or_2 (or_2_out, and_3_out, and_4_out);
  or or_3 (or_3_out, and_5_out, and_6_out);
  or or_4 (or_4_out, and_7_out, and_8_out);
  // Digital_Oscilloscope #(.nState(10), .frontlines("rising"), .showclock("true")) digital_oscilloscope_1: pin names not known; wires that end beside it: digital_oscilloscope_1_p1, CP, X, Y1, Y2, Z, X, not_1_out
  J_K_Flip_Flop #(.trigger("rising"), .Pre_Clr_Positions("ABOVE_BELOW"), .NegatePresetClear("false"), .enable("false"), .NewFFLayout("true")) u_Y1 (
    .J(or_1_out), .clk(CP), .K(or_2_out), .Q(Y1), .Qn(digital_oscilloscope_1_p1));  // open: preset, reset
  J_K_Flip_Flop #(.trigger("rising"), .Pre_Clr_Positions("ABOVE_BELOW"), .NegatePresetClear("false"), .enable("false"), .NewFFLayout("true")) u_Y2 (
    .J(or_3_out), .clk(CP), .K(or_4_out), .Q(Y2), .Qn(Y2_qn));  // open: preset, reset
  and and_9 (and_9_out, not_1_out, Y2);
  or or_5 (Z, and_9_out, and_10_out);
  and and_10 (and_10_out, digital_oscilloscope_1_p1, Y2);
endmodule

module _5_15 (
  input  X,
  input  in_2,
  output Y1,
  output Y2,
  output Y3,
  output Y4
);

  wire and_1_out, and_2_out, and_3_out, and_4_out, clock_1_out, not_1_out, or_1_out, T1_qn, T2_qn, T3_qn,
       T4_qn;

  Clock #(.highDuration(1), .lowDuration(1)) clock_1 (.out(clock_1_out));
  not not_1 (not_1_out, X);
  and and_1 (and_1_out, Y1, Y4);
  and and_2 (and_2_out, Y1, Y2, Y3);
  and and_3 (and_3_out, Y1, T4_qn);
  and and_4 (and_4_out, Y1, Y2);
  or or_1 (or_1_out, and_1_out, and_2_out);
  T_Flip_Flop #(.trigger("rising"), .Pre_Clr_Positions("ABOVE_BELOW"), .NegatePresetClear("false"), .enable("false"), .NewFFLayout("true")) T1 (
    .clk(clock_1_out), .T(in_2), .Q(Y1), .Qn(T1_qn));  // open: preset, reset
  T_Flip_Flop #(.trigger("rising"), .Pre_Clr_Positions("ABOVE_BELOW"), .NegatePresetClear("false"), .enable("false"), .NewFFLayout("true")) T2 (
    .clk(clock_1_out), .T(and_3_out), .Q(Y2), .Qn(T2_qn));  // open: preset, reset
  T_Flip_Flop #(.trigger("rising"), .Pre_Clr_Positions("ABOVE_BELOW"), .NegatePresetClear("false"), .enable("false"), .NewFFLayout("true")) T3 (
    .clk(clock_1_out), .T(and_4_out), .Q(Y3), .Qn(T3_qn));  // open: preset, reset
  T_Flip_Flop #(.trigger("rising"), .Pre_Clr_Positions("ABOVE_BELOW"), .NegatePresetClear("false"), .enable("false"), .NewFFLayout("true")) T4 (
    .clk(clock_1_out), .T(or_1_out), .Q(Y4), .Qn(T4_qn));  // open: preset, reset
endmodule
