// Logisim project 逻辑代数基础验证.circ as structural Verilog: 27 circuits, main circuit 逻辑函数的真值表
module \逻辑函数的真值表  (
  output F
);

  wire A, and_1_out, and_2_out, B, button_1_out, C, clock_1_out, not_1_out, not_2_out;

  Counter #(.width(3), .max('h7), .ongoal("wrap"), .trigger("rising"), .behavior("new")) counter_1 (
    .Q({A, B, C}), .clk(clock_1_out), .clr(button_1_out));  // open: load, D, count, carry, preset, down
  Clock #(.highDuration(1), .lowDuration(1)) clock_1 (.out(clock_1_out));
  Button button_1 (.out(button_1_out));
  // Probe on A
  // Probe on B
  // Probe on C
  not not_1 (not_1_out, B);
  not not_2 (not_2_out, A);
  and and_1 (and_1_out, A, not_1_out);
  and and_2 (and_2_out, not_2_out, C);
  or or_1 (F, and_1_out, and_2_out);
endmodule

module \代入规则_1  (
  output F,
  output F_2
);

  wire A, and_1_out, and_2_out, B, button_1_out, buzzer_1_p2, C, clock_1_out, comparator_1_eq, or_1_out;

  Counter #(.width(3), .max('h7), .ongoal("wrap"), .trigger("rising"), .behavior("new")) counter_1 (
    .Q({A, B, C}), .clk(clock_1_out), .clr(button_1_out));  // open: load, D, count, carry, preset, down
  Clock #(.highDuration(1), .lowDuration(1)) clock_1 (.out(clock_1_out));
  Button button_1 (.out(button_1_out));
  // Probe on A
  // Probe on B
  // Probe on C
  // Probe on A
  // Probe on B
  // Probe on C
  or or_1 (or_1_out, B, C);
  and and_1 (and_1_out, A, B);
  and and_2 (and_2_out, A, C);
  and and_3 (F, A, or_1_out);
  or or_2 (F_2, and_1_out, and_2_out);
  // Buzzer #(.freq_measure("Hz"), .vol_width(1)) buzzer_1: pin names not known; wires that end beside it: A, buzzer_1_p2
  not not_1 (buzzer_1_p2, comparator_1_eq);
  Comparator #(.width(1), .mode("twosComplement")) comparator_1 (.a(F), .b(F_2), .eq(comparator_1_eq));  // open: gt, lt
  LED #(.active("false")) led_1 (.in(comparator_1_eq));
endmodule

module \代入规则_2  (
  output F,
  output F_2
);

  wire A, and_1_out, and_2_out, B, button_1_out, buzzer_1_p2, C, clock_1_out, comparator_1_eq, D, or_1_out,
       or_2_out, or_3_out;

  Clock #(.highDuration(1), .lowDuration(1)) clock_1 (.out(clock_1_out));
  Button button_1 (.out(button_1_out));
  Counter #(.width(4), .max('hf), .ongoal("wrap"), .trigger("rising"), .behavior("new")) counter_1 (
    .Q({A, B, C, D}), .clk(clock_1_out), .clr(button_1_out));  // open: load, D, count, carry, preset, down
  // Probe on A
  // Probe on B
  // Probe on C
  // Probe on D
  // Probe on A
  // Probe on B
  // Probe on C
  // Probe on D
  or or_1 (or_1_out, C, D);
  or or_2 (or_2_out, C, D);
  or or_3 (or_3_out, B, or_1_out);
  and and_1 (and_1_out, A, B);
  and and_2 (and_2_out, A, or_2_out);
  and and_3 (F, A, or_3_out);
  or or_4 (F_2, and_1_out, and_2_out);
  Comparator #(.width(1), .mode("twosComplement")) comparator_1 (.a(F), .b(F_2), .eq(comparator_1_eq));  // open: gt, lt
  // Buzzer #(.freq_measure("Hz"), .vol_width(1)) buzzer_1: pin names not known; wires that end beside it: A, buzzer_1_p2
  not not_1 (buzzer_1_p2, comparator_1_eq);
  LED #(.active("false")) led_1 (.in(comparator_1_eq));
endmodule

module \反演规则  (
  output F,
  output nF
);

  wire A, and_1_out, and_2_out, B, button_1_out, buzzer_1_p1, C, clock_1_out, comparator_1_eq, D, not_1_out,
       not_2_out, not_3_out, not_4_out, not_5_out, or_1_out, or_2_out;

  Clock #(.highDuration(1), .lowDuration(1)) clock_1 (.out(clock_1_out));
  Button button_1 (.out(button_1_out));
  Counter #(.width(4), .max('hf), .ongoal("wrap"), .trigger("rising"), .behavior("new")) counter_1 (
    .Q({A, B, C, D}), .clk(clock_1_out), .clr(button_1_out));  // open: load, D, count, carry, preset, down
  // Probe on A
  // Probe on B
  // Probe on C
  // Probe on D
  // Probe on A
  // Probe on B
  // Probe on C
  // Probe on D
  not not_1 (not_1_out, A);
  and and_1 (and_1_out, not_1_out, B);
  and and_2 (and_2_out, C, not_2_out);
  not not_2 (not_2_out, D);
  not not_3 (not_3_out, B);
  not not_4 (not_4_out, C);
  or or_1 (or_1_out, A, not_3_out);
  or or_2 (or_2_out, not_4_out, D);
  or or_3 (F, and_1_out, and_2_out);
  not not_5 (not_5_out, nF);
  and and_3 (nF, or_1_out, or_2_out);
  Comparator #(.width(1), .mode("twosComplement")) comparator_1 (
    .a(F), .b(not_5_out), .eq(comparator_1_eq));  // open: gt, lt
  // Buzzer #(.freq_measure("Hz"), .vol_width(1)) buzzer_1: pin names not known; wires that end beside it: buzzer_1_p1
  not not_6 (buzzer_1_p1, comparator_1_eq);
  LED #(.active("false")) led_1 (.in(comparator_1_eq));
endmodule

module \对偶规则  (
  output F,
  output G,
  output F_prime,
  output G_prime
);

  wire A, and_1_out, and_2_out, and_3_out, and_4_out, B, button_1_out, buzzer_1_p1, buzzer_2_p1, C,
       clock_1_out, comparator_1_eq, comparator_2_eq, not_1_out, not_2_out, not_3_out, not_4_out, or_1_out,
       or_2_out, or_3_out, or_4_out;

  Counter #(.width(3), .max('h7), .ongoal("wrap"), .trigger("rising"), .behavior("new")) counter_1 (
    .Q({A, B, C}), .clk(clock_1_out), .clr(button_1_out));  // open: load, D, count, carry, preset, down
  Clock #(.highDuration(1), .lowDuration(1)) clock_1 (.out(clock_1_out));
  Button button_1 (.out(button_1_out));
  // Probe on A
  // Probe on B
  // Probe on C
  // Probe on A
  // Probe on B
  // Probe on C
  // Probe on A
  // Probe on B
  // Probe on C
  // Probe on A
  // Probe on B
  // Probe on C
  not not_1 (not_1_out, A);
  not not_2 (not_2_out, B);
  not not_3 (not_3_out, A);
  not not_4 (not_4_out, B);
  and and_1 (and_1_out, A, B);
  and and_2 (and_2_out, not_1_out, C);
  and and_3 (and_3_out, not_2_out, C);
  and and_4 (and_4_out, A, B);
  or or_1 (or_1_out, A, B);
  or or_2 (or_2_out, not_3_out, C);
  or or_3 (or_3_out, not_4_out, C);
  or or_4 (or_4_out, A, B);
  or or_5 (F, and_1_out, and_2_out, and_3_out);
  or or_6 (G, and_4_out, C);
  and and_5 (F_prime, or_1_out, or_2_out, or_3_out);
  Comparator #(.width(1), .mode("twosComplement")) comparator_1 (.a(F), .b(G), .eq(comparator_1_eq));  // open: gt, lt
  and and_6 (G_prime, or_4_out, C);
  // Buzzer #(.freq_measure("Hz"), .vol_width(1)) buzzer_1: pin names not known; wires that end beside it: buzzer_1_p1
  not not_5 (buzzer_1_p1, comparator_1_eq);
  LED #(.active("false")) led_1 (.in(comparator_1_eq));
  // Buzzer #(.freq_measure("Hz"), .vol_width(1)) buzzer_2: pin names not known; wires that end beside it: buzzer_2_p1
  not not_6 (buzzer_2_p1, comparator_2_eq);
  LED #(.active("false")) led_2 (.in(comparator_2_eq));
  Comparator #(.width(1), .mode("twosComplement")) comparator_2 (
    .a(F_prime), .b(G_prime), .eq(comparator_2_eq));  // open: gt, lt
endmodule

module \使用_与非门_实现与_或_非逻辑  (
  input  A,
  input  A_2,
  input  B,
  input  B_2,
  input  A_3,
  output F,
  output F_2,
  output F_3
);

  wire nand_1_out, nand_4_out, nand_5_out;

  nand nand_1 (nand_1_out, A_2, B);
  nand nand_2 (F_2, nand_1_out, 1'b1);
  nand nand_3 (F_3, A_3, 1'b1);
  nand nand_4 (nand_4_out, A, 1'b1);
  nand nand_5 (nand_5_out, 1'b1, B_2);
  nand nand_6 (F, nand_4_out, nand_5_out);

  // Notes on the sheet:
  //   利用与非门实现与逻辑：F = AB
  //   利用与非门实现非逻辑：F = /A
  //   利用与非门实现或逻辑：F = A+B
endmodule

module \使用_或非门_实现与_或_非逻辑  (
  input  A,
  input  A_2,
  input  B,
  input  B_2,
  input  A_3,
  output F,
  output F_2,
  output F_3
);

  wire nor_1_out, nor_2_out, nor_5_out;

  nor nor_1 (nor_1_out, A, 1'b0);
  nor nor_2 (nor_2_out, 1'b0, B_2);
  nor nor_3 (F, nor_1_out, nor_2_out);
  nor nor_4 (F_3, A_3, 1'b0);
  nor nor_5 (nor_5_out, A_2, B);
  nor nor_6 (F_2, nor_5_out, 1'b0);

  // Notes on the sheet:
  //   利用或非门实现与逻辑：F = AB
  //   利用或非门实现非逻辑：F = /A
  //   利用或非门实现或逻辑：F = A+B
endmodule

module \使用_与或非门_实现与_或_非逻辑  (
  input  A,
  input  A_2,
  input  B,
  input  B_2,
  input  A_3,
  output F,
  output F_2,
  output F_3
);

  wire \与或非门_1_f , \与或非门_4_f ;

  \与或非门  \u_与或非门_1  (.A(A), .B(B), .C(1'b0), .D(1'b0), .F(\与或非门_1_f ));
  \与或非门  \u_与或非门_2  (.A(\与或非门_1_f ), .B(1'b1), .C(1'b0), .D(1'b0), .F(F));
  \与或非门  \u_与或非门_3  (.A(A_3), .B(1'b1), .C(1'b0), .D(1'b0), .F(F_3));
  \与或非门  \u_与或非门_4  (.A(A_2), .B(1'b1), .C(1'b1), .D(B_2), .F(\与或非门_4_f ));
  \与或非门  \u_与或非门_5  (.A(\与或非门_4_f ), .B(1'b1), .C(1'b0), .D(1'b0), .F(F_2));

  // Notes on the sheet:
  //   利用与或非门实现与门：F = AB
  //   利用与或非门实现非门：F = /A
  //   利用与或非门实现或门：F = A+B
endmodule

module \使用_与或非门_实现逻辑公式  (
  output F,
  output F_2
);

  wire A, and_1_out, B, button_1_out, C, clock_1_out, comparator_1_eq, not_1_out, not_2_out, not_3_out,
       not_4_out;

  Clock #(.highDuration(1), .lowDuration(1)) clock_1 (.out(clock_1_out));
  Button button_1 (.out(button_1_out));
  Counter #(.width(3), .max('h7), .ongoal("wrap"), .trigger("rising"), .behavior("new")) counter_1 (
    .Q({A, B, C}), .clk(clock_1_out), .clr(button_1_out));  // open: load, D, count, carry, preset, down
  // Probe on A
  // Probe on B
  // Probe on C
  // Probe on A
  // Probe on B
  // Probe on C
  not not_1 (not_1_out, A);
  not not_2 (not_2_out, B);
  not not_3 (not_3_out, C);
  and and_1 (and_1_out, not_1_out, B);
  or or_1 (F, and_1_out, C);
  \与或非门  \u_与或非门_1  (.A(A), .B(not_3_out), .C(not_2_out), .D(not_3_out), .F(F_2));
  Comparator #(.width(1), .mode("twosComplement")) comparator_1 (.a(F), .b(F_2), .eq(comparator_1_eq));  // open: gt, lt
  not not_4 (not_4_out, comparator_1_eq);
  // Buzzer #(.freq_measure("Hz"), .vol_width(7)) buzzer_1: pin names not known; wires that end beside it: not_4_out
  LED #(.active("false")) led_1 (.in(comparator_1_eq));

  // Notes on the sheet:
  //   利用与或非门实现逻辑公式 F = /AB +C
endmodule

module \与或非门  (
  input  A,
  input  B,
  input  C,
  input  D,
  output F
);

  wire and_1_out, and_2_out;

  and and_1 (and_1_out, A, B);
  and and_2 (and_2_out, C, D);
  nor nor_1 (F, and_1_out, and_2_out);

  // Notes on the sheet:
  //   与或非门    F = /(AB + CD)
endmodule

module \与_或_表达式和_或_与_表达式  (
  output F,
  output F_2,
  output F_3
);

  wire A, and_1_out, and_2_out, and_3_out, and_4_out, B, button_1_out, buzzer_1_p1, C, clock_1_out,
       comparator_1_eq, comparator_2_eq, nand_1_out, not_1_out, not_2_out, not_3_out, not_4_out, not_5_out,
       not_6_out, not_7_out, not_9_out, or_1_out, or_2_out, or_3_out, or_4_out, or_5_out;

  Counter #(.width(3), .max('h7), .ongoal("wrap"), .trigger("rising"), .behavior("new")) counter_1 (
    .Q({A, B, C}), .clk(clock_1_out), .clr(button_1_out));  // open: load, D, count, carry, preset, down
  Clock #(.highDuration(1), .lowDuration(1)) clock_1 (.out(clock_1_out));
  Button button_1 (.out(button_1_out));
  // Probe on A
  // Probe on B
  // Probe on C
  // Probe on A
  // Probe on B
  // Probe on C
  // Probe on A
  // Probe on B
  // Probe on C
  not not_1 (not_1_out, A);
  not not_2 (not_2_out, B);
  not not_3 (not_3_out, C);
  not not_4 (not_4_out, A);
  not not_5 (not_5_out, B);
  not not_6 (not_6_out, A);
  not not_7 (not_7_out, B);
  and and_1 (and_1_out, A, not_2_out);
  nand nand_1 (nand_1_out, B, not_3_out);
  and and_2 (and_2_out, A, not_5_out);
  and and_3 (and_3_out, not_4_out, C);
  or or_1 (or_1_out, A, not_7_out, C);
  or or_2 (or_2_out, not_6_out, not_7_out, C);
  or or_3 (or_3_out, not_7_out, C);
  or or_4 (or_4_out, and_1_out, C);
  or or_5 (or_5_out, not_1_out, nand_1_out);
  and and_4 (and_4_out, or_4_out, or_5_out);
  or or_6 (F_2, and_2_out, and_3_out, not_5_out, C);
  and and_5 (F_3, or_1_out, or_2_out, or_3_out);
  or or_7 (F, and_4_out, not_2_out);
  Comparator #(.width(1), .mode("twosComplement")) comparator_1 (.a(F), .b(F_2), .eq(comparator_1_eq));  // open: gt, lt
  Comparator #(.width(1), .mode("twosComplement")) comparator_2 (.a(F), .b(F_3), .eq(comparator_2_eq));  // open: gt, lt
  // Buzzer #(.freq_measure("Hz"), .vol_width(7)) buzzer_1: pin names not known; wires that end beside it: buzzer_1_p1
  not not_8 (buzzer_1_p1, comparator_1_eq);
  LED #(.active("false")) led_1 (.in(comparator_1_eq));
  not not_9 (not_9_out, comparator_2_eq);
  // Buzzer #(.freq_measure("Hz"), .vol_width(7)) buzzer_2: pin names not known; wires that end beside it: not_9_out
  LED #(.active("false")) led_2 (.in(comparator_2_eq));
endmodule

module \标准_与_或_表达式_1  (
  output F,
  output F_2
);

  wire A, and_1_out, and_2_out, and_3_out, and_4_out, and_5_out, and_6_out, and_7_out, B, button_1_out, C,
       clock_1_out, comparator_1_eq, nand_1_out, not_1_out, not_2_out, not_3_out, not_4_out, not_5_out,
       not_6_out, or_1_out;

  Counter #(.width(3), .max('h7), .ongoal("wrap"), .trigger("rising"), .behavior("new")) counter_1 (
    .Q({A, B, C}), .clk(clock_1_out), .clr(button_1_out));  // open: load, D, count, carry, preset, down
  Clock #(.highDuration(1), .lowDuration(1)) clock_1 (.out(clock_1_out));
  Button button_1 (.out(button_1_out));
  // Probe on A
  // Probe on B
  // Probe on C
  // Probe on A
  // Probe on B
  // Probe on C
  not not_1 (not_1_out, A);
  not not_2 (not_2_out, B);
  not not_3 (not_3_out, C);
  not not_4 (not_4_out, B);
  not not_5 (not_5_out, C);
  and and_1 (and_1_out, A, not_4_out);
  and and_2 (and_2_out, B, not_5_out);
  nand nand_1 (nand_1_out, A, B);
  and and_3 (and_3_out, not_1_out, not_2_out, not_3_out);
  and and_4 (and_4_out, not_1_out, not_2_out, C);
  and and_5 (and_5_out, not_1_out, B, C);
  and and_6 (and_6_out, A, B, not_3_out);
  and and_7 (and_7_out, A, B, C);
  or or_1 (or_1_out, and_1_out, and_2_out);
  nand nand_2 (F, or_1_out, nand_1_out);
  or or_2 (F_2, and_3_out, and_4_out, and_5_out, and_6_out, and_7_out);
  Comparator #(.width(1), .mode("twosComplement")) comparator_1 (.a(F), .b(F_2), .eq(comparator_1_eq));  // open: gt, lt
  not not_6 (not_6_out, comparator_1_eq);
  // Buzzer #(.freq_measure("Hz"), .vol_width(7)) buzzer_1: pin names not known; wires that end beside it: not_6_out
  LED #(.active("false")) led_1 (.in(comparator_1_eq));
endmodule

module \标准_与_或_表达式_2  (
  output F,
  output F_2
);

  wire A, and_1_out, and_2_out, and_3_out, and_4_out, and_5_out, and_6_out, B, button_1_out, C, clock_1_out,
       comparator_1_eq, not_1_out, not_2_out, not_3_out, not_4_out, not_5_out, not_6_out;

  Counter #(.width(3), .max('h7), .ongoal("wrap"), .trigger("rising"), .behavior("new")) counter_1 (
    .Q({A, B, C}), .clk(clock_1_out), .clr(button_1_out));  // open: load, D, count, carry, preset, down
  Clock #(.highDuration(1), .lowDuration(1)) clock_1 (.out(clock_1_out));
  Button button_1 (.out(button_1_out));
  // Probe on A
  // Probe on B
  // Probe on C
  // Probe on A
  // Probe on B
  // Probe on C
  not not_1 (not_1_out, A);
  not not_2 (not_2_out, B);
  not not_3 (not_3_out, C);
  not not_4 (not_4_out, B);
  not not_5 (not_5_out, C);
  and and_1 (and_1_out, A, not_4_out);
  or or_1 (F, and_1_out, and_2_out);
  and and_2 (and_2_out, B, not_5_out);
  and and_3 (and_3_out, not_1_out, B, not_3_out);
  and and_4 (and_4_out, A, not_2_out, not_3_out);
  and and_5 (and_5_out, A, not_2_out, C);
  and and_6 (and_6_out, A, B, not_3_out);
  or or_2 (F_2, and_3_out, and_4_out, and_5_out, and_6_out);
  Comparator #(.width(1), .mode("twosComplement")) comparator_1 (.a(F), .b(F_2), .eq(comparator_1_eq));  // open: gt, lt
  not not_6 (not_6_out, comparator_1_eq);
  // Buzzer #(.freq_measure("Hz"), .vol_width(7)) buzzer_1: pin names not known; wires that end beside it: not_6_out
  LED #(.active("false")) led_1 (.in(comparator_1_eq));
endmodule

module \标准_或_与_表达式_1  (
  output F,
  output F_2
);

  wire A, and_1_out, and_2_out, and_3_out, B, button_1_out, C, clock_1_out, comparator_1_eq, nor_1_out,
       not_1_out, not_2_out, not_3_out, not_4_out, not_5_out, not_6_out, or_1_out, or_2_out, or_3_out;

  Counter #(.width(3), .max('h7), .ongoal("wrap"), .trigger("rising"), .behavior("new")) counter_1 (
    .Q({A, B, C}), .clk(clock_1_out), .clr(button_1_out));  // open: load, D, count, carry, preset, down
  Clock #(.highDuration(1), .lowDuration(1)) clock_1 (.out(clock_1_out));
  Button button_1 (.out(button_1_out));
  // Probe on A
  // Probe on B
  // Probe on C
  // Probe on A
  // Probe on B
  // Probe on C
  not not_1 (not_1_out, A);
  not not_2 (not_2_out, B);
  not not_3 (not_3_out, C);
  not not_4 (not_4_out, A);
  not not_5 (not_5_out, B);
  and and_1 (and_1_out, A, B);
  and and_2 (and_2_out, not_4_out, C);
  and and_3 (and_3_out, not_5_out, C);
  or or_1 (or_1_out, A, not_2_out, not_3_out);
  or or_2 (or_2_out, not_1_out, not_2_out, C);
  or or_3 (or_3_out, not_1_out, not_2_out, not_3_out);
  nor nor_1 (nor_1_out, and_1_out, and_2_out);
  or or_4 (F, nor_1_out, and_3_out);
  and and_4 (F_2, or_1_out, or_2_out, or_3_out);
  Comparator #(.width(1), .mode("twosComplement")) comparator_1 (.a(F), .b(F_2), .eq(comparator_1_eq));  // open: gt, lt
  not not_6 (not_6_out, comparator_1_eq);
  // Buzzer #(.freq_measure("Hz"), .vol_width(7)) buzzer_1: pin names not known; wires that end beside it: not_6_out
  LED #(.active("false")) led_1 (.in(comparator_1_eq));
endmodule

module \标准_或_与_表达式_2  (
  output F,
  output F_2
);

  wire A, and_1_out, and_2_out, B, button_1_out, buzzer_1_p1, C, clock_1_out, comparator_1_eq, not_1_out,
       not_2_out, not_3_out, not_4_out, not_5_out, not_6_out, or_1_out, or_2_out, or_3_out, or_4_out,
       or_5_out;

  Counter #(.width(3), .max('h7), .ongoal("wrap"), .trigger("rising"), .behavior("new")) counter_1 (
    .Q({A, B, C}), .clk(clock_1_out), .clr(button_1_out));  // open: load, D, count, carry, preset, down
  Clock #(.highDuration(1), .lowDuration(1)) clock_1 (.out(clock_1_out));
  Button button_1 (.out(button_1_out));
  // Probe on A
  // Probe on B
  // Probe on C
  // Probe on A
  // Probe on B
  // Probe on C
  not not_1 (not_1_out, A);
  not not_2 (not_2_out, B);
  not not_3 (not_3_out, C);
  not not_4 (not_4_out, A);
  not not_5 (not_5_out, B);
  not not_6 (not_6_out, C);
  and and_1 (and_1_out, not_4_out, C);
  and and_2 (and_2_out, A, not_5_out, not_6_out);
  or or_1 (or_1_out, A, B, C);
  or or_2 (or_2_out, A, not_2_out, C);
  or or_3 (or_3_out, not_1_out, B, not_3_out);
  or or_4 (or_4_out, not_1_out, not_2_out, C);
  or or_5 (or_5_out, not_1_out, not_2_out, not_3_out);
  or or_6 (F, and_1_out, and_2_out);
  and and_3 (F_2, or_1_out, or_2_out, or_3_out, or_4_out, or_5_out);
  Comparator #(.width(1), .mode("twosComplement")) comparator_1 (.a(F), .b(F_2), .eq(comparator_1_eq));  // open: gt, lt
  // Buzzer #(.freq_measure("Hz"), .vol_width(7)) buzzer_1: pin names not known; wires that end beside it: buzzer_1_p1
  not not_7 (buzzer_1_p1, comparator_1_eq);
  LED #(.active("false")) led_1 (.in(comparator_1_eq));
endmodule

module \代数化简法_1  (
  output F,
  output F_2
);

  wire A, and_1_out, and_2_out, and_3_out, and_4_out, and_5_out, and_6_out, and_7_out, and_8_out, and_9_out,
       and_10_out, B, button_1_out, buzzer_1_p2, C, clock_1_out, comparator_1_eq, D, E, not_1_out, not_2_out,
       not_3_out, not_4_out;

  Counter #(.width(5), .max('h1f), .ongoal("wrap"), .trigger("rising"), .behavior("new")) counter_1 (
    .Q({A, B, C, D, E}), .clk(clock_1_out), .clr(button_1_out));  // open: load, D, count, carry, preset, down
  Clock #(.highDuration(1), .lowDuration(1)) clock_1 (.out(clock_1_out));
  Button button_1 (.out(button_1_out));
  // Probe on A
  // Probe on B
  // Probe on C
  // Probe on D
  // Probe on E
  // Probe on A
  // Probe on B
  // Probe on C
  // Probe on D
  // Probe on E
  not not_1 (not_1_out, A);
  not not_2 (not_2_out, B);
  not not_3 (not_3_out, D);
  not not_4 (not_4_out, B);
  and and_1 (and_1_out, A, D);
  and and_2 (and_2_out, A, not_3_out);
  and and_3 (and_3_out, A, B);
  and and_4 (and_4_out, not_1_out, C);
  and and_5 (and_5_out, B, D);
  and and_6 (and_6_out, not_2_out, E);
  and and_7 (and_7_out, D, E);
  and and_8 (and_8_out, B, D);
  and and_9 (and_9_out, not_4_out, E);
  and and_10 (and_10_out, D, E);
  or or_1 (F, and_1_out, and_2_out, and_3_out, and_4_out, and_5_out, and_6_out, and_7_out);
  or or_2 (F_2, A, C, and_8_out, and_9_out, and_10_out);
  // Buzzer #(.freq_measure("Hz"), .vol_width(1)) buzzer_1: pin names not known; wires that end beside it: B, buzzer_1_p2
  not not_5 (buzzer_1_p2, comparator_1_eq);
  Comparator #(.width(1), .mode("twosComplement")) comparator_1 (.a(F), .b(F_2), .eq(comparator_1_eq));  // open: gt, lt
  LED #(.active("false")) led_1 (.in(comparator_1_eq));
endmodule

module \代数化简法_2  (
  output F,
  output F_2
);

  wire A, and_1_out, and_2_out, and_3_out, and_4_out, and_5_out, B, button_1_out, buzzer_1_p1, C,
       clock_1_out, comparator_1_eq, D, not_1_out, not_2_out, not_3_out, not_4_out, not_5_out, not_6_out,
       or_1_out;

  Counter #(.width(4), .max('hf), .ongoal("wrap"), .trigger("rising"), .behavior("new")) counter_1 (
    .Q({A, B, C, D}), .clk(clock_1_out), .clr(button_1_out));  // open: load, D, count, carry, preset, down
  Clock #(.highDuration(1), .lowDuration(1)) clock_1 (.out(clock_1_out));
  Button button_1 (.out(button_1_out));
  // Probe on A
  // Probe on B
  // Probe on C
  // Probe on D
  // Probe on A
  // Probe on B
  // Probe on C
  // Probe on D
  not not_1 (not_1_out, A);
  not not_2 (not_2_out, B);
  not not_3 (not_3_out, C);
  not not_4 (not_4_out, A);
  not not_5 (not_5_out, B);
  not not_6 (not_6_out, C);
  and and_1 (and_1_out, B, D);
  or or_1 (or_1_out, not_2_out, and_1_out);
  and and_2 (and_2_out, not_4_out, not_5_out, not_6_out);
  and and_3 (and_3_out, not_6_out, D);
  and and_4 (and_4_out, not_1_out, not_3_out, or_1_out);
  and and_5 (and_5_out, A, not_3_out, D);
  or or_2 (F, and_4_out, and_5_out);
  or or_3 (F_2, and_2_out, and_3_out);
  Comparator #(.width(1), .mode("twosComplement")) comparator_1 (.a(F), .b(F_2), .eq(comparator_1_eq));  // open: gt, lt
  // Buzzer #(.freq_measure("Hz"), .vol_width(1)) buzzer_1: pin names not known; wires that end beside it: buzzer_1_p1
  not not_7 (buzzer_1_p1, comparator_1_eq);
  LED #(.active("false")) led_1 (.in(comparator_1_eq));
endmodule

module \代数化简法_3  (
  output F,
  output F_2
);

  wire A, and_1_out, and_2_out, and_3_out, and_4_out, and_5_out, and_6_out, and_7_out, and_8_out, and_9_out,
       and_10_out, B, button_1_out, buzzer_1_p1, C, clock_1_out, comparator_1_eq, D, E, not_1_out, not_2_out,
       not_3_out, not_4_out, not_5_out, not_6_out;

  Counter #(.width(5), .max('h1f), .ongoal("wrap"), .trigger("rising"), .behavior("new")) counter_1 (
    .Q({A, B, C, D, E}), .clk(clock_1_out), .clr(button_1_out));  // open: load, D, count, carry, preset, down
  Clock #(.highDuration(1), .lowDuration(1)) clock_1 (.out(clock_1_out));
  Button button_1 (.out(button_1_out));
  // Probe on A
  // Probe on B
  // Probe on C
  // Probe on D
  // Probe on E
  // Probe on A
  // Probe on B
  // Probe on C
  // Probe on D
  // Probe on E
  not not_1 (not_1_out, B);
  not not_2 (not_2_out, C);
  not not_3 (not_3_out, D);
  not not_4 (not_4_out, B);
  not not_5 (not_5_out, C);
  not not_6 (not_6_out, D);
  and and_1 (and_1_out, A, B);
  and and_2 (and_2_out, A, not_2_out);
  and and_3 (and_3_out, not_1_out, C);
  and and_4 (and_4_out, B, not_2_out);
  and and_5 (and_5_out, not_1_out, D);
  and and_6 (and_6_out, B, not_3_out);
  and and_7 (and_7_out, A, D, E);
  and and_8 (and_8_out, C, not_6_out);
  and and_9 (and_9_out, not_4_out, D);
  and and_10 (and_10_out, B, not_5_out);
  or or_1 (F, and_1_out, and_2_out, and_3_out, and_4_out, and_5_out, and_6_out, and_7_out);
  or or_2 (F_2, A, and_8_out, and_9_out, and_10_out);
  // Buzzer #(.freq_measure("Hz"), .vol_width(1)) buzzer_1: pin names not known; wires that end beside it: buzzer_1_p1
  not not_7 (buzzer_1_p1, comparator_1_eq);
  Comparator #(.width(1), .mode("twosComplement")) comparator_1 (.a(F), .b(F_2), .eq(comparator_1_eq));  // open: gt, lt
  LED #(.active("false")) led_1 (.in(comparator_1_eq));
endmodule

module \代数化简法_4  (
  output F,
  output F_2
);

  wire A, B, button_1_out, buzzer_1_p1, C, clock_1_out, comparator_1_eq, D, not_1_out, or_1_out, or_2_out,
       or_3_out, or_4_out, or_5_out;

  Counter #(.width(4), .max('hf), .ongoal("wrap"), .trigger("rising"), .behavior("new")) counter_1 (
    .Q({A, B, C, D}), .clk(clock_1_out), .clr(button_1_out));  // open: load, D, count, carry, preset, down
  Clock #(.highDuration(1), .lowDuration(1)) clock_1 (.out(clock_1_out));
  Button button_1 (.out(button_1_out));
  // Probe on A
  // Probe on B
  // Probe on C
  // Probe on D
  // Probe on A
  // Probe on B
  // Probe on C
  // Probe on D
  not not_1 (not_1_out, B);
  or or_1 (or_1_out, A, B);
  or or_2 (or_2_out, A, not_1_out);
  or or_3 (or_3_out, B, C);
  or or_4 (or_4_out, B, C, D);
  or or_5 (or_5_out, B, C);
  and and_1 (F, or_1_out, or_2_out, or_3_out, or_4_out);
  and and_2 (F_2, A, or_5_out);
  Comparator #(.width(1), .mode("twosComplement")) comparator_1 (.a(F), .b(F_2), .eq(comparator_1_eq));  // open: gt, lt
  // Buzzer #(.freq_measure("Hz"), .vol_width(1)) buzzer_1: pin names not known; wires that end beside it: buzzer_1_p1
  not not_2 (buzzer_1_p1, comparator_1_eq);
  LED #(.active("false")) led_1 (.in(comparator_1_eq));
endmodule

module \代数化简法_5  (
  output F,
  output F_2
);

  wire A, B, button_1_out, buzzer_1_p1, C, clock_1_out, comparator_1_eq, not_1_out, not_2_out, not_3_out,
       not_4_out, or_1_out, or_2_out, or_3_out, or_4_out, or_5_out, or_6_out;

  Counter #(.width(3), .max('h7), .ongoal("wrap"), .trigger("rising"), .behavior("new")) counter_1 (
    .Q({A, B, C}), .clk(clock_1_out), .clr(button_1_out));  // open: load, D, count, carry, preset, down
  Clock #(.highDuration(1), .lowDuration(1)) clock_1 (.out(clock_1_out));
  Button button_1 (.out(button_1_out));
  // Probe on A
  // Probe on B
  // Probe on C
  // Probe on A
  // Probe on B
  // Probe on C
  not not_1 (not_1_out, A);
  not not_2 (not_2_out, B);
  not not_3 (not_3_out, A);
  not not_4 (not_4_out, B);
  or or_1 (or_1_out, A, not_2_out);
  or or_2 (or_2_out, not_1_out, B);
  or or_3 (or_3_out, B, C);
  or or_4 (or_4_out, not_1_out, C);
  or or_5 (or_5_out, A, not_4_out);
  or or_6 (or_6_out, not_3_out, B);
  and and_1 (F, or_1_out, or_2_out, or_3_out, or_4_out);
  and and_2 (F_2, or_5_out, or_6_out, C);
  Comparator #(.width(1), .mode("twosComplement")) comparator_1 (.a(F), .b(F_2), .eq(comparator_1_eq));  // open: gt, lt
  // Buzzer #(.freq_measure("Hz"), .vol_width(7)) buzzer_1: pin names not known; wires that end beside it: buzzer_1_p1
  not not_5 (buzzer_1_p1, comparator_1_eq);
  LED #(.active("false")) led_1 (.in(comparator_1_eq));
endmodule

module \卡诺图化简法_1  (
  output F,
  output F_2
);

  wire A, and_1_out, and_2_out, and_3_out, and_4_out, and_5_out, and_6_out, and_7_out, and_8_out, and_9_out,
       and_10_out, and_11_out, and_12_out, and_13_out, and_14_out, B, button_1_out, buzzer_1_p1, C,
       clock_1_out, comparator_1_eq, D, not_1_out, not_2_out, not_3_out, not_4_out, not_5_out, not_6_out,
       not_7_out, not_8_out;

  Counter #(.width(4), .max('hf), .ongoal("wrap"), .trigger("rising"), .behavior("new")) counter_1 (
    .Q({A, B, C, D}), .clk(clock_1_out), .clr(button_1_out));  // open: load, D, count, carry, preset, down
  Clock #(.highDuration(1), .lowDuration(1)) clock_1 (.out(clock_1_out));
  Button button_1 (.out(button_1_out));
  // Probe on A
  // Probe on B
  // Probe on C
  // Probe on D
  // Probe on A
  // Probe on B
  // Probe on C
  // Probe on D
  not not_1 (not_1_out, A);
  not not_2 (not_2_out, B);
  not not_3 (not_3_out, C);
  not not_4 (not_4_out, D);
  not not_5 (not_5_out, A);
  not not_6 (not_6_out, B);
  not not_7 (not_7_out, C);
  not not_8 (not_8_out, D);
  and and_1 (and_1_out, not_1_out, not_2_out, not_3_out, not_4_out);
  and and_2 (and_2_out, not_1_out, not_2_out, C, D);
  and and_3 (and_3_out, not_1_out, B, not_3_out, D);
  and and_4 (and_4_out, not_1_out, B, C, not_4_out);
  and and_5 (and_5_out, not_1_out, B, C, D);
  and and_6 (and_6_out, A, not_2_out, C, not_4_out);
  and and_7 (and_7_out, A, not_2_out, C, D);
  and and_8 (and_8_out, A, B, not_3_out, D);
  and and_9 (and_9_out, A, B, C, D);
  and and_10 (and_10_out, not_5_out, not_6_out, not_7_out, not_8_out);
  and and_11 (and_11_out, not_5_out, B, C);
  and and_12 (and_12_out, A, not_6_out, C);
  and and_13 (and_13_out, B, D);
  and and_14 (and_14_out, C, D);
  or or_1 (F, and_1_out, and_2_out, and_3_out, and_4_out, and_5_out, and_6_out, and_7_out, and_8_out, and_9_out);
  or or_2 (F_2, and_10_out, and_11_out, and_12_out, and_13_out, and_14_out);
  Comparator #(.width(1), .mode("twosComplement")) comparator_1 (.a(F), .b(F_2), .eq(comparator_1_eq));  // open: gt, lt
  // Buzzer #(.freq_measure("Hz"), .vol_width(1)) buzzer_1: pin names not known; wires that end beside it: buzzer_1_p1
  not not_9 (buzzer_1_p1, comparator_1_eq);
  LED #(.active("false")) led_1 (.in(comparator_1_eq));
endmodule

module \卡诺图化简法_2  (
  output F,
  output F_2,
  output F_3
);

  wire A, and_1_out, and_2_out, and_3_out, and_4_out, and_5_out, and_6_out, and_7_out, and_8_out, and_9_out,
       and_10_out, and_11_out, B, button_1_out, buzzer_1_p1, buzzer_2_p2, C, clock_1_out, comparator_1_eq,
       comparator_2_eq, D, not_1_out, not_2_out, not_3_out, not_4_out, not_5_out, not_6_out, not_7_out,
       not_8_out, not_9_out, not_10_out, not_11_out, not_12_out;

  Counter #(.width(4), .max('hf), .ongoal("wrap"), .trigger("rising"), .behavior("new")) counter_1 (
    .Q({A, B, C, D}), .clk(clock_1_out), .clr(button_1_out));  // open: load, D, count, carry, preset, down
  Clock #(.highDuration(1), .lowDuration(1)) clock_1 (.out(clock_1_out));
  Button button_1 (.out(button_1_out));
  // Probe on A
  // Probe on B
  // Probe on C
  // Probe on D
  // Probe on A
  // Probe on B
  // Probe on C
  // Probe on D
  // Probe on A
  // Probe on B
  // Probe on C
  // Probe on D
  not not_1 (not_1_out, A);
  not not_2 (not_2_out, B);
  not not_3 (not_3_out, C);
  not not_4 (not_4_out, D);
  not not_5 (not_5_out, A);
  not not_6 (not_6_out, B);
  not not_7 (not_7_out, C);
  not not_8 (not_8_out, D);
  not not_9 (not_9_out, A);
  not not_10 (not_10_out, B);
  not not_11 (not_11_out, C);
  not not_12 (not_12_out, D);
  and and_1 (and_1_out, not_1_out, C, D);
  and and_2 (and_2_out, not_2_out, C, not_4_out);
  and and_3 (and_3_out, not_1_out, B, C, not_4_out);
  and and_4 (and_4_out, A, not_2_out, not_4_out);
  and and_5 (and_5_out, A, B, not_3_out, not_4_out);
  and and_6 (and_6_out, not_5_out, C);
  and and_7 (and_7_out, A, not_7_out, not_8_out);
  and and_8 (and_8_out, A, not_6_out, not_8_out);
  and and_9 (and_9_out, not_9_out, C);
  and and_10 (and_10_out, A, not_11_out, not_12_out);
  and and_11 (and_11_out, not_10_out, C, not_12_out);
  or or_1 (F, and_1_out, and_2_out, and_3_out, and_4_out, and_5_out);
  or or_2 (F_2, and_6_out, and_7_out, and_8_out);
  or or_3 (F_3, and_9_out, and_10_out, and_11_out);
  Comparator #(.width(1), .mode("twosComplement")) comparator_1 (.a(F), .b(F_2), .eq(comparator_1_eq));  // open: gt, lt
  Comparator #(.width(1), .mode("twosComplement")) comparator_2 (.a(F), .b(F_3), .eq(comparator_2_eq));  // open: gt, lt
  // Buzzer #(.freq_measure("Hz"), .vol_width(1)) buzzer_1: pin names not known; wires that end beside it: buzzer_1_p1
  not not_13 (buzzer_1_p1, comparator_1_eq);
  LED #(.active("false")) led_1 (.in(comparator_1_eq));
  // Buzzer #(.freq_measure("Hz"), .vol_width(1)) buzzer_2: pin names not known; wires that end beside it: F_3, buzzer_2_p2
  not not_14 (buzzer_2_p2, comparator_2_eq);
  LED #(.active("false")) led_2 (.in(comparator_2_eq));
endmodule

module \卡诺图化简法_3  (
  output F,
  output F_2
);

  wire A, and_1_out, and_2_out, and_3_out, and_4_out, B, button_1_out, buzzer_1_p1, C, clock_1_out,
       comparator_1_eq, D, not_1_out, not_2_out, not_3_out, not_4_out, or_1_out, or_2_out;

  Counter #(.width(4), .max('hf), .ongoal("wrap"), .trigger("rising"), .behavior("new")) counter_1 (
    .Q({A, B, C, D}), .clk(clock_1_out), .clr(button_1_out));  // open: load, D, count, carry, preset, down
  Clock #(.highDuration(1), .lowDuration(1)) clock_1 (.out(clock_1_out));
  Button button_1 (.out(button_1_out));
  // Probe on A
  // Probe on B
  // Probe on C
  // Probe on D
  // Probe on A
  // Probe on B
  // Probe on C
  // Probe on D
  not not_1 (not_1_out, B);
  not not_2 (not_2_out, C);
  not not_3 (not_3_out, B);
  not not_4 (not_4_out, C);
  and and_1 (and_1_out, A, not_2_out);
  and and_2 (and_2_out, A, D);
  and and_3 (and_3_out, not_1_out, not_2_out);
  and and_4 (and_4_out, not_1_out, D);
  or or_1 (or_1_out, A, not_3_out);
  or or_2 (or_2_out, not_4_out, D);
  or or_3 (F, and_1_out, and_2_out, and_3_out, and_4_out);
  and and_5 (F_2, or_1_out, or_2_out);
  Comparator #(.width(1), .mode("twosComplement")) comparator_1 (.a(F), .b(F_2), .eq(comparator_1_eq));  // open: gt, lt
  // Buzzer #(.freq_measure("Hz"), .vol_width(1)) buzzer_1: pin names not known; wires that end beside it: buzzer_1_p1
  not not_5 (buzzer_1_p1, comparator_1_eq);
  LED #(.active("false")) led_1 (.in(comparator_1_eq));
endmodule

module \卡诺图化简法_4  (
  output F,
  output F_2
);

  wire A, B, button_1_out, buzzer_1_p1, C, clock_1_out, comparator_1_eq, D, not_1_out, not_2_out, not_3_out,
       or_1_out, or_2_out, or_3_out, or_4_out;

  Counter #(.width(4), .max('hf), .ongoal("wrap"), .trigger("rising"), .behavior("new")) counter_1 (
    .Q({A, B, C, D}), .clk(clock_1_out), .clr(button_1_out));  // open: load, D, count, carry, preset, down
  Clock #(.highDuration(1), .lowDuration(1)) clock_1 (.out(clock_1_out));
  Button button_1 (.out(button_1_out));
  // Probe on A
  // Probe on B
  // Probe on C
  // Probe on D
  // Probe on A
  // Probe on B
  // Probe on C
  // Probe on D
  not not_1 (not_1_out, A);
  not not_2 (not_2_out, D);
  not not_3 (not_3_out, A);
  or or_1 (or_1_out, not_3_out, D);
  and and_1 (F_2, or_1_out, B);
  or or_2 (or_2_out, not_1_out, D);
  or or_3 (or_3_out, B, not_2_out);
  or or_4 (or_4_out, A, B);
  and and_2 (F, or_2_out, or_3_out, or_4_out);
  Comparator #(.width(1), .mode("twosComplement")) comparator_1 (.a(F), .b(F_2), .eq(comparator_1_eq));  // open: gt, lt
  // Buzzer #(.freq_measure("Hz"), .vol_width(1)) buzzer_1: pin names not known; wires that end beside it: buzzer_1_p1
  not not_4 (buzzer_1_p1, comparator_1_eq);
  LED #(.active("false")) led_1 (.in(comparator_1_eq));
endmodule

module \卡诺图化简法_5  (
  output F,
  output F_2
);

  wire A, B, button_1_out, buzzer_1_p1, C, clock_1_out, comparator_1_eq, D, not_1_out, not_2_out, not_3_out,
       not_4_out, not_5_out, not_6_out, not_7_out, not_8_out, or_1_out, or_2_out, or_3_out, or_4_out,
       or_5_out, or_6_out, or_7_out, or_8_out, or_9_out, or_10_out, or_11_out, or_12_out;

  Counter #(.width(4), .max('hf), .ongoal("wrap"), .trigger("rising"), .behavior("new")) counter_1 (
    .Q({A, B, C, D}), .clk(clock_1_out), .clr(button_1_out));  // open: load, D, count, carry, preset, down
  Clock #(.highDuration(1), .lowDuration(1)) clock_1 (.out(clock_1_out));
  Button button_1 (.out(button_1_out));
  // Probe on A
  // Probe on B
  // Probe on C
  // Probe on D
  // Probe on A
  // Probe on B
  // Probe on C
  // Probe on D
  not not_1 (not_1_out, A);
  not not_2 (not_2_out, B);
  not not_3 (not_3_out, C);
  not not_4 (not_4_out, D);
  not not_5 (not_5_out, A);
  not not_6 (not_6_out, B);
  not not_7 (not_7_out, C);
  not not_8 (not_8_out, D);
  or or_1 (or_1_out, A, B, not_3_out, not_4_out);
  or or_2 (or_2_out, A, not_2_out, C, D);
  or or_3 (or_3_out, A, not_2_out, not_3_out, D);
  or or_4 (or_4_out, A, not_2_out, not_3_out, not_4_out);
  or or_5 (or_5_out, not_1_out, B, not_3_out, not_4_out);
  or or_6 (or_6_out, not_1_out, not_2_out, C, D);
  or or_7 (or_7_out, not_1_out, not_2_out, C, not_4_out);
  or or_8 (or_8_out, not_1_out, not_2_out, not_3_out, D);
  or or_9 (or_9_out, not_1_out, not_2_out, not_3_out, not_4_out);
  or or_10 (or_10_out, not_5_out, not_6_out);
  or or_11 (or_11_out, not_7_out, not_8_out);
  or or_12 (or_12_out, not_6_out, D);
  and and_1 (F, or_1_out, or_2_out, or_3_out, or_4_out, or_5_out, or_6_out, or_7_out, or_8_out, or_9_out);
  and and_2 (F_2, or_10_out, or_11_out, or_12_out);
  Comparator #(.width(1), .mode("twosComplement")) comparator_1 (.a(F), .b(F_2), .eq(comparator_1_eq));  // open: gt, lt
  // Buzzer #(.freq_measure("Hz"), .vol_width(1)) buzzer_1: pin names not known; wires that end beside it: buzzer_1_p1
  not not_9 (buzzer_1_p1, comparator_1_eq);
  LED #(.active("false")) led_1 (.in(comparator_1_eq));
endmodule

module \列表化简法_1  (
  output F,
  output F_2
);

  wire A, and_1_out, and_2_out, and_3_out, and_4_out, and_5_out, and_6_out, and_7_out, and_8_out, and_9_out,
       and_10_out, and_11_out, and_12_out, and_13_out, B, button_1_out, buzzer_1_p1, C, clock_1_out,
       comparator_1_eq, D, not_1_out, not_2_out, not_3_out, not_4_out, not_5_out, not_6_out, not_7_out,
       not_8_out;

  Counter #(.width(4), .max('hf), .ongoal("wrap"), .trigger("rising"), .behavior("new")) counter_1 (
    .Q({A, B, C, D}), .clk(clock_1_out), .clr(button_1_out));  // open: load, D, count, carry, preset, down
  Clock #(.highDuration(1), .lowDuration(1)) clock_1 (.out(clock_1_out));
  Button button_1 (.out(button_1_out));
  // Probe on A
  // Probe on B
  // Probe on C
  // Probe on D
  // Probe on A
  // Probe on B
  // Probe on C
  // Probe on D
  not not_1 (not_1_out, A);
  not not_2 (not_2_out, B);
  not not_3 (not_3_out, C);
  not not_4 (not_4_out, D);
  not not_5 (not_5_out, A);
  not not_6 (not_6_out, B);
  not not_7 (not_7_out, C);
  not not_8 (not_8_out, D);
  and and_1 (and_1_out, not_1_out, not_2_out, not_3_out, not_4_out);
  and and_2 (and_2_out, not_1_out, B, not_3_out, D);
  and and_3 (and_3_out, not_1_out, B, C, D);
  and and_4 (and_4_out, A, not_2_out, not_3_out, not_4_out);
  and and_5 (and_5_out, A, not_2_out, not_3_out, D);
  and and_6 (and_6_out, A, not_2_out, C, not_4_out);
  and and_7 (and_7_out, A, not_2_out, C, D);
  and and_8 (and_8_out, A, B, C, not_4_out);
  and and_9 (and_9_out, A, B, C, D);
  and and_10 (and_10_out, A, C);
  and and_11 (and_11_out, A, not_6_out);
  and and_12 (and_12_out, not_5_out, B, D);
  and and_13 (and_13_out, not_6_out, not_7_out, not_8_out);
  or or_1 (F, and_1_out, and_2_out, and_3_out, and_4_out, and_5_out, and_6_out, and_7_out, and_8_out, and_9_out);
  or or_2 (F_2, and_10_out, and_11_out, and_12_out, and_13_out);
  Comparator #(.width(1), .mode("twosComplement")) comparator_1 (.a(F), .b(F_2), .eq(comparator_1_eq));  // open: gt, lt
  // Buzzer #(.freq_measure("Hz"), .vol_width(1)) buzzer_1: pin names not known; wires that end beside it: buzzer_1_p1
  not not_9 (buzzer_1_p1, comparator_1_eq);
  LED #(.active("false")) led_1 (.in(comparator_1_eq));
endmodule

module \列表化简法_2  (
  output F,
  output F_2,
  output F_3
);

  wire A, and_1_out, and_2_out, and_3_out, and_4_out, and_5_out, and_6_out, and_7_out, and_8_out, and_9_out,
       and_10_out, and_11_out, and_12_out, and_13_out, and_14_out, and_15_out, and_16_out, and_17_out, B,
       button_1_out, buzzer_1_p1, buzzer_2_p1, C, clock_1_out, comparator_1_eq, comparator_2_eq, D,
       not_1_out, not_2_out, not_3_out, not_4_out, not_5_out, not_6_out, not_7_out, not_8_out, not_9_out,
       not_10_out, not_11_out, not_12_out;

  Counter #(.width(4), .max('hf), .ongoal("wrap"), .trigger("rising"), .behavior("new")) counter_1 (
    .Q({A, B, C, D}), .clk(clock_1_out), .clr(button_1_out));  // open: load, D, count, carry, preset, down
  Clock #(.highDuration(1), .lowDuration(1)) clock_1 (.out(clock_1_out));
  Button button_1 (.out(button_1_out));
  // Probe on A
  // Probe on B
  // Probe on C
  // Probe on D
  // Probe on A
  // Probe on B
  // Probe on C
  // Probe on D
  // Probe on A
  // Probe on B
  // Probe on C
  // Probe on D
  not not_1 (not_1_out, A);
  not not_2 (not_2_out, B);
  not not_3 (not_3_out, C);
  not not_4 (not_4_out, D);
  not not_5 (not_5_out, A);
  not not_6 (not_6_out, B);
  not not_7 (not_7_out, C);
  not not_8 (not_8_out, D);
  not not_9 (not_9_out, A);
  not not_10 (not_10_out, B);
  not not_11 (not_11_out, C);
  not not_12 (not_12_out, D);
  and and_1 (and_1_out, not_1_out, not_2_out, not_3_out, not_4_out);
  and and_2 (and_2_out, not_1_out, not_2_out, C, D);
  and and_3 (and_3_out, not_1_out, B, not_3_out, not_4_out);
  and and_4 (and_4_out, not_1_out, B, not_3_out, D);
  and and_5 (and_5_out, not_1_out, B, C, not_4_out);
  and and_6 (and_6_out, not_1_out, B, C, D);
  and and_7 (and_7_out, A, not_2_out, not_3_out, not_4_out);
  and and_8 (and_8_out, A, not_2_out, C, not_4_out);
  and and_9 (and_9_out, A, not_2_out, C, D);
  and and_10 (and_10_out, not_5_out, B);
  and and_11 (and_11_out, A, not_6_out, C);
  and and_12 (and_12_out, not_6_out, C, D);
  and and_13 (and_13_out, not_6_out, not_7_out, not_8_out);
  and and_14 (and_14_out, not_9_out, B);
  and and_15 (and_15_out, A, not_10_out, not_12_out);
  and and_16 (and_16_out, not_10_out, C, D);
  and and_17 (and_17_out, not_10_out, not_11_out, not_12_out);
  or or_1 (F, and_1_out, and_2_out, and_3_out, and_4_out, and_5_out, and_6_out, and_7_out, and_8_out, and_9_out);
  or or_2 (F_2, and_10_out, and_11_out, and_12_out, and_13_out);
  or or_3 (F_3, and_14_out, and_15_out, and_16_out, and_17_out);
  Comparator #(.width(1), .mode("twosComplement")) comparator_1 (.a(F), .b(F_2), .eq(comparator_1_eq));  // open: gt, lt
  // Buzzer #(.freq_measure("Hz"), .vol_width(1)) buzzer_1: pin names not known; wires that end beside it: buzzer_1_p1
  not not_13 (buzzer_1_p1, comparator_2_eq);
  Comparator #(.width(1), .mode("twosComplement")) comparator_2 (.a(F), .b(F_3), .eq(comparator_2_eq));  // open: gt, lt
  // Buzzer #(.freq_measure("Hz"), .vol_width(1)) buzzer_2: pin names not known; wires that end beside it: buzzer_2_p1
  not not_14 (buzzer_2_p1, comparator_1_eq);
  LED #(.active("false")) led_1 (.in(comparator_1_eq));
  LED #(.active("false")) led_2 (.in(comparator_2_eq));
endmodule
