// Logisim project Logisim自带的各种触发器.circ as structural Verilog: 4 circuits, main circuit Logisim自带的D触发器
module \Logisim自带的D触发器  (
  input  RD,
  input  D,
  input  SD,
  output Q,
  output nQ
);

  wire CP_out;

  Clock #(.highDuration(1), .lowDuration(1)) CP (.out(CP_out));
  D_Flip_Flop #(.trigger("rising"), .Pre_Clr_Positions("BELOW_ABOVE"), .NegatePresetClear("true"), .enable("false"), .NewFFLayout("true")) d_ff_1 (
    .clk(CP_out), .D(D), .Q(Q), .Qn(nQ), .preset(SD), .reset(RD));

  // Notes on the sheet:
  //   Logisim自带的D触发器
endmodule

module \Logisim自带的T触发器  (
  input  RD,
  input  T,
  input  SD,
  output Q,
  output nQ
);

  wire CP_out;

  Clock #(.highDuration(1), .lowDuration(1)) CP (.out(CP_out));
  T_Flip_Flop #(.trigger("rising"), .Pre_Clr_Positions("BELOW_ABOVE"), .NegatePresetClear("true"), .enable("false"), .NewFFLayout("true")) t_ff_1 (
    .clk(CP_out), .T(T), .Q(Q), .Qn(nQ), .preset(SD), .reset(RD));

  // Notes on the sheet:
  //   Logisim自带的T触发器
endmodule

module \Logisim自带的J_K触发器  (
  input  RD,
  input  J,
  input  K,
  input  SD,
  output Q,
  output nQ
);

  wire CP_out;

  Clock #(.highDuration(1), .lowDuration(1)) CP (.out(CP_out));
  J_K_Flip_Flop #(.trigger("falling"), .Pre_Clr_Positions("BELOW_ABOVE"), .NegatePresetClear("true"), .enable("false"), .NewFFLayout("true")) j_k_ff_1 (
    .J(J), .clk(CP_out), .K(K), .Q(Q), .Qn(nQ), .preset(SD), .reset(RD));

  // Notes on the sheet:
  //   Logisim自带的J-K触发器
endmodule

module \Logisim自带的S_R触发器  (
  input  RD,
  input  S,
  input  R,
  input  SD,
  output Q,
  output nQ
);

  wire CP_out;

  Clock #(.highDuration(1), .lowDuration(1)) CP (.out(CP_out));
  S_R_Flip_Flop #(.trigger("falling"), .Pre_Clr_Positions("BELOW_ABOVE"), .NegatePresetClear("true"), .enable("false"), .NewFFLayout("true")) s_r_ff_1 (
    .S(S), .clk(CP_out), .R(R), .Q(Q), .Qn(nQ), .preset(SD), .reset(RD));

  // Notes on the sheet:
  //   Logisim自带的S-R触发器
endmodule
