// Logisim project 习题3.13的仿真结果.circ as structural Verilog: 2 circuits, main circuit 教材图3.54钟控D触发器的仿真结果
module \习题3_13D触发器的仿真结果  (
  output Q,
  output nQ
);

  wire CLK, CP, D, nand_2_out, nand_4_out, not_1_out;
  wire [0:0] \计数器_q ;

  // Digital_Oscilloscope #(.nState(35), .frontlines("rising"), .showclock("false")) digital_oscilloscope_1: pin names not known; wires that end beside it: CLK, CP, D, Q
  Clock #(.highDuration(1), .lowDuration(1)) clock_1 (.out(CLK));
  Counter #(.width(2), .max('h3), .ongoal("wrap"), .trigger("rising"), .behavior("new")) \u_计数器  (
    .Q({CP, \计数器_q [0]}), .clk(CLK));  // open: load, D, count, carry, clr, preset, down
  // ProgrammableGenerator #(.nState(3), .Contents("8 4 4 8 8 50")) 函数发生器: pin names not known; wires that end beside it: D
  nand nand_1 (Q, nand_2_out, nQ);
  nand nand_2 (nand_2_out, D, CP);
  nand nand_3 (nQ, Q, nand_4_out);
  nand nand_4 (nand_4_out, not_1_out, CP);
  not not_1 (not_1_out, D);
endmodule

module \教材图3_54钟控D触发器的仿真结果  (
  output nQ,
  output Q
);

  wire CLK, CP, D, nand_2_out, nand_4_out;
  wire [0:0] \计数器_q ;

  // Digital_Oscilloscope #(.nState(35), .frontlines("rising"), .showclock("false")) digital_oscilloscope_1: pin names not known; wires that end beside it: CLK, CP, D, Q
  Clock #(.highDuration(1), .lowDuration(1)) clock_1 (.out(CLK));
  // ProgrammableGenerator #(.nState(3), .Contents("8 4 4 8 8 50")) programmablegenerator_1: pin names not known; wires that end beside it: D
  Counter #(.width(2), .max('h3), .ongoal("wrap"), .trigger("rising"), .behavior("new")) \u_计数器  (
    .Q({CP, \计数器_q [0]}), .clk(CLK));  // open: load, D, count, carry, clr, preset, down
  nand nand_1 (nQ, nand_2_out, Q);
  nand nand_2 (nand_2_out, CP, nand_4_out);
  nand nand_3 (Q, nQ, nand_4_out);
  nand nand_4 (nand_4_out, CP, D);
endmodule
