// Logisim project 在Logisim上实现各种触发器.circ as structural Verilog: 10 circuits, main circuit 与非门构成的基本R-S触发器
module \与非门构成的基本R_S触发器  (
  input  R,
  input  S,
  output nQ,
  output Q
);

  nand nand_1 (nQ, R, Q);
  nand nand_2 (Q, nQ, S);

  // Notes on the sheet:
  //   与非门构成的基本R-S触发器
endmodule

module \或非门构成的基本R_S触发器  (
  input  S,
  input  R,
  output nQ,
  output Q
);

  nor nor_1 (nQ, S, Q);
  nor nor_2 (Q, nQ, R);

  // Notes on the sheet:
  //   或非门构成的基本R-S触发器
endmodule

module \钟控R_S触发器  (
  input  R,
  input  S,
  output nQ,
  output Q
);

  wire CP_out, nand_2_out, nand_4_out;

  nand nand_1 (nQ, nand_2_out, Q);
  nand nand_2 (nand_2_out, R, CP_out);
  Clock #(.highDuration(1), .lowDuration(1)) CP (.out(CP_out));
  nand nand_3 (Q, nQ, nand_4_out);
  nand nand_4 (nand_4_out, CP_out, S);

  // Notes on the sheet:
  //   钟控R-S触发器
endmodule

module \钟控D触发器  (
  input  D,
  output nQ,
  output Q
);

  wire CP_out, nand_2_out, nand_4_out;

  nand nand_1 (nQ, nand_2_out, Q);
  nand nand_2 (nand_2_out, CP_out, nand_4_out);
  Clock #(.highDuration(1), .lowDuration(1)) CP (.out(CP_out));
  nand nand_3 (Q, nQ, nand_4_out);
  nand nand_4 (nand_4_out, CP_out, D);

  // Notes on the sheet:
  //   钟控D触发器
endmodule

module \钟控J_K触发器  (
  input  K,
  input  J,
  output nQ,
  output Q
);

  wire CP, nand_1_out, nand_2_out, nand_4_out, \延时_1_y , \延时_2_y , \延时_3_y , \延时_4_y ;

  nand nand_1 (nand_1_out, nand_2_out, \延时_2_y );
  \延时  \u_延时_1  (.x(Q), .y(\延时_1_y ));
  not not_1 (nQ, Q);
  \延时  \u_延时_2  (.x(Q), .y(\延时_2_y ));
  \延时  \u_延时_3  (.x(nand_1_out), .y(\延时_3_y ));
  nand nand_2 (nand_2_out, \延时_1_y , K, CP);
  Clock #(.highDuration(1), .lowDuration(1)) u_CP (.out(CP));
  nand nand_3 (Q, \延时_3_y , nand_4_out);
  \延时  \u_延时_4  (.x(nand_1_out), .y(\延时_4_y ));
  nand nand_4 (nand_4_out, CP, J, \延时_4_y );

  // Notes on the sheet:
  //   钟控J-K触发器
endmodule

module \钟控T触发器  (
  input  T,
  output nQ,
  output Q
);

  wire CP_out, nand_2_out, nand_3_out, nand_4_out, \延时_1_y , \延时_2_y , \延时_3_y , \延时_4_y ;

  nand nand_1 (nQ, nand_2_out, \延时_3_y );
  \延时  \u_延时_1  (.x(nand_3_out), .y(\延时_1_y ));
  not not_1 (Q, nQ);
  \延时  \u_延时_2  (.x(nQ), .y(\延时_2_y ));
  \延时  \u_延时_3  (.x(nand_3_out), .y(\延时_3_y ));
  nand nand_2 (nand_2_out, \延时_1_y , T, CP_out);
  Clock #(.highDuration(1), .lowDuration(1)) CP (.out(CP_out));
  nand nand_3 (nand_3_out, \延时_2_y , nand_4_out);
  nand nand_4 (nand_4_out, CP_out, T, \延时_4_y );
  \延时  \u_延时_4  (.x(nQ), .y(\延时_4_y ));

  // Notes on the sheet:
  //   钟控T触发器
endmodule

module \主从R_S触发器  (
  input  RD,
  input  SD,
  input  RD_2,
  input  SD_2,
  input  RD_3,
  input  SD_3,
  input  RD_4,
  input  SD_4,
  input  RD_5,
  input  SD_5,
  input  RD_6,
  input  SD_6,
  input  R,
  input  S,
  input  R_2,
  input  S_2,
  input  R_3,
  input  S_3,
  input  R_4,
  input  S_4,
  input  R_5,
  input  S_5,
  input  R_6,
  input  S_6,
  output nQ,
  output Q,
  output nQ_2,
  output Q_2,
  output nQ_3,
  output Q_3,
  output nQ_4,
  output Q_4,
  output nQ_5,
  output Q_5,
  output nQ_6,
  output Q_6
);

  wire CP_2_out, CP_3_out, CP_4_out, CP_5_out, CP_6_out, CP_out, nand_2_out, nand_3_out, nand_4_out,
       nand_6_out, nand_7_out, nand_8_out, nand_10_out, nand_11_out, nand_12_out, nand_14_out, nand_15_out,
       nand_16_out, nand_18_out, nand_19_out, nand_20_out, nand_22_out, nand_23_out, nand_24_out,
       nand_26_out, nand_27_out, nand_28_out, nand_30_out, nand_31_out, nand_32_out, nand_34_out,
       nand_35_out, nand_36_out, nand_38_out, nand_39_out, nand_40_out, nand_42_out, nand_43_out,
       nand_44_out, nand_46_out, nand_47_out, nand_48_out, not_1_out, not_2_out, not_3_out, not_4_out,
       not_5_out, not_6_out;

  not not_1 (not_1_out, CP_out);
  nand nand_1 (nQ, RD, nand_2_out, Q);
  nand nand_2 (nand_2_out, nand_3_out, not_1_out);
  nand nand_3 (nand_3_out, RD, nand_4_out, nand_7_out);
  nand nand_4 (nand_4_out, R, CP_out);
  Clock #(.highDuration(1), .lowDuration(1)) CP (.out(CP_out));
  nand nand_5 (Q, nQ, nand_6_out, SD);
  nand nand_6 (nand_6_out, not_1_out, nand_7_out);
  nand nand_7 (nand_7_out, nand_3_out, nand_8_out, SD);
  nand nand_8 (nand_8_out, CP_out, S);
  not not_2 (not_2_out, CP_2_out);
  nand nand_9 (nQ_2, RD_2, nand_10_out, Q_2);
  nand nand_10 (nand_10_out, nand_11_out, not_2_out);
  nand nand_11 (nand_11_out, RD_2, nand_12_out, nand_15_out);
  nand nand_12 (nand_12_out, R_2, CP_2_out);
  nand nand_13 (Q_2, nQ_2, nand_14_out, SD_2);
  nand nand_14 (nand_14_out, not_2_out, nand_15_out);
  nand nand_15 (nand_15_out, nand_11_out, nand_16_out, SD_2);
  nand nand_16 (nand_16_out, CP_2_out, S_2);
  Clock #(.highDuration(1), .lowDuration(1)) CP_2 (.out(CP_2_out));
  not not_3 (not_3_out, CP_3_out);
  nand nand_17 (nQ_3, RD_3, nand_18_out, Q_3);
  nand nand_18 (nand_18_out, nand_19_out, not_3_out);
  nand nand_19 (nand_19_out, RD_3, nand_20_out, nand_23_out);
  nand nand_20 (nand_20_out, R_3, CP_3_out);
  Clock #(.highDuration(1), .lowDuration(1)) CP_3 (.out(CP_3_out));
  nand nand_21 (Q_3, nQ_3, nand_22_out, SD_3);
  nand nand_22 (nand_22_out, not_3_out, nand_23_out);
  nand nand_23 (nand_23_out, nand_19_out, nand_24_out, SD_3);
  nand nand_24 (nand_24_out, CP_3_out, S_3);
  not not_4 (not_4_out, CP_4_out);
  nand nand_25 (nQ_4, RD_4, nand_26_out, Q_4);
  nand nand_26 (nand_26_out, nand_27_out, not_4_out);
  nand nand_27 (nand_27_out, RD_4, nand_28_out, nand_31_out);
  nand nand_28 (nand_28_out, R_4, CP_4_out);
  nand nand_29 (Q_4, nQ_4, nand_30_out, SD_4);
  nand nand_30 (nand_30_out, not_4_out, nand_31_out);
  nand nand_31 (nand_31_out, nand_27_out, nand_32_out, SD_4);
  nand nand_32 (nand_32_out, CP_4_out, S_4);
  Clock #(.highDuration(1), .lowDuration(1)) CP_4 (.out(CP_4_out));
  not not_5 (not_5_out, CP_5_out);
  nand nand_33 (nQ_5, RD_5, nand_34_out, Q_5);
  nand nand_34 (nand_34_out, nand_35_out, not_5_out);
  nand nand_35 (nand_35_out, RD_5, nand_36_out, nand_39_out);
  nand nand_36 (nand_36_out, R_5, CP_5_out);
  Clock #(.highDuration(1), .lowDuration(1)) CP_5 (.out(CP_5_out));
  nand nand_37 (Q_5, nQ_5, nand_38_out, SD_5);
  nand nand_38 (nand_38_out, not_5_out, nand_39_out);
  nand nand_39 (nand_39_out, nand_35_out, nand_40_out, SD_5);
  nand nand_40 (nand_40_out, CP_5_out, S_5);
  not not_6 (not_6_out, CP_6_out);
  nand nand_41 (nQ_6, RD_6, nand_42_out, Q_6);
  nand nand_42 (nand_42_out, nand_43_out, not_6_out);
  nand nand_43 (nand_43_out, RD_6, nand_44_out, nand_47_out);
  nand nand_44 (nand_44_out, R_6, CP_6_out);
  nand nand_45 (Q_6, nQ_6, nand_46_out, SD_6);
  nand nand_46 (nand_46_out, not_6_out, nand_47_out);
  nand nand_47 (nand_47_out, nand_43_out, nand_48_out, SD_6);
  nand nand_48 (nand_48_out, CP_6_out, S_6);
  Clock #(.highDuration(1), .lowDuration(1)) CP_6 (.out(CP_6_out));

  // Notes on the sheet:
  //   主从R-S触发器
  //   主从R-S触发器
  //   主从R-S触发器
  //   主从R-S触发器
  //   主从R-S触发器
  //   主从R-S触发器
endmodule

module \主从J_K触发器  (
  input  RD,
  input  SD,
  input  K,
  input  J,
  output nQ,
  output Q
);

  wire CP_out, nand_2_out, nand_3_out, nand_4_out, nand_6_out, nand_7_out, nand_8_out, not_1_out;

  not not_1 (not_1_out, CP_out);
  nand nand_1 (nQ, RD, nand_2_out, Q);
  nand nand_2 (nand_2_out, nand_3_out, not_1_out);
  nand nand_3 (nand_3_out, RD, nand_4_out, nand_7_out);
  nand nand_4 (nand_4_out, Q, K, CP_out);
  Clock #(.highDuration(1), .lowDuration(1)) CP (.out(CP_out));
  nand nand_5 (Q, nQ, nand_6_out, SD);
  nand nand_6 (nand_6_out, not_1_out, nand_7_out);
  nand nand_7 (nand_7_out, nand_3_out, nand_8_out, SD);
  nand nand_8 (nand_8_out, CP_out, J, nQ);

  // Notes on the sheet:
  //   主从J-K触发器
endmodule

module \维持_阻塞D触发器  (
  input  RD,
  input  SD,
  input  D,
  output nQ,
  output Q
);

  wire CP_out, nand_2_out, nand_3_out, nand_5_out, nand_6_out;

  nand nand_1 (nQ, RD, nand_2_out, Q);
  nand nand_2 (nand_2_out, CP_out, nand_3_out, nand_5_out);
  nand nand_3 (nand_3_out, nand_2_out, RD, D);
  nand nand_4 (Q, nQ, nand_5_out, SD);
  nand nand_5 (nand_5_out, RD, nand_6_out, CP_out);
  nand nand_6 (nand_6_out, nand_3_out, SD, nand_5_out);
  Clock #(.highDuration(1), .lowDuration(1)) CP (.out(CP_out));

  // Notes on the sheet:
  //   维持-阻塞D触发器
endmodule

module \延时  (
  input  x,
  output y
);

  wire CP_out;

  Clock #(.highDuration(1), .lowDuration(1)) CP (.out(CP_out));
  D_Flip_Flop #(.trigger("rising"), .Pre_Clr_Positions("ABOVE_BELOW"), .NegatePresetClear("false"), .enable("false"), .NewFFLayout("true")) d_ff_1 (
    .clk(CP_out), .D(x), .Q(y));  // open: Qn, preset, reset

  // Notes on the sheet:
  //   延时
endmodule
