// Logisim project 在Logisim上实现教材第4章的例题和习题.circ as structural Verilog: 22 circuits, main circuit 例题4.1
module \例题4_1  (
  output F,
  output F_2
);

  wire A, B, button_1_out, buzzer_1_p1, C, clock_1_out, comparator_1_eq, nand_1_out, nand_2_out, nand_3_out,
       not_1_out, or_1_out;

  Clock #(.highDuration(1), .lowDuration(1)) clock_1 (.out(clock_1_out));
  Button button_1 (.out(button_1_out));
  Counter #(.width(3), .max('h7), .ongoal("wrap"), .trigger("rising"), .behavior("new")) counter_1 (
    .Q({A, B, C}), .clk(clock_1_out), .clr(button_1_out));  // open: load, D, count, carry, preset, down
  // Probe on A
  // Probe on B
  // Probe on C
  not not_1 (not_1_out, A);
  or or_1 (or_1_out, B, C);
  nand nand_1 (nand_1_out, C, B);
  nand nand_2 (nand_2_out, not_1_out, or_1_out);
  nand nand_3 (nand_3_out, A, nand_1_out);
  nand nand_4 (F, nand_2_out, nand_3_out);
  ROM #(.addrWidth(3), .dataWidth(1), .Select("low")) rom_1 (.addr({A, B, C}), .data(F_2));
  Comparator #(.width(1), .mode("twosComplement")) comparator_1 (.a(F), .b(F_2), .eq(comparator_1_eq));  // open: gt, lt
  // Buzzer #(.freq_measure("Hz"), .vol_width(7)) buzzer_1: pin names not known; wires that end beside it: buzzer_1_p1
  not not_2 (buzzer_1_p1, comparator_1_eq);
  LED #(.active("false")) led_1 (.in(comparator_1_eq));

  // Notes on the sheet:
  //   contents of rom_1 (hex, n*v repeats v):
  //   0 6*1
endmodule

module \例题4_2  (
  output S,
  output C,
  output S_2,
  output C_2
);

  wire A, B, button_1_out, clock_1_out, comparator_1_eq, nand_1_out, nand_2_out, nand_3_out, not_2_out;

  Clock #(.highDuration(1), .lowDuration(1)) clock_1 (.out(clock_1_out));
  Button button_1 (.out(button_1_out));
  Counter #(.width(2), .max('h3), .ongoal("wrap"), .trigger("rising"), .behavior("new")) counter_1 (
    .Q({B, A}), .clk(clock_1_out), .clr(button_1_out));  // open: load, D, count, carry, preset, down
  // Probe on A
  // Probe on B
  nand nand_1 (nand_1_out, A, B);
  not not_1 (C, nand_1_out);
  nand nand_2 (nand_2_out, A, nand_1_out);
  nand nand_3 (nand_3_out, nand_1_out, B);
  ROM #(.addrWidth(2), .dataWidth(2), .Select("low")) rom_1 (.addr({A, B}), .data({S_2, C_2}));
  nand nand_4 (S, nand_2_out, nand_3_out);
  Comparator #(.width(2), .mode("twosComplement")) comparator_1 (
    .a({S, C}), .b({S_2, C_2}), .eq(comparator_1_eq));  // open: gt, lt
  not not_2 (not_2_out, comparator_1_eq);
  // Buzzer #(.freq_measure("Hz"), .vol_width(7)) buzzer_1: pin names not known; wires that end beside it: not_2_out
  LED #(.active("false")) led_1 (.in(comparator_1_eq));

  // Notes on the sheet:
  //   contents of rom_1 (hex, n*v repeats v):
  //   0 2 2 1
endmodule

module \例题4_3  (
  output W,
  output X,
  output Y,
  output Z,
  output W_2,
  output X_2,
  output Y_2,
  output Z_2
);

  wire A, and_1_out, B, button_1_out, C, clock_1_out, comparator_1_eq, D, not_2_out, or_1_out;
  wire [3:0] and_2_out, and_3_out, rom_2_data;

  Clock #(.highDuration(1), .lowDuration(1)) clock_1 (.out(clock_1_out));
  Button button_1 (.out(button_1_out));
  Counter #(.width(4), .max('hf), .ongoal("wrap"), .trigger("rising"), .behavior("new")) counter_1 (
    .Q({A, B, C, D}), .clk(clock_1_out), .clr(button_1_out));  // open: load, D, count, carry, preset, down
  // Probe on A
  // Probe on B
  // Probe on C
  // Probe on D
  and and_1 (and_1_out, B, or_1_out);
  or or_1 (or_1_out, D, C);
  not not_1 (Z, D);
  ROM #(.addrWidth(4), .dataWidth(4), .Select("low")) rom_1 (.addr({A, B, C, D}), .data({W_2, X_2, Y_2, Z_2}));
  ROM #(.addrWidth(4), .dataWidth(4), .Select("low")) rom_2 (.addr({A, B, C, D}), .data(rom_2_data));
  xor xor_1 (W, A, and_1_out);
  xor xor_2 (X, B, or_1_out);
  xor xor_3 (Y, C, Z);
  assign and_2_out = {W_2, X_2, Y_2, Z_2} & rom_2_data;  // AND_Gate and_2, 4 bits wide
  assign and_3_out = {W, X, Y, Z} & rom_2_data;  // AND_Gate and_3, 4 bits wide
  not not_2 (not_2_out, comparator_1_eq);
  Comparator #(.width(4), .mode("twosComplement")) comparator_1 (
    .a(and_3_out), .b(and_2_out), .eq(comparator_1_eq));  // open: gt, lt
  // Buzzer #(.freq_measure("Hz"), .vol_width(7)) buzzer_1: pin names not known; wires that end beside it: not_2_out
  LED #(.active("false")) led_1 (.in(comparator_1_eq));

  // Notes on the sheet:
  //   ROM1
  //   ROM2
  //   contents of rom_1 (hex, n*v repeats v):
  //   3 4 5 6 7 8 9 a b c
  //   contents of rom_2 (hex, n*v repeats v):
  //   10*f
endmodule

module \例题4_4  (
  output F,
  output F_2
);

  wire A, B, button_1_out, C, clock_1_out, comparator_1_eq, nand_1_out, nand_2_out, nand_3_out, not_1_out;

  Clock #(.highDuration(1), .lowDuration(1)) clock_1 (.out(clock_1_out));
  Button button_1 (.out(button_1_out));
  Counter #(.width(3), .max('h7), .ongoal("wrap"), .trigger("rising"), .behavior("new")) counter_1 (
    .Q({A, B, C}), .clk(clock_1_out), .clr(button_1_out));  // open: load, D, count, carry, preset, down
  // Probe on A
  // Probe on B
  // Probe on C
  nand nand_1 (nand_1_out, A, B);
  nand nand_2 (nand_2_out, B, C);
  nand nand_3 (nand_3_out, C, A);
  ROM #(.addrWidth(3), .dataWidth(1), .Select("low")) rom_1 (.addr({A, B, C}), .data(F_2));
  nand nand_4 (F, nand_1_out, nand_2_out, nand_3_out);
  not not_1 (not_1_out, comparator_1_eq);
  Comparator #(.width(1), .mode("twosComplement")) comparator_1 (.a(F), .b(F_2), .eq(comparator_1_eq));  // open: gt, lt
  // Buzzer #(.freq_measure("Hz"), .vol_width(7)) buzzer_1: pin names not known; wires that end beside it: not_1_out
  LED #(.active("false")) led_1 (.in(comparator_1_eq));

  // Notes on the sheet:
  //   contents of rom_1 (hex, n*v repeats v):
  //   0 0 0 1 0 1 1 1
endmodule

module \例题4_5  (
  output F,
  output F_2
);

  wire a1, a2, a3, b1, b2, b3, button_1_out, clock_1_out, comparator_2_eq, not_1_out, xor_1_out, xor_2_out,
       xor_3_out;

  Counter #(.width(6), .max('h3f), .ongoal("wrap"), .trigger("rising"), .behavior("new")) counter_1 (
    .Q({a3, b3, a2, b2, a1, b1}), .clk(clock_1_out), .clr(button_1_out));  // open: load, D, count, carry, preset, down
  Clock #(.highDuration(1), .lowDuration(1)) clock_1 (.out(clock_1_out));
  Button button_1 (.out(button_1_out));
  // Probe on a3
  // Probe on b3
  // Probe on a2
  // Probe on b2
  // Probe on a1
  // Probe on b1
  xor xor_1 (xor_1_out, a3, b3);
  xor xor_2 (xor_2_out, a2, b2);
  xor xor_3 (xor_3_out, a1, b1);
  nor nor_1 (F, xor_1_out, xor_2_out, xor_3_out);
  Comparator #(.width(3), .mode("twosComplement")) comparator_1 (
    .a({a3, a2, a1}), .b({b3, b2, b1}), .eq(F_2));  // open: gt, lt
  not not_1 (not_1_out, comparator_2_eq);
  Comparator #(.width(1), .mode("twosComplement")) comparator_2 (.a(F), .b(F_2), .eq(comparator_2_eq));  // open: gt, lt
  // Buzzer #(.freq_measure("Hz"), .vol_width(7)) buzzer_1: pin names not known; wires that end beside it: not_1_out
  LED #(.active("false")) led_1 (.in(comparator_2_eq));
endmodule

module \例题4_6  (
  output M0,
  output M1,
  output M2,
  output M3,
  output M3_2,
  output M2_2,
  output M1_2,
  output M0_2
);

  wire A0, A1, and_1_out, and_2_out, and_3_out, and_7_out, and_8_out, and_9_out, and_10_out, and_11_out,
       and_12_out, B0, B1, button_1_out, buzzer_2_p1, clock_1_out, comparator_1_eq, comparator_2_eq,
       not_1_out, not_2_out, not_3_out, not_4_out, not_5_out;
  wire [1:0] multiplier_1_cout, multiplier_1_out;

  Clock #(.highDuration(1), .lowDuration(1)) clock_1 (.out(clock_1_out));
  Button button_1 (.out(button_1_out));
  Counter #(.width(4), .max('hf), .ongoal("wrap"), .trigger("rising"), .behavior("new")) counter_1 (
    .Q({A1, A0, B1, B0}), .clk(clock_1_out), .clr(button_1_out));  // open: load, D, count, carry, preset, down
  // Probe on A1
  // Probe on A0
  // Probe on B1
  // Probe on B0
  not not_1 (not_1_out, A1);
  not not_2 (not_2_out, A0);
  not not_3 (not_3_out, B1);
  not not_4 (not_4_out, B0);
  and and_1 (and_1_out, A1, B0);
  and and_2 (and_2_out, B1, A0);
  // Probe on {A1, A0}
  // Probe on {B1, B0}
  and and_3 (and_3_out, A1, B1);
  and and_4 (M3_2, and_2_out, and_1_out);
  xor xor_1 (M1_2, and_1_out, and_2_out);
  and and_5 (M0_2, A0, B0);
  and and_6 (M0, A0, B0);
  and and_7 (and_7_out, A0, B1, not_4_out);
  and and_8 (and_8_out, not_1_out, A0, B1);
  and and_9 (and_9_out, A1, not_2_out, B0);
  and and_10 (and_10_out, A1, not_3_out, B0);
  and and_11 (and_11_out, A1, B1, not_4_out);
  and and_12 (and_12_out, A1, not_2_out, B1);
  and and_13 (M3, A1, A0, B1, B0);
  xor xor_2 (M2_2, and_3_out, M3_2);
  Multiplier #(.width(2)) multiplier_1 (
    .a({A1, A0}), .b({B1, B0}), .out(multiplier_1_out), .cout(multiplier_1_cout));  // open: cin
  or or_1 (M1, and_7_out, and_8_out, and_9_out, and_10_out);
  or or_2 (M2, and_11_out, and_12_out);
  // Probe on {M3_2, M2_2, M1_2, M0_2}
  // Probe on {M3, M2, M1, M0}
  // Probe on {multiplier_1_cout, multiplier_1_out}
  not not_5 (not_5_out, comparator_1_eq);
  Comparator #(.width(4), .mode("twosComplement")) comparator_1 (
    .a({M3, M2, M1, M0}), .b({multiplier_1_cout, multiplier_1_out}), .eq(comparator_1_eq));  // open: gt, lt
  Comparator #(.width(4), .mode("twosComplement")) comparator_2 (
    .a({M3_2, M2_2, M1_2, M0_2}), .b({multiplier_1_cout, multiplier_1_out}), .eq(comparator_2_eq));  // open: gt, lt
  // Buzzer #(.freq_measure("Hz"), .vol_width(7)) buzzer_1: pin names not known; wires that end beside it: not_5_out
  LED #(.active("false")) led_1 (.in(comparator_1_eq));
  // Buzzer #(.freq_measure("Hz"), .vol_width(7)) buzzer_2: pin names not known; wires that end beside it: buzzer_2_p1
  not not_6 (buzzer_2_p1, comparator_2_eq);
  LED #(.active("false")) led_2 (.in(comparator_2_eq));
endmodule

module \例题4_7  (
  output F,
  output F_2,
  output MASK
);

  wire A, and_1_out, and_2_out, B, button_1_out, buzzer_1_p1, C, clock_1_out, comparator_1_eq, D, nand_1_out,
       nand_2_out, nand_3_out;

  Counter #(.width(4), .max('hf), .ongoal("wrap"), .trigger("rising"), .behavior("new")) counter_1 (
    .Q({A, B, C, D}), .clk(clock_1_out), .clr(button_1_out));  // open: load, D, count, carry, preset, down
  Clock #(.highDuration(1), .lowDuration(1)) clock_1 (.out(clock_1_out));
  Button button_1 (.out(button_1_out));
  // Probe on A
  // Probe on B
  // Probe on C
  // Probe on D
  nand nand_1 (nand_1_out, A, B);
  nand nand_2 (nand_2_out, A, D);
  nand nand_3 (nand_3_out, C, B, D);
  nand nand_4 (F, nand_1_out, nand_2_out, nand_3_out);
  ROM #(.addrWidth(4), .dataWidth(1), .Select("low")) rom_1 (.addr({A, B, C, D}), .data(F_2));
  ROM #(.addrWidth(4), .dataWidth(1), .Select("low")) rom_2 (.addr({A, B, C, D}), .data(MASK));
  and and_1 (and_1_out, F, MASK);
  and and_2 (and_2_out, F_2, MASK);
  Comparator #(.width(1), .mode("twosComplement")) comparator_1 (
    .a(and_1_out), .b(and_2_out), .eq(comparator_1_eq));  // open: gt, lt
  // Buzzer #(.freq_measure("Hz"), .vol_width(7)) buzzer_1: pin names not known; wires that end beside it: buzzer_1_p1
  not not_1 (buzzer_1_p1, comparator_1_eq);
  LED #(.active("false")) led_1 (.in(comparator_1_eq));

  // Notes on the sheet:
  //   ROM1
  //   ROM2
  //   contents of rom_1 (hex, n*v repeats v):
  //   7*0 1 0 1 0 1 1
  //   contents of rom_2 (hex, n*v repeats v):
  //   0 0 0 10*1
endmodule

module \例题4_8  (
  output F1,
  output F2,
  output F1_2,
  output F2_2
);

  wire A, B, button_1_out, buzzer_2_p1, C, clock_1_out, comparator_1_eq, comparator_2_eq, nand_1_out,
       nand_2_out, nand_3_out, nand_4_out, nand_5_out, nand_6_out, nand_7_out, not_1_out, not_2_out,
       not_3_out, not_4_out, not_5_out;
  wire [1:0] rom_1_data;

  Clock #(.highDuration(1), .lowDuration(1)) clock_1 (.out(clock_1_out));
  Button button_1 (.out(button_1_out));
  Counter #(.width(3), .max('h7), .ongoal("wrap"), .trigger("rising"), .behavior("new")) counter_1 (
    .Q({A, B, C}), .clk(clock_1_out), .clr(button_1_out));  // open: load, D, count, carry, preset, down
  // Probe on A
  // Probe on B
  // Probe on C
  not not_1 (not_1_out, A);
  not not_2 (not_2_out, C);
  not not_3 (not_3_out, A);
  not not_4 (not_4_out, C);
  nand nand_1 (nand_1_out, not_1_out, C);
  nand nand_2 (nand_2_out, B, C);
  nand nand_3 (nand_3_out, A, B);
  nand nand_4 (nand_4_out, not_2_out, B);
  nand nand_5 (nand_5_out, not_3_out, C);
  nand nand_6 (nand_6_out, B, A, C);
  nand nand_7 (nand_7_out, not_4_out, B);
  ROM #(.addrWidth(3), .dataWidth(2), .Select("low")) rom_1 (.addr({A, B, C}), .data(rom_1_data));
  nand nand_8 (F1, nand_1_out, nand_2_out);
  nand nand_9 (F2, nand_3_out, nand_4_out);
  nand nand_10 (F1_2, nand_5_out, nand_6_out);
  nand nand_11 (F2_2, nand_6_out, nand_7_out);
  Comparator #(.width(2), .mode("twosComplement")) comparator_1 (
    .a({F1, F2}), .b(rom_1_data), .eq(comparator_1_eq));  // open: gt, lt
  Comparator #(.width(2), .mode("twosComplement")) comparator_2 (
    .a({F1_2, F2_2}), .b(rom_1_data), .eq(comparator_2_eq));  // open: gt, lt
  not not_5 (not_5_out, comparator_1_eq);
  // Buzzer #(.freq_measure("Hz"), .vol_width(7)) buzzer_1: pin names not known; wires that end beside it: not_5_out
  LED #(.active("false")) led_1 (.in(comparator_1_eq));
  // Buzzer #(.freq_measure("Hz"), .vol_width(7)) buzzer_2: pin names not known; wires that end beside it: buzzer_2_p1
  not not_6 (buzzer_2_p1, comparator_2_eq);
  LED #(.active("false")) led_2 (.in(comparator_2_eq));

  // Notes on the sheet:
  //   contents of rom_1 (hex, n*v repeats v):
  //   0 2 1 2 0 0 1 3
endmodule

module \例题4_9  (
  output Si,
  output Ci,
  output Si_2,
  output Ci_2
);

  wire Ai, Bi, button_1_out, Ci_1, clock_1_out, comparator_1_eq, comparator_2_eq, nand_1_out, nand_2_out,
       nand_3_out, nand_4_out, nand_5_out, not_1_out, not_2_out, xor_1_out, xor_2_out;
  wire [1:0] rom_1_data;

  Clock #(.highDuration(1), .lowDuration(1)) clock_1 (.out(clock_1_out));
  Button button_1 (.out(button_1_out));
  Counter #(.width(3), .max('h7), .ongoal("wrap"), .trigger("rising"), .behavior("new")) counter_1 (
    .Q({Ai, Bi, Ci_1}), .clk(clock_1_out), .clr(button_1_out));  // open: load, D, count, carry, preset, down
  // Probe on Ai
  // Probe on Bi
  // Probe on Ci_1
  xor xor_1 (xor_1_out, Ai, Bi);
  nand nand_1 (nand_1_out, xor_1_out, Ci_1);
  xor xor_2 (xor_2_out, Ai, Bi);
  nand nand_2 (nand_2_out, Ci_1, Bi);
  nand nand_3 (nand_3_out, Ai, Ci_1);
  nand nand_4 (nand_4_out, Bi, Ai);
  nand nand_5 (nand_5_out, Ai, Bi);
  ROM #(.addrWidth(3), .dataWidth(2), .Select("low")) rom_1 (.addr({Ai, Bi, Ci_1}), .data(rom_1_data));
  xor xor_3 (Si, xor_2_out, Ci_1);
  nand nand_6 (Ci, nand_2_out, nand_3_out, nand_4_out);
  xor xor_4 (Si_2, xor_1_out, Ci_1);
  nand nand_7 (Ci_2, nand_1_out, nand_5_out);
  Comparator #(.width(2), .mode("twosComplement")) comparator_1 (
    .a({Si, Ci}), .b(rom_1_data), .eq(comparator_1_eq));  // open: gt, lt
  Comparator #(.width(2), .mode("twosComplement")) comparator_2 (
    .a({Si_2, Ci_2}), .b(rom_1_data), .eq(comparator_2_eq));  // open: gt, lt
  not not_1 (not_1_out, comparator_1_eq);
  // Buzzer #(.freq_measure("Hz"), .vol_width(7)) buzzer_1: pin names not known; wires that end beside it: not_1_out
  LED #(.active("false")) led_1 (.in(comparator_1_eq));
  not not_2 (not_2_out, comparator_2_eq);
  // Buzzer #(.freq_measure("Hz"), .vol_width(7)) buzzer_2: pin names not known; wires that end beside it: not_2_out
  LED #(.active("false")) led_2 (.in(comparator_2_eq));

  // Notes on the sheet:
  //   contents of rom_1 (hex, n*v repeats v):
  //   0 2 2 1 2 1 1 3
endmodule

module \例题4_10  (
  output F,
  output F_2
);

  wire A, B, button_1_out, C, clock_1_out, comparator_1_eq, D, nand_1_out, nand_2_out, nand_3_out,
       nand_4_out, nand_5_out, nand_6_out, nand_8_out, nand_9_out, not_1_out, not_2_out, not_3_out,
       not_4_out, not_5_out;

  Clock #(.highDuration(1), .lowDuration(1)) clock_1 (.out(clock_1_out));
  Button button_1 (.out(button_1_out));
  Counter #(.width(4), .max('hf), .ongoal("wrap"), .trigger("rising"), .behavior("new")) counter_1 (
    .Q({A, B, C, D}), .clk(clock_1_out), .clr(button_1_out));  // open: load, D, count, carry, preset, down
  // Probe on A
  // Probe on B
  // Probe on C
  // Probe on D
  not not_1 (not_1_out, A);
  not not_2 (not_2_out, B);
  not not_3 (not_3_out, C);
  not not_4 (not_4_out, D);
  nand nand_1 (nand_1_out, B, not_1_out);
  nand nand_2 (nand_2_out, B, not_3_out);
  nand nand_3 (nand_3_out, A, C, not_2_out);
  nand nand_4 (nand_4_out, A, C, not_4_out);
  nand nand_5 (nand_5_out, A, C);
  nand nand_6 (nand_6_out, B, D);
  nand nand_7 (F, nand_1_out, nand_2_out, nand_3_out, nand_4_out);
  nand nand_8 (nand_8_out, nand_5_out, B);
  nand nand_9 (nand_9_out, A, nand_6_out, C);
  nand nand_10 (F_2, nand_8_out, nand_9_out);
  not not_5 (not_5_out, comparator_1_eq);
  Comparator #(.width(1), .mode("twosComplement")) comparator_1 (.a(F), .b(F_2), .eq(comparator_1_eq));  // open: gt, lt
  // Buzzer #(.freq_measure("Hz"), .vol_width(7)) buzzer_1: pin names not known; wires that end beside it: not_5_out
  LED #(.active("false")) led_1 (.in(comparator_1_eq));
endmodule

module \例题4_11  (
  output F,
  output F_2
);

  wire A, and_1_out, B, button_1_out, buzzer_1_p1, C, clock_1_out, comparator_1_eq, nand_1_out, nand_2_out,
       nand_3_out, not_1_out, not_2_out, not_3_out;

  Clock #(.highDuration(1), .lowDuration(1)) clock_1 (.out(clock_1_out));
  Button button_1 (.out(button_1_out));
  Counter #(.width(3), .max('h7), .ongoal("wrap"), .trigger("rising"), .behavior("new")) counter_1 (
    .Q({A, B, C}), .clk(clock_1_out), .clr(button_1_out));  // open: load, D, count, carry, preset, down
  // Probe on A
  // Probe on B
  // Probe on C
  not not_1 (not_1_out, A);
  not not_2 (not_2_out, B);
  not not_3 (not_3_out, C);
  and and_1 (and_1_out, A, C);
  nand nand_1 (nand_1_out, not_1_out, B);
  nand nand_2 (nand_2_out, not_2_out, A, C);
  nand nand_3 (nand_3_out, not_3_out, B);
  xor xor_1 (F_2, and_1_out, B);
  nand nand_4 (F, nand_1_out, nand_2_out, nand_3_out);
  Comparator #(.width(1), .mode("twosComplement")) comparator_1 (.a(F), .b(F_2), .eq(comparator_1_eq));  // open: gt, lt
  // Buzzer #(.freq_measure("Hz"), .vol_width(7)) buzzer_1: pin names not known; wires that end beside it: buzzer_1_p1
  not not_4 (buzzer_1_p1, comparator_1_eq);
  LED #(.active("false")) led_1 (.in(comparator_1_eq));
endmodule

module \例题4_12_a  (
  output F,
  output F_2
);

  wire button_1_out, clock_1_out, comparator_1_eq, nand_1_out, nand_2_out, nand_3_out, nand_4_out, not_1_out,
       not_2_out, not_3_out, not_4_out, not_5_out, W, X, Y, Z;

  Counter #(.width(4), .max('hf), .ongoal("wrap"), .trigger("rising"), .behavior("new")) counter_1 (
    .Q({W, X, Y, Z}), .clk(clock_1_out), .clr(button_1_out));  // open: load, D, count, carry, preset, down
  Clock #(.highDuration(1), .lowDuration(1)) clock_1 (.out(clock_1_out));
  Button button_1 (.out(button_1_out));
  // Probe on W
  // Probe on X
  // Probe on Y
  // Probe on Z
  not not_1 (not_1_out, W);
  not not_2 (not_2_out, X);
  not not_3 (not_3_out, Y);
  not not_4 (not_4_out, Z);
  nand nand_1 (nand_1_out, not_4_out, not_2_out, not_1_out);
  nand nand_2 (nand_2_out, not_4_out, Y);
  nand nand_3 (nand_3_out, W, X);
  nand nand_4 (nand_4_out, not_3_out, X, Z);
  ROM #(.addrWidth(4), .dataWidth(1), .Select("low")) rom_1 (.addr({W, X, Y, Z}), .data(F_2));
  nand nand_5 (F, nand_1_out, nand_2_out, nand_3_out, nand_4_out);
  not not_5 (not_5_out, comparator_1_eq);
  Comparator #(.width(1), .mode("twosComplement")) comparator_1 (.a(F), .b(F_2), .eq(comparator_1_eq));  // open: gt, lt
  // Buzzer #(.freq_measure("Hz"), .vol_width(7)) buzzer_1: pin names not known; wires that end beside it: not_5_out
  LED #(.active("false")) led_1 (.in(comparator_1_eq));

  // Notes on the sheet:
  //   contents of rom_1 (hex, n*v repeats v):
  //   1 0 1 0 0 1 1 0 0 0 1 0 4*1
endmodule

module \例题4_12_b  (
  output F,
  output F_2
);

  wire button_1_out, clock_1_out, comparator_1_eq, nor_1_out, nor_2_out, not_1_out, not_2_out, not_3_out, W,
       X, Y, Z;

  Counter #(.width(4), .max('hf), .ongoal("wrap"), .trigger("rising"), .behavior("new")) counter_1 (
    .Q({W, X, Y, Z}), .clk(clock_1_out), .clr(button_1_out));  // open: load, D, count, carry, preset, down
  Clock #(.highDuration(1), .lowDuration(1)) clock_1 (.out(clock_1_out));
  Button button_1 (.out(button_1_out));
  // Probe on W
  // Probe on X
  // Probe on Y
  // Probe on Z
  not not_1 (not_1_out, W);
  not not_2 (not_2_out, X);
  nor nor_1 (nor_1_out, not_1_out, Y);
  nor nor_2 (nor_2_out, not_2_out, Z);
  ROM #(.addrWidth(4), .dataWidth(1), .Select("low")) rom_1 (.addr({W, X, Y, Z}), .data(F_2));
  nor nor_3 (F, nor_1_out, nor_2_out);
  not not_3 (not_3_out, comparator_1_eq);
  Comparator #(.width(1), .mode("twosComplement")) comparator_1 (.a(F), .b(F_2), .eq(comparator_1_eq));  // open: gt, lt
  // Buzzer #(.freq_measure("Hz"), .vol_width(7)) buzzer_1: pin names not known; wires that end beside it: not_3_out
  LED #(.active("false")) led_1 (.in(comparator_1_eq));

  // Notes on the sheet:
  //   contents of rom_1 (hex, n*v repeats v):
  //   4*1 0 1 0 1 0 0 1 1 0 0 0 1
endmodule

module \例题4_16  (
  output F,
  output F_2
);

  wire A, B, button_1_out, buzzer_1_p1, C, clock_1_out, comparator_1_eq, nand_1_out, nand_2_out, nand_3_out,
       nand_4_out, nand_5_out, not_1_out, not_2_out;

  Clock #(.highDuration(1), .lowDuration(1)) clock_1 (.out(clock_1_out));
  Button button_1 (.out(button_1_out));
  Counter #(.width(3), .max('h7), .ongoal("wrap"), .trigger("rising"), .behavior("new")) counter_1 (
    .Q({A, B, C}), .clk(clock_1_out), .clr(button_1_out));  // open: load, D, count, carry, preset, down
  // Probe on A
  // Probe on B
  // Probe on C
  not not_1 (not_1_out, A);
  not not_2 (not_2_out, A);
  nand nand_1 (nand_1_out, A, B);
  nand nand_2 (nand_2_out, not_1_out, C);
  nand nand_3 (nand_3_out, A, B);
  nand nand_4 (nand_4_out, not_2_out, C);
  nand nand_5 (nand_5_out, C, B);
  nand nand_6 (F, nand_1_out, nand_2_out);
  nand nand_7 (F_2, nand_3_out, nand_4_out, nand_5_out);
  Comparator #(.width(1), .mode("twosComplement")) comparator_1 (.a(F), .b(F_2), .eq(comparator_1_eq));  // open: gt, lt
  // Buzzer #(.freq_measure("Hz"), .vol_width(7)) buzzer_1: pin names not known; wires that end beside it: buzzer_1_p1
  not not_3 (buzzer_1_p1, comparator_1_eq);
  LED #(.active("false")) led_1 (.in(comparator_1_eq));
endmodule

module \例题4_17  (
  output F,
  output F_2
);

  wire A, and_1_out, and_2_out, and_3_out, and_4_out, and_5_out, and_6_out, and_7_out, and_8_out, B,
       button_1_out, C, clock_1_out, comparator_1_eq, D, not_1_out, not_2_out, not_3_out, not_4_out,
       not_5_out, not_6_out, not_7_out;

  Clock #(.highDuration(1), .lowDuration(1)) clock_1 (.out(clock_1_out));
  Button button_1 (.out(button_1_out));
  Counter #(.width(4), .max('hf), .ongoal("wrap"), .trigger("rising"), .behavior("new")) counter_1 (
    .Q({A, B, C, D}), .clk(clock_1_out), .clr(button_1_out));  // open: load, D, count, carry, preset, down
  // Probe on A
  // Probe on B
  // Probe on C
  // Probe on D
  not not_1 (not_1_out, A);
  not not_2 (not_2_out, B);
  not not_3 (not_3_out, C);
  not not_4 (not_4_out, A);
  not not_5 (not_5_out, B);
  not not_6 (not_6_out, C);
  and and_1 (and_1_out, not_4_out, C);
  and and_2 (and_2_out, B, not_6_out, D);
  and and_3 (and_3_out, A, not_5_out, not_6_out);
  and and_4 (and_4_out, C, not_1_out);
  and and_5 (and_5_out, B, not_3_out, D);
  and and_6 (and_6_out, A, not_2_out, not_3_out);
  and and_7 (and_7_out, not_1_out, B, D);
  and and_8 (and_8_out, A, not_3_out, D);
  or or_1 (F, and_1_out, and_2_out, and_3_out);
  or or_2 (F_2, and_4_out, and_5_out, and_6_out, and_7_out, and_8_out);
  not not_7 (not_7_out, comparator_1_eq);
  Comparator #(.width(1), .mode("twosComplement")) comparator_1 (.a(F), .b(F_2), .eq(comparator_1_eq));  // open: gt, lt
  // Buzzer #(.freq_measure("Hz"), .vol_width(7)) buzzer_1: pin names not known; wires that end beside it: not_7_out
  LED #(.active("false")) led_1 (.in(comparator_1_eq));
endmodule

module \习题4_2  (
  output F,
  output F_2
);

  wire A, B, button_1_out, C, clock_1_out, comparator_1_eq, nor_1_out, nor_2_out, nor_3_out, nor_4_out,
       nor_5_out, nor_6_out, not_1_out, not_2_out, not_3_out, not_4_out, xor_1_out;

  Clock #(.highDuration(1), .lowDuration(1)) clock_1 (.out(clock_1_out));
  Button button_1 (.out(button_1_out));
  Counter #(.width(3), .max('h7), .ongoal("wrap"), .trigger("rising"), .behavior("new")) counter_1 (
    .Q({A, B, C}), .clk(clock_1_out), .clr(button_1_out));  // open: load, D, count, carry, preset, down
  // Probe on A
  // Probe on B
  // Probe on C
  not not_1 (not_1_out, A);
  not not_2 (not_2_out, B);
  not not_3 (not_3_out, C);
  nor nor_1 (nor_1_out, A, B);
  xor xor_1 (xor_1_out, not_1_out, not_2_out);
  nor nor_2 (nor_2_out, A, nor_1_out);
  nor nor_3 (nor_3_out, nor_1_out, B);
  xor xor_2 (F_2, xor_1_out, not_3_out);
  nor nor_4 (nor_4_out, nor_2_out, nor_3_out, C);
  nor nor_5 (nor_5_out, nor_3_out, nor_2_out, nor_4_out);
  nor nor_6 (nor_6_out, nor_4_out, C);
  nor nor_7 (F, nor_5_out, nor_6_out);
  Comparator #(.width(1), .mode("twosComplement")) comparator_1 (.a(F), .b(F_2), .eq(comparator_1_eq));  // open: gt, lt
  not not_4 (not_4_out, comparator_1_eq);
  // Buzzer #(.freq_measure("Hz"), .vol_width(7)) buzzer_1: pin names not known; wires that end beside it: not_4_out
  LED #(.active("false")) led_1 (.in(comparator_1_eq));
endmodule

module \习题4_6_1  (
  output Y3,
  output Y2,
  output Y1,
  output Y0
);

  wire button_1_out, clock_1_out, comparator_1_eq, not_1_out, not_2_out, X1;
  wire [1:0] multiplier_1_cout, multiplier_1_out;

  Counter #(.width(2), .max('h3), .ongoal("wrap"), .trigger("rising"), .behavior("new")) counter_1 (
    .Q({X1, Y0}), .clk(clock_1_out), .clr(button_1_out));  // open: load, D, count, carry, preset, down
  Clock #(.highDuration(1), .lowDuration(1)) clock_1 (.out(clock_1_out));
  Button button_1 (.out(button_1_out));
  // Probe on X1
  // Probe on Y0
  not not_1 (not_1_out, Y0);
  and and_1 (Y3, X1, Y0);
  and and_2 (Y2, X1, not_1_out);
  Multiplier #(.width(2)) multiplier_1 (
    .a({X1, Y0}), .b({X1, Y0}), .out(multiplier_1_out), .cout(multiplier_1_cout));  // open: cin
  // Probe on {Y3, Y2, 1'b0, Y0}
  // Probe on {multiplier_1_cout, multiplier_1_out}
  Comparator #(.width(4), .mode("twosComplement")) comparator_1 (
    .a({Y3, Y2, 1'b0, Y0}), .b({multiplier_1_cout, multiplier_1_out}), .eq(comparator_1_eq));  // open: gt, lt
  not not_2 (not_2_out, comparator_1_eq);
  // Buzzer #(.freq_measure("Hz"), .vol_width(7)) buzzer_1: pin names not known; wires that end beside it: not_2_out
  LED #(.active("false")) led_1 (.in(comparator_1_eq));

  assign Y1 = 1'b0;

  // Other names for the same wires on the sheet: X0 = Y0
endmodule

module \习题4_6_2  (
  output Y4,
  output Y3,
  output Y2,
  output Y1,
  output Y0
);

  wire button_1_out, buzzer_1_p1, clock_1_out, comparator_1_eq;
  wire [1:0] multiplier_1_cout, multiplier_1_out;
  wire [3:0] multiplier_2_cout, multiplier_2_out;

  Counter #(.width(2), .max('h3), .ongoal("wrap"), .trigger("rising"), .behavior("new")) counter_1 (
    .Q({Y3, Y0}), .clk(clock_1_out), .clr(button_1_out));  // open: load, D, count, carry, preset, down
  Clock #(.highDuration(1), .lowDuration(1)) clock_1 (.out(clock_1_out));
  Button button_1 (.out(button_1_out));
  // Probe on Y3
  // Probe on Y0
  Multiplier #(.width(2)) multiplier_1 (
    .a({Y3, Y0}), .b({Y3, Y0}), .out(multiplier_1_out), .cout(multiplier_1_cout));  // open: cin
  and and_1 (Y4, Y3, Y0);
  and and_2 (Y1, Y3, Y0);
  Multiplier #(.width(4)) multiplier_2 (
    .a({multiplier_1_cout, multiplier_1_out}), .b({2'b00, Y3, Y0}), .out(multiplier_2_out),
    .cout(multiplier_2_cout));  // open: cin
  // Probe on {Y4, Y3, 1'b0, Y1, Y0}
  // Probe on {multiplier_2_cout[0], multiplier_2_out}
  Comparator #(.width(5), .mode("twosComplement")) comparator_1 (
    .a({Y4, Y3, 1'b0, Y1, Y0}), .b({multiplier_2_cout[0], multiplier_2_out}), .eq(comparator_1_eq));  // open: gt, lt
  // Buzzer #(.freq_measure("Hz"), .vol_width(7)) buzzer_1: pin names not known; wires that end beside it: buzzer_1_p1
  not not_1 (buzzer_1_p1, comparator_1_eq);
  LED #(.active("false")) led_1 (.in(comparator_1_eq));

  assign Y2 = 1'b0;

  // Other names for the same wires on the sheet: X0 = Y0; X1 = Y3
endmodule

module \习题4_7_a  (
  output F,
  output F_2
);

  wire A, and_1_out, and_2_out, and_3_out, and_4_out, and_5_out, and_6_out, and_7_out, B, button_1_out,
       buzzer_3_p1, C, clock_1_out, comparator_1_eq, comparator_2_eq, comparator_3_eq, D, MASK, nand_1_out,
       nand_2_out, nand_3_out, nand_4_out, nand_5_out, nand_6_out, not_1_out, not_2_out, not_3_out,
       not_4_out, not_5_out, rom_2_data;

  Counter #(.width(4), .max('hf), .ongoal("wrap"), .trigger("rising"), .behavior("new")) counter_1 (
    .Q({A, B, C, D}), .clk(clock_1_out), .clr(button_1_out));  // open: load, D, count, carry, preset, down
  Clock #(.highDuration(1), .lowDuration(1)) clock_1 (.out(clock_1_out));
  Button button_1 (.out(button_1_out));
  // Probe on A
  // Probe on B
  // Probe on C
  // Probe on D
  nand nand_1 (nand_1_out, A, A);
  nand nand_2 (nand_2_out, B, B);
  nand nand_3 (nand_3_out, C, C);
  not not_1 (not_1_out, A);
  not not_2 (not_2_out, B);
  not not_3 (not_3_out, C);
  nand nand_4 (nand_4_out, A, nand_2_out);
  nand nand_5 (nand_5_out, nand_1_out, C);
  nand nand_6 (nand_6_out, A, nand_3_out, D);
  and and_1 (and_1_out, A, not_2_out);
  and and_2 (and_2_out, not_1_out, C);
  and and_3 (and_3_out, A, not_3_out, D);
  nand nand_7 (F, nand_4_out, nand_5_out, nand_6_out);
  or or_1 (F_2, and_1_out, and_2_out, and_3_out);
  ROM #(.addrWidth(4), .dataWidth(1), .Select("low")) rom_1 (.addr({A, B, C, D}), .data(MASK));
  ROM #(.addrWidth(4), .dataWidth(1), .Select("low")) rom_2 (.addr({A, B, C, D}), .data(rom_2_data));
  and and_4 (and_4_out, F, MASK);
  and and_5 (and_5_out, MASK, rom_2_data);
  and and_6 (and_6_out, F_2, MASK);
  and and_7 (and_7_out, MASK, rom_2_data);
  Comparator #(.width(1), .mode("twosComplement")) comparator_1 (
    .a(and_4_out), .b(and_5_out), .eq(comparator_1_eq));  // open: gt, lt
  Comparator #(.width(1), .mode("twosComplement")) comparator_2 (
    .a(and_6_out), .b(and_7_out), .eq(comparator_2_eq));  // open: gt, lt
  Comparator #(.width(1), .mode("twosComplement")) comparator_3 (.a(F), .b(F_2), .eq(comparator_3_eq));  // open: gt, lt
  not not_4 (not_4_out, comparator_1_eq);
  // Buzzer #(.freq_measure("Hz"), .vol_width(7)) buzzer_1: pin names not known; wires that end beside it: not_4_out
  LED #(.active("false")) led_1 (.in(comparator_1_eq));
  not not_5 (not_5_out, comparator_2_eq);
  // Buzzer #(.freq_measure("Hz"), .vol_width(7)) buzzer_2: pin names not known; wires that end beside it: not_5_out
  LED #(.active("false")) led_2 (.in(comparator_2_eq));
  // Buzzer #(.freq_measure("Hz"), .vol_width(7)) buzzer_3: pin names not known; wires that end beside it: buzzer_3_p1
  not not_6 (buzzer_3_p1, comparator_3_eq);
  LED #(.active("false")) led_3 (.in(comparator_3_eq));

  // Notes on the sheet:
  //   ROM1
  //   ROM2
  //   contents of rom_1 (hex, n*v repeats v):
  //   5*1 6*0 5*1
  //   contents of rom_2 (hex, n*v repeats v):
  //   0 0 1 1 7*0 1 0 1
endmodule

module \习题4_7_b  (
  output F,
  output F_2
);

  wire A, and_1_out, and_2_out, and_3_out, and_4_out, and_5_out, and_6_out, and_7_out, B, button_1_out, C,
       clock_1_out, comparator_1_eq, comparator_2_eq, comparator_3_eq, D, MASK, nand_1_out, nand_2_out,
       nand_3_out, nand_4_out, nand_5_out, not_1_out, not_2_out, not_3_out, not_4_out, not_5_out, rom_2_data;

  Counter #(.width(4), .max('hf), .ongoal("wrap"), .trigger("rising"), .behavior("new")) counter_1 (
    .Q({A, B, C, D}), .clk(clock_1_out), .clr(button_1_out));  // open: load, D, count, carry, preset, down
  Clock #(.highDuration(1), .lowDuration(1)) clock_1 (.out(clock_1_out));
  Button button_1 (.out(button_1_out));
  // Probe on A
  // Probe on B
  // Probe on C
  // Probe on D
  nand nand_1 (nand_1_out, B, B);
  nand nand_2 (nand_2_out, C, C);
  not not_1 (not_1_out, B);
  not not_2 (not_2_out, C);
  nand nand_3 (nand_3_out, A, nand_1_out);
  nand nand_4 (nand_4_out, nand_1_out, C);
  nand nand_5 (nand_5_out, A, nand_2_out, D);
  and and_1 (and_1_out, A, not_1_out);
  and and_2 (and_2_out, not_1_out, C);
  and and_3 (and_3_out, A, not_2_out, D);
  nand nand_6 (F, nand_3_out, nand_4_out, nand_5_out);
  or or_1 (F_2, and_1_out, and_2_out, and_3_out);
  ROM #(.addrWidth(4), .dataWidth(1), .Select("low")) rom_1 (.addr({A, B, C, D}), .data(MASK));
  ROM #(.addrWidth(4), .dataWidth(1), .Select("low")) rom_2 (.addr({A, B, C, D}), .data(rom_2_data));
  and and_4 (and_4_out, F, MASK);
  and and_5 (and_5_out, MASK, rom_2_data);
  and and_6 (and_6_out, F_2, MASK);
  and and_7 (and_7_out, MASK, rom_2_data);
  Comparator #(.width(1), .mode("twosComplement")) comparator_1 (
    .a(and_4_out), .b(and_5_out), .eq(comparator_1_eq));  // open: gt, lt
  Comparator #(.width(1), .mode("twosComplement")) comparator_2 (
    .a(and_6_out), .b(and_7_out), .eq(comparator_2_eq));  // open: gt, lt
  Comparator #(.width(1), .mode("twosComplement")) comparator_3 (.a(F), .b(F_2), .eq(comparator_3_eq));  // open: gt, lt
  not not_3 (not_3_out, comparator_1_eq);
  // Buzzer #(.freq_measure("Hz"), .vol_width(7)) buzzer_1: pin names not known; wires that end beside it: not_3_out
  LED #(.active("false")) led_1 (.in(comparator_1_eq));
  not not_4 (not_4_out, comparator_2_eq);
  // Buzzer #(.freq_measure("Hz"), .vol_width(7)) buzzer_2: pin names not known; wires that end beside it: not_4_out
  LED #(.active("false")) led_2 (.in(comparator_2_eq));
  not not_5 (not_5_out, comparator_3_eq);
  // Buzzer #(.freq_measure("Hz"), .vol_width(7)) buzzer_3: pin names not known; wires that end beside it: not_5_out
  LED #(.active("false")) led_3 (.in(comparator_3_eq));

  // Notes on the sheet:
  //   ROM1
  //   ROM2
  //   contents of rom_1 (hex, n*v repeats v):
  //   5*1 6*0 5*1
  //   contents of rom_2 (hex, n*v repeats v):
  //   0 0 1 1 7*0 1 0 1
endmodule

module \习题4_11_1  (
  output F,
  output F_2
);

  wire A, and_1_out, and_2_out, and_3_out, B, button_1_out, buzzer_1_p1, C, clock_1_out, comparator_1_eq,
       nand_1_out, nand_2_out, nand_3_out, nand_4_out, not_1_out, not_2_out, not_3_out;

  Clock #(.highDuration(1), .lowDuration(1)) clock_1 (.out(clock_1_out));
  Button button_1 (.out(button_1_out));
  Counter #(.width(3), .max('h7), .ongoal("wrap"), .trigger("rising"), .behavior("new")) counter_1 (
    .Q({A, B, C}), .clk(clock_1_out), .clr(button_1_out));  // open: load, D, count, carry, preset, down
  // Probe on A
  // Probe on B
  // Probe on C
  nand nand_1 (nand_1_out, A, B, C);
  not not_1 (not_1_out, A);
  not not_2 (not_2_out, B);
  not not_3 (not_3_out, C);
  nand nand_2 (nand_2_out, A, nand_1_out);
  nand nand_3 (nand_3_out, B, nand_1_out);
  nand nand_4 (nand_4_out, nand_1_out, C);
  and and_1 (and_1_out, A, not_2_out);
  and and_2 (and_2_out, not_1_out, C);
  and and_3 (and_3_out, not_3_out, B);
  nand nand_5 (F_2, nand_2_out, nand_3_out, nand_4_out);
  or or_1 (F, and_1_out, and_2_out, and_3_out);
  Comparator #(.width(1), .mode("twosComplement")) comparator_1 (.a(F), .b(F_2), .eq(comparator_1_eq));  // open: gt, lt
  // Buzzer #(.freq_measure("Hz"), .vol_width(7)) buzzer_1: pin names not known; wires that end beside it: buzzer_1_p1
  not not_4 (buzzer_1_p1, comparator_1_eq);
  LED #(.active("false")) led_1 (.in(comparator_1_eq));
endmodule

module \习题4_11_2  (
  output F,
  output F_2
);

  wire A, and_1_out, and_2_out, and_3_out, and_4_out, B, button_1_out, C, clock_1_out, comparator_1_eq, D,
       nand_1_out, nand_2_out, nand_3_out, nand_4_out, nand_5_out, not_1_out, not_2_out, not_3_out, not_4_out;

  Counter #(.width(4), .max('hf), .ongoal("wrap"), .trigger("rising"), .behavior("new")) counter_1 (
    .Q({A, B, C, D}), .clk(clock_1_out), .clr(button_1_out));  // open: load, D, count, carry, preset, down
  Clock #(.highDuration(1), .lowDuration(1)) clock_1 (.out(clock_1_out));
  Button button_1 (.out(button_1_out));
  // Probe on A
  // Probe on B
  // Probe on C
  // Probe on D
  nand nand_1 (nand_1_out, C, C);
  not not_1 (not_1_out, B);
  not not_2 (not_2_out, C);
  not not_3 (not_3_out, D);
  nand nand_2 (nand_2_out, B, D);
  and and_1 (and_1_out, not_2_out, not_1_out, A);
  and and_2 (and_2_out, B, not_3_out, C);
  and and_3 (and_3_out, A, not_2_out, not_3_out);
  and and_4 (and_4_out, not_1_out, C, D);
  nand nand_3 (nand_3_out, A, nand_1_out, nand_2_out);
  nand nand_4 (nand_4_out, nand_2_out, B, C);
  nand nand_5 (nand_5_out, C, nand_2_out, D);
  or or_1 (F, and_1_out, and_2_out, and_3_out, and_4_out);
  nand nand_6 (F_2, nand_3_out, nand_4_out, nand_5_out);
  Comparator #(.width(1), .mode("twosComplement")) comparator_1 (.a(F), .b(F_2), .eq(comparator_1_eq));  // open: gt, lt
  not not_4 (not_4_out, comparator_1_eq);
  // Buzzer #(.freq_measure("Hz"), .vol_width(7)) buzzer_1: pin names not known; wires that end beside it: not_4_out
  LED #(.active("false")) led_1 (.in(comparator_1_eq));
endmodule
