// Logisim project 第5章例题电路的实现.circ as structural Verilog: 14 circuits, main circuit 例题5.2
module \例题5_1  (
  input  x,
  output y2,
  output y1
);

  wire CP_out, xor_1_out;

  Clock #(.highDuration(1), .lowDuration(1)) CP (.out(CP_out));
  xor xor_1 (xor_1_out, y1, x);
  J_K_Flip_Flop #(.trigger("falling"), .Pre_Clr_Positions("ABOVE_BELOW"), .NegatePresetClear("false"), .enable("false"), .NewFFLayout("true")) j_k_ff_1 (
    .J(xor_1_out), .clk(CP_out), .K(xor_1_out), .Q(y2));  // open: Qn, preset, reset
  J_K_Flip_Flop #(.trigger("falling"), .Pre_Clr_Positions("ABOVE_BELOW"), .NegatePresetClear("false"), .enable("false"), .NewFFLayout("true")) j_k_ff_2 (
    .J(1'b1), .clk(CP_out), .K(1'b1), .Q(y1));  // open: Qn, preset, reset
  // Probe on {y2, y1}
endmodule

module \例题5_2  (
  input  x,
  output Z
);

  wire CP_out, d_ff_1_q, d_ff_1_qn, d_ff_2_q, d_ff_2_qn, nor_1_out, nor_3_out;

  Clock #(.highDuration(1), .lowDuration(1)) CP (.out(CP_out));
  D_Flip_Flop #(.trigger("rising"), .Pre_Clr_Positions("ABOVE_BELOW"), .NegatePresetClear("true"), .enable("false"), .NewFFLayout("true")) d_ff_1 (
    .clk(CP_out), .D(nor_3_out), .Q(d_ff_1_q), .Qn(d_ff_1_qn));  // open: preset, reset
  D_Flip_Flop #(.trigger("rising"), .Pre_Clr_Positions("ABOVE_BELOW"), .NegatePresetClear("true"), .enable("false"), .NewFFLayout("true")) d_ff_2 (
    .clk(CP_out), .D(x), .Q(d_ff_2_q), .Qn(d_ff_2_qn));  // open: preset, reset
  nor nor_1 (nor_1_out, x, x, x);
  nor nor_2 (Z, nor_1_out, d_ff_1_qn, d_ff_2_q);
  nor nor_3 (nor_3_out, d_ff_1_q, d_ff_2_qn, x);

  // Notes on the sheet:
  //   D触发器2
  //   D触发器1
  //   D2
  //   D1
  //   y2
  //   /y2
  //   y1
  //   /y1
  //   /x
  //   D2
endmodule

module \例题5_2的仿真  (
  output Z
);

  wire CP, d_ff_1_qn, d_ff_2_qn, nor_1_out, nor_3_out, x, y1, y2;

  Clock #(.highDuration(1), .lowDuration(1)) u_CP (.out(CP));
  // ProgrammableGenerator #(.nState(3), .Contents("2 4 2*3 15")) x: pin names not known; wires that end beside it: x
  // Digital_Oscilloscope #(.nState(15), .frontlines("rising"), .showclock("true")) digital_oscilloscope_1: pin names not known; wires that end beside it: CP, x, y2, y1, Z
  D_Flip_Flop #(.trigger("rising"), .Pre_Clr_Positions("ABOVE_BELOW"), .NegatePresetClear("true"), .enable("false"), .NewFFLayout("true")) d_ff_1 (
    .clk(CP), .D(nor_3_out), .Q(y2), .Qn(d_ff_1_qn));  // open: preset, reset
  D_Flip_Flop #(.trigger("rising"), .Pre_Clr_Positions("ABOVE_BELOW"), .NegatePresetClear("true"), .enable("false"), .NewFFLayout("true")) d_ff_2 (
    .clk(CP), .D(x), .Q(y1), .Qn(d_ff_2_qn));  // open: preset, reset
  nor nor_1 (nor_1_out, x, x, x);
  nor nor_2 (Z, nor_1_out, d_ff_1_qn, y1);
  nor nor_3 (nor_3_out, y2, d_ff_2_qn, x);

  // Notes on the sheet:
  //   D触发器2
  //   D触发器1
  //   D2
  //   D1
  //   y2
  //   /y2
  //   y1
  //   /y1
  //   /x
  //   D2
endmodule

module \例题5_3  (
  input  x1,
  input  x2,
  output Z
);

  wire CP_out, d_ff_1_q, nand_1_out, nand_2_out, nand_3_out, xor_1_out;

  Clock #(.highDuration(1), .lowDuration(1)) CP (.out(CP_out));
  D_Flip_Flop #(.trigger("rising"), .Pre_Clr_Positions("ABOVE_BELOW"), .NegatePresetClear("false"), .enable("false"), .NewFFLayout("true")) d_ff_1 (
    .clk(CP_out), .D(nand_3_out), .Q(d_ff_1_q));  // open: Qn, preset, reset
  xor xor_1 (xor_1_out, x1, x2);
  nand nand_1 (nand_1_out, xor_1_out, d_ff_1_q);
  nand nand_2 (nand_2_out, x2, x1);
  xor xor_2 (Z, xor_1_out, d_ff_1_q);
  nand nand_3 (nand_3_out, nand_1_out, nand_2_out);

  // Notes on the sheet:
  //   y
endmodule

module \例题5_3的仿真  (
  output Z
);

  wire CP, nand_1_out, nand_2_out, nand_3_out, x1, x1_p1, x2, x2_p1, xor_1_out, y;

  // ProgrammableGenerator #(.nState(3), .Contents("8 2 100 4 4 1")) x1: pin names not known; wires that end beside it: x1_p1
  not not_1 (x1, x1_p1);
  // ProgrammableGenerator #(.nState(3), .Contents("6 2 100 2 6 1")) x2: pin names not known; wires that end beside it: x2_p1
  not not_2 (x2, x2_p1);
  Clock #(.highDuration(1), .lowDuration(1)) u_CP (.out(CP));
  // Digital_Oscilloscope #(.nState(15), .frontlines("rising"), .showclock("true")) digital_oscilloscope_1: pin names not known; wires that end beside it: CP, x1, x2, y, Z
  D_Flip_Flop #(.trigger("rising"), .Pre_Clr_Positions("ABOVE_BELOW"), .NegatePresetClear("false"), .enable("false"), .NewFFLayout("true")) d_ff_1 (
    .clk(CP), .D(nand_3_out), .Q(y));  // open: Qn, preset, reset
  xor xor_1 (xor_1_out, x1, x2);
  nand nand_1 (nand_1_out, xor_1_out, y);
  nand nand_2 (nand_2_out, x2, x1);
  xor xor_2 (Z, xor_1_out, y);
  nand nand_3 (nand_3_out, nand_1_out, nand_2_out);

  // Notes on the sheet:
  //   y
endmodule

module \例题5_4  (
  input  x,
  output Z
);

  wire buzzer_2_p1, comparator_1_eq, comparator_2_eq, CP, not_1_out, xor_1_out, xor_2_out, xor_3_out,
       xor_4_out, xor_6_out, xor_7_out, y1, y2, y3;
  wire [2:0] shift_register_1_q2;

  Clock #(.highDuration(1), .lowDuration(1)) u_CP (.out(CP));
  xor xor_1 (xor_1_out, y3, y2);
  xor xor_2 (xor_2_out, y2, y1);
  Shift_Register #(.width(1), .length(3), .parallel("true"), .trigger("rising")) shift_register_1 (
    .in(x), .clk(CP), .q0(shift_register_1_q2[2]), .q1(shift_register_1_q2[1]), .q2(shift_register_1_q2[0]));  // open: shift, out, load, clr, d0, d1, d2
  xor xor_3 (xor_3_out, y1, x);
  T_Flip_Flop #(.trigger("rising"), .Pre_Clr_Positions("ABOVE_BELOW"), .NegatePresetClear("false"), .enable("false"), .NewFFLayout("true")) t_ff_1 (
    .clk(CP), .T(xor_1_out), .Q(y3));  // open: Qn, preset, reset
  T_Flip_Flop #(.trigger("rising"), .Pre_Clr_Positions("ABOVE_BELOW"), .NegatePresetClear("false"), .enable("false"), .NewFFLayout("true")) t_ff_2 (
    .clk(CP), .T(xor_2_out), .Q(y2));  // open: Qn, preset, reset
  T_Flip_Flop #(.trigger("rising"), .Pre_Clr_Positions("ABOVE_BELOW"), .NegatePresetClear("false"), .enable("false"), .NewFFLayout("true")) t_ff_3 (
    .clk(CP), .T(xor_3_out), .Q(y1));  // open: Qn, preset, reset
  xor xor_4 (xor_4_out, y3, y2);
  xor xor_5 (Z, xor_4_out, y1);
  not not_1 (not_1_out, comparator_1_eq);
  Comparator #(.width(3), .mode("twosComplement")) comparator_1 (
    .a({y1, y2, y3}), .b(shift_register_1_q2), .eq(comparator_1_eq));  // open: gt, lt
  // Buzzer #(.freq_measure("Hz"), .vol_width(7)) buzzer_1: pin names not known; wires that end beside it: not_1_out
  LED #(.active("false")) led_1 (.in(comparator_1_eq));
  xor xor_6 (xor_6_out, shift_register_1_q2[0], shift_register_1_q2[1]);
  xor xor_7 (xor_7_out, xor_6_out, shift_register_1_q2[2]);
  Comparator #(.width(1), .mode("twosComplement")) comparator_2 (
    .a(Z), .b(xor_7_out), .eq(comparator_2_eq));  // open: gt, lt
  // Buzzer #(.freq_measure("Hz"), .vol_width(7)) buzzer_2: pin names not known; wires that end beside it: buzzer_2_p1
  not not_2 (buzzer_2_p1, comparator_2_eq);
  LED #(.active("false")) led_2 (.in(comparator_2_eq));

  // Notes on the sheet:
  //   移位寄存器
  //   y3
  //   y2
  //   y1
endmodule

module \例题5_10_1  (
  input  x,
  output Z
);

  wire CP_out, j_k_ff_1_q, j_k_ff_2_q, nor_1_out, not_1_out, or_1_out;

  Clock #(.highDuration(1), .lowDuration(1)) CP (.out(CP_out));
  not not_1 (not_1_out, x);
  nor nor_1 (nor_1_out, j_k_ff_2_q, x);
  J_K_Flip_Flop #(.trigger("falling"), .Pre_Clr_Positions("ABOVE_BELOW"), .NegatePresetClear("false"), .enable("false"), .NewFFLayout("true")) j_k_ff_1 (
    .J(nor_1_out), .clk(CP_out), .K(not_1_out), .Q(j_k_ff_1_q));  // open: Qn, preset, reset
  J_K_Flip_Flop #(.trigger("falling"), .Pre_Clr_Positions("ABOVE_BELOW"), .NegatePresetClear("false"), .enable("false"), .NewFFLayout("true")) j_k_ff_2 (
    .J(1'b1), .clk(CP_out), .K(1'b1), .Q(j_k_ff_2_q));  // open: Qn, preset, reset
  // Probe on j_k_ff_1_q
  or or_1 (or_1_out, j_k_ff_1_q, x);
  // Probe on j_k_ff_2_q
  and and_1 (Z, or_1_out, j_k_ff_2_q);
endmodule

module \例题5_10_2  (
  input  x,
  output Z
);

  wire and_1_out, CP_out, d_ff_1_q, d_ff_2_q, d_ff_2_qn, nor_1_out, or_1_out, or_2_out;

  Clock #(.highDuration(1), .lowDuration(1)) CP (.out(CP_out));
  and and_1 (and_1_out, d_ff_1_q, x);
  nor nor_1 (nor_1_out, d_ff_1_q, x, d_ff_2_q);
  or or_1 (or_1_out, and_1_out, nor_1_out);
  D_Flip_Flop #(.trigger("rising"), .Pre_Clr_Positions("ABOVE_BELOW"), .NegatePresetClear("false"), .enable("false"), .NewFFLayout("true")) d_ff_1 (
    .clk(CP_out), .D(or_1_out), .Q(d_ff_1_q));  // open: Qn, preset, reset
  D_Flip_Flop #(.trigger("rising"), .Pre_Clr_Positions("ABOVE_BELOW"), .NegatePresetClear("false"), .enable("false"), .NewFFLayout("true")) d_ff_2 (
    .clk(CP_out), .D(d_ff_2_qn), .Q(d_ff_2_q), .Qn(d_ff_2_qn));  // open: preset, reset
  // Probe on d_ff_1_q
  // Probe on d_ff_2_q
  or or_2 (or_2_out, d_ff_1_q, x);
  and and_2 (Z, or_2_out, d_ff_2_q);
endmodule

module \例题5_14  (
  input  x,
  output Z
);

  wire and_1_out, CP_out, t_ff_1_qn, t_ff_2_qn, y1, y2;

  Clock #(.highDuration(1), .lowDuration(1)) CP (.out(CP_out));
  and and_1 (and_1_out, x, t_ff_2_qn);
  T_Flip_Flop #(.trigger("rising"), .Pre_Clr_Positions("ABOVE_BELOW"), .NegatePresetClear("false"), .enable("false"), .NewFFLayout("true")) t_ff_1 (
    .clk(CP_out), .T(and_1_out), .Q(y2), .Qn(t_ff_1_qn));  // open: preset, reset
  T_Flip_Flop #(.trigger("rising"), .Pre_Clr_Positions("ABOVE_BELOW"), .NegatePresetClear("false"), .enable("false"), .NewFFLayout("true")) t_ff_2 (
    .clk(CP_out), .T(x), .Q(y1), .Qn(t_ff_2_qn));  // open: preset, reset
  // Probe on y2
  // Probe on y1
  and and_2 (Z, t_ff_1_qn, x, t_ff_2_qn);
  // Probe on {y2, y1}
endmodule

module \例题5_15  (
  input  x2,
  input  x1,
  output y2,
  output y1
);

  wire and_1_out, and_2_out, and_3_out, and_4_out, CP_out, not_1_out, or_1_out, or_2_out;

  Clock #(.highDuration(1), .lowDuration(1)) CP (.out(CP_out));
  not not_1 (not_1_out, x2);
  and and_1 (and_1_out, not_1_out, x1);
  and and_2 (and_2_out, x2, y1);
  and and_3 (and_3_out, y2, not_1_out);
  and and_4 (and_4_out, x2, x1);
  or or_1 (or_1_out, and_1_out, and_2_out);
  or or_2 (or_2_out, and_3_out, and_4_out);
  D_Flip_Flop #(.trigger("rising"), .Pre_Clr_Positions("ABOVE_BELOW"), .NegatePresetClear("true"), .enable("false"), .NewFFLayout("true")) d_ff_1 (
    .clk(CP_out), .D(or_1_out), .Q(y2));  // open: Qn, preset, reset
  D_Flip_Flop #(.trigger("rising"), .Pre_Clr_Positions("ABOVE_BELOW"), .NegatePresetClear("true"), .enable("false"), .NewFFLayout("true")) d_ff_2 (
    .clk(CP_out), .D(or_2_out), .Q(y1));  // open: Qn, preset, reset

  // Notes on the sheet:
  //   D2
  //   D1
endmodule

module \例题5_16  (
  input  x,
  output Z
);

  wire and_1_out, CP_out, j_k_ff_1_q, j_k_ff_2_q, not_1_out, xor_1_out;

  Clock #(.highDuration(1), .lowDuration(1)) CP (.out(CP_out));
  not not_1 (not_1_out, x);
  and and_1 (and_1_out, not_1_out, j_k_ff_2_q);
  xor xor_1 (xor_1_out, not_1_out, j_k_ff_2_q);
  J_K_Flip_Flop #(.trigger("falling"), .Pre_Clr_Positions("ABOVE_BELOW"), .NegatePresetClear("false"), .enable("false"), .NewFFLayout("true")) j_k_ff_1 (
    .J(and_1_out), .clk(CP_out), .K(xor_1_out), .Q(j_k_ff_1_q));  // open: Qn, preset, reset
  J_K_Flip_Flop #(.trigger("falling"), .Pre_Clr_Positions("ABOVE_BELOW"), .NegatePresetClear("false"), .enable("false"), .NewFFLayout("true")) j_k_ff_2 (
    .J(x), .clk(CP_out), .K(not_1_out), .Q(j_k_ff_2_q));  // open: Qn, preset, reset
  and and_2 (Z, j_k_ff_1_q, j_k_ff_2_q);
endmodule

module \例题5_16的仿真  (
  output Z
);

  wire and_1_out, CP, j_k_ff_1_q, j_k_ff_2_q, not_2_out, x, x_p1, xor_1_out;

  Clock #(.highDuration(1), .lowDuration(1)) u_CP (.out(CP));
  // ProgrammableGenerator #(.nState(5), .Contents("")) x: pin names not known; wires that end beside it: x_p1
  not not_1 (x, x_p1);
  // Digital_Oscilloscope #(.nState(15), .frontlines("rising"), .showclock("true")) digital_oscilloscope_1: pin names not known; wires that end beside it: CP, x, Z
  not not_2 (not_2_out, x);
  and and_1 (and_1_out, not_2_out, j_k_ff_2_q);
  xor xor_1 (xor_1_out, not_2_out, j_k_ff_2_q);
  J_K_Flip_Flop #(.trigger("falling"), .Pre_Clr_Positions("ABOVE_BELOW"), .NegatePresetClear("false"), .enable("false"), .NewFFLayout("true")) j_k_ff_1 (
    .J(and_1_out), .clk(CP), .K(xor_1_out), .Q(j_k_ff_1_q));  // open: Qn, preset, reset
  J_K_Flip_Flop #(.trigger("falling"), .Pre_Clr_Positions("ABOVE_BELOW"), .NegatePresetClear("false"), .enable("false"), .NewFFLayout("true")) j_k_ff_2 (
    .J(x), .clk(CP), .K(not_2_out), .Q(j_k_ff_2_q));  // open: Qn, preset, reset
  and and_2 (Z, j_k_ff_1_q, j_k_ff_2_q);
endmodule

module \例题5_17  (
  input  x,
  output Z
);

  wire and_1_out, and_2_out, CP_out, d_ff_1_q, d_ff_1_qn, d_ff_2_q, d_ff_3_q, nor_1_out, or_1_out, xor_1_out,
       xor_2_out;

  Clock #(.highDuration(1), .lowDuration(1)) CP (.out(CP_out));
  and and_1 (and_1_out, x, d_ff_1_qn);
  xor xor_1 (xor_1_out, d_ff_1_q, x);
  or or_1 (or_1_out, and_1_out, d_ff_2_q);
  nor nor_1 (nor_1_out, d_ff_2_q, d_ff_1_q);
  and and_2 (and_2_out, d_ff_2_q, xor_1_out);
  D_Flip_Flop #(.trigger("rising"), .Pre_Clr_Positions("ABOVE_BELOW"), .NegatePresetClear("false"), .enable("false"), .NewFFLayout("true")) d_ff_1 (
    .clk(CP_out), .D(or_1_out), .Q(d_ff_1_q), .Qn(d_ff_1_qn));  // open: preset, reset
  D_Flip_Flop #(.trigger("rising"), .Pre_Clr_Positions("ABOVE_BELOW"), .NegatePresetClear("false"), .enable("false"), .NewFFLayout("true")) d_ff_2 (
    .clk(CP_out), .D(nor_1_out), .Q(d_ff_2_q));  // open: Qn, preset, reset
  D_Flip_Flop #(.trigger("rising"), .Pre_Clr_Positions("ABOVE_BELOW"), .NegatePresetClear("false"), .enable("false"), .NewFFLayout("true")) d_ff_3 (
    .clk(CP_out), .D(and_2_out), .Q(d_ff_3_q));  // open: Qn, preset, reset
  xor xor_2 (xor_2_out, d_ff_3_q, x);
  nor nor_2 (Z, d_ff_1_qn, d_ff_2_q, xor_2_out);

  // Notes on the sheet:
  //   y3
  //   y2
  //   y1
endmodule

module \例题5_17的仿真  (
  output Z
);

  wire and_1_out, and_2_out, CP, d_ff_1_qn, nor_1_out, or_1_out, x, xor_1_out, xor_2_out, y1, y2, y3;

  Clock #(.highDuration(1), .lowDuration(1)) u_CP (.out(CP));
  // ProgrammableGenerator #(.nState(7), .Contents("")) x: pin names not known; wires that end beside it: x
  // Digital_Oscilloscope #(.nState(35), .frontlines("rising"), .showclock("true")) digital_oscilloscope_1: pin names not known; wires that end beside it: CP, x, Z
  and and_1 (and_1_out, x, d_ff_1_qn);
  xor xor_1 (xor_1_out, y3, x);
  or or_1 (or_1_out, and_1_out, y2);
  nor nor_1 (nor_1_out, y2, y3);
  and and_2 (and_2_out, y2, xor_1_out);
  D_Flip_Flop #(.trigger("rising"), .Pre_Clr_Positions("ABOVE_BELOW"), .NegatePresetClear("false"), .enable("false"), .NewFFLayout("true")) d_ff_1 (
    .clk(CP), .D(or_1_out), .Q(y3), .Qn(d_ff_1_qn));  // open: preset, reset
  D_Flip_Flop #(.trigger("rising"), .Pre_Clr_Positions("ABOVE_BELOW"), .NegatePresetClear("false"), .enable("false"), .NewFFLayout("true")) d_ff_2 (
    .clk(CP), .D(nor_1_out), .Q(y2));  // open: Qn, preset, reset
  D_Flip_Flop #(.trigger("rising"), .Pre_Clr_Positions("ABOVE_BELOW"), .NegatePresetClear("false"), .enable("false"), .NewFFLayout("true")) d_ff_3 (
    .clk(CP), .D(and_2_out), .Q(y1));  // open: Qn, preset, reset
  xor xor_2 (xor_2_out, y1, x);
  nor nor_2 (Z, d_ff_1_qn, y2, xor_2_out);

  // Notes on the sheet:
  //   y3
  //   y2
  //   y1
endmodule
