// Logisim project 第7章例题电路的实现（第1部分）.circ as structural Verilog: 28 circuits, main circuit 例题7.1
module \_4位二进制串行加法器  (
  input  C0,
  input  [3:0] A,
  input  [3:0] B,
  output [3:0] F,
  output C4
);

  wire adder_1_cout, adder_2_cout, adder_3_cout;

  // Probe on A
  // Probe on B
  Adder #(.width(1)) adder_1 (.a(A[0]), .b(B[0]), .out(F[0]), .cin(C0), .cout(adder_1_cout));
  Adder #(.width(1)) adder_2 (.a(A[1]), .b(B[1]), .out(F[1]), .cin(adder_1_cout), .cout(adder_2_cout));
  Adder #(.width(1)) adder_3 (.a(A[2]), .b(B[2]), .out(F[2]), .cin(adder_2_cout), .cout(adder_3_cout));
  // Probe on F
  Adder #(.width(1)) adder_4 (.a(A[3]), .b(B[3]), .out(F[3]), .cin(adder_3_cout), .cout(C4));
endmodule

module \_4位二进制并行加法器_超前进位  (
  input  [3:0] A,
  input  [3:0] B,
  input  C0,
  output [3:0] F,
  output C4
);

  // Probe on A
  // Probe on B
  _74283 #(.VccGndPorts("false"), .ShowInternalStructure("false")) u_74283_1 (
    .pin1(F[1]), .pin2(B[1]), .pin3(A[1]), .pin4(F[0]), .pin5(A[0]), .pin6(B[0]), .pin7(C0), .pin15(B[2]),
    .pin14(A[2]), .pin13(F[2]), .pin12(A[3]), .pin11(B[3]), .pin10(F[3]), .pin9(C4));
  // Probe on F
  // also tied to GND on the sheet: C4
endmodule

module \例题7_1  (
);

  wire buzzer_1_p1, CLK_out, comparator_1_eq, n74283_1_pin7, RST_out;
  wire [3:0] counter_1_q, n74283_1_pin4, n74283_1_pin6, rom_1_data;

  // Probe on counter_1_q
  Counter #(.width(4), .max('hf), .ongoal("wrap"), .trigger("rising"), .behavior("new")) counter_1 (
    .Q(counter_1_q), .clk(CLK_out), .clr(RST_out));  // open: load, D, count, carry, preset, down
  Clock #(.highDuration(1), .lowDuration(1)) CLK (.out(CLK_out));
  Button RST (.out(RST_out));
  _74283 #(.VccGndPorts("false"), .ShowInternalStructure("false")) u_74283_1 (
    .pin1(n74283_1_pin4[1]), .pin2(n74283_1_pin6[1]), .pin3(counter_1_q[1]), .pin4(n74283_1_pin4[0]),
    .pin5(counter_1_q[0]), .pin6(n74283_1_pin6[0]), .pin7(n74283_1_pin7), .pin15(n74283_1_pin6[2]),
    .pin14(counter_1_q[2]), .pin13(n74283_1_pin4[2]), .pin12(counter_1_q[3]), .pin11(n74283_1_pin6[3]),
    .pin10(n74283_1_pin4[3]));  // open: pin9
  ROM #(.addrWidth(4), .dataWidth(4), .Select("low")) rom_1 (.addr(counter_1_q), .data(rom_1_data));
  // Probe on n74283_1_pin4
  // Buzzer #(.freq_measure("Hz"), .vol_width(1)) buzzer_1: pin names not known; wires that end beside it: buzzer_1_p1
  not not_1 (buzzer_1_p1, comparator_1_eq);
  Comparator #(.width(4), .mode("twosComplement")) comparator_1 (
    .a(n74283_1_pin4), .b(rom_1_data), .eq(comparator_1_eq));  // open: gt, lt
  LED #(.active("false")) led_1 (.in(comparator_1_eq));
  // also tied to GND on the sheet: {n74283_1_pin6[2], n74283_1_pin6[3], n74283_1_pin7}
  // also tied to VCC on the sheet: {n74283_1_pin6[0], n74283_1_pin6[1]}

  // Notes on the sheet:
  //   contents of rom_1 (hex, n*v repeats v):
  //   3 4 5 6 7 8 9 a b c d e f 0 1 2
endmodule

module \例题7_2  (
  input  [3:0] A,
  input  [3:0] B,
  input  M,
  output [3:0] F
);

  wire xor_1_out, xor_2_out, xor_3_out, xor_4_out;

  // Probe on A
  // Probe on B
  xor xor_1 (xor_1_out, B[3], M);
  xor xor_2 (xor_2_out, B[2], M);
  xor xor_3 (xor_3_out, B[1], M);
  xor xor_4 (xor_4_out, B[0], M);
  _74283 #(.VccGndPorts("false"), .ShowInternalStructure("false")) u_74283_1 (
    .pin1(F[1]), .pin2(xor_3_out), .pin3(A[1]), .pin4(F[0]), .pin5(A[0]), .pin6(xor_4_out), .pin7(M),
    .pin15(xor_2_out), .pin14(A[2]), .pin13(F[2]), .pin12(A[3]), .pin11(xor_1_out), .pin10(F[3]));  // open: pin9
  // Probe on F
endmodule

module \例题7_3  (
  input  [3:0] A,
  input  [3:0] B,
  input  Cin,
  output [3:0] F,
  output Cout
);

  wire n74283_1_pin2, n74283_1_pin5, n74283_1_pin6, n74283_1_pin7, n74283_1_pin11, n74283_1_pin14,
       n74283_1_pin15;

  _74283 #(.VccGndPorts("false"), .ShowInternalStructure("false")) u_74283_1 (
    .pin1(F[1]), .pin2(n74283_1_pin2), .pin3(Cout), .pin4(F[0]), .pin5(n74283_1_pin5), .pin6(n74283_1_pin6),
    .pin7(n74283_1_pin7), .pin15(n74283_1_pin15), .pin14(n74283_1_pin14), .pin13(F[2]),
    .pin12(n74283_1_pin14), .pin11(n74283_1_pin11), .pin10(F[3]));  // open: pin9
  _74283 #(.VccGndPorts("false"), .ShowInternalStructure("false")) u_74283_2 (
    .pin1(n74283_1_pin2), .pin2(B[1]), .pin3(A[1]), .pin4(n74283_1_pin6), .pin5(A[0]), .pin6(B[0]),
    .pin7(Cin), .pin15(B[2]), .pin14(A[2]), .pin13(n74283_1_pin15), .pin12(A[3]), .pin11(B[3]),
    .pin10(n74283_1_pin11), .pin9(Cout));
  not not_1 (n74283_1_pin14, Cout);
  // also tied to GND on the sheet: n74283_1_pin7
  // also tied to VCC on the sheet: n74283_1_pin5
endmodule

module \例题7_4  (
  input  [3:0] A,
  input  [3:0] B,
  output [7:0] F
);

  wire buzzer_1_p1, comparator_1_eq, n74283_1_pin2, n74283_1_pin6, n74283_1_pin7, n74283_1_pin11,
       n74283_1_pin15, n74283_2_pin2, n74283_2_pin6, n74283_2_pin7, n74283_2_pin11, n74283_2_pin15,
       n74283_3_pin7, n74283_3_pin11, yx01, yx02, yx03, yx10, yx11, yx12, yx13, yx20, yx21, yx22, yx23, yx30,
       yx31, yx32, yx33;
  wire [7:0] multiplier_1_out;

  // Probe on A
  // Probe on B
  and and_1 (yx33, A[3], B[3]);
  and and_2 (yx23, A[3], B[2]);
  and and_3 (yx13, A[3], B[1]);
  and and_4 (yx03, A[3], B[0]);
  and and_5 (yx32, A[2], B[3]);
  and and_6 (yx22, A[2], B[2]);
  and and_7 (yx12, A[2], B[1]);
  and and_8 (yx02, A[2], B[0]);
  and and_9 (yx31, A[1], B[3]);
  and and_10 (yx21, A[1], B[2]);
  and and_11 (yx11, A[1], B[1]);
  and and_12 (yx01, A[1], B[0]);
  and and_13 (yx30, A[0], B[3]);
  and and_14 (yx20, A[0], B[2]);
  and and_15 (yx10, A[0], B[1]);
  and and_16 (F[0], A[0], B[0]);
  _74283 #(.VccGndPorts("false"), .ShowInternalStructure("false")) u_74283_1 (
    .pin1(F[4]), .pin2(n74283_1_pin2), .pin3(yx31), .pin4(F[3]), .pin5(yx30), .pin6(n74283_1_pin6),
    .pin7(n74283_1_pin7), .pin15(n74283_1_pin15), .pin14(yx32), .pin13(F[5]), .pin12(yx33),
    .pin11(n74283_1_pin11), .pin10(F[6]), .pin9(F[7]));
  _74283 #(.VccGndPorts("false"), .ShowInternalStructure("false")) u_74283_2 (
    .pin1(n74283_1_pin6), .pin2(n74283_2_pin2), .pin3(yx21), .pin4(F[2]), .pin5(yx20), .pin6(n74283_2_pin6),
    .pin7(n74283_2_pin7), .pin15(n74283_2_pin15), .pin14(yx22), .pin13(n74283_1_pin2), .pin12(yx23),
    .pin11(n74283_2_pin11), .pin10(n74283_1_pin15), .pin9(n74283_1_pin11));
  Multiplier #(.width(8)) multiplier_1 (.a({4'b0000, B}), .b({4'b0000, A}), .out(multiplier_1_out));  // open: cin, cout
  _74283 #(.VccGndPorts("false"), .ShowInternalStructure("false")) u_74283_3 (
    .pin1(n74283_2_pin6), .pin2(yx02), .pin3(yx11), .pin4(F[1]), .pin5(yx10), .pin6(yx01),
    .pin7(n74283_3_pin7), .pin15(yx03), .pin14(yx12), .pin13(n74283_2_pin2), .pin12(yx13),
    .pin11(n74283_3_pin11), .pin10(n74283_2_pin15), .pin9(n74283_2_pin11));
  // Probe on F
  Comparator #(.width(8), .mode("twosComplement")) comparator_1 (
    .a(F), .b(multiplier_1_out), .eq(comparator_1_eq));  // open: gt, lt
  // Buzzer #(.freq_measure("Hz"), .vol_width(1)) buzzer_1: pin names not known; wires that end beside it: buzzer_1_p1
  not not_1 (buzzer_1_p1, comparator_1_eq);
  LED #(.active("false")) led_1 (.in(comparator_1_eq));
  // also tied to GND on the sheet: {n74283_1_pin7, n74283_2_pin7, n74283_3_pin11, n74283_3_pin7}

  // Other names for the same wires on the sheet: yx00 = F[0]
endmodule

module \译码器_1_2译码器_2_4译码器_3_8译码器_4_16译码器  (
  input  A,
  input  [1:0] A_2,
  input  [3:0] A_3,
  input  [2:0] A_4,
  output Y0,
  output Y0_2,
  output Y1,
  output Y1_2,
  output Y2,
  output Y3,
  output Y4,
  output Y0_3,
  output Y5,
  output Y1_3,
  output Y6,
  output Y2_2,
  output Y7,
  output Y3_2,
  output Y8,
  output Y9,
  output Y10,
  output Y0_4,
  output Y11,
  output Y1_4,
  output Y12,
  output Y2_3,
  output Y13,
  output Y3_3,
  output Y14,
  output Y4_2,
  output Y15,
  output Y5_2,
  output Y6_2,
  output Y7_2
);

  Decoder #(.select(1), .tristate("false"), .disabled("Z"), .enable("true")) decoder_1 (
    .out0(Y0), .out1(Y1), .sel(A), .en(1'b1));
  Decoder #(.select(2), .tristate("false"), .disabled("Z"), .enable("true")) decoder_2 (
    .out0(Y0_3), .out1(Y1_3), .out2(Y2_2), .out3(Y3_2), .sel(A_2), .en(1'b1));
  Decoder #(.select(3), .tristate("false"), .disabled("Z"), .enable("true")) decoder_3 (
    .out0(Y0_4), .out1(Y1_4), .out2(Y2_3), .out3(Y3_3), .out4(Y4_2), .out5(Y5_2), .out6(Y6_2), .out7(Y7_2),
    .sel(A_4), .en(1'b1));
  Decoder #(.select(4), .tristate("false"), .disabled("Z"), .enable("true")) decoder_4 (
    .out0(Y0_2), .out1(Y1_2), .out2(Y2), .out3(Y3), .out4(Y4), .out5(Y5), .out6(Y6), .out7(Y7), .out8(Y8),
    .out9(Y9), .out10(Y10), .out11(Y11), .out12(Y12), .out13(Y13), .out14(Y14), .out15(Y15), .sel(A_3),
    .en(1'b1));
endmodule

// 74138
module \_74138_3_8译码器  (
  input  S1,
  input  nS2,
  input  nS3,
  input  A2,
  input  A1,
  input  A0,
  output nY0,
  output nY1,
  output nY2,
  output nY3,
  output nY4,
  output nY5,
  output nY6,
  output nY7
);

  wire and_1_out, decoder_1_out0, decoder_1_out1, decoder_1_out2, decoder_1_out3, decoder_1_out4,
       decoder_1_out5, decoder_1_out6, decoder_1_out7, not_1_out, not_2_out, not_3_out, not_4_out, not_5_out,
       not_6_out, not_7_out, not_8_out, not_9_out, not_10_out, not_11_out, or_1_out;

  not not_1 (not_1_out, S1);
  not not_2 (not_2_out, nS2);
  not not_3 (not_3_out, nS3);
  or or_1 (or_1_out, not_1_out, nS2, nS3);
  and and_1 (and_1_out, S1, not_2_out, not_3_out);
  Decoder #(.select(3), .tristate("false"), .disabled("Z"), .enable("true")) decoder_1 (
    .out0(decoder_1_out0), .out1(decoder_1_out1), .out2(decoder_1_out2), .out3(decoder_1_out3),
    .out4(decoder_1_out4), .out5(decoder_1_out5), .out6(decoder_1_out6), .out7(decoder_1_out7),
    .sel({A2, A1, A0}), .en(and_1_out));
  not not_4 (not_4_out, decoder_1_out0);
  not not_5 (not_5_out, decoder_1_out1);
  not not_6 (not_6_out, decoder_1_out2);
  not not_7 (not_7_out, decoder_1_out3);
  not not_8 (not_8_out, decoder_1_out4);
  not not_9 (not_9_out, decoder_1_out5);
  not not_10 (not_10_out, decoder_1_out6);
  not not_11 (not_11_out, decoder_1_out7);
  or or_2 (nY0, or_1_out, not_4_out);
  or or_3 (nY1, or_1_out, not_5_out);
  or or_4 (nY2, or_1_out, not_6_out);
  or or_5 (nY3, or_1_out, not_7_out);
  or or_6 (nY4, or_1_out, not_8_out);
  or or_7 (nY5, or_1_out, not_9_out);
  or or_8 (nY6, or_1_out, not_10_out);
  or or_9 (nY7, or_1_out, not_11_out);
endmodule

module \例题7_5  (
  input  Ai,
  input  Bi,
  input  Gi_1,
  output Di,
  output Gi
);

  wire \n74138_3_8译码器_1_ny1 , \n74138_3_8译码器_1_ny2 , \n74138_3_8译码器_1_ny3 , \n74138_3_8译码器_1_ny4 ,
       \n74138_3_8译码器_1_ny7 ;

  \_74138_3_8译码器  \u_74138_3_8译码器_1  (
    .S1(1'b1), .nS2(1'b0), .nS3(1'b0), .A2(Ai), .A1(Bi), .A0(Gi_1), .nY1(\n74138_3_8译码器_1_ny1 ),
    .nY2(\n74138_3_8译码器_1_ny2 ), .nY3(\n74138_3_8译码器_1_ny3 ), .nY4(\n74138_3_8译码器_1_ny4 ),
    .nY7(\n74138_3_8译码器_1_ny7 ));  // open: nY0, nY5, nY6
  nand nand_1 (Di, \n74138_3_8译码器_1_ny1 , \n74138_3_8译码器_1_ny2 , \n74138_3_8译码器_1_ny4 , \n74138_3_8译码器_1_ny7 );
  nand nand_2 (Gi, \n74138_3_8译码器_1_ny1 , \n74138_3_8译码器_1_ny2 , \n74138_3_8译码器_1_ny3 , \n74138_3_8译码器_1_ny7 );
endmodule

module \例题7_6  (
  output F
);

  wire A, B, C, CLK_out, D, \n74138_3_8译码器_1_ny2 , \n74138_3_8译码器_1_ny4 , \n74138_3_8译码器_1_ny6 ,
       \n74138_3_8译码器_2_ny0 , \n74138_3_8译码器_2_ny2 , \n74138_3_8译码器_2_ny4 , \n74138_3_8译码器_2_ny6 , RST_out;

  Counter #(.width(4), .max('hf), .ongoal("wrap"), .trigger("rising"), .behavior("new")) counter_1 (
    .Q({A, B, C, D}), .clk(CLK_out), .clr(RST_out));  // open: load, D, count, carry, preset, down
  Clock #(.highDuration(1), .lowDuration(1)) CLK (.out(CLK_out));
  Button RST (.out(RST_out));
  // Probe on {A, B, C, D}
  \_74138_3_8译码器  \u_74138_3_8译码器_1  (
    .S1(1'b1), .nS2(A), .nS3(1'b0), .A2(B), .A1(C), .A0(D), .nY2(\n74138_3_8译码器_1_ny2 ),
    .nY4(\n74138_3_8译码器_1_ny4 ), .nY6(\n74138_3_8译码器_1_ny6 ));  // open: nY0, nY1, nY3, nY5, nY7
  nand nand_1 (F, \n74138_3_8译码器_1_ny2 , \n74138_3_8译码器_1_ny4 , \n74138_3_8译码器_1_ny6 , \n74138_3_8译码器_2_ny0 , \n74138_3_8译码器_2_ny2 , \n74138_3_8译码器_2_ny4 , \n74138_3_8译码器_2_ny6 );
  \_74138_3_8译码器  \u_74138_3_8译码器_2  (
    .S1(A), .nS2(1'b0), .nS3(1'b0), .A2(B), .A1(C), .A0(D), .nY0(\n74138_3_8译码器_2_ny0 ),
    .nY2(\n74138_3_8译码器_2_ny2 ), .nY4(\n74138_3_8译码器_2_ny4 ), .nY6(\n74138_3_8译码器_2_ny6 ));  // open: nY1, nY3, nY5, nY7
endmodule

// 7442
module \_7442_二十进制译码器  (
  input  A3,
  input  A2,
  input  A1,
  input  A0,
  output nY0,
  output nY1,
  output nY2,
  output nY3,
  output nY4,
  output nY5,
  output nY6,
  output nY7,
  output nY8,
  output nY9
);

  wire not_1_out, not_2_out, not_3_out, not_4_out;

  not not_1 (not_1_out, A3);
  not not_2 (not_2_out, A2);
  not not_3 (not_3_out, A1);
  not not_4 (not_4_out, A0);
  or or_1 (nY0, A3, A2, A1, A0);
  or or_2 (nY1, A3, A2, A1, not_4_out);
  or or_3 (nY2, A3, A2, not_3_out, A0);
  or or_4 (nY3, A3, A2, not_3_out, not_4_out);
  or or_5 (nY4, A3, not_2_out, A1, A0);
  or or_6 (nY5, A3, not_2_out, A1, not_4_out);
  or or_7 (nY6, A3, not_2_out, not_3_out, A0);
  or or_8 (nY7, A3, not_2_out, not_3_out, not_4_out);
  or or_9 (nY8, not_1_out, A2, A1, A0);
  or or_10 (nY9, not_1_out, A2, A1, not_4_out);
endmodule

module \_7442_二十进制译码器_的使用  (
  output [9:0] out_1
);

  wire CLK_out, RST_out;
  wire [3:0] counter_1_q;

  Clock #(.highDuration(1), .lowDuration(1)) CLK (.out(CLK_out));
  Button RST (.out(RST_out));
  // Probe on counter_1_q
  Counter #(.width(4), .max('hf), .ongoal("wrap"), .trigger("rising"), .behavior("new")) counter_1 (
    .Q(counter_1_q), .clk(CLK_out), .clr(RST_out));  // open: load, D, count, carry, preset, down
  \_7442_二十进制译码器  \u_7442_二十进制译码器_1  (
    .A3(counter_1_q[3]), .A2(counter_1_q[2]), .A1(counter_1_q[1]), .A0(counter_1_q[0]), .nY0(out_1[9]),
    .nY1(out_1[8]), .nY2(out_1[7]), .nY3(out_1[6]), .nY4(out_1[5]), .nY5(out_1[4]), .nY6(out_1[3]),
    .nY7(out_1[2]), .nY8(out_1[1]), .nY9(out_1[0]));
endmodule

module \_7447_七段显示译码器  (
  input  LT,
  input  BI,
  input  RBI
);

  wire CLK_out, n7447_1_pin9, n7447_1_pin10, n7447_1_pin11, n7447_1_pin12, n7447_1_pin13, n7447_1_pin14,
       n7447_1_pin15, RST_out;
  wire [3:0] counter_1_q;

  // Probe on counter_1_q
  Counter #(.width(4), .max('hf), .ongoal("wrap"), .trigger("rising"), .behavior("new")) counter_1 (
    .Q(counter_1_q), .clk(CLK_out), .clr(RST_out));  // open: load, D, count, carry, preset, down
  Clock #(.highDuration(1), .lowDuration(1)) CLK (.out(CLK_out));
  Button RST (.out(RST_out));
  _7447 #(.VccGndPorts("false"), .ShowInternalStructure("false")) u_7447_1 (
    .pin1(counter_1_q[1]), .pin2(counter_1_q[2]), .pin3(LT), .pin4(BI), .pin5(RBI), .pin6(counter_1_q[3]),
    .pin7(counter_1_q[0]), .pin15(n7447_1_pin15), .pin14(n7447_1_pin14), .pin13(n7447_1_pin13),
    .pin12(n7447_1_pin12), .pin11(n7447_1_pin11), .pin10(n7447_1_pin10), .pin9(n7447_1_pin9));
  _7_Segment_Display #(.active("true")) u_7_segment_display_1 (
    .g(n7447_1_pin14), .f(n7447_1_pin15), .a(n7447_1_pin13), .b(n7447_1_pin12), .e(n7447_1_pin9),
    .d(n7447_1_pin10), .c(n7447_1_pin11), .dp(1'b0));
endmodule

module \七段显示译码器  (
  input  en,
  input  RBI,
  input  BI,
  input  LT
);

  wire CLK_out, displaydecoder_1_p2, displaydecoder_1_p3, displaydecoder_1_p4, displaydecoder_1_p5,
       displaydecoder_1_p7, displaydecoder_1_p8, displaydecoder_1_p9, RST_out;
  wire [3:0] counter_1_q;

  // Probe on counter_1_q
  Counter #(.width(4), .max('hf), .ongoal("wrap"), .trigger("rising"), .behavior("new")) counter_1 (
    .Q(counter_1_q), .clk(CLK_out), .clr(RST_out));  // open: load, D, count, carry, preset, down
  Clock #(.highDuration(1), .lowDuration(1)) CLK (.out(CLK_out));
  Button RST (.out(RST_out));
  _7_Segment_Display #(.active("true")) u_7_segment_display_1 (
    .g(displaydecoder_1_p9), .f(displaydecoder_1_p8), .a(displaydecoder_1_p2), .b(displaydecoder_1_p3),
    .e(displaydecoder_1_p7), .d(displaydecoder_1_p5), .c(displaydecoder_1_p4), .dp(1'b0));
  // DisplayDecoder #(.multibit("true")) displaydecoder_1: pin names not known; wires that end beside it: en, displaydecoder_1_p2, displaydecoder_1_p3, displaydecoder_1_p4, displaydecoder_1_p5, counter_1_q, displaydecoder_1_p7, displaydecoder_1_p8, displaydecoder_1_p9, RBI, BI, LT
endmodule

module \_8421码编码器  (
  input  I0,
  input  I1,
  input  I2,
  input  I3,
  input  I4,
  input  I5,
  input  I6,
  input  I7,
  input  I8,
  input  I9,
  output A,
  output B,
  output C,
  output D,
  output S
);

  wire nor_1_out;

  nand nand_1 (A, I8, I9);
  nand nand_2 (B, I6, I7, I5, I4);
  nand nand_3 (C, I6, I7, I3, I2);
  nand nand_4 (D, I9, I7, I5, I3, I1);
  nor nor_1 (nor_1_out, A, B, C, D);
  nand nand_5 (S, nor_1_out, I0);
endmodule

// 74148
module \_74148_优先编码器  (
  input  nI0,
  input  nI1,
  input  nI2,
  input  nI3,
  input  nI4,
  input  nI5,
  input  nI6,
  input  nI7,
  input  nIs,
  output Os,
  output nQex,
  output nQa,
  output nQb,
  output nQc
);

  wire and_1_out, not_1_out, not_2_out, not_3_out, not_4_out, not_5_out, not_6_out, not_7_out, not_8_out,
       not_9_out, not_10_out, not_11_out, not_12_out, not_13_out, or_2_out, priority_encoder_1_en_out;
  wire [2:0] priority_encoder_1_out;

  and and_1 (and_1_out, nI0, nI1, nI2, nI3, nI4, nI5, nI6, nI7);
  not not_1 (not_1_out, nI0);
  not not_2 (not_2_out, nI1);
  not not_3 (not_3_out, nI2);
  not not_4 (not_4_out, nI3);
  not not_5 (not_5_out, nI4);
  not not_6 (not_6_out, nI5);
  not not_7 (not_7_out, nI6);
  not not_8 (not_8_out, nI7);
  Priority_Encoder #(.select(3), .disabled(0)) priority_encoder_1 (
    .in0(not_1_out), .in1(not_2_out), .in2(not_3_out), .in3(not_4_out), .in4(not_5_out), .in5(not_6_out),
    .in6(not_7_out), .in7(not_8_out), .out(priority_encoder_1_out), .en_out(priority_encoder_1_en_out),
    .en_in(not_9_out));  // open: gs
  not not_9 (not_9_out, nIs);
  not not_10 (not_10_out, and_1_out);
  or or_1 (nQex, nIs, priority_encoder_1_en_out);
  not not_11 (not_11_out, priority_encoder_1_out[0]);
  not not_12 (not_12_out, priority_encoder_1_out[1]);
  not not_13 (not_13_out, priority_encoder_1_out[2]);
  or or_2 (or_2_out, and_1_out, nIs);
  or or_3 (Os, not_10_out, nIs);
  or or_4 (nQa, or_2_out, not_11_out);
  or or_5 (nQb, or_2_out, not_12_out);
  or or_6 (nQc, not_13_out, or_2_out);
endmodule

module \例题7_7  (
  input  nIzs,
  input  nIz15,
  input  nIz14,
  input  nIz13,
  input  nIz12,
  input  nIz11,
  input  nIz10,
  input  nIz9,
  input  nIz8,
  input  nIz7,
  input  nIz6,
  input  nIz5,
  input  nIz4,
  input  nIz3,
  input  nIz2,
  input  nIz1,
  input  nIz0,
  output nQzex,
  output nQzd,
  output nQzc,
  output nQzb,
  output nQza,
  output Ozs
);

  wire \n74148_优先编码器_1_nqa , \n74148_优先编码器_1_nqb , \n74148_优先编码器_1_nqc , \n74148_优先编码器_1_os ,
       \n74148_优先编码器_2_nqa , \n74148_优先编码器_2_nqb , \n74148_优先编码器_2_nqc , \n74148_优先编码器_2_nqex ;

  \_74148_优先编码器  \u_74148_优先编码器_1  (
    .nI0(nIz8), .nI1(nIz9), .nI2(nIz10), .nI3(nIz11), .nI4(nIz12), .nI5(nIz13), .nI6(nIz14), .nI7(nIz15),
    .nIs(nIzs), .Os(\n74148_优先编码器_1_os ), .nQex(nQzd), .nQa(\n74148_优先编码器_1_nqa ),
    .nQb(\n74148_优先编码器_1_nqb ), .nQc(\n74148_优先编码器_1_nqc ));
  \_74148_优先编码器  \u_74148_优先编码器_2  (
    .nI0(nIz0), .nI1(nIz1), .nI2(nIz2), .nI3(nIz3), .nI4(nIz4), .nI5(nIz5), .nI6(nIz6), .nI7(nIz7),
    .nIs(\n74148_优先编码器_1_os ), .Os(Ozs), .nQex(\n74148_优先编码器_2_nqex ), .nQa(\n74148_优先编码器_2_nqa ),
    .nQb(\n74148_优先编码器_2_nqb ), .nQc(\n74148_优先编码器_2_nqc ));
  and and_1 (nQzex, nQzd, \n74148_优先编码器_2_nqex );
  and and_2 (nQzc, \n74148_优先编码器_1_nqc , \n74148_优先编码器_2_nqc );
  and and_3 (nQzb, \n74148_优先编码器_1_nqb , \n74148_优先编码器_2_nqb );
  and and_4 (nQza, \n74148_优先编码器_1_nqa , \n74148_优先编码器_2_nqa );
endmodule

// 74152
module \_74152_8路多路选择器  (
  input  D0,
  input  D1,
  input  D2,
  input  D3,
  input  D4,
  input  D5,
  input  D6,
  input  D7,
  input  A2,
  input  A1,
  input  A0,
  output Y
);

  Multiplexer #(.select(3), .width(1), .disabled("Z"), .enable("false")) multiplexer_1 (
    .in0(D0), .in1(D1), .in2(D2), .in3(D3), .in4(D4), .in5(D5), .in6(D6), .in7(D7), .out(Y),
    .sel({A2, A1, A0}));
endmodule

// 74153
module \_74153_双4路多路选择器  (
  input  _1D0,
  input  _2D0,
  input  _1D1,
  input  _2D1,
  input  _1D2,
  input  _2D2,
  input  _1D3,
  input  _2D3,
  input  A1,
  input  A0,
  input  _1G,
  input  _2G,
  output _1Y,
  output _2Y
);

  wire multiplexer_1_out, multiplexer_2_out, not_1_out, not_2_out;

  not not_1 (not_1_out, _1G);
  Multiplexer #(.select(2), .width(1), .disabled("Z"), .enable("true")) multiplexer_1 (
    .in0(_1D0), .in1(_1D1), .in2(_1D2), .in3(_1D3), .out(multiplexer_1_out), .sel({A1, A0}), .en(not_1_out));
  and and_1 (_1Y, multiplexer_1_out, not_1_out);
  not not_2 (not_2_out, _2G);
  Multiplexer #(.select(2), .width(1), .disabled("Z"), .enable("true")) multiplexer_2 (
    .in0(_2D0), .in1(_2D1), .in2(_2D2), .in3(_2D3), .out(multiplexer_2_out), .sel({A1, A0}), .en(not_2_out));
  and and_2 (_2Y, multiplexer_2_out, not_2_out);
endmodule

module \例题7_8_1  (
  output F
);

  wire A, B, C, CLK_out, RST_out;

  // Probe on {A, B, C}
  Counter #(.width(3), .max('h7), .ongoal("wrap"), .trigger("rising"), .behavior("new")) counter_1 (
    .Q({A, B, C}), .clk(CLK_out), .clr(RST_out));  // open: load, D, count, carry, preset, down
  Clock #(.highDuration(1), .lowDuration(1)) CLK (.out(CLK_out));
  Button RST (.out(RST_out));
  \_74152_8路多路选择器  \u_74152_8路多路选择器_1  (
    .D4(1'b0), .D5(1'b1), .D6(1'b1), .D7(1'b0), .A2(A), .A1(B), .Y(F), .A0(C), .D0(1'b0), .D1(1'b0),
    .D2(1'b1), .D3(1'b1));
endmodule

module \例题7_8_2  (
  output F
);

  wire A, B, C, CLK_out, not_1_out, RST_out;

  // Probe on {A, B, C}
  Counter #(.width(3), .max('h7), .ongoal("wrap"), .trigger("rising"), .behavior("new")) counter_1 (
    .Q({A, B, C}), .clk(CLK_out), .clr(RST_out));  // open: load, D, count, carry, preset, down
  Clock #(.highDuration(1), .lowDuration(1)) CLK (.out(CLK_out));
  Button RST (.out(RST_out));
  not not_1 (not_1_out, C);
  \_74153_双4路多路选择器  \u_74153_双4路多路选择器_1  (
    ._1D0(1'b0), ._1D1(1'b1), ._1D2(C), ._1D3(not_1_out), .A1(A), .A0(B), ._1G(1'b0), ._1Y(F));  // open: _2D0, _2D1, _2D2, _2D3, _2G, _2Y
endmodule

module \例题7_9_1  (
  output F
);

  wire A, and_1_out, and_2_out, B, C, CLK_out, D, not_1_out, not_2_out, not_3_out, or_1_out, RST_out;

  // Probe on {A, B, C, D}
  Counter #(.width(4), .max('hf), .ongoal("wrap"), .trigger("rising"), .behavior("new")) counter_1 (
    .Q({A, B, C, D}), .clk(CLK_out), .clr(RST_out));  // open: load, D, count, carry, preset, down
  Clock #(.highDuration(1), .lowDuration(1)) CLK (.out(CLK_out));
  Button RST (.out(RST_out));
  not not_1 (not_1_out, C);
  not not_2 (not_2_out, D);
  and and_1 (and_1_out, not_1_out, D);
  or or_1 (or_1_out, not_2_out, C);
  and and_2 (and_2_out, D, C);
  not not_3 (not_3_out, and_2_out);
  \_74153_双4路多路选择器  \u_74153_双4路多路选择器_1  (
    ._1D0(or_1_out), ._1D1(and_2_out), ._1D2(not_3_out), ._1D3(and_1_out), .A1(A), .A0(B), ._1G(1'b0), ._1Y(F));  // open: _2D0, _2D1, _2D2, _2D3, _2G, _2Y
endmodule

module \例题7_9_2  (
  output F
);

  wire A, B, C, CLK_out, D, not_1_out, not_2_out, RST_out;

  // Probe on {A, B, C, D}
  Counter #(.width(4), .max('hf), .ongoal("wrap"), .trigger("rising"), .behavior("new")) counter_1 (
    .Q({A, B, C, D}), .clk(CLK_out), .clr(RST_out));  // open: load, D, count, carry, preset, down
  Clock #(.highDuration(1), .lowDuration(1)) CLK (.out(CLK_out));
  Button RST (.out(RST_out));
  not not_1 (not_1_out, A);
  not not_2 (not_2_out, B);
  \_74153_双4路多路选择器  \u_74153_双4路多路选择器_1  (
    ._1D0(not_2_out), ._1D1(A), ._1D2(not_2_out), ._1D3(not_1_out), .A1(C), .A0(D), ._1G(1'b0), ._1Y(F));  // open: _2D0, _2D1, _2D2, _2D3, _2G, _2Y
endmodule

module \例题7_10  (
  output F1,
  output F2
);

  wire A, and_1_out, B, C, CLK_out, D, not_1_out, not_2_out, or_1_out, RST_out;

  Counter #(.width(4), .max('hf), .ongoal("wrap"), .trigger("rising"), .behavior("new")) counter_1 (
    .Q({A, B, C, D}), .clk(CLK_out), .clr(RST_out));  // open: load, D, count, carry, preset, down
  Clock #(.highDuration(1), .lowDuration(1)) CLK (.out(CLK_out));
  Button RST (.out(RST_out));
  // Probe on {A, B, C, D}
  not not_1 (not_1_out, C);
  not not_2 (not_2_out, D);
  or or_1 (or_1_out, D, not_1_out);
  and and_1 (and_1_out, C, not_2_out);
  \_74153_双4路多路选择器  \u_74153_双4路多路选择器_1  (
    ._1D0(not_1_out), ._2D0(1'b0), ._1D1(D), ._2D1(1'b0), ._1D2(and_1_out), ._2D2(not_2_out), ._1D3(D),
    ._2D3(or_1_out), .A1(A), .A0(B), ._1G(1'b0), ._2G(1'b0), ._1Y(F1), ._2Y(F2));
endmodule

module \_4路多路分配器  (
  input  D,
  input  A1,
  input  A0,
  output f0,
  output f1,
  output f2,
  output f3
);

  Demultiplexer #(.select(2), .width(1), .tristate("false"), .disabled("Z"), .enable("false")) demultiplexer_1 (
    .out0(f0), .out1(f1), .out2(f2), .out3(f3), .in(D), .sel({A1, A0}));
endmodule

module \_8路多路分配器  (
  input  D,
  input  A2,
  input  A1,
  input  A0,
  output f0,
  output f1,
  output f2,
  output f3,
  output f4,
  output f5,
  output f6,
  output f7
);

  Demultiplexer #(.select(3), .width(1), .tristate("false"), .disabled("Z"), .enable("false")) demultiplexer_1 (
    .out0(f0), .out1(f1), .out2(f2), .out3(f3), .out4(f4), .out5(f5), .out6(f6), .out7(f7), .in(D),
    .sel({A2, A1, A0}));
endmodule

module \_8路数据传输  (
  input  D0,
  input  D1,
  input  D2,
  input  D3,
  input  D4,
  input  D5,
  input  D6,
  input  D7,
  input  A,
  input  B,
  input  C,
  output f0,
  output f1,
  output f2,
  output f3,
  output f4,
  output f5,
  output f6,
  output f7
);

  wire \n74152_8路多路选择器_1_y ;

  \_74152_8路多路选择器  \u_74152_8路多路选择器_1  (
    .D4(D4), .D5(D5), .D6(D6), .D7(D7), .A2(A), .A1(B), .Y(\n74152_8路多路选择器_1_y ), .A0(C), .D0(D0), .D1(D1),
    .D2(D2), .D3(D3));
  \_8路多路分配器  \u_8路多路分配器_1  (
    .D(\n74152_8路多路选择器_1_y ), .A2(A), .A1(B), .A0(C), .f0(f0), .f1(f1), .f2(f2), .f3(f3), .f4(f4), .f5(f5),
    .f6(f6), .f7(f7));
endmodule

module \例题7_11  (
  output F
);

  wire A, B, C, CLK_2_out, CLK_out, \n74138_3_8译码器_1_ny0 , \n74138_3_8译码器_1_ny1 , \n74138_3_8译码器_1_ny2 ,
       \n74138_3_8译码器_1_ny3 , \n74138_3_8译码器_1_ny4 , \n74138_3_8译码器_1_ny5 , \n74138_3_8译码器_1_ny6 ,
       \n74138_3_8译码器_1_ny7 , RST_2_out, RST_out, X, Y, Z;

  // Probe on {X, Y, Z}
  Counter #(.width(3), .max('h7), .ongoal("wrap"), .trigger("rising"), .behavior("new")) counter_1 (
    .Q({X, Y, Z}), .clk(CLK_out), .clr(RST_out));  // open: load, D, count, carry, preset, down
  Clock #(.highDuration(1), .lowDuration(1)) CLK (.out(CLK_out));
  Button RST (.out(RST_out));
  // Probe on {A, B, C}
  Counter #(.width(3), .max('h7), .ongoal("wrap"), .trigger("rising"), .behavior("new")) counter_2 (
    .Q({A, B, C}), .clk(CLK_2_out), .clr(RST_2_out));  // open: load, D, count, carry, preset, down
  Clock #(.highDuration(1), .lowDuration(1)) CLK_2 (.out(CLK_2_out));
  Button RST_2 (.out(RST_2_out));
  \_74138_3_8译码器  \u_74138_3_8译码器_1  (
    .S1(1'b1), .nS2(1'b0), .nS3(1'b0), .A2(A), .A1(B), .A0(C), .nY0(\n74138_3_8译码器_1_ny0 ),
    .nY1(\n74138_3_8译码器_1_ny1 ), .nY2(\n74138_3_8译码器_1_ny2 ), .nY3(\n74138_3_8译码器_1_ny3 ),
    .nY4(\n74138_3_8译码器_1_ny4 ), .nY5(\n74138_3_8译码器_1_ny5 ), .nY6(\n74138_3_8译码器_1_ny6 ),
    .nY7(\n74138_3_8译码器_1_ny7 ));
  \_74152_8路多路选择器  \u_74152_8路多路选择器_1  (
    .D4(\n74138_3_8译码器_1_ny4 ), .D5(\n74138_3_8译码器_1_ny5 ), .D6(\n74138_3_8译码器_1_ny6 ),
    .D7(\n74138_3_8译码器_1_ny7 ), .A2(X), .A1(Y), .Y(F), .A0(Z), .D0(\n74138_3_8译码器_1_ny0 ),
    .D1(\n74138_3_8译码器_1_ny1 ), .D2(\n74138_3_8译码器_1_ny2 ), .D3(\n74138_3_8译码器_1_ny3 ));
endmodule
