// Logisim project 第7章例题电路的实现（第2部分）.circ as structural Verilog: 22 circuits, main circuit 例题7.12
// 74193
module \_74193芯片  (
  input  A,
  input  B,
  input  C,
  input  D,
  input  CPu,
  input  CPd,
  input  CLR,
  input  nLD,
  output Qa,
  output Qb,
  output Qc,
  output Qd_,
  output nQcc,
  output nQcb
);

  wire counter_1_carry, CP, EN, Inv, LOAD, not_1_out, or_1_out;
  wire [3:0] OUT, register_1_q;

  // Probe on {D, C, B, A}
  and and_1 (CP, CPu, CPd);
  or or_1 (or_1_out, CLR, LOAD);
  nor nor_1 (LOAD, CLR, nLD);
  // Probe on OUT
  Counter #(.width(4), .max('hf), .ongoal("wrap"), .trigger("rising"), .behavior("new")) counter_1 (
    .load(1'b0), .D({D, C, B, A}), .count(EN), .Q(OUT), .carry(counter_1_carry), .clk(CP), .clr(or_1_out),
    .preset(1'b0), .down(Inv));
  D_Flip_Flop #(.trigger("rising"), .Pre_Clr_Positions("ABOVE_BELOW"), .NegatePresetClear("false"), .enable("false"), .NewFFLayout("true")) d_ff_1 (
    .clk(CP), .D(counter_1_carry), .Qn(nQcb));  // open: Q, preset, reset
  and and_2 (EN, nLD, ~CLR);  // AND_Gate
  Register #(.width(4), .trigger("rising"), .Select("low")) register_1 (
    .D({D, C, B, A}), .Q(register_1_q), .clk(LOAD), .clr(CLR));  // open: en
  not not_1 (not_1_out, CPu);
  // Probe on register_1_q
  Register #(.width(1), .trigger("rising"), .Select("low")) register_2 (
    .Q(Inv), .clr(not_1_out), .preset(CPu));  // open: D, en, clk, cs
  Adder #(.width(4)) adder_1 (.a(register_1_q), .b(OUT), .out({Qd_, Qc, Qb, Qa}));  // open: cin, cout
  // Probe on {Qd_, Qc, Qb, Qa}

  assign nQcc = nQcb;

  // Other names for the same wires on the sheet: ABCD[3:0] = {D, C, B, A}

  // Notes on the sheet:
  //   74193芯片（双时钟4位二进制同步可逆计数器）
endmodule

module \_74193芯片_置0_置数  (
  input  CPu,
  input  CPd,
  input  A,
  input  B,
  input  C,
  input  D,
  input  CLR,
  input  nLD,
  output Qa,
  output Qb,
  output Qc,
  output Qd
);

  \_74193芯片  \u_74193芯片_1  (
    .A(A), .B(B), .C(C), .D(D), .CPu(CPu), .CPd(CPd), .CLR(CLR), .nLD(nLD), .Qa(Qa), .Qb(Qb), .Qc(Qc),
    .Qd_(Qd));  // open: nQcc, nQcb
  // Probe on {Qd, Qc, Qb, Qa}

  // Notes on the sheet:
  //   74193芯片（置0、置数）
endmodule

module \_74193芯片_累加计数  (
  input  CPd,
  input  A,
  input  B,
  input  C,
  input  D,
  input  CLR,
  input  nLD,
  output Qa,
  output Qb,
  output Qc,
  output Qd,
  output nQcc
);

  wire CPu_out;

  Clock #(.highDuration(1), .lowDuration(1)) CPu (.out(CPu_out));
  \_74193芯片  \u_74193芯片_1  (
    .A(A), .B(B), .C(C), .D(D), .CPu(CPu_out), .CPd(CPd), .CLR(CLR), .nLD(nLD), .Qa(Qa), .Qb(Qb), .Qc(Qc),
    .Qd_(Qd), .nQcc(nQcc));  // open: nQcb
  // Probe on {Qd, Qc, Qb, Qa}

  // Notes on the sheet:
  //   74193芯片（累加计数）
endmodule

module \_74193芯片_累减计数  (
  input  CPu,
  input  A,
  input  B,
  input  C,
  input  D,
  input  CLR,
  input  nLD,
  output Qa,
  output Qb,
  output Qc,
  output Qd,
  output nQcb
);

  wire CPd_out;

  Clock #(.highDuration(1), .lowDuration(1)) CPd (.out(CPd_out));
  \_74193芯片  \u_74193芯片_1  (
    .A(A), .B(B), .C(C), .D(D), .CPu(CPu), .CPd(CPd_out), .CLR(CLR), .nLD(nLD), .Qa(Qa), .Qb(Qb), .Qc(Qc),
    .Qd_(Qd), .nQcb(nQcb));  // open: nQcc
  // Probe on {Qd, Qc, Qb, Qa}

  // Notes on the sheet:
  //   74193芯片（累减计数）
endmodule

module \例题7_12  (
  output Q0,
  output Q1,
  output Q2,
  output Q3
);

  wire and_1_out, clock_1_out;

  Clock #(.highDuration(1), .lowDuration(1)) clock_1 (.out(clock_1_out));
  \_74193芯片  \u_74193芯片_1  (
    .CPu(clock_1_out), .CPd(1'b1), .CLR(and_1_out), .nLD(1'b1), .Qa(Q0), .Qb(Q1), .Qc(Q2), .Qd_(Q3));  // open: A, B, C, D, nQcc, nQcb
  and and_1 (and_1_out, Q3, Q1);
  // Probe on {Q3, Q2, Q1, Q0}

  // Notes on the sheet:
  //   CPu
  //   CPd
  //   CLR
  //   /LD
  //   例题7.12（模10加法计数器）
endmodule

module \例题7_13  (
  output Q0,
  output Q1,
  output Q2,
  output Q3
);

  wire button_1_out, clock_1_out, or_1_out, xor_1_out;

  Clock #(.highDuration(1), .lowDuration(1)) clock_1 (.out(clock_1_out));
  Button button_1 (.out(button_1_out));
  \_74193芯片  \u_74193芯片_1  (
    .A(1'b1), .B(1'b1), .C(1'b1), .D(1'b1), .CPu(1'b1), .CPd(clock_1_out), .CLR(1'b0), .nLD(xor_1_out),
    .Qa(Q0), .Qb(Q1), .Qc(Q2), .Qd_(Q3));  // open: nQcc, nQcb
  xor xor_1 (xor_1_out, button_1_out, or_1_out);
  // Probe on {Q3, Q2, Q1, Q0}
  or or_1 (or_1_out, Q3, Q2);

  // Notes on the sheet:
  //   CPu
  //   CPd
  //   Reset
  //   例题7.13（模12减法计数器）
  //   CLR
  //   /LD
endmodule

module \模256减法计数器  (
);

  wire clock_1_out, \n74193芯片_1_nqcb , not_1_out, \复位_out ;
  wire [7:0] \n74193芯片_1_qa ;

  Clock #(.highDuration(1), .lowDuration(1)) clock_1 (.out(clock_1_out));
  Button \u_复位  (.out(\复位_out ));
  // Probe on \n74193芯片_1_qa 
  \_74193芯片  \u_74193芯片_1  (
    .CPu(1'b1), .CPd(clock_1_out), .CLR(\复位_out ), .Qa(\n74193芯片_1_qa [0]), .Qb(\n74193芯片_1_qa [1]),
    .Qc(\n74193芯片_1_qa [2]), .Qd_(\n74193芯片_1_qa [3]), .nQcb(\n74193芯片_1_nqcb ));  // open: A, B, C, D, nLD, nQcc
  not not_1 (not_1_out, \n74193芯片_1_nqcb );
  \_74193芯片  \u_74193芯片_2  (
    .CPu(1'b1), .CPd(not_1_out), .CLR(\复位_out ), .Qa(\n74193芯片_1_qa [4]), .Qb(\n74193芯片_1_qa [5]),
    .Qc(\n74193芯片_1_qa [6]), .Qd_(\n74193芯片_1_qa [7]));  // open: A, B, C, D, nLD, nQcc, nQcb

  // Notes on the sheet:
  //   CPu
  //   CPd
  //   /Qcb
  //   模256减法计数器
  //   CPu
  //   CPd
endmodule

module \例题7_14  (
  output Q0,
  output Q1,
  output Q2,
  output Q3,
  output Q4,
  output Q5,
  output Q6,
  output Q7
);

  wire and_1_out, button_1_out, clock_1_out, \n74193芯片_1_nqcc , not_1_out, or_1_out;

  Clock #(.highDuration(1), .lowDuration(1)) clock_1 (.out(clock_1_out));
  \_74193芯片  \u_74193芯片_1  (
    .CPu(clock_1_out), .CPd(1'b1), .CLR(or_1_out), .nLD(1'b1), .Qa(Q0), .Qb(Q1), .Qc(Q2), .Qd_(Q3),
    .nQcc(\n74193芯片_1_nqcc ));  // open: A, B, C, D, nQcb
  not not_1 (not_1_out, \n74193芯片_1_nqcc );
  \_74193芯片  \u_74193芯片_2  (
    .CPu(not_1_out), .CPd(1'b1), .CLR(or_1_out), .nLD(1'b1), .Qa(Q4), .Qb(Q5), .Qc(Q6), .Qd_(Q7));  // open: A, B, C, D, nQcc, nQcb
  and and_1 (and_1_out, Q0, Q1, Q4, Q7);
  or or_1 (or_1_out, and_1_out, button_1_out);
  // Probe on {Q7, Q6, Q5, Q4, Q3, Q2, Q1, Q0}
  Button button_1 (.out(button_1_out));

  // Notes on the sheet:
  //   CPu
  //   CPd
  //   /LD
  //   CLR
  //   /Qcc
  //   CPu
  //   CPd
  //   例题7.14（模147加法计数器）
  //   CLR
  //   /LD
  //   Reset
endmodule

// 74290
module \_74290芯片  (
  input  CPa,
  input  CPb,
  input  R0a,
  input  R0b,
  input  R9a,
  input  R9b,
  input  S1,
  input  S0,
  output Qa,
  output Qb,
  output Qc,
  output Qd
);

  wire and_1_out, and_4_out, and_5_out, and_6_out, CLR, nand_1_out, or_1_out, or_2_out, or_3_out, or_4_out,
       SEL1;
  wire [0:0] _1Q;
  wire [2:2] SEL2;
  wire [3:0] _3Q, _4Q, multiplexer_1_out;
  wire [3:1] _2Q;

  and and_1 (and_1_out, R0a, R0b);
  nand nand_1 (nand_1_out, R9a, R9b);
  and and_2 (CLR, and_1_out, nand_1_out);
  and and_3 (SEL1, R9a, R9b);
  nor nor_1 (SEL2[2], CLR, SEL1);
  Counter #(.width(3), .max('h7), .ongoal("wrap"), .trigger("falling"), .behavior("new")) counter_1 (
    .Q(_2Q), .clk(CPb), .clr(or_1_out));  // open: load, D, count, carry, preset, down
  or or_1 (or_1_out, and_5_out, CLR);
  Counter #(.width(4), .max('hf), .ongoal("wrap"), .trigger("falling"), .behavior("new")) counter_2 (
    .Q(_3Q), .clk(CPa), .clr(or_3_out));  // open: load, D, count, carry, preset, down
  Counter #(.width(3), .max('h7), .ongoal("wrap"), .trigger("falling"), .behavior("new")) counter_3 (
    .Q(_4Q[3:1]), .clk(CPb), .clr(or_2_out));  // open: load, D, count, carry, preset, down
  or or_2 (or_2_out, and_4_out, CLR);
  Counter #(.width(1), .max('h1), .ongoal("wrap"), .trigger("falling"), .behavior("new")) counter_4 (
    .Q(_1Q[0]), .clk(CPa), .clr(CLR));  // open: load, D, count, carry, preset, down
  // Probe on _3Q
  or or_3 (or_3_out, and_6_out, CLR);
  and and_4 (and_4_out, _4Q[1], _4Q[3]);
  and and_5 (and_5_out, _2Q[1], _2Q[3]);
  or or_4 (or_4_out, _4Q[1], _4Q[2], _4Q[3]);
  and and_6 (and_6_out, _3Q[1], _3Q[3]);
  T_Flip_Flop #(.trigger("falling"), .Pre_Clr_Positions("ABOVE_BELOW"), .NegatePresetClear("false"), .enable("false"), .NewFFLayout("true")) t_ff_1 (
    .clk(or_4_out), .T(1'b1), .Q(_4Q[0]));  // open: Qn, preset, reset
  Multiplexer #(.select(1), .width(4), .disabled("Z"), .enable("false")) multiplexer_1 (
    .in0(4'b0000), .in1(4'b1001), .out(multiplexer_1_out), .sel(SEL1));
  Multiplexer #(.select(3), .width(4), .disabled("Z"), .enable("false")) multiplexer_2 (
    .in0(multiplexer_1_out), .in1(multiplexer_1_out), .in2(multiplexer_1_out), .in3(multiplexer_1_out),
    .in4({3'b000, _1Q[0]}), .in5({_2Q, 1'b0}), .in6(_3Q), .in7(_4Q), .out({Qd, Qc, Qb, Qa}),
    .sel({SEL2[2], S1, S0}));

  // Other names for the same wires on the sheet: _1Qa = _1Q[0]; _2Qb = _2Q[1]; _2Qc = _2Q[2]; _2Qd = _2Q[3];
  //   _3Qa = _3Q[0]; _3Qb = _3Q[1]; _3Qc = _3Q[2]; _3Qd = _3Q[3]; _4Qa = _4Q[0]; _4Qb = _4Q[1]; _4Qc = _4Q[2];
  //   _4Qd = _4Q[3]; SEL2[1:0] = {S1, S0}; T = SEL2[2]

  // Notes on the sheet:
  //   74290芯片（二-五-十进制加法计数器）
endmodule

module \_74290芯片_异步清零_异步置9  (
  input  S1,
  input  S0,
  input  R0b,
  input  R0a,
  input  R9b,
  input  R9a,
  output Qd,
  output Qc,
  output Qb,
  output Qa
);

  wire CPa_out, CPb_out;

  Clock #(.highDuration(1), .lowDuration(1)) CPb (.out(CPb_out));
  Clock #(.highDuration(1), .lowDuration(1)) CPa (.out(CPa_out));
  \_74290芯片  \u_74290芯片_1  (
    .CPa(CPa_out), .CPb(CPb_out), .R0a(R0a), .R0b(R0b), .R9a(R9a), .R9b(R9b), .S1(S1), .S0(S0), .Qa(Qa),
    .Qb(Qb), .Qc(Qc), .Qd(Qd));

  // Notes on the sheet:
  //   74290芯片（异步清零、异步置9）
endmodule

module \_74290芯片测试_模2计数器  (
  input  R0b,
  input  R0a,
  input  R9b,
  input  R9a,
  output Qd,
  output Qc,
  output Qb,
  output Qa
);

  wire CPa;

  // Digital_Oscilloscope #(.nState(35), .frontlines("rising"), .showclock("true")) digital_oscilloscope_1: pin names not known; wires that end beside it: CPa, Qa
  Clock #(.highDuration(1), .lowDuration(1)) u_CPa (.out(CPa));
  \_74290芯片  \u_74290芯片_1  (
    .CPa(CPa), .R0a(R0a), .R0b(R0b), .R9a(R9a), .R9b(R9b), .S1(1'b0), .S0(1'b0), .Qa(Qa), .Qb(Qb), .Qc(Qc),
    .Qd(Qd));  // open: CPb

  // Notes on the sheet:
  //   74290芯片（模2计数器）
  //   S1
  //   S0
endmodule

module \_74290芯片测试_模5计数器  (
  input  R0b,
  input  R0a,
  input  R9b,
  input  R9a,
  output Qd,
  output Qc,
  output Qb,
  output Qa
);

  wire CPb_out;

  Clock #(.highDuration(1), .lowDuration(1)) CPb (.out(CPb_out));
  \_74290芯片  \u_74290芯片_1  (
    .CPb(CPb_out), .R0a(R0a), .R0b(R0b), .R9a(R9a), .R9b(R9b), .S1(1'b0), .S0(1'b1), .Qa(Qa), .Qb(Qb),
    .Qc(Qc), .Qd(Qd));  // open: CPa
  // Probe on {Qd, Qc, Qb}
  // Probe on {Qd, Qc, Qb}

  // Notes on the sheet:
  //   74290芯片（模5计数器）
  //   Qd Qc Qb
  //   S1
  //   S0
endmodule

module \_74290芯片测试_模10计数器__8421码  (
  input  R0b,
  input  R0a,
  input  R9b,
  input  R9a,
  output Qd,
  output Qc,
  output Qb,
  output Qa
);

  wire CPa_out;

  Clock #(.highDuration(1), .lowDuration(1)) CPa (.out(CPa_out));
  \_74290芯片  \u_74290芯片_1  (
    .CPa(CPa_out), .R0a(R0a), .R0b(R0b), .R9a(R9a), .R9b(R9b), .S1(1'b1), .S0(1'b0), .Qa(Qa), .Qb(Qb),
    .Qc(Qc), .Qd(Qd));  // open: CPb
  // Probe on {Qd, Qc, Qb, Qa}
  // Probe on {Qd, Qc, Qb, Qa}

  // Notes on the sheet:
  //   74290芯片（模10计数器——8421码）
  //   S1
  //   S0
  //   Qd Qc Qb Qa
endmodule

module \_74290芯片测试_模10计数器__5421码  (
  input  R0b,
  input  R0a,
  input  R9b,
  input  R9b_2,
  output Qd,
  output Qc,
  output Qb,
  output Qa
);

  wire CPb_out;
  wire [3:0] adder_1_out, adder_3_out, multiplier_1_out, multiplier_2_out, multiplier_3_out, Q;

  Clock #(.highDuration(1), .lowDuration(1)) CPb (.out(CPb_out));
  \_74290芯片  \u_74290芯片_1  (
    .CPb(CPb_out), .R0a(R0a), .R0b(R0b), .R9a(R9b_2), .R9b(R9b), .S1(1'b1), .S0(1'b1), .Qa(Qa), .Qb(Qb),
    .Qc(Qc), .Qd(Qd));  // open: CPa
  // Probe on {Qa, Qd, Qc, Qb}
  // Probe on Q
  Multiplier #(.width(4)) multiplier_1 (.a({3'b000, Qa}), .b(4'b0101), .out(multiplier_1_out));  // open: cin, cout
  Multiplier #(.width(4)) multiplier_2 (.a({3'b000, Qd}), .b(4'b0100), .out(multiplier_2_out));  // open: cin, cout
  Multiplier #(.width(4)) multiplier_3 (.a({3'b000, Qc}), .b(4'b0010), .out(multiplier_3_out));  // open: cin, cout
  Adder #(.width(4)) adder_1 (.a(multiplier_1_out), .b(multiplier_2_out), .out(adder_1_out));  // open: cin, cout
  Adder #(.width(4)) adder_2 (.a(adder_1_out), .b(adder_3_out), .out(Q));  // open: cin, cout
  Adder #(.width(4)) adder_3 (.a(multiplier_3_out), .b({3'b000, Qb}), .out(adder_3_out));  // open: cin, cout

  // Notes on the sheet:
  //   74290芯片（模10计数器——5421码）
  //   Qa Qd Qc Qb
  //   S1
  //   S0
endmodule

module \例题7_15  (
  output Qd,
  output Qc,
  output Qb,
  output Qa
);

  wire CPa_out, or_1_out, Reset_out;

  Clock #(.highDuration(1), .lowDuration(1)) CPa (.out(CPa_out));
  or or_1 (or_1_out, Reset_out, Qd);
  Button Reset (.out(Reset_out));
  \_74290芯片  \u_74290芯片_1  (
    .CPa(CPa_out), .R0a(or_1_out), .R0b(or_1_out), .R9a(1'b0), .R9b(1'b0), .S1(1'b1), .S0(1'b0), .Qa(Qa),
    .Qb(Qb), .Qc(Qc), .Qd(Qd));  // open: CPb
  // Probe on {Qd, Qc, Qb, Qa}
  // Probe on {Qd, Qc, Qb, Qa}

  // Notes on the sheet:
  //   例题7.15（模8加法计数器）
  //   S1
  //   S0
endmodule

// 74194
module \_74194芯片  (
  input  nCLR,
  input  CP,
  input  S1,
  input  S0,
  input  DR,
  input  DL,
  input  D,
  input  C,
  input  B,
  input  A,
  output Qd,
  output Qc,
  output Qb,
  output Qa
);

  wire Din, Load, nCLR_t, not_2_out, SEL1, SEL2, shift_register_1_out;
  wire [3:0] QL;

  not not_1 (nCLR_t, nCLR);
  not not_2 (not_2_out, S1);
  Multiplexer #(.select(1), .width(1), .disabled("Z"), .enable("false")) multiplexer_1 (
    .in0(DR), .in1(DL), .out(Din), .sel(SEL1));
  nand nand_1 (SEL1, not_2_out, S0);
  not not_3 (SEL2, S0);
  and and_1 (Load, S1, S0);
  Shift_Register #(.width(1), .length(4), .parallel("true"), .trigger("rising")) shift_register_1 (
    .shift(CP), .in(Din), .clk(CP), .out(shift_register_1_out), .load(Load), .clr(nCLR_t), .d0(D),
    .q0(QL[0]), .d1(C), .q1(QL[1]), .d2(B), .q2(QL[2]), .d3(A), .q3(QL[3]));
  Multiplexer #(.select(1), .width(4), .disabled("Z"), .enable("false")) multiplexer_2 (
    .in0({QL[0], QL[1], QL[2], QL[3]}), .in1(QL), .out({Qd, Qc, Qb, Qa}), .sel(SEL2));
  // Probe on shift_register_1_out
  // Probe on {Qd, Qc, Qb, Qa}
  // Probe on {QL[0], QL[1], QL[2], QL[3]}
  // Probe on QL

  // Other names for the same wires on the sheet: EN = CP; QR[3:0] = {QL[0], QL[1], QL[2], QL[3]}

  // Notes on the sheet:
  //   74194芯片（4位双向移位寄存器）
endmodule

module \_74194芯片_清零_保持  (
  input  nCLR,
  input  D,
  input  C,
  input  B,
  input  A,
  output Qd,
  output Qc,
  output Qb,
  output Qa
);

  wire CP_out;

  Clock #(.highDuration(1), .lowDuration(1)) CP (.out(CP_out));
  \_74194芯片  \u_74194芯片_1  (
    .nCLR(nCLR), .CP(CP_out), .S1(1'b0), .S0(1'b0), .D(D), .C(C), .B(B), .A(A), .Qd(Qd), .Qc(Qc), .Qb(Qb),
    .Qa(Qa));  // open: DR, DL

  // Notes on the sheet:
  //   S1
  //   S0
  //   74194芯片（清零、保持）
endmodule

module \_74194芯片_并行输入  (
  input  nCLR,
  input  D,
  input  C,
  input  B,
  input  A,
  output Qd,
  output Qc,
  output Qb,
  output Qa
);

  wire CP_out;

  Clock #(.highDuration(1), .lowDuration(1)) CP (.out(CP_out));
  \_74194芯片  \u_74194芯片_1  (
    .nCLR(nCLR), .CP(CP_out), .S1(1'b1), .S0(1'b1), .D(D), .C(C), .B(B), .A(A), .Qd(Qd), .Qc(Qc), .Qb(Qb),
    .Qa(Qa));  // open: DR, DL

  // Notes on the sheet:
  //   S1
  //   S0
  //   74194芯片（并行输入）
endmodule

module \_74194芯片_右移  (
  input  nCLR,
  input  DR,
  input  D,
  input  C,
  input  B,
  input  A,
  output Qd,
  output Qc,
  output Qb,
  output Qa
);

  wire CP_out;

  Clock #(.highDuration(1), .lowDuration(1)) CP (.out(CP_out));
  \_74194芯片  \u_74194芯片_1  (
    .nCLR(nCLR), .CP(CP_out), .S1(1'b0), .S0(1'b1), .DR(DR), .D(D), .C(C), .B(B), .A(A), .Qd(Qd), .Qc(Qc),
    .Qb(Qb), .Qa(Qa));  // open: DL

  // Notes on the sheet:
  //   S1
  //   S0
  //   74194芯片（右移）
endmodule

module \_74194芯片_左移  (
  input  nCLR,
  input  D,
  input  C,
  input  B,
  input  A,
  input  DL,
  output Qd,
  output Qc,
  output Qb,
  output Qa
);

  wire CP_out;

  Clock #(.highDuration(1), .lowDuration(1)) CP (.out(CP_out));
  \_74194芯片  \u_74194芯片_1  (
    .nCLR(nCLR), .CP(CP_out), .S1(1'b1), .S0(1'b0), .DL(DL), .D(D), .C(C), .B(B), .A(A), .Qd(Qd), .Qc(Qc),
    .Qb(Qb), .Qa(Qa));  // open: DR

  // Notes on the sheet:
  //   S1
  //   S0
  //   74194芯片（左移）
endmodule

module \例题7_16  (
  input  nCLR,
  output Qd,
  output Qc,
  output Qb,
  output Qa
);

  wire CP_out, not_1_out;

  Clock #(.highDuration(1), .lowDuration(1)) CP (.out(CP_out));
  \_74194芯片  \u_74194芯片_1  (
    .nCLR(nCLR), .CP(CP_out), .S1(1'b1), .S0(1'b0), .DL(not_1_out), .Qd(Qd), .Qc(Qc), .Qb(Qb), .Qa(Qa));  // open: DR, D, C, B, A
  not not_1 (not_1_out, Qd);

  // Notes on the sheet:
  //   S1
  //   S0
  //   例题7.16（模8计数器）
  //   DL
endmodule

module \例题7_17  (
  input  S1,
  input  S0,
  input  nCLR,
  output Qd,
  output Qc,
  output Qb
);

  wire CP, not_1_out, or_1_out, xor_1_out;

  // Digital_Oscilloscope #(.nState(35), .frontlines("rising"), .showclock("true")) digital_oscilloscope_1: pin names not known; wires that end beside it: CP, Qb
  Clock #(.highDuration(1), .lowDuration(1)) u_CP (.out(CP));
  \_74194芯片  \u_74194芯片_1  (
    .nCLR(nCLR), .CP(CP), .S1(S1), .S0(S0), .DR(xor_1_out), .D(1'b1), .C(1'b0), .B(1'b0), .Qd(Qd), .Qc(Qc),
    .Qb(Qb));  // open: DL, A, Qa
  not not_1 (not_1_out, Qd);
  or or_1 (or_1_out, not_1_out, Qc);
  xor xor_1 (xor_1_out, or_1_out, Qb);

  // Other names for the same wires on the sheet: Z = Qb

  // Notes on the sheet:
  //   DR
  //   例题7.17（00101110序列发生器）
endmodule
