// Logisim project 第9章综合应用举例电路的实现.circ as structural Verilog: 12 circuits, main circuit 74LS153
module \简单运算器  (
  input  K,
  input  S1,
  input  S0,
  input  A3,
  input  A2,
  input  A1,
  input  A0,
  input  B3,
  input  B2,
  input  B1,
  input  B0,
  input  C3,
  input  C2,
  input  C1,
  input  C0,
  input  D3,
  input  D2,
  input  D1,
  input  D0
);

  wire and_1_out, and_2_out, and_3_out, and_4_out, and_5_out, and_6_out, and_7_out, and_8_out, CP_out,
       n74ls139_1__2y0, n74ls139_1__2y1, n74ls139_1__2y2, n74ls139_1__2y3, n74ls153_1__1y, n74ls153_2__1y,
       n74ls153_3__1y, n74ls153_4__1y, n74ls194_2_qa, n74ls194_2_qb, n74ls194_2_qc, n74ls194_2_qd,
       n74ls194_3_qa, n74ls194_3_qb, n74ls194_3_qc, n74ls194_3_qd, n74ls194_4_qa, n74ls194_4_qb,
       n74ls194_4_qc, n74ls194_4_qd, n74283_1_pin1, n74283_1_pin2, n74283_1_pin3, n74283_1_pin4,
       n74283_1_pin5, n74283_1_pin6, n74283_1_pin10, n74283_1_pin11, n74283_1_pin12, n74283_1_pin13,
       n74283_1_pin14, n74283_1_pin15, not_1_out, not_2_out, not_3_out, not_4_out, xor_5_out, xor_6_out,
       xor_7_out, xor_8_out;

  not not_1 (not_1_out, n74ls139_1__2y3);
  Clock #(.highDuration(1), .lowDuration(1)) CP (.out(CP_out));
  _74LS139 u_74ls139_1 (
    ._2G(K), ._2A(S0), ._2B(S1), ._2Y0(n74ls139_1__2y0), ._2Y1(n74ls139_1__2y1), ._2Y2(n74ls139_1__2y2),
    ._2Y3(n74ls139_1__2y3));  // open: _1G, _1A, _1B, _1Y0, _1Y1, _1Y2, _1Y3
  not not_2 (not_2_out, n74ls139_1__2y0);
  not not_3 (not_3_out, n74ls139_1__2y1);
  not not_4 (not_4_out, n74ls139_1__2y2);
  LED #(.active("true")) Y3 (.in(n74ls153_1__1y));
  _74283 #(.VccGndPorts("false"), .ShowInternalStructure("false")) u_74283_1 (
    .pin1(n74283_1_pin1), .pin2(n74283_1_pin2), .pin3(n74283_1_pin3), .pin4(n74283_1_pin4),
    .pin5(n74283_1_pin5), .pin6(n74283_1_pin6), .pin7(not_3_out), .pin15(n74283_1_pin15),
    .pin14(n74283_1_pin14), .pin13(n74283_1_pin13), .pin12(n74283_1_pin12), .pin11(n74283_1_pin11),
    .pin10(n74283_1_pin10));  // open: pin9
  and and_1 (and_1_out, not_2_out, CP_out);
  _74LS153 u_74ls153_1 (
    ._1D0(n74283_1_pin10), ._1D1(n74283_1_pin10), ._1D2(and_3_out), ._1D3(xor_5_out), .A1(S1), .A0(S0),
    ._1G(K), ._1Y(n74ls153_1__1y));  // open: _2D0, _2D1, _2D2, _2D3, _2G, _2Y
  _74LS194 u_74ls194_1 (
    .nCLR(1'b1), .CP(and_1_out), .S1(1'b1), .S0(1'b1), .D(A3), .C(A2), .B(A1), .A(A0), .Qd(n74283_1_pin12),
    .Qc(n74283_1_pin14), .Qb(n74283_1_pin3), .Qa(n74283_1_pin5));  // open: DR, DL
  xor xor_1 (n74283_1_pin11, not_3_out, n74ls194_2_qd);
  xor xor_2 (n74283_1_pin15, not_3_out, n74ls194_2_qc);
  and and_2 (and_2_out, not_3_out, CP_out);
  LED #(.active("true")) Y2 (.in(n74ls153_2__1y));
  _74LS153 u_74ls153_2 (
    ._1D0(n74283_1_pin13), ._1D1(n74283_1_pin13), ._1D2(and_4_out), ._1D3(xor_7_out), .A1(S1), .A0(S0),
    ._1G(K), ._1Y(n74ls153_2__1y));  // open: _2D0, _2D1, _2D2, _2D3, _2G, _2Y
  and and_3 (and_3_out, n74283_1_pin12, n74ls194_3_qd);
  xor xor_3 (n74283_1_pin2, not_3_out, n74ls194_2_qb);
  xor xor_4 (n74283_1_pin6, not_3_out, n74ls194_2_qa);
  _74LS194 u_74ls194_2 (
    .nCLR(1'b1), .CP(and_2_out), .S1(1'b1), .S0(1'b1), .D(B3), .C(B2), .B(B1), .A(B0), .Qd(n74ls194_2_qd),
    .Qc(n74ls194_2_qc), .Qb(n74ls194_2_qb), .Qa(n74ls194_2_qa));  // open: DR, DL
  and and_4 (and_4_out, n74283_1_pin14, n74ls194_3_qc);
  and and_5 (and_5_out, n74283_1_pin3, n74ls194_3_qb);
  LED #(.active("true")) Y1 (.in(n74ls153_3__1y));
  and and_6 (and_6_out, n74283_1_pin5, n74ls194_3_qa);
  and and_7 (and_7_out, not_4_out, CP_out);
  _74LS153 u_74ls153_3 (
    ._1D0(n74283_1_pin1), ._1D1(n74283_1_pin1), ._1D2(and_5_out), ._1D3(xor_6_out), .A1(S1), .A0(S0),
    ._1G(K), ._1Y(n74ls153_3__1y));  // open: _2D0, _2D1, _2D2, _2D3, _2G, _2Y
  xor xor_5 (xor_5_out, n74283_1_pin12, n74ls194_4_qd);
  _74LS194 u_74ls194_3 (
    .nCLR(1'b1), .CP(and_7_out), .S1(1'b1), .S0(1'b1), .D(C3), .C(C2), .B(C1), .A(C0), .Qd(n74ls194_3_qd),
    .Qc(n74ls194_3_qc), .Qb(n74ls194_3_qb), .Qa(n74ls194_3_qa));  // open: DR, DL
  LED #(.active("true")) Y0 (.in(n74ls153_4__1y));
  xor xor_6 (xor_6_out, n74283_1_pin3, n74ls194_4_qb);
  xor xor_7 (xor_7_out, n74283_1_pin14, n74ls194_4_qc);
  and and_8 (and_8_out, not_1_out, CP_out);
  _74LS153 u_74ls153_4 (
    ._1D0(n74283_1_pin4), ._1D1(n74283_1_pin4), ._1D2(and_6_out), ._1D3(xor_8_out), .A1(S1), .A0(S0),
    ._1G(K), ._1Y(n74ls153_4__1y));  // open: _2D0, _2D1, _2D2, _2D3, _2G, _2Y
  xor xor_8 (xor_8_out, n74283_1_pin5, n74ls194_4_qa);
  _74LS194 u_74ls194_4 (
    .nCLR(1'b1), .CP(and_8_out), .S1(1'b1), .S0(1'b1), .D(D3), .C(D2), .B(D1), .A(D0), .Qd(n74ls194_4_qd),
    .Qc(n74ls194_4_qc), .Qb(n74ls194_4_qb), .Qa(n74ls194_4_qa));  // open: DR, DL
endmodule

module _74LS153 (
  input  _1D0,
  input  _2D0,
  input  _1D1,
  input  _2D1,
  input  _1D2,
  input  _2D2,
  input  _1D3,
  input  _2D3,
  input  A1,
  input  A0,
  input  _1G,
  input  _2G,
  output _1Y,
  output _2Y
);

  wire multiplexer_1_out, multiplexer_2_out, not_1_out, not_2_out;

  not not_1 (not_1_out, _1G);
  Multiplexer #(.select(2), .width(1), .disabled("Z"), .enable("true")) multiplexer_1 (
    .in0(_1D0), .in1(_1D1), .in2(_1D2), .in3(_1D3), .out(multiplexer_1_out), .sel({A1, A0}), .en(not_1_out));
  and and_1 (_1Y, multiplexer_1_out, not_1_out);
  not not_2 (not_2_out, _2G);
  Multiplexer #(.select(2), .width(1), .disabled("Z"), .enable("true")) multiplexer_2 (
    .in0(_2D0), .in1(_2D1), .in2(_2D2), .in3(_2D3), .out(multiplexer_2_out), .sel({A1, A0}), .en(not_2_out));
  and and_2 (_2Y, multiplexer_2_out, not_2_out);

  // Notes on the sheet:
  //   74LS153芯片（双4路多路选择器）
endmodule

module _74LS139 (
  input  _1G,
  input  _1A,
  input  _1B,
  input  _2G,
  input  _2A,
  input  _2B,
  output _1Y0,
  output _1Y1,
  output _1Y2,
  output _1Y3,
  output _2Y0,
  output _2Y1,
  output _2Y2,
  output _2Y3
);

  wire decoder_1_out0, decoder_1_out1, decoder_1_out2, decoder_1_out3, decoder_2_out0, decoder_2_out1,
       decoder_2_out2, decoder_2_out3, not_1_out, not_2_out, not_3_out, not_4_out, not_5_out, not_6_out,
       not_7_out, not_8_out, not_9_out, not_10_out;

  not not_1 (not_1_out, _1G);
  Decoder #(.select(2), .tristate("false"), .disabled("Z"), .enable("true")) decoder_1 (
    .out0(decoder_1_out0), .out1(decoder_1_out1), .out2(decoder_1_out2), .out3(decoder_1_out3),
    .sel({_1B, _1A}), .en(not_1_out));
  Decoder #(.select(2), .tristate("false"), .disabled("Z"), .enable("true")) decoder_2 (
    .out0(decoder_2_out0), .out1(decoder_2_out1), .out2(decoder_2_out2), .out3(decoder_2_out3),
    .sel({_2B, _2A}), .en(not_2_out));
  not not_2 (not_2_out, _2G);
  not not_3 (not_3_out, decoder_1_out0);
  not not_4 (not_4_out, decoder_1_out1);
  not not_5 (not_5_out, decoder_1_out2);
  not not_6 (not_6_out, decoder_1_out3);
  not not_7 (not_7_out, decoder_2_out0);
  not not_8 (not_8_out, decoder_2_out1);
  not not_9 (not_9_out, decoder_2_out2);
  not not_10 (not_10_out, decoder_2_out3);
  or or_1 (_1Y0, _1G, not_3_out);
  or or_2 (_1Y1, _1G, not_4_out);
  or or_3 (_1Y2, not_5_out, _1G);
  or or_4 (_1Y3, not_6_out, _1G);
  or or_5 (_2Y0, _2G, not_7_out);
  or or_6 (_2Y1, _2G, not_8_out);
  or or_7 (_2Y2, not_9_out, _2G);
  or or_8 (_2Y3, not_10_out, _2G);

  // Notes on the sheet:
  //   74LS139芯片（双2-4译码器）
endmodule

module _74LS194 (
  input  nCLR,
  input  CP,
  input  S1,
  input  S0,
  input  DR,
  input  DL,
  input  D,
  input  C,
  input  B,
  input  A,
  output Qd,
  output Qc,
  output Qb,
  output Qa
);

  wire Din, Load, nCLR_t, not_2_out, SEL1, SEL2, shift_register_1_out;
  wire [3:0] QL;

  not not_1 (nCLR_t, nCLR);
  not not_2 (not_2_out, S1);
  Multiplexer #(.select(1), .width(1), .disabled("Z"), .enable("false")) multiplexer_1 (
    .in0(DR), .in1(DL), .out(Din), .sel(SEL1));
  nand nand_1 (SEL1, not_2_out, S0);
  not not_3 (SEL2, S0);
  and and_1 (Load, S1, S0);
  Shift_Register #(.width(1), .length(4), .parallel("true"), .trigger("rising")) shift_register_1 (
    .shift(CP), .in(Din), .clk(CP), .out(shift_register_1_out), .load(Load), .clr(nCLR_t), .d0(D),
    .q0(QL[0]), .d1(C), .q1(QL[1]), .d2(B), .q2(QL[2]), .d3(A), .q3(QL[3]));
  Multiplexer #(.select(1), .width(4), .disabled("Z"), .enable("false")) multiplexer_2 (
    .in0({QL[0], QL[1], QL[2], QL[3]}), .in1(QL), .out({Qd, Qc, Qb, Qa}), .sel(SEL2));
  // Probe on shift_register_1_out
  // Probe on {Qd, Qc, Qb, Qa}
  // Probe on {QL[0], QL[1], QL[2], QL[3]}
  // Probe on QL

  // Other names for the same wires on the sheet: EN = CP; QR[3:0] = {QL[0], QL[1], QL[2], QL[3]}

  // Notes on the sheet:
  //   74LS194芯片（4位双向移位寄存器）
endmodule

module \时序信号发生器  (
  input  nCLR
);

  wire CP, d_ff_1_qn, d_ff_2_q, n74ls175_1_nq2, n74ls175_1_nq3, nand_1_out, nand_2_out, nand_3_out,
       nand_4_out, nCP, not_4_out, not_5_out, Q2, Q3, Q4, QA, START_out, STOP_out, T1, T2, T3, T4, T11, T22,
       T33, T44;

  // Digital_Oscilloscope #(.nState(35), .frontlines("rising"), .showclock("true")) digital_oscilloscope_1: pin names not known; wires that end beside it: CP, T1, T2, T3, T4
  // Digital_Oscilloscope #(.nState(35), .frontlines("rising"), .showclock("true")) digital_oscilloscope_2: pin names not known; wires that end beside it: CP, nCP, QA, Q4, Q3, Q2, T11, T22, T33, T44
  Clock #(.highDuration(1), .lowDuration(1)) u_CP (.out(CP));
  and and_1 (T1, d_ff_2_q, T11);
  and and_2 (T11, Q4, n74ls175_1_nq3);
  not not_1 (nCP, CP);
  and and_3 (T3, d_ff_2_q, T33);
  and and_4 (T2, d_ff_2_q, T22);
  and and_5 (T22, Q3, n74ls175_1_nq2);
  not not_2 (T33, n74ls175_1_nq2);
  _74LS175 u_74ls175_1 (
    .Q2(Q2), .nQ2(n74ls175_1_nq2), .Q3(Q3), .nQ3(n74ls175_1_nq3), .Q4(Q4), .CLK(nand_1_out), .D2(Q3),
    .D3(Q4), .D4(1'b1), .CLR(nand_2_out));  // open: Q1, nQ1, nQ4, D1
  nand nand_1 (nand_1_out, nCP, d_ff_1_qn);
  nand nand_2 (nand_2_out, QA, CP);
  D_Flip_Flop #(.trigger("rising"), .Pre_Clr_Positions("ABOVE_BELOW"), .NegatePresetClear("true"), .enable("false"), .NewFFLayout("true")) d_ff_1 (
    .clk(nCP), .D(Q2), .Q(QA), .Qn(d_ff_1_qn), .reset(nCLR));  // open: preset
  and and_6 (T4, T44, d_ff_2_q);
  not not_3 (T44, Q4);
  nand nand_3 (nand_3_out, not_4_out, nand_4_out);
  D_Flip_Flop #(.trigger("rising"), .Pre_Clr_Positions("ABOVE_BELOW"), .NegatePresetClear("true"), .enable("false"), .NewFFLayout("true")) d_ff_2 (
    .clk(Q4), .D(nand_3_out), .Q(d_ff_2_q), .reset(nCLR));  // open: Qn, preset
  nand nand_4 (nand_4_out, nand_3_out, not_5_out, nCLR);
  not not_4 (not_4_out, START_out);
  Button START (.out(START_out));
  not not_5 (not_5_out, STOP_out);
  Button STOP (.out(STOP_out));
endmodule

module _74LS175 (
  input  CLK,
  input  D1,
  input  D2,
  input  D3,
  input  D4,
  input  CLR,
  output Q1,
  output nQ1,
  output Q2,
  output nQ2,
  output Q3,
  output nQ3,
  output Q4,
  output nQ4
);

  D_Flip_Flop #(.trigger("rising"), .Pre_Clr_Positions("ABOVE_BELOW"), .NegatePresetClear("true"), .enable("false"), .NewFFLayout("true")) d_ff_1 (
    .clk(CLK), .D(D1), .Q(Q1), .Qn(nQ1), .reset(CLR));  // open: preset
  D_Flip_Flop #(.trigger("rising"), .Pre_Clr_Positions("ABOVE_BELOW"), .NegatePresetClear("true"), .enable("false"), .NewFFLayout("true")) d_ff_2 (
    .clk(CLK), .D(D2), .Q(Q2), .Qn(nQ2), .reset(CLR));  // open: preset
  D_Flip_Flop #(.trigger("rising"), .Pre_Clr_Positions("ABOVE_BELOW"), .NegatePresetClear("true"), .enable("false"), .NewFFLayout("true")) d_ff_3 (
    .clk(CLK), .D(D3), .Q(Q3), .Qn(nQ3), .reset(CLR));  // open: preset
  D_Flip_Flop #(.trigger("rising"), .Pre_Clr_Positions("ABOVE_BELOW"), .NegatePresetClear("true"), .enable("false"), .NewFFLayout("true")) d_ff_4 (
    .clk(CLK), .D(D4), .Q(Q4), .Qn(nQ4), .reset(CLR));  // open: preset

  // Notes on the sheet:
  //   74LS175芯片（4D触发器）
endmodule

module \弹道计时器  (
  input  \清_0 
);

  wire and_1_out, and_2_out, and_3_out, and_4_out, and_5_out, and_6_out, and_7_out, and_8_out, and_9_out,
       and_10_out, CLK, CP, j_k_ff_2_q, j_k_ff_3_q, j_k_ff_3_qn, n7447_1_pin3, n7447_2_pin3, n7447_3_pin3,
       n7447_4_pin3, nand_1_out, nand_2_out, nand_3_out, not_1_out, not_2_out, not_3_out, not_4_out,
       or_1_out, or_2_out, or_3_out, or_4_out, or_5_out, SP_out, ST_out;
  wire [3:0] Data0, Data1, Data2, Data3;
  wire [6:0] LED0, LED1, LED2, LED3;

  Button ST (.out(ST_out));
  Button SP (.out(SP_out));
  _7447 #(.VccGndPorts("false"), .ShowInternalStructure("false")) u_7447_1 (
    .pin1(Data3[1]), .pin2(Data3[2]), .pin3(n7447_1_pin3), .pin4(n7447_1_pin3), .pin5(n7447_1_pin3),
    .pin6(Data3[3]), .pin7(Data3[0]), .pin15(LED3[6]), .pin14(LED3[5]), .pin13(LED3[4]), .pin12(LED3[3]),
    .pin11(LED3[2]), .pin10(LED3[1]), .pin9(LED3[0]));
  _7_Segment_Display #(.active("true")) u_7_segment_display_1 (
    .g(LED3[5]), .f(LED3[6]), .a(LED3[4]), .b(LED3[3]), .e(LED3[0]), .d(LED3[1]), .c(LED3[2]));  // open: dp
  Clock #(.highDuration(1), .lowDuration(1)) clock_1 (.out(CP));
  not not_1 (not_1_out, ST_out);
  not not_2 (not_2_out, SP_out);
  not not_3 (not_3_out, CP);
  and and_1 (and_1_out, not_1_out, j_k_ff_3_q);
  and and_2 (and_2_out, not_2_out, j_k_ff_3_qn);
  _7_Segment_Display #(.active("true")) u_7_segment_display_2 (
    .g(LED2[5]), .f(LED2[6]), .a(LED2[4]), .b(LED2[3]), .e(LED2[0]), .d(LED2[1]), .c(LED2[2]));  // open: dp
  J_K_Flip_Flop #(.trigger("falling"), .Pre_Clr_Positions("ABOVE_BELOW"), .NegatePresetClear("false"), .enable("false"), .NewFFLayout("true")) j_k_ff_1 (
    .J(1'b1), .clk(not_3_out), .K(1'b1), .Q(CLK));  // open: Qn, preset, reset
  J_K_Flip_Flop #(.trigger("falling"), .Pre_Clr_Positions("ABOVE_BELOW"), .NegatePresetClear("true"), .enable("false"), .NewFFLayout("true")) j_k_ff_2 (
    .J(and_1_out), .clk(CLK), .K(and_2_out), .Q(j_k_ff_2_q), .reset(\清_0 ));  // open: Qn, preset
  J_K_Flip_Flop #(.trigger("falling"), .Pre_Clr_Positions("ABOVE_BELOW"), .NegatePresetClear("true"), .enable("false"), .NewFFLayout("true")) j_k_ff_3 (
    .J(ST_out), .clk(CLK), .K(SP_out), .Q(j_k_ff_3_q), .Qn(j_k_ff_3_qn), .reset(\清_0 ));  // open: preset
  _7447 #(.VccGndPorts("false"), .ShowInternalStructure("false")) u_7447_2 (
    .pin1(Data2[1]), .pin2(Data2[2]), .pin3(n7447_2_pin3), .pin4(n7447_2_pin3), .pin5(n7447_2_pin3),
    .pin6(Data2[3]), .pin7(Data2[0]), .pin15(LED2[6]), .pin14(LED2[5]), .pin13(LED2[4]), .pin12(LED2[3]),
    .pin11(LED2[2]), .pin10(LED2[1]), .pin9(LED2[0]));
  _7_Segment_Display #(.active("true")) u_7_segment_display_3 (
    .g(LED1[5]), .f(LED1[6]), .a(LED1[4]), .b(LED1[3]), .e(LED1[0]), .d(LED1[1]), .c(LED1[2]));  // open: dp
  and and_3 (and_3_out, j_k_ff_2_q, SP_out);
  or or_1 (or_1_out, and_3_out, and_4_out);
  and and_4 (and_4_out, j_k_ff_3_q, not_1_out);
  and and_5 (and_5_out, j_k_ff_2_q, j_k_ff_3_qn, not_2_out);
  _7447 #(.VccGndPorts("false"), .ShowInternalStructure("false")) u_7447_3 (
    .pin1(Data1[1]), .pin2(Data1[2]), .pin3(n7447_3_pin3), .pin4(n7447_3_pin3), .pin5(n7447_3_pin3),
    .pin6(Data1[3]), .pin7(Data1[0]), .pin15(LED1[6]), .pin14(LED1[5]), .pin13(LED1[4]), .pin12(LED1[3]),
    .pin11(LED1[2]), .pin10(LED1[1]), .pin9(LED1[0]));
  _7_Segment_Display #(.active("true")) u_7_segment_display_4 (
    .g(LED0[5]), .f(LED0[6]), .a(LED0[4]), .b(LED0[3]), .e(LED0[0]), .d(LED0[1]), .c(LED0[2]));  // open: dp
  LED #(.active("true")) \u_计数脉冲  (.in(and_6_out));
  and and_6 (and_6_out, CLK, or_1_out);
  not not_4 (not_4_out, and_6_out);
  LED #(.active("true")) \u_锁存  (.in(and_5_out));
  LED #(.active("true")) \u_复位  (.in(ST_out));
  or or_2 (or_2_out, ST_out, and_7_out);
  or or_3 (or_3_out, ST_out, and_8_out);
  or or_4 (or_4_out, ST_out, and_9_out);
  or or_5 (or_5_out, ST_out, and_10_out);
  _7447 #(.VccGndPorts("false"), .ShowInternalStructure("false")) u_7447_4 (
    .pin1(Data0[1]), .pin2(Data0[2]), .pin3(n7447_4_pin3), .pin4(n7447_4_pin3), .pin5(n7447_4_pin3),
    .pin6(Data0[3]), .pin7(Data0[0]), .pin15(LED0[6]), .pin14(LED0[5]), .pin13(LED0[4]), .pin12(LED0[3]),
    .pin11(LED0[2]), .pin10(LED0[1]), .pin9(LED0[0]));
  _74LS193 u_74ls193_1 (
    .CPu(nand_1_out), .CPd(1'b1), .CLR(or_2_out), .nLD(1'b1), .Qa(Data3[0]), .Qb(Data3[1]), .Qc(Data3[2]),
    .Qd_(Data3[3]));  // open: A, B, C, D, nQcc, nQcb
  _74LS193 u_74ls193_2 (
    .CPu(nand_2_out), .CPd(1'b1), .CLR(or_3_out), .nLD(1'b1), .Qa(Data2[0]), .Qb(Data2[1]), .Qc(Data2[2]),
    .Qd_(Data2[3]));  // open: A, B, C, D, nQcc, nQcb
  _74LS193 u_74ls193_3 (
    .CPu(nand_3_out), .CPd(1'b1), .CLR(or_4_out), .nLD(1'b1), .Qa(Data1[0]), .Qb(Data1[1]), .Qc(Data1[2]),
    .Qd_(Data1[3]));  // open: A, B, C, D, nQcc, nQcb
  _74LS193 u_74ls193_4 (
    .CPu(not_4_out), .CPd(1'b1), .CLR(or_5_out), .nLD(1'b1), .Qa(Data0[0]), .Qb(Data0[1]), .Qc(Data0[2]),
    .Qd_(Data0[3]));  // open: A, B, C, D, nQcc, nQcb
  and and_7 (and_7_out, Data3[1], Data3[3]);
  and and_8 (and_8_out, Data2[1], Data2[3]);
  and and_9 (and_9_out, Data1[1], Data1[3]);
  and and_10 (and_10_out, Data0[1], Data0[3]);
  nand nand_1 (nand_1_out, Data2[0], Data2[3]);
  nand nand_2 (nand_2_out, Data1[0], Data1[3]);
  nand nand_3 (nand_3_out, Data0[0], Data0[3]);
  // also tied to VCC on the sheet: {n7447_1_pin3, n7447_2_pin3, n7447_3_pin3, n7447_4_pin3}
endmodule

module _74LS193 (
  input  A,
  input  B,
  input  C,
  input  D,
  input  CPu,
  input  CPd,
  input  CLR,
  input  nLD,
  output Qa,
  output Qb,
  output Qc,
  output Qd_,
  output nQcc,
  output nQcb
);

  wire counter_1_carry, CP, EN, Inv, LOAD, not_1_out, or_1_out;
  wire [3:0] OUT, register_1_q;

  // Probe on {D, C, B, A}
  and and_1 (CP, CPu, CPd);
  or or_1 (or_1_out, CLR, LOAD);
  nor nor_1 (LOAD, CLR, nLD);
  // Probe on OUT
  Counter #(.width(4), .max('hf), .ongoal("wrap"), .trigger("rising"), .behavior("new")) counter_1 (
    .load(1'b0), .D({D, C, B, A}), .count(EN), .Q(OUT), .carry(counter_1_carry), .clk(CP), .clr(or_1_out),
    .preset(1'b0), .down(Inv));
  D_Flip_Flop #(.trigger("rising"), .Pre_Clr_Positions("ABOVE_BELOW"), .NegatePresetClear("false"), .enable("false"), .NewFFLayout("true")) d_ff_1 (
    .clk(CP), .D(counter_1_carry), .Qn(nQcb));  // open: Q, preset, reset
  and and_2 (EN, nLD, ~CLR);  // AND_Gate
  Register #(.width(4), .trigger("rising"), .Select("low")) register_1 (
    .D({D, C, B, A}), .Q(register_1_q), .clk(LOAD), .clr(CLR));  // open: en
  not not_1 (not_1_out, CPu);
  // Probe on register_1_q
  Register #(.width(1), .trigger("rising"), .Select("low")) register_2 (
    .Q(Inv), .clr(not_1_out), .preset(CPu));  // open: D, en, clk, cs
  Adder #(.width(4)) adder_1 (.a(register_1_q), .b(OUT), .out({Qd_, Qc, Qb, Qa}));  // open: cin, cout
  // Probe on {Qd_, Qc, Qb, Qa}

  assign nQcc = nQcb;

  // Other names for the same wires on the sheet: ABCD[3:0] = {D, C, B, A}

  // Notes on the sheet:
  //   74193芯片（双时钟4位二进制同步可逆计数器）
endmodule

module \汽车尾灯控制器  (
  input  K1,
  input  K0
);

  wire CP_out, j_k_ff_1_q, j_k_ff_1_qn, j_k_ff_2_q, n74ls138_1_ny0, n74ls138_1_ny1, n74ls138_1_ny2,
       n74ls138_1_ny4, n74ls138_1_ny5, n74ls138_1_ny6, nand_1_out, nand_2_out, nand_3_out, nand_4_out,
       nand_5_out, nand_6_out, nand_7_out, not_1_out, xor_1_out;

  Clock #(.highDuration(1), .lowDuration(1)) CP (.out(CP_out));
  not not_1 (not_1_out, CP_out);
  J_K_Flip_Flop #(.trigger("falling"), .Pre_Clr_Positions("ABOVE_BELOW"), .NegatePresetClear("false"), .enable("false"), .NewFFLayout("true")) j_k_ff_1 (
    .J(j_k_ff_2_q), .clk(CP_out), .K(1'b1), .Q(j_k_ff_1_q), .Qn(j_k_ff_1_qn));  // open: preset, reset
  J_K_Flip_Flop #(.trigger("falling"), .Pre_Clr_Positions("ABOVE_BELOW"), .NegatePresetClear("false"), .enable("false"), .NewFFLayout("true")) j_k_ff_2 (
    .J(j_k_ff_1_qn), .clk(CP_out), .K(1'b1), .Q(j_k_ff_2_q));  // open: Qn, preset, reset
  xor xor_1 (xor_1_out, K1, K0);
  nand nand_1 (nand_1_out, K0, K1, not_1_out);
  _74LS138 u_74ls138_1 (
    .S1(xor_1_out), .nS2(1'b0), .nS3(1'b0), .A2(K1), .A1(j_k_ff_1_q), .A0(j_k_ff_2_q), .nY0(n74ls138_1_ny0),
    .nY1(n74ls138_1_ny1), .nY2(n74ls138_1_ny2), .nY4(n74ls138_1_ny4), .nY5(n74ls138_1_ny5),
    .nY6(n74ls138_1_ny6));  // open: nY3, nY7
  nand nand_2 (nand_2_out, n74ls138_1_ny0, nand_1_out);
  nand nand_3 (nand_3_out, n74ls138_1_ny1, nand_1_out);
  nand nand_4 (nand_4_out, n74ls138_1_ny2, nand_1_out);
  nand nand_5 (nand_5_out, n74ls138_1_ny4, nand_1_out);
  nand nand_6 (nand_6_out, n74ls138_1_ny5, nand_1_out);
  nand nand_7 (nand_7_out, n74ls138_1_ny6, nand_1_out);
  LED #(.active("true")) led_1 (.in(nand_7_out));
  LED #(.active("true")) led_2 (.in(nand_6_out));
  LED #(.active("true")) led_3 (.in(nand_5_out));
  LED #(.active("true")) led_4 (.in(nand_3_out));
  LED #(.active("true")) led_5 (.in(nand_2_out));
  LED #(.active("true")) led_6 (.in(nand_4_out));

  // Notes on the sheet:
  //   G
  //   F
  //   左侧3个灯
  //   右侧3个灯
endmodule

module _74LS138 (
  input  S1,
  input  nS2,
  input  nS3,
  input  A2,
  input  A1,
  input  A0,
  output nY0,
  output nY1,
  output nY2,
  output nY3,
  output nY4,
  output nY5,
  output nY6,
  output nY7
);

  wire and_1_out, decoder_1_out0, decoder_1_out1, decoder_1_out2, decoder_1_out3, decoder_1_out4,
       decoder_1_out5, decoder_1_out6, decoder_1_out7, not_1_out, not_2_out, not_3_out, not_4_out, not_5_out,
       not_6_out, not_7_out, not_8_out, not_9_out, not_10_out, not_11_out, or_1_out;

  not not_1 (not_1_out, S1);
  not not_2 (not_2_out, nS2);
  not not_3 (not_3_out, nS3);
  or or_1 (or_1_out, not_1_out, nS2, nS3);
  and and_1 (and_1_out, S1, not_2_out, not_3_out);
  Decoder #(.select(3), .tristate("false"), .disabled("Z"), .enable("true")) decoder_1 (
    .out0(decoder_1_out0), .out1(decoder_1_out1), .out2(decoder_1_out2), .out3(decoder_1_out3),
    .out4(decoder_1_out4), .out5(decoder_1_out5), .out6(decoder_1_out6), .out7(decoder_1_out7),
    .sel({A2, A1, A0}), .en(and_1_out));
  not not_4 (not_4_out, decoder_1_out0);
  not not_5 (not_5_out, decoder_1_out1);
  not not_6 (not_6_out, decoder_1_out2);
  not not_7 (not_7_out, decoder_1_out3);
  not not_8 (not_8_out, decoder_1_out4);
  not not_9 (not_9_out, decoder_1_out5);
  not not_10 (not_10_out, decoder_1_out6);
  not not_11 (not_11_out, decoder_1_out7);
  or or_2 (nY0, or_1_out, not_4_out);
  or or_3 (nY1, or_1_out, not_5_out);
  or or_4 (nY2, or_1_out, not_6_out);
  or or_5 (nY3, or_1_out, not_7_out);
  or or_6 (nY4, or_1_out, not_8_out);
  or or_7 (nY5, or_1_out, not_9_out);
  or or_8 (nY6, or_1_out, not_10_out);
  or or_9 (nY7, or_1_out, not_11_out);

  // Notes on the sheet:
  //   74LS138（3-8译码器）
endmodule

module \数字钟  (
  input  K3,
  input  K2,
  input  K1,
  input  K0
);

  wire _1Hz, _10Hz, _100Hz, _500Hz, A, and_1_out, C, E, F, Fh, Fm, Fs, G, Min1, n7447_1_pin3, n7447_2_pin3,
       n7447_3_pin3, n7447_4_pin3, n7447_5_pin3, n7447_6_pin3, nand_2_out, nand_3_out, nand_4_out,
       nand_6_out, nand_7_out, nand_8_out, nand_10_out, nand_11_out, nand_12_out, not_1_out, not_2_out,
       not_3_out, not_4_out, or_2_out, or_3_out, RST, Sec0, Sec1, undriven, \单脉冲_out ;
  wire [1:0] Hour0;
  wire [2:0] Minute0, Second0;
  wire [3:0] Hour1, Minute1, Second1;
  wire [6:0] LED1, LED2, LED3, LED4, LED5, LED6;

  _74LS290 u_74ls290_1 (
    .CPa(Fh), .R0a(F), .R0b(F), .R9a(1'b0), .R9b(1'b0), .Qa(Hour0[0]), .Qb(Hour0[1]), .Qc(G), .Qd(E));  // open: CPb
  _74LS290 u_74ls290_2 (
    .CPa(Fm), .R0a(1'b0), .R0b(1'b0), .R9a(1'b0), .R9b(1'b0), .Qa(Minute0[0]), .Qb(Minute0[1]),
    .Qc(Minute0[2]), .Qd(C));  // open: CPb
  _74LS290 u_74ls290_3 (
    .CPa(Fs), .R0a(1'b0), .R0b(1'b0), .R9a(1'b0), .R9b(1'b0), .Qa(Second0[0]), .Qb(Second0[1]),
    .Qc(Second0[2]), .Qd(A));  // open: CPb
  Clock #(.highDuration(1), .lowDuration(1)) _1kHz ();  // open: out
  // Probe on {E, G, Hour0}
  // Probe on {C, Minute0}
  // Probe on {A, Second0}
  _74LS290 u_74ls290_4 (
    .CPa(undriven), .R0a(1'b0), .R0b(1'b0), .R9a(1'b0), .R9b(1'b0), .Qa(_500Hz), .Qd(_100Hz));  // open: CPb, Qb, Qc
  and and_1 (and_1_out, Hour1[1], G);
  and and_2 (Min1, Minute1[1], Minute1[2]);
  and and_3 (Sec1, Second1[1], Second1[2]);
  _7_Segment_Display #(.active("true")) u_7_segment_display_1 (
    .g(LED6[5]), .f(LED6[6]), .a(LED6[4]), .b(LED6[3]), .e(LED6[0]), .d(LED6[1]), .c(LED6[2]));  // open: dp
  or or_1 (F, and_1_out, RST);
  or or_2 (or_2_out, Min1, RST);
  or or_3 (or_3_out, Sec1, RST);
  _74LS290 u_74ls290_5 (
    .CPa(_100Hz), .R0a(1'b0), .R0b(1'b0), .R9a(1'b0), .R9b(1'b0), .Qd(_10Hz));  // open: CPb, Qa, Qb, Qc
  _74LS290 u_74ls290_6 (
    .CPa(E), .R0a(F), .R0b(F), .R9a(1'b0), .R9b(1'b0), .Qa(Hour1[0]), .Qb(Hour1[1]), .Qc(Hour1[2]),
    .Qd(Hour1[3]));  // open: CPb
  _74LS290 u_74ls290_7 (
    .CPa(C), .R0a(or_2_out), .R0b(or_2_out), .R9a(1'b0), .R9b(1'b0), .Qa(Minute1[0]), .Qb(Minute1[1]),
    .Qc(Minute1[2]), .Qd(Minute1[3]));  // open: CPb
  _74LS290 u_74ls290_8 (
    .CPa(A), .R0a(or_3_out), .R0b(or_3_out), .R9a(1'b0), .R9b(1'b0), .Qa(Second1[0]), .Qb(Second1[1]),
    .Qc(Second1[2]), .Qd(Second1[3]));  // open: CPb
  _7_Segment_Display #(.active("true")) u_7_segment_display_2 (
    .g(LED5[5]), .f(LED5[6]), .a(LED5[4]), .b(LED5[3]), .e(LED5[0]), .d(LED5[1]), .c(LED5[2]));  // open: dp
  nand nand_1 (Fh, nand_3_out, nand_2_out, nand_4_out);
  nand nand_2 (nand_2_out, \单脉冲_out , not_4_out, K3);
  nand nand_3 (nand_3_out, Sec0, K0, K3);
  not not_1 (not_1_out, K3);
  _74LS290 u_74ls290_9 (
    .CPa(_10Hz), .R0a(1'b0), .R0b(1'b0), .R9a(1'b0), .R9b(1'b0), .Qd(_1Hz));  // open: CPb, Qa, Qb, Qc
  nand nand_4 (nand_4_out, not_1_out, Min1);
  // Probe on Hour1
  // Probe on Minute1
  // Probe on Second1
  _7_Segment_Display #(.active("true")) u_7_segment_display_3 (
    .g(LED4[5]), .f(LED4[6]), .a(LED4[4]), .b(LED4[3]), .e(LED4[0]), .d(LED4[1]), .c(LED4[2]));  // open: dp
  nand nand_5 (Fm, nand_6_out, nand_7_out, nand_8_out);
  nand nand_6 (nand_6_out, Sec0, K2, K0);
  nand nand_7 (nand_7_out, \单脉冲_out , not_4_out, K2);
  nand nand_8 (nand_8_out, not_2_out, Sec1);
  not not_2 (not_2_out, K2);
  _7447 #(.VccGndPorts("false"), .ShowInternalStructure("false")) u_7447_1 (
    .pin1(Second0[1]), .pin2(Second0[2]), .pin3(n7447_1_pin3), .pin4(n7447_1_pin3), .pin5(n7447_1_pin3),
    .pin6(A), .pin7(Second0[0]), .pin15(LED1[6]), .pin14(LED1[5]), .pin13(LED1[4]), .pin12(LED1[3]),
    .pin11(LED1[2]), .pin10(LED1[1]), .pin9(LED1[0]));
  _7447 #(.VccGndPorts("false"), .ShowInternalStructure("false")) u_7447_2 (
    .pin1(Minute1[1]), .pin2(Minute1[2]), .pin3(n7447_2_pin3), .pin4(n7447_2_pin3), .pin5(n7447_2_pin3),
    .pin6(Minute1[3]), .pin7(Minute1[0]), .pin15(LED4[6]), .pin14(LED4[5]), .pin13(LED4[4]), .pin12(LED4[3]),
    .pin11(LED4[2]), .pin10(LED4[1]), .pin9(LED4[0]));
  _7_Segment_Display #(.active("true")) u_7_segment_display_4 (
    .g(LED3[5]), .f(LED3[6]), .a(LED3[4]), .b(LED3[3]), .e(LED3[0]), .d(LED3[1]), .c(LED3[2]));  // open: dp
  nand nand_9 (Fs, nand_11_out, nand_10_out, nand_12_out);
  nand nand_10 (nand_10_out, not_4_out, \单脉冲_out , K1);
  nand nand_11 (nand_11_out, not_3_out, Sec0);
  not not_3 (not_3_out, K1);
  nand nand_12 (nand_12_out, K0, Sec0);
  not not_4 (not_4_out, K0);
  _7_Segment_Display #(.active("true")) u_7_segment_display_5 (
    .g(LED2[5]), .f(LED2[6]), .a(LED2[4]), .b(LED2[3]), .e(LED2[0]), .d(LED2[1]), .c(LED2[2]));  // open: dp
  Button \u_单脉冲  (.out(\单脉冲_out ));
  _7447 #(.VccGndPorts("false"), .ShowInternalStructure("false")) u_7447_3 (
    .pin1(Second1[1]), .pin2(Second1[2]), .pin3(n7447_3_pin3), .pin4(n7447_3_pin3), .pin5(n7447_3_pin3),
    .pin6(Second1[3]), .pin7(Second1[0]), .pin15(LED2[6]), .pin14(LED2[5]), .pin13(LED2[4]), .pin12(LED2[3]),
    .pin11(LED2[2]), .pin10(LED2[1]), .pin9(LED2[0]));
  _7447 #(.VccGndPorts("false"), .ShowInternalStructure("false")) u_7447_4 (
    .pin1(Hour0[1]), .pin2(G), .pin3(n7447_4_pin3), .pin4(n7447_4_pin3), .pin5(n7447_4_pin3), .pin6(E),
    .pin7(Hour0[0]), .pin15(LED5[6]), .pin14(LED5[5]), .pin13(LED5[4]), .pin12(LED5[3]), .pin11(LED5[2]),
    .pin10(LED5[1]), .pin9(LED5[0]));
  _7_Segment_Display #(.active("true")) u_7_segment_display_6 (
    .g(LED1[5]), .f(LED1[6]), .a(LED1[4]), .b(LED1[3]), .e(LED1[0]), .d(LED1[1]), .c(LED1[2]));  // open: dp
  Button Reset (.out(RST));
  _7447 #(.VccGndPorts("false"), .ShowInternalStructure("false")) u_7447_5 (
    .pin1(Minute0[1]), .pin2(Minute0[2]), .pin3(n7447_5_pin3), .pin4(n7447_5_pin3), .pin5(n7447_5_pin3),
    .pin6(C), .pin7(Minute0[0]), .pin15(LED3[6]), .pin14(LED3[5]), .pin13(LED3[4]), .pin12(LED3[3]),
    .pin11(LED3[2]), .pin10(LED3[1]), .pin9(LED3[0]));
  _7447 #(.VccGndPorts("false"), .ShowInternalStructure("false")) u_7447_6 (
    .pin1(Hour1[1]), .pin2(Hour1[2]), .pin3(n7447_6_pin3), .pin4(n7447_6_pin3), .pin5(n7447_6_pin3),
    .pin6(Hour1[3]), .pin7(Hour1[0]), .pin15(LED6[6]), .pin14(LED6[5]), .pin13(LED6[4]), .pin12(LED6[3]),
    .pin11(LED6[2]), .pin10(LED6[1]), .pin9(LED6[0]));
  Clock #(.highDuration(1), .lowDuration(1)) u__1Hz (.out(Sec0));
  // also tied to VCC on the sheet: {n7447_1_pin3, n7447_2_pin3, n7447_4_pin3, n7447_3_pin3, n7447_5_pin3, n7447_6_pin3}

  // Other names for the same wires on the sheet: Hour0[3:2] = {E, G}; Minute0[3] = C; Second0[3] = A
endmodule

module _74LS290 (
  input  CPa,
  input  CPb,
  input  R0a,
  input  R0b,
  input  R9a,
  input  R9b,
  output Qa,
  output Qb,
  output Qc,
  output Qd
);

  wire and_1_out, and_4_out, and_5_out, and_6_out, CLR, nand_1_out, or_1_out, or_2_out, or_3_out, or_4_out,
       SEL1;
  wire [0:0] _1Q;
  wire [2:2] SEL2;
  wire [3:0] _3Q, _4Q, multiplexer_1_out;
  wire [3:1] _2Q;

  and and_1 (and_1_out, R0a, R0b);
  nand nand_1 (nand_1_out, R9a, R9b);
  and and_2 (CLR, and_1_out, nand_1_out);
  and and_3 (SEL1, R9a, R9b);
  nor nor_1 (SEL2[2], CLR, SEL1);
  Counter #(.width(3), .max('h7), .ongoal("wrap"), .trigger("falling"), .behavior("new")) counter_1 (
    .Q(_2Q), .clk(CPb), .clr(or_1_out));  // open: load, D, count, carry, preset, down
  or or_1 (or_1_out, and_5_out, CLR);
  Counter #(.width(4), .max('hf), .ongoal("wrap"), .trigger("falling"), .behavior("new")) counter_2 (
    .Q(_3Q), .clk(CPa), .clr(or_3_out));  // open: load, D, count, carry, preset, down
  Counter #(.width(3), .max('h7), .ongoal("wrap"), .trigger("falling"), .behavior("new")) counter_3 (
    .Q(_4Q[3:1]), .clk(CPb), .clr(or_2_out));  // open: load, D, count, carry, preset, down
  or or_2 (or_2_out, and_4_out, CLR);
  Counter #(.width(1), .max('h1), .ongoal("wrap"), .trigger("falling"), .behavior("new")) counter_4 (
    .Q(_1Q[0]), .clk(CPa), .clr(CLR));  // open: load, D, count, carry, preset, down
  // Probe on _3Q
  or or_3 (or_3_out, and_6_out, CLR);
  and and_4 (and_4_out, _4Q[1], _4Q[3]);
  and and_5 (and_5_out, _2Q[1], _2Q[3]);
  or or_4 (or_4_out, _4Q[1], _4Q[2], _4Q[3]);
  and and_6 (and_6_out, _3Q[1], _3Q[3]);
  T_Flip_Flop #(.trigger("falling"), .Pre_Clr_Positions("ABOVE_BELOW"), .NegatePresetClear("false"), .enable("false"), .NewFFLayout("true")) t_ff_1 (
    .clk(or_4_out), .T(1'b1), .Q(_4Q[0]));  // open: Qn, preset, reset
  Multiplexer #(.select(1), .width(4), .disabled("Z"), .enable("false")) multiplexer_1 (
    .in0(4'b0000), .in1(4'b1001), .out(multiplexer_1_out), .sel(SEL1));
  Multiplexer #(.select(3), .width(4), .disabled("Z"), .enable("false")) multiplexer_2 (
    .in0(multiplexer_1_out), .in1(multiplexer_1_out), .in2(multiplexer_1_out), .in3(multiplexer_1_out),
    .in4({3'b000, _1Q[0]}), .in5({_2Q, 1'b0}), .in6(_3Q), .in7(_4Q), .out({Qd, Qc, Qb, Qa}),
    .sel({SEL2[2], 2'b10}));

  // Other names for the same wires on the sheet: _1Qa = _1Q[0]; _2Qb = _2Q[1]; _2Qc = _2Q[2]; _2Qd = _2Q[3];
  //   _3Qa = _3Q[0]; _3Qb = _3Q[1]; _3Qc = _3Q[2]; _3Qd = _3Q[3]; _4Qa = _4Q[0]; _4Qb = _4Q[1]; _4Qc = _4Q[2];
  //   _4Qd = _4Q[3]; T = SEL2[2]

  // Notes on the sheet:
  //   74290芯片（二-五-十进制加法计数器）
endmodule
