// Logisim project 单总线结构MIPS处理器（单级中断+硬布线控制器+6条指令）.circ as structural Verilog: 10 circuits, main circuit 指令译码器
module \单总线结构MIPS处理器数据通路_硬布线控制器  (
);

  wire Add, Add4, Addrout, and_2_out, ARin, CLK, comparator_1_eq, d_ff_1_qn, DREin, DREout, DRin, DRout,
       EPCin, EPCout, equal, IR_A_out, IR_I_out, IRin, IRQ0, IRQ1, IRQ2, IRQ3, Mcal, Mex, Mif, Mint,
       mips_alu_1_equal, not_1_out, PCin, PCout, PSWin, READ, RegDst, RegTgt, Rin, Rout, RST, Slt, T1, T2,
       T3, T4, Write, Xin, Zout, \中断控制器_1_intr , \中断控制器_1_ir0w , \中断控制器_1_ir1w , \中断控制器_1_ir2w ,
       \中断控制器_1_ir3w , \中断请求 ;
  wire [1:0] \中断控制信号 , \中断控制器_1_intno ;
  wire [4:0] registerfile_1_p5, registerfile_1_p6;
  wire [11:0] \指令数 , \时钟数 ;
  wire [31:0] AR_q, bit_extender_1_out, controlled_buffer_1_out, controlled_buffer_2_out, DR_q, EPC_q, IR,
       mips_alu_1_result, multiplexer_3_out, PC_q, ram_1_data, registerfile_1_p7, shifter_1_out, X_q, Z_q,
       \内部总线 ;

  LED #(.active("true")) led_1 (.in(Mif));
  LED #(.active("true")) led_2 (.in(Mcal));
  // Probe on \时钟数 
  Button u_IRQ0 (.out(IRQ0));
  Button u_IRQ2 (.out(IRQ2));
  Register #(.width(32), .trigger("rising"), .Select("low")) AR (.D(\内部总线 ), .en(ARin), .Q(AR_q), .clk(CLK), .clr(RST));
  LED #(.active("true")) led_3 (.in(T1));
  LED #(.active("true")) led_4 (.in(Mint));
  LED #(.active("true")) led_5 (.in(Mex));
  // Probe on \指令数 
  Button u_IRQ1 (.out(IRQ1));
  Button u_IRQ3 (.out(IRQ3));
  Register #(.width(32), .trigger("rising"), .Select("low")) X (.D(\内部总线 ), .en(Xin), .Q(X_q), .clk(CLK), .clr(RST));
  LED #(.active("true")) led_6 (.in(T4));
  LED #(.active("true")) led_7 (.in(T2));
  LED #(.active("true")) led_8 (.in(T3));
  Clock #(.highDuration(1), .lowDuration(1)) clock_1 (.out(CLK));
  Button u_RST (.out(RST));
  RAM #(.addrWidth(10), .dataWidth(32), .bus("separate"), .Select("high")) ram_1 (
    .addr(AR_q[11:2]), .din(controlled_buffer_1_out), .data(ram_1_data), .str(Write), .clk(CLK), .ld(READ));  // open: sel, clr
  assign controlled_buffer_1_out = DREout ? DR_q : 32'bz;  // Controlled_Buffer controlled_buffer_1
  MIPS_ALU mips_alu_1 (
    .X(X_q), .Y(\内部总线 ), .Equal(mips_alu_1_equal), .Result(mips_alu_1_result), .ADD(Add), .ADD4(Add4),
    .SLT(Slt));  // open: SUB
  assign controlled_buffer_2_out = DRin ? \内部总线  : 32'bz;  // Controlled_Buffer controlled_buffer_2
  assign controlled_buffer_2_out = DREin ? ram_1_data : 32'bz;  // Controlled_Buffer controlled_buffer_3
  assign \内部总线  = PCout ? PC_q : 32'bz;  // Controlled_Buffer controlled_buffer_4
  Register #(.width(32), .trigger("rising"), .Select("low")) PC (.D(\内部总线 ), .en(PCin), .Q(PC_q), .clk(CLK), .clr(RST));
  assign \内部总线  = DRout ? DR_q : 32'bz;  // Controlled_Buffer controlled_buffer_5
  Register #(.width(32), .trigger("rising"), .Select("low")) DR (
    .D(controlled_buffer_2_out), .Q(DR_q), .clk(CLK), .clr(RST));  // open: en
  Register #(.width(1), .trigger("rising"), .Select("low")) PSW (
    .D(mips_alu_1_equal), .en(PSWin), .Q(equal), .clk(CLK), .clr(RST));
  assign \内部总线  = Zout ? Z_q : 32'bz;  // Controlled_Buffer controlled_buffer_6
  Register #(.width(32), .trigger("rising"), .Select("low")) Z (
    .D(mips_alu_1_result), .Q(Z_q), .clk(CLK), .clr(RST));  // open: en
  Register #(.width(32), .trigger("rising"), .Select("low")) u_IR (.D(\内部总线 ), .en(IRin), .Q(IR), .clk(CLK), .clr(RST));
  assign \内部总线  = IR_I_out ? bit_extender_1_out : 32'bz;  // Controlled_Buffer controlled_buffer_7
  assign \内部总线  = IR_A_out ? shifter_1_out : 32'bz;  // Controlled_Buffer controlled_buffer_8
  \硬布线控制器  \u_硬布线控制器_1  (
    .CLK(CLK), .IR(IR), .EQUAL(equal), .M_T({Mif, Mcal, Mex, Mint, T1, T2, T3, T4}),
    .ControlBus({PCout, DRout, Zout, Rout, IR_I_out, IR_A_out, DREout, PCin, ARin, DREin, DRin, Xin, Rin, IRin, PSWin, RegTgt, RegDst, Add, Add4, Slt, READ, Write}),
    .IntSignals({EPCout, EPCin, Addrout, \中断控制信号 }), .IntR(\中断请求 ));
  // Probe on IR
  // RegisterFile registerfile_1: pin names not known; wires that end beside it: \内部总线 , CLK, DREout, Rin, registerfile_1_p5, registerfile_1_p6, registerfile_1_p7
  assign bit_extender_1_out = {{16{IR[15]}}, IR[15:0]};  // Bit_Extender bit_extender_1
  assign \内部总线  = Rout ? registerfile_1_p7 : 32'bz;  // Controlled_Buffer controlled_buffer_9
  Multiplexer #(.select(1), .width(5), .disabled("Z"), .enable("false")) multiplexer_1 (
    .in0(IR[25:21]), .in1(IR[20:16]), .out(registerfile_1_p6), .sel(RegTgt));
  Multiplexer #(.select(1), .width(5), .disabled("Z"), .enable("false")) multiplexer_2 (
    .in0(IR[20:16]), .in1(IR[15:11]), .out(registerfile_1_p5), .sel(RegDst));
  Shifter #(.width(32), .shift("ll")) shifter_1 (.in(bit_extender_1_out), .\dist (5'b00010), .out(shifter_1_out));
  D_Flip_Flop #(.trigger("rising"), .Pre_Clr_Positions("LEGACY"), .NegatePresetClear("false"), .enable("true"), .NewFFLayout("false")) d_ff_1 (
    .Qn(d_ff_1_qn), .preset(\中断控制信号 [0]), .reset(\中断控制信号 [1]));  // open: clk, D, Q, en
  and and_1 (\中断请求 , d_ff_1_qn, \中断控制器_1_intr );
  LED #(.active("true")) IRQ0_2 (.in(\中断控制器_1_ir0w ));
  \中断控制器  \u_中断控制器_1  (
    .CLK(CLK), .Key1(IRQ1), .Key2(IRQ2), .Clr(\中断控制信号 [1]), .IR0W(\中断控制器_1_ir0w ), .IR1W(\中断控制器_1_ir1w ),
    .IR2W(\中断控制器_1_ir2w ), .IntNo(\中断控制器_1_intno ), .IntR(\中断控制器_1_intr ), .EDU_TEST(4'b0000), .Key3(IRQ3),
    .Key0(IRQ0), .IR3W(\中断控制器_1_ir3w ));
  LED #(.active("true")) IRQ1_2 (.in(\中断控制器_1_ir1w ));
  LED #(.active("true")) IRQ2_2 (.in(\中断控制器_1_ir2w ));
  LED #(.active("true")) IRQ3_2 (.in(\中断控制器_1_ir3w ));
  Comparator #(.width(32), .mode("twosComplement")) comparator_1 (
    .a(IR), .b(32'h1000ffff), .eq(comparator_1_eq));  // open: gt, lt
  not not_1 (not_1_out, comparator_1_eq);
  Register #(.width(32), .trigger("rising"), .Select("low")) EPC (
    .D(\内部总线 ), .en(EPCin), .Q(EPC_q), .clk(CLK), .clr(RST));
  Counter #(.width(12), .max('hfff), .ongoal("wrap"), .trigger("falling"), .behavior("new")) counter_1 (
    .count(not_1_out), .Q(\时钟数 ), .clk(CLK), .clr(RST));  // open: load, D, carry, preset, down
  assign \内部总线  = EPCout ? EPC_q : 32'bz;  // Controlled_Buffer controlled_buffer_10
  Multiplexer #(.select(2), .width(32), .disabled("Z"), .enable("false")) multiplexer_3 (
    .in0(32'h400), .in1(32'h600), .in2(32'h800), .in3(32'ha00), .out(multiplexer_3_out), .sel(\中断控制器_1_intno ));
  assign \内部总线  = Addrout ? multiplexer_3_out : 32'bz;  // Controlled_Buffer controlled_buffer_11
  and and_2 (and_2_out, not_1_out, Mif, T1);
  Counter #(.width(12), .max('hfff), .ongoal("wrap"), .trigger("falling"), .behavior("old")) counter_2 (
    .count(and_2_out), .Q(\指令数 ), .clk(CLK), .clr(RST));  // open: load, D, carry, preset

  // Other names for the same wires on the sheet: rd[4:0] = IR[15:11]; rt[4:0] = IR[20:16]; rs[4:0] = IR[25:21];
  //   关中断 = \中断控制信号 [0]; 开中断 = \中断控制信号 [1]; 中断控制信号[4:2] = {EPCout, EPCin, Addrout};
  //   控制总线[21:0] = {PCout, DRout, Zout, Rout, IR_I_out, IR_A_out, DREout, PCin, ARin, DREin, DRin, Xin, Rin, IRin, PSWin, RegTgt, RegDst, Add, Add4, Slt, READ, Write};
  //   状态节拍信号[7:0] = {Mif, Mcal, Mex, Mint, T1, T2, T3, T4}

  // Notes on the sheet:
  //   RAM
  //   外部总线
  //   内部总线
  //   单总线结构 MIPS 处理器数据通路（硬布线控制器+单级中断+6条指令）
  //   三级时序+中断
  //   Immidate32
  //   BranchAddress32
  //   中断使能寄存器 IE
  //   IRQ2
  //   IRQ1
  //   IRQ0
  //   中断请求信号
  //   IRQ3
  //   EPC用于保存断点
  //   送控制器
  //   执行ERET时开中断，同时清除中断源
  //   中断逻辑
endmodule

module \硬布线控制器  (
  input  CLK,
  input  [31:0] IR,
  input  EQUAL,
  input  IntR,
  output [7:0] M_T,
  output [21:0] ControlBus,
  output [4:0] IntSignals
);

  wire ADD, ADDI, BEQ, ERET, LW, not_1_out, Other, PCin1, PCout1, \中断控制信号_pcin , \中断控制信号_pcout ;
  wire [3:0] OCInput, register_1_q, \状态机_1_n0 ;

  Register #(.width(4), .trigger("rising"), .Select("low")) register_1 (
    .D(\状态机_1_n0 ), .Q(register_1_q), .clk(not_1_out));  // open: en, clr
  not not_1 (not_1_out, CLK);
  \状态机  \u_状态机_1  (
    .LW(LW), .SW(OCInput[3]), .BEQ(BEQ), .N3(\状态机_1_n0 [3]), .SLT(OCInput[0]), .ADDI(ADDI), .ADD(ADD),
    .ERET(ERET), .IntR(IntR), .S3(register_1_q[3]), .S2(register_1_q[2]), .S1(register_1_q[1]),
    .S0(register_1_q[0]), .N2(\状态机_1_n0 [2]), .N1(\状态机_1_n0 [1]), .N0(\状态机_1_n0 [0]));
  // Probe on register_1_q
  // Probe on \状态机_1_n0 
  \输出函数  \u_输出函数_1  (
    .S3(register_1_q[3]), .S2(register_1_q[2]), .S1(register_1_q[1]), .S0(register_1_q[0]), .Mif(M_T[7]),
    .Mcal(M_T[6]), .Mex(M_T[5]), .Mint(M_T[4]), .T1(M_T[3]), .T2(M_T[2]), .T3(M_T[1]), .T4(M_T[0]));
  \中断控制信号  \u_中断控制信号  (
    .ERET(ERET), .Mex(M_T[5]), .Mint(M_T[4]), .T1(M_T[3]), .T2(M_T[2]), .Pcout(\中断控制信号_pcout ),
    .PCin(\中断控制信号_pcin ), .EPCout(IntSignals[4]), .EPCin(IntSignals[3]), .Addrout(IntSignals[2]),
    .STI(IntSignals[1]), .CLI(IntSignals[0]));
  \指令译码器  \u_指令译码器_1  (
    .IR(IR), .LW(LW), .SW(OCInput[3]), .BEQ(BEQ), .SLT(OCInput[0]), .ADDI(ADDI), .ERET(ERET),
    .OtherInstr(Other), .ADD(ADD));
  or or_1 (ControlBus[21], PCout1, \中断控制信号_pcout );
  or or_2 (ControlBus[14], \中断控制信号_pcin , PCin1);
  \硬布线控制器组合逻辑单元  \u_硬布线控制器组合逻辑单元_1  (
    .SLT(OCInput[0]), .Pcout(PCout1), .ADDI(ADDI), .LW(LW), .DRout(ControlBus[20]), .SW(OCInput[3]),
    .BEQ(BEQ), .ADD(ADD), .Mif(M_T[7]), .Mcal(M_T[6]), .Zout(ControlBus[19]), .Mex(M_T[5]), .T1(M_T[3]),
    .T2(M_T[2]), .T3(M_T[1]), .T4(M_T[0]), .EQUAL(EQUAL), .Rout(ControlBus[18]), .IRiout(ControlBus[17]),
    .IRaout(ControlBus[16]), .DREout(ControlBus[15]), .Pcin(PCin1), .ARin(ControlBus[13]),
    .DREin(ControlBus[12]), .DRin(ControlBus[11]), .Xin(ControlBus[10]), .Rin(ControlBus[9]),
    .IRin(ControlBus[8]), .PSWin(ControlBus[7]), .RegTgt(ControlBus[6]), .RegDst(ControlBus[5]),
    .Add_2(ControlBus[4]), .Add4(ControlBus[3]), .Slt_2(ControlBus[2]), .READ(ControlBus[1]),
    .WRITE(ControlBus[0]));

  // Other names for the same wires on the sheet: PCin = ControlBus[14]; PCout = ControlBus[21]; Mint = M_T[4];
  //   SLT = OCInput[0];
  //   OCInput (some bits) = {EQUAL, M_T[0], M_T[1], M_T[2], M_T[3], M_T[5], M_T[6], M_T[7], ADD, BEQ, LW, ADDI};
  //   SW = OCInput[3]; Mif = M_T[7]; Mcal = M_T[6]; Mex = M_T[5]; T1 = M_T[3]; T2 = M_T[2]; T3 = M_T[1]; T4 = M_T[0];
  //   指令字[31:0] = IR

  // Notes on the sheet:
  //   指令译码信号
  //   次态
  //   中断控制相关信号生成逻辑
  //   输入引脚
  //   现态
  //   状态寄存器
  //   现态
  //   中断请求信号
  //   次态
  //   输出引脚
  //   时序产生器TG
  //   硬布线控制器（三级时序、变长指令周期、支持中断）
  //   指令译码器
  //   操作控制器OC
  //   指令译码信号
  //   指令译码逻辑ID
endmodule

module \指令译码器  (
  input  [31:0] IR,
  output LW,
  output SW,
  output BEQ,
  output SLT,
  output ADDI,
  output ERET,
  output OtherInstr,
  output ADD
);

  wire comparator_6_eq, comparator_7_eq, comparator_8_eq;

  Comparator #(.width(6), .mode("twosComplement")) comparator_1 (
    .a(IR[31:26]), .b(6'b100011), .eq(LW));  // open: gt, lt
  Comparator #(.width(6), .mode("twosComplement")) comparator_2 (
    .a(IR[31:26]), .b(6'b101011), .eq(SW));  // open: gt, lt
  Comparator #(.width(6), .mode("twosComplement")) comparator_3 (
    .a(IR[31:26]), .b(6'b010000), .eq(ERET));  // open: gt, lt
  Comparator #(.width(6), .mode("twosComplement")) comparator_4 (
    .a(IR[31:26]), .b(6'b000100), .eq(BEQ));  // open: gt, lt
  Comparator #(.width(6), .mode("twosComplement")) comparator_5 (
    .a(IR[31:26]), .b(6'b001000), .eq(ADDI));  // open: gt, lt
  Comparator #(.width(6), .mode("twosComplement")) comparator_6 (
    .a(IR[31:26]), .b({6{1'b0}}), .eq(comparator_6_eq));  // open: gt, lt
  Comparator #(.width(6), .mode("twosComplement")) comparator_7 (
    .a(IR[5:0]), .b(6'b101010), .eq(comparator_7_eq));  // open: gt, lt
  Comparator #(.width(6), .mode("twosComplement")) comparator_8 (
    .a(IR[5:0]), .b(6'b100000), .eq(comparator_8_eq));  // open: gt, lt
  and and_1 (SLT, comparator_7_eq, comparator_6_eq);
  and and_2 (ADD, comparator_6_eq, comparator_8_eq);
  nor nor_1 (OtherInstr, ADD, BEQ, SW, LW, ADDI, SLT, ERET);

  // Other names for the same wires on the sheet: FUNCT[5:0] = IR[5:0]; OP[5:0] = IR[31:26]

  // Notes on the sheet:
  //   指令译码器
endmodule

module \状态机  (
  input  LW,
  input  SW,
  input  BEQ,
  input  SLT,
  input  ADDI,
  input  ADD,
  input  ERET,
  input  IntR,
  input  S3,
  input  S2,
  input  S1,
  input  S0,
  output N3,
  output N2,
  output N1,
  output N0
);

  wire and_1_out, and_2_out, and_3_out, and_4_out, and_5_out, and_6_out, and_7_out, and_8_out, and_9_out,
       and_10_out, and_11_out, and_12_out, and_13_out, and_14_out, and_15_out, and_16_out, and_17_out,
       and_18_out, and_19_out, and_20_out, and_21_out, and_22_out, and_23_out, and_24_out, and_25_out,
       and_26_out, and_27_out, not_1_out, not_2_out, not_3_out, not_4_out, not_5_out, not_6_out, not_7_out,
       not_8_out, not_9_out, not_10_out, not_11_out, not_12_out, not_13_out, not_14_out, not_15_out,
       not_16_out, not_17_out, not_18_out, not_19_out, not_20_out, not_21_out, not_22_out, not_23_out,
       not_24_out, not_25_out, not_26_out, not_27_out, not_28_out, not_29_out, not_30_out, not_31_out,
       not_32_out, not_33_out, not_34_out, not_35_out, not_36_out, not_37_out, not_38_out, not_39_out,
       not_40_out, not_41_out, not_42_out, not_43_out, not_44_out, not_45_out, not_46_out, not_47_out,
       not_48_out, not_49_out, not_50_out, not_51_out, not_52_out, not_53_out, not_54_out, not_55_out,
       not_56_out, not_57_out, not_58_out, not_59_out, not_60_out, not_61_out, not_62_out;

  not not_1 (not_1_out, S3);
  not not_2 (not_2_out, S2);
  not not_3 (not_3_out, S1);
  not not_4 (not_4_out, S0);
  not not_5 (not_5_out, S2);
  not not_6 (not_6_out, S1);
  not not_7 (not_7_out, S3);
  not not_8 (not_8_out, S2);
  not not_9 (not_9_out, S3);
  not not_10 (not_10_out, S2);
  not not_11 (not_11_out, S3);
  not not_12 (not_12_out, S2);
  not not_13 (not_13_out, S3);
  not not_14 (not_14_out, S2);
  not not_15 (not_15_out, S3);
  not not_16 (not_16_out, S2);
  not not_17 (not_17_out, S3);
  not not_18 (not_18_out, S2);
  not not_19 (not_19_out, S3);
  not not_20 (not_20_out, S1);
  not not_21 (not_21_out, S0);
  not not_22 (not_22_out, S3);
  not not_23 (not_23_out, S1);
  not not_24 (not_24_out, S3);
  not not_25 (not_25_out, S0);
  not not_26 (not_26_out, S3);
  not not_27 (not_27_out, S2);
  not not_28 (not_28_out, S3);
  not not_29 (not_29_out, S2);
  not not_30 (not_30_out, S1);
  not not_31 (not_31_out, S3);
  not not_32 (not_32_out, S2);
  not not_33 (not_33_out, S0);
  not not_34 (not_34_out, S3);
  not not_35 (not_35_out, S2);
  not not_36 (not_36_out, S3);
  not not_37 (not_37_out, S2);
  not not_38 (not_38_out, S3);
  not not_39 (not_39_out, S2);
  not not_40 (not_40_out, S3);
  not not_41 (not_41_out, S1);
  not not_42 (not_42_out, S3);
  not not_43 (not_43_out, S0);
  not not_44 (not_44_out, S2);
  not not_45 (not_45_out, S1);
  not not_46 (not_46_out, S3);
  not not_47 (not_47_out, S2);
  not not_48 (not_48_out, S3);
  not not_49 (not_49_out, S2);
  not not_50 (not_50_out, S1);
  not not_51 (not_51_out, S0);
  not not_52 (not_52_out, S3);
  not not_53 (not_53_out, S2);
  not not_54 (not_54_out, S0);
  not not_55 (not_55_out, S3);
  not not_56 (not_56_out, S1);
  not not_57 (not_57_out, S0);
  not not_58 (not_58_out, S3);
  not not_59 (not_59_out, S0);
  not not_60 (not_60_out, S2);
  not not_61 (not_61_out, S1);
  not not_62 (not_62_out, S0);
  and and_1 (and_1_out, not_1_out, S2, S1, S0);
  and and_2 (and_2_out, S3, not_2_out, not_3_out, not_4_out, IntR);
  or or_1 (N3, and_1_out, and_2_out, and_3_out);
  and and_3 (and_3_out, S3, not_5_out, not_6_out, S0);
  and and_4 (and_4_out, not_7_out, not_8_out, S1, S0, LW);
  and and_5 (and_5_out, not_9_out, not_10_out, S1, S0, SW);
  and and_6 (and_6_out, not_11_out, not_12_out, S1, S0, BEQ);
  and and_7 (and_7_out, not_13_out, not_14_out, S1, S0, SLT);
  and and_8 (and_8_out, not_15_out, not_16_out, S1, S0, ADDI);
  and and_9 (and_9_out, not_17_out, not_18_out, S1, S0, ERET);
  and and_10 (and_10_out, not_19_out, S2, not_20_out, not_21_out);
  and and_11 (and_11_out, not_22_out, S2, not_23_out, S0);
  and and_12 (and_12_out, not_24_out, S2, S1, not_25_out);
  and and_13 (and_13_out, not_26_out, not_27_out, S1, S0, ADD);
  and and_14 (and_14_out, not_28_out, not_29_out, not_30_out, S0);
  and and_15 (and_15_out, not_31_out, not_32_out, S1, not_33_out);
  and and_16 (and_16_out, not_34_out, not_35_out, S1, S0, SLT);
  and and_17 (and_17_out, not_36_out, not_37_out, S1, S0, ADDI);
  and and_18 (and_18_out, not_38_out, not_39_out, S1, S0, ERET);
  and and_19 (and_19_out, not_40_out, S2, not_41_out, S0);
  and and_20 (and_20_out, not_42_out, S2, S1, not_43_out);
  and and_21 (and_21_out, S3, not_44_out, not_45_out, S0);
  and and_22 (and_22_out, not_46_out, not_47_out, S1, S0, ADD);
  and and_23 (and_23_out, not_48_out, not_49_out, not_50_out, not_51_out);
  and and_24 (and_24_out, not_52_out, not_53_out, S1, not_54_out);
  and and_25 (and_25_out, not_55_out, S2, not_56_out, not_57_out);
  and and_26 (and_26_out, not_58_out, S2, S1, not_59_out);
  and and_27 (and_27_out, S3, not_60_out, not_61_out, not_62_out, IntR);
  or or_2 (N2, and_4_out, and_5_out, and_6_out, and_7_out, and_8_out, and_9_out, and_10_out, and_11_out, and_12_out, and_13_out);
  or or_3 (N1, and_14_out, and_15_out, and_16_out, and_17_out, and_18_out, and_19_out, and_20_out, and_21_out, and_22_out);
  or or_4 (N0, and_23_out, and_24_out, and_25_out, and_26_out, and_27_out);
endmodule

module \输出函数  (
  input  S3,
  input  S2,
  input  S1,
  input  S0,
  output Mif,
  output Mcal,
  output Mex,
  output Mint,
  output T1,
  output T2,
  output T3,
  output T4
);

  wire and_1_out, and_2_out, and_3_out, and_4_out, and_5_out, and_6_out, and_7_out, and_8_out, and_9_out,
       and_10_out, and_11_out, and_12_out, and_13_out, and_14_out, and_15_out, and_16_out, and_17_out,
       and_18_out, and_19_out, and_20_out, and_21_out, not_1_out, not_2_out, not_3_out, not_4_out, not_5_out,
       not_6_out, not_7_out, not_8_out, not_9_out, not_10_out, not_11_out, not_12_out, not_13_out,
       not_14_out, not_15_out, not_16_out, not_17_out, not_18_out, not_19_out, not_20_out, not_21_out,
       not_22_out, not_23_out, not_24_out, not_25_out, not_26_out, not_27_out, not_28_out, not_29_out,
       not_30_out, not_31_out, not_32_out, not_33_out, not_34_out, not_35_out, not_36_out, not_37_out,
       not_38_out, not_39_out, not_40_out, not_41_out, not_42_out, not_43_out, not_44_out, not_45_out,
       not_46_out, not_47_out, not_48_out, not_49_out, not_50_out, not_51_out, not_52_out, not_53_out,
       not_54_out;

  not not_1 (not_1_out, S3);
  not not_2 (not_2_out, S2);
  not not_3 (not_3_out, S1);
  not not_4 (not_4_out, S0);
  not not_5 (not_5_out, S3);
  not not_6 (not_6_out, S2);
  not not_7 (not_7_out, S1);
  not not_8 (not_8_out, S3);
  not not_9 (not_9_out, S2);
  not not_10 (not_10_out, S0);
  not not_11 (not_11_out, S3);
  not not_12 (not_12_out, S2);
  not not_13 (not_13_out, S3);
  not not_14 (not_14_out, S1);
  not not_15 (not_15_out, S0);
  not not_16 (not_16_out, S3);
  not not_17 (not_17_out, S1);
  not not_18 (not_18_out, S3);
  not not_19 (not_19_out, S0);
  not not_20 (not_20_out, S3);
  not not_21 (not_21_out, S2);
  not not_22 (not_22_out, S1);
  not not_23 (not_23_out, S0);
  not not_24 (not_24_out, S2);
  not not_25 (not_25_out, S1);
  not not_26 (not_26_out, S2);
  not not_27 (not_27_out, S0);
  not not_28 (not_28_out, S3);
  not not_29 (not_29_out, S2);
  not not_30 (not_30_out, S1);
  not not_31 (not_31_out, S0);
  not not_32 (not_32_out, S3);
  not not_33 (not_33_out, S1);
  not not_34 (not_34_out, S0);
  not not_35 (not_35_out, S3);
  not not_36 (not_36_out, S0);
  not not_37 (not_37_out, S2);
  not not_38 (not_38_out, S1);
  not not_39 (not_39_out, S3);
  not not_40 (not_40_out, S2);
  not not_41 (not_41_out, S1);
  not not_42 (not_42_out, S3);
  not not_43 (not_43_out, S1);
  not not_44 (not_44_out, S3);
  not not_45 (not_45_out, S2);
  not not_46 (not_46_out, S0);
  not not_47 (not_47_out, S3);
  not not_48 (not_48_out, S2);
  not not_49 (not_49_out, S0);
  not not_50 (not_50_out, S2);
  not not_51 (not_51_out, S1);
  not not_52 (not_52_out, S0);
  not not_53 (not_53_out, S3);
  not not_54 (not_54_out, S2);
  and and_1 (and_1_out, not_1_out, not_2_out, not_3_out, not_4_out);
  and and_2 (and_2_out, not_5_out, not_6_out, not_7_out, S0);
  and and_3 (and_3_out, not_8_out, not_9_out, S1, not_10_out);
  and and_4 (and_4_out, not_11_out, not_12_out, S1, S0);
  and and_5 (and_5_out, not_13_out, S2, not_14_out, not_15_out);
  or or_1 (Mcal, and_5_out, and_6_out);
  and and_6 (and_6_out, not_16_out, S2, not_17_out, S0);
  and and_7 (and_7_out, not_18_out, S2, S1, not_19_out);
  or or_2 (Mex, and_7_out, and_8_out, and_9_out);
  and and_8 (and_8_out, not_20_out, S2, S1, S0);
  and and_9 (and_9_out, S3, not_21_out, not_22_out, not_23_out);
  and and_10 (and_10_out, S3, not_24_out, not_25_out, S0);
  or or_3 (Mint, and_10_out, and_11_out);
  and and_11 (and_11_out, S3, not_26_out, S1, not_27_out);
  and and_12 (and_12_out, not_28_out, not_29_out, not_30_out, not_31_out);
  and and_13 (and_13_out, not_32_out, S2, not_33_out, not_34_out);
  and and_14 (and_14_out, not_35_out, S2, S1, not_36_out);
  and and_15 (and_15_out, S3, not_37_out, not_38_out, S0);
  and and_16 (and_16_out, not_39_out, not_40_out, not_41_out, S0);
  and and_17 (and_17_out, not_42_out, S2, not_43_out, S0);
  and and_18 (and_18_out, not_44_out, S2, S1, S0);
  and and_19 (and_19_out, S3, not_45_out, S1, not_46_out);
  and and_20 (and_20_out, not_47_out, not_48_out, S1, not_49_out);
  or or_4 (T3, and_20_out, and_21_out);
  and and_21 (and_21_out, S3, not_50_out, not_51_out, not_52_out);
  and and_22 (T4, not_53_out, not_54_out, S1, S0);
  or or_5 (Mif, and_1_out, and_2_out, and_3_out, and_4_out);
  or or_6 (T1, and_12_out, and_13_out, and_14_out, and_15_out);
  or or_7 (T2, and_16_out, and_17_out, and_18_out, and_19_out);
endmodule

module \硬布线控制器组合逻辑单元  (
  input  SLT,
  input  ADDI,
  input  LW,
  input  SW,
  input  BEQ,
  input  ADD,
  input  Mif,
  input  Mcal,
  input  Mex,
  input  T1,
  input  T2,
  input  T3,
  input  T4,
  input  EQUAL,
  output Pcout,
  output DRout,
  output Zout,
  output Rout,
  output IRiout,
  output IRaout,
  output DREout,
  output Pcin,
  output ARin,
  output DREin,
  output DRin,
  output Xin,
  output Rin,
  output IRin,
  output PSWin,
  output RegTgt,
  output RegDst,
  output Add_2,
  output Add4,
  output Slt_2,
  output READ,
  output WRITE
);

  wire and_1_out, and_2_out, and_3_out, and_4_out, and_5_out, and_6_out, and_7_out, and_8_out, and_9_out,
       and_10_out, and_11_out, and_12_out, and_13_out, and_14_out, and_15_out, and_16_out, and_17_out,
       and_18_out, and_19_out, and_20_out, and_21_out, and_22_out, and_23_out, and_24_out, and_27_out,
       and_28_out, and_29_out, and_30_out, and_31_out, and_32_out, and_33_out, and_35_out, and_36_out,
       and_37_out, and_38_out, and_39_out, and_40_out, and_41_out, and_42_out, and_43_out, and_44_out,
       and_45_out, and_46_out, and_49_out, and_50_out, and_51_out, and_52_out, and_53_out, and_54_out,
       and_55_out, and_56_out, and_57_out, and_58_out, and_59_out, and_62_out, and_63_out;

  and and_1 (and_1_out, Mif, T1);
  and and_2 (and_2_out, BEQ, Mex, T1);
  and and_3 (and_3_out, Mif, T4);
  and and_4 (and_4_out, LW, Mex, T3);
  and and_5 (and_5_out, Mif, T3);
  and and_6 (and_6_out, Mex, T1, LW);
  and and_7 (and_7_out, Mex, T1, SW);
  and and_8 (and_8_out, Mex, T3, BEQ, EQUAL);
  and and_9 (and_9_out, Mex, T3, SLT);
  and and_10 (and_10_out, Mex, T3, ADDI);
  and and_11 (and_11_out, Mex, T3, ADD);
  and and_12 (and_12_out, Mcal, T1, LW);
  and and_13 (and_13_out, Mcal, T1, SW);
  and and_14 (and_14_out, Mex, T2, SW);
  and and_15 (and_15_out, Mcal, T1, BEQ);
  and and_16 (and_16_out, Mcal, T2, BEQ);
  and and_17 (and_17_out, Mex, T1, SLT);
  and and_18 (and_18_out, Mex, T2, SLT);
  and and_19 (and_19_out, Mex, T1, ADDI);
  and and_20 (and_20_out, Mex, T1, ADD);
  and and_21 (and_21_out, Mex, T2, ADD);
  and and_22 (and_22_out, SW, Mcal, T2);
  and and_23 (and_23_out, LW, Mcal, T2);
  and and_24 (and_24_out, ADDI, Mex, T2);
  and and_25 (IRaout, BEQ, Mex, T2);
  and and_26 (DREout, SW, Mex, T3);
  and and_27 (and_27_out, Mif, T3);
  and and_28 (and_28_out, BEQ, Mex, T3, EQUAL);
  and and_29 (and_29_out, Mif, T1);
  and and_30 (and_30_out, SW, Mex, T1);
  and and_31 (and_31_out, LW, Mex, T1);
  and and_32 (and_32_out, Mif, T3);
  and and_33 (and_33_out, LW, Mex, T2);
  and and_34 (DRin, SW, Mex, T2);
  and and_35 (and_35_out, Mif, T1);
  and and_36 (and_36_out, Mcal, T1, LW);
  and and_37 (and_37_out, Mcal, T1, SW);
  and and_38 (and_38_out, Mcal, T1, BEQ);
  and and_39 (and_39_out, Mex, T1, BEQ);
  and and_40 (and_40_out, Mex, T1, SLT);
  and and_41 (and_41_out, Mex, T1, ADDI);
  and and_42 (and_42_out, Mex, T1, ADD);
  and and_43 (and_43_out, Mex, T3, LW);
  and and_44 (and_44_out, Mex, T3, SLT);
  and and_45 (and_45_out, Mex, T3, ADDI);
  and and_46 (and_46_out, Mex, T3, ADD);
  and and_47 (IRin, Mif, T4);
  and and_48 (PSWin, BEQ, Mcal, T2);
  and and_49 (and_49_out, Mex, T2, SW);
  and and_50 (and_50_out, Mcal, T2, BEQ);
  and and_51 (and_51_out, Mex, T2, SLT);
  and and_52 (and_52_out, Mex, T2, ADD);
  and and_53 (and_53_out, Mex, T3, SLT);
  and and_54 (and_54_out, Mex, T3, ADD);
  and and_55 (and_55_out, Mcal, T2, LW);
  and and_56 (and_56_out, Mcal, T2, SW);
  and and_57 (and_57_out, Mex, T2, BEQ);
  and and_58 (and_58_out, Mex, T2, ADDI);
  and and_59 (and_59_out, Mex, T2, ADD);
  and and_60 (Add4, Mif, T2);
  and and_61 (Slt_2, SLT, Mex, T2);
  and and_62 (and_62_out, Mif, T3);
  and and_63 (and_63_out, LW, Mex, T2);
  and and_64 (WRITE, SW, Mex, T3);
  or or_1 (Pcout, and_1_out, and_2_out);
  or or_2 (DRout, and_3_out, and_4_out);
  or or_3 (Zout, and_5_out, and_6_out, and_7_out, and_8_out, and_9_out, and_10_out, and_11_out);
  or or_4 (IRiout, and_22_out, and_23_out, and_24_out);
  or or_5 (Pcin, and_27_out, and_28_out);
  or or_6 (ARin, and_29_out, and_30_out, and_31_out);
  or or_7 (DREin, and_32_out, and_33_out);
  or or_8 (Xin, and_35_out, and_36_out, and_37_out, and_38_out, and_39_out, and_40_out, and_41_out, and_42_out);
  or or_9 (Rin, and_43_out, and_44_out, and_45_out, and_46_out);
  or or_10 (RegTgt, and_49_out, and_50_out, and_51_out, and_52_out);
  or or_11 (RegDst, and_53_out, and_54_out);
  or or_12 (Add_2, and_55_out, and_56_out, and_57_out, and_58_out, and_59_out);
  or or_13 (READ, and_62_out, and_63_out);
  or or_14 (Rout, and_12_out, and_13_out, and_14_out, and_15_out, and_16_out, and_17_out, and_18_out, and_19_out, and_20_out, and_21_out);
endmodule

module \中断控制信号  (
  input  ERET,
  input  Mex,
  input  Mint,
  input  T1,
  input  T2,
  output Pcout,
  output PCin,
  output EPCout,
  output EPCin,
  output Addrout,
  output STI,
  output CLI
);

  wire and_2_out, and_3_out;

  and and_1 (Pcout, Mint, T1);
  and and_2 (and_2_out, Mint, T2);
  and and_3 (and_3_out, ERET, Mex, T1);
  and and_4 (EPCout, ERET, Mex, T1);
  and and_5 (EPCin, Mint, T1);
  and and_6 (Addrout, Mint, T2);
  and and_7 (STI, ERET, Mex, T1);
  and and_8 (CLI, Mint, T1);
  or or_1 (PCin, and_2_out, and_3_out);
endmodule

// ALU
module MIPS_ALU (
  input  ADD,
  input  ADD4,
  input  [31:0] X,
  input  [31:0] Y,
  input  SUB,
  input  SLT,
  output Equal,
  output [31:0] Result
);

  wire [0:0] comparator_1_lt;
  wire [1:0] priority_encoder_1_out;
  wire [31:0] adder_1_out, adder_2_out, subtractor_1_out;

  Pull_Resistor #(.pull(0)) pull_resistor_1 (.node(Y));
  Adder #(.width(32)) adder_1 (.a(X), .b(Y), .out(adder_1_out));  // open: cin, cout
  Adder #(.width(32)) adder_2 (.a(X), .b(32'h4), .out(adder_2_out));  // open: cin, cout
  Subtractor #(.width(32)) subtractor_1 (.a(X), .b(Y), .out(subtractor_1_out));  // open: bin, bout
  Comparator #(.width(32), .mode("twosComplement")) comparator_1 (
    .a(X), .b(Y), .eq(Equal), .lt(comparator_1_lt[0]));  // open: gt
  Priority_Encoder #(.select(2), .disabled("Z")) priority_encoder_1 (
    .in0(ADD), .in1(ADD4), .in2(SUB), .in3(SLT), .out(priority_encoder_1_out));  // open: gs, en_out, en_in
  Pull_Resistor #(.pull(0)) pull_resistor_2 (.node(priority_encoder_1_out));
  Multiplexer #(.select(2), .width(32), .disabled("Z"), .enable("false")) multiplexer_1 (
    .in0(adder_1_out), .in1(adder_2_out), .in2(subtractor_1_out), .in3({{31{1'b0}}, comparator_1_lt[0]}),
    .out(Result), .sel(priority_encoder_1_out));

  // Notes on the sheet:
  //   输入引脚
  //   算术逻辑单元ALU
  //   输出引脚
endmodule

module \中断控制器  (
  input  CLK,
  input  Clr,
  input  Key0,
  input  [3:0] EDU_TEST,
  input  Key1,
  input  Key2,
  input  Key3,
  output IR0W,
  output IR1W,
  output [1:0] IntNo,
  output IntR,
  output IR2W,
  output IR3W
);

  wire and_1_out, and_2_out, and_3_out, and_4_out, Clr0, Clr1, Clr2, Clr3, d_ff_1_q, d_ff_2_q, d_ff_3_q,
       d_ff_4_q, IR0_q, IR1_q, IR2_q, IR3_q, or_1_out, or_3_out, or_5_out, or_7_out, or_9_out, or_10_out,
       or_11_out, or_12_out;

  or or_1 (or_1_out, Key0, EDU_TEST[3]);
  or or_2 (IR0W, IR0_q, d_ff_2_q);
  or or_3 (or_3_out, Key1, EDU_TEST[2]);
  or or_4 (IR1W, IR1_q, d_ff_3_q);
  or or_5 (or_5_out, Key2, EDU_TEST[1]);
  D_Flip_Flop #(.trigger("rising"), .Pre_Clr_Positions("LEGACY"), .NegatePresetClear("false"), .enable("true"), .NewFFLayout("false")) d_ff_1 (
    .clk(or_5_out), .D(1'b1), .Q(d_ff_1_q), .reset(IR2_q));  // open: Qn, preset, en
  or or_6 (IR2W, IR2_q, d_ff_1_q);
  or or_7 (or_7_out, Key3, EDU_TEST[0]);
  or or_8 (IR3W, IR3_q, d_ff_4_q);
  D_Flip_Flop #(.trigger("rising"), .Pre_Clr_Positions("LEGACY"), .NegatePresetClear("false"), .enable("true"), .NewFFLayout("false")) d_ff_2 (
    .clk(or_1_out), .D(1'b1), .Q(d_ff_2_q), .reset(IR0_q));  // open: Qn, preset, en
  D_Flip_Flop #(.trigger("rising"), .Pre_Clr_Positions("LEGACY"), .NegatePresetClear("false"), .enable("true"), .NewFFLayout("false")) d_ff_3 (
    .clk(or_3_out), .D(1'b1), .Q(d_ff_3_q), .reset(IR1_q));  // open: Qn, preset, en
  D_Flip_Flop #(.trigger("rising"), .Pre_Clr_Positions("LEGACY"), .NegatePresetClear("false"), .enable("true"), .NewFFLayout("false")) d_ff_4 (
    .clk(or_7_out), .D(1'b1), .Q(d_ff_4_q), .reset(IR3_q));  // open: Qn, preset, en
  Pull_Resistor #(.pull(0)) pull_resistor_1 (.node(EDU_TEST));
  or or_9 (or_9_out, d_ff_2_q, IR0_q);
  and and_1 (and_1_out, or_9_out, ~Clr0);  // AND_Gate
  or or_10 (or_10_out, d_ff_3_q, IR1_q);
  and and_2 (and_2_out, or_10_out, ~Clr1);  // AND_Gate
  or or_11 (or_11_out, d_ff_1_q, IR2_q);
  and and_3 (and_3_out, or_11_out, ~Clr2);  // AND_Gate
  or or_12 (or_12_out, d_ff_4_q, IR3_q);
  and and_4 (and_4_out, or_12_out, ~Clr3);  // AND_Gate
  D_Flip_Flop #(.trigger("rising"), .Pre_Clr_Positions("LEGACY"), .NegatePresetClear("false"), .enable("true"), .NewFFLayout("false")) IR0 (
    .clk(CLK), .D(and_1_out), .Q(IR0_q));  // open: Qn, preset, en, reset
  D_Flip_Flop #(.trigger("rising"), .Pre_Clr_Positions("LEGACY"), .NegatePresetClear("false"), .enable("true"), .NewFFLayout("false")) IR1 (
    .clk(CLK), .D(and_2_out), .Q(IR1_q));  // open: Qn, preset, en, reset
  D_Flip_Flop #(.trigger("rising"), .Pre_Clr_Positions("LEGACY"), .NegatePresetClear("false"), .enable("true"), .NewFFLayout("false")) IR2 (
    .clk(CLK), .D(and_3_out), .Q(IR2_q));  // open: Qn, preset, en, reset
  D_Flip_Flop #(.trigger("rising"), .Pre_Clr_Positions("LEGACY"), .NegatePresetClear("false"), .enable("true"), .NewFFLayout("false")) IR3 (
    .clk(CLK), .D(and_4_out), .Q(IR3_q));  // open: Qn, preset, en, reset
  Priority_Encoder #(.select(2), .disabled("Z")) priority_encoder_1 (
    .in0(IR0_q), .in1(IR1_q), .in2(IR2_q), .in3(IR3_q), .out(IntNo), .gs(IntR));  // open: en_out, en_in
  Decoder #(.select(2), .tristate("false"), .disabled(0), .enable("true")) decoder_1 (
    .out0(Clr0), .out1(Clr1), .out2(Clr2), .out3(Clr3), .sel(IntNo), .en(Clr));

  // Other names for the same wires on the sheet: EDU_INT3 = EDU_TEST[0]; EDU_INT2 = EDU_TEST[1];
  //   EDU_INT1 = EDU_TEST[2]; EDU_INT0 = EDU_TEST[3]

  // Notes on the sheet:
  //   中断等待
  //   中断等待
  //   中断等待
  //   中断等待
  //   Reset 
  //   Reset 
  //   Reset 
  //   Reset 
  //   中断控制器
  //   中断优先编码器
endmodule

module \测试  (
  input  [4:0] in_1
);

  wire [6:0] \中断控制信号_1_cli ;

  // Probe on in_1
  // Probe on \中断控制信号_1_cli 
  \中断控制信号  \u_中断控制信号_1  (
    .ERET(in_1[4]), .Mex(in_1[3]), .Mint(in_1[2]), .T1(in_1[1]), .T2(in_1[0]), .Pcout(\中断控制信号_1_cli [6]),
    .PCin(\中断控制信号_1_cli [5]), .EPCout(\中断控制信号_1_cli [4]), .EPCin(\中断控制信号_1_cli [3]),
    .Addrout(\中断控制信号_1_cli [2]), .STI(\中断控制信号_1_cli [1]), .CLI(\中断控制信号_1_cli [0]));
endmodule
